// Logisim project 1GB RAM.circ as structural Verilog: 6 circuits, main circuit manual adress 2 GIG RAM
module _1GB_RAM (
  input  Power,
  input  Reset,
  input  [31:0] Data_in,
  input  [27:0] Address,
  input  Write,
  output [31:0] Data_out,
  output Address_Contains_Data
);

  wire clock_1_out, decoder_1_out0, decoder_1_out1, decoder_1_out2, decoder_1_out3, decoder_1_out4,
       decoder_1_out5, decoder_1_out6, decoder_1_out7, decoder_1_out8, decoder_1_out9, decoder_1_out10,
       decoder_1_out11, decoder_1_out12, decoder_1_out13, decoder_1_out14, decoder_1_out15, not_1_out,
       not_2_out, not_3_out, not_4_out, not_5_out, not_6_out, not_7_out, not_8_out, not_9_out, not_10_out,
       not_11_out, not_12_out, not_13_out, not_14_out, not_15_out, not_16_out, not_17_out, not_18_out,
       or_1_out, or_3_out, or_4_out, or_5_out, or_6_out, or_7_out, or_8_out, or_9_out, or_10_out, or_11_out,
       or_12_out, or_13_out, or_14_out, or_15_out, or_16_out, or_17_out, or_18_out, or_20_out,
       pull_resistor_1_node, pull_resistor_2_node, ram_1_data, ram_2_data, ram_3_data, ram_4_data,
       ram_5_data, ram_6_data, ram_7_data, ram_8_data, ram_9_data, ram_10_data, ram_11_data, ram_12_data,
       ram_13_data, ram_14_data, ram_15_data, ram_16_data, register_1_q, register_2_q, register_3_q,
       register_4_q, register_5_q, register_6_q, register_7_q, register_8_q, register_9_q, register_10_q,
       register_11_q, register_12_q, register_13_q, register_14_q, register_15_q, register_16_q, xor_1_out;
  wire [3:0] bitselector_2_out, buffer_2_out;
  wire [23:0] bitselector_1_out, buffer_1_out;
  wire [31:0] ram_17_data, ram_18_data, ram_19_data, ram_20_data, ram_21_data, ram_22_data, ram_23_data,
       ram_24_data, ram_25_data, ram_26_data, ram_27_data, ram_28_data, ram_29_data, ram_30_data,
       ram_31_data, ram_32_data, register_17_q, register_18_q, register_19_q, register_20_q, register_21_q,
       register_22_q, register_23_q, register_24_q, register_25_q, register_26_q, register_27_q,
       register_28_q, register_29_q, register_30_q, register_31_q, register_32_q;

  Pull_Resistor pull_resistor_1 (.node(pull_resistor_1_node));
  Pull_Resistor pull_resistor_2 (.node(pull_resistor_2_node));
  Clock clock_1 (.out(clock_1_out));
  not not_1 (not_1_out, Write);
  xor xor_1 (xor_1_out, not_1_out, Write);
  or or_1 (or_1_out, ~Power, Reset);  // OR_Gate
  assign pull_resistor_1_node = xor_1_out ? Write : 1'bz;  // Controlled_Buffer controlled_buffer_1
  assign pull_resistor_2_node = xor_1_out ? not_1_out : 1'bz;  // Controlled_Buffer controlled_buffer_2
  or or_2 (Address_Contains_Data, register_16_q, register_15_q, register_14_q, register_13_q, register_12_q, register_11_q, register_10_q, register_9_q, register_7_q, register_6_q, register_5_q, register_4_q, register_3_q, register_2_q, register_1_q, register_8_q);
  assign buffer_1_out = bitselector_1_out;  // Buffer buffer_1, 24 bits wide
  BitSelector #(.width(28), .group(24)) bitselector_1 (.in(Address), .out(bitselector_1_out), .sel(1'b0));
  assign buffer_2_out = bitselector_2_out;  // Buffer buffer_2, 4 bits wide
  BitSelector #(.width(28), .group(4)) bitselector_2 (.in(Address), .out(bitselector_2_out), .sel(3'b110));
  Decoder #(.select(4), .enable("false")) decoder_1 (
    .out0(decoder_1_out0), .out1(decoder_1_out1), .out2(decoder_1_out2), .out3(decoder_1_out3),
    .out4(decoder_1_out4), .out5(decoder_1_out5), .out6(decoder_1_out6), .out7(decoder_1_out7),
    .out8(decoder_1_out8), .out9(decoder_1_out9), .out10(decoder_1_out10), .out11(decoder_1_out11),
    .out12(decoder_1_out12), .out13(decoder_1_out13), .out14(decoder_1_out14), .out15(decoder_1_out15),
    .sel(buffer_2_out));
  not not_2 (not_2_out, pull_resistor_1_node);
  RAM #(.addrWidth(24), .dataWidth(1), .bus("separate")) ram_1 (
    .addr(buffer_1_out), .din(or_20_out), .data(ram_1_data), .str(pull_resistor_1_node),
    .sel(decoder_1_out0), .clk(clock_1_out), .ld(not_2_out), .clr(or_1_out));
  RAM #(.addrWidth(24), .dataWidth(1), .bus("separate")) ram_2 (
    .addr(buffer_1_out), .din(or_20_out), .data(ram_2_data), .str(pull_resistor_1_node),
    .sel(decoder_1_out1), .clk(clock_1_out), .ld(not_2_out), .clr(or_1_out));
  RAM #(.addrWidth(24), .dataWidth(1), .bus("separate")) ram_3 (
    .addr(buffer_1_out), .din(or_20_out), .data(ram_3_data), .str(pull_resistor_1_node),
    .sel(decoder_1_out2), .clk(clock_1_out), .ld(not_2_out), .clr(or_1_out));
  RAM #(.addrWidth(24), .dataWidth(1), .bus("separate")) ram_4 (
    .addr(buffer_1_out), .din(or_20_out), .data(ram_4_data), .str(pull_resistor_1_node),
    .sel(decoder_1_out3), .clk(clock_1_out), .ld(not_2_out), .clr(or_1_out));
  RAM #(.addrWidth(24), .dataWidth(1), .bus("separate")) ram_5 (
    .addr(buffer_1_out), .din(or_20_out), .data(ram_5_data), .str(pull_resistor_1_node),
    .sel(decoder_1_out4), .clk(clock_1_out), .ld(not_2_out), .clr(or_1_out));
  RAM #(.addrWidth(24), .dataWidth(1), .bus("separate")) ram_6 (
    .addr(buffer_1_out), .din(or_20_out), .data(ram_6_data), .str(pull_resistor_1_node),
    .sel(decoder_1_out5), .clk(clock_1_out), .ld(not_2_out), .clr(or_1_out));
  RAM #(.addrWidth(24), .dataWidth(1), .bus("separate")) ram_7 (
    .addr(buffer_1_out), .din(or_20_out), .data(ram_7_data), .str(pull_resistor_1_node),
    .sel(decoder_1_out6), .clk(clock_1_out), .ld(not_2_out), .clr(or_1_out));
  RAM #(.addrWidth(24), .dataWidth(1), .bus("separate")) ram_8 (
    .addr(buffer_1_out), .din(or_20_out), .data(ram_8_data), .str(pull_resistor_1_node),
    .sel(decoder_1_out7), .clk(clock_1_out), .ld(not_2_out), .clr(or_1_out));
  RAM #(.addrWidth(24), .dataWidth(1), .bus("separate")) ram_9 (
    .addr(buffer_1_out), .din(or_20_out), .data(ram_9_data), .str(pull_resistor_1_node),
    .sel(decoder_1_out8), .clk(clock_1_out), .ld(not_2_out), .clr(or_1_out));
  RAM #(.addrWidth(24), .dataWidth(1), .bus("separate")) ram_10 (
    .addr(buffer_1_out), .din(or_20_out), .data(ram_10_data), .str(pull_resistor_1_node),
    .sel(decoder_1_out9), .clk(clock_1_out), .ld(not_2_out), .clr(or_1_out));
  RAM #(.addrWidth(24), .dataWidth(1), .bus("separate")) ram_11 (
    .addr(buffer_1_out), .din(or_20_out), .data(ram_11_data), .str(pull_resistor_1_node),
    .sel(decoder_1_out10), .clk(clock_1_out), .ld(not_2_out), .clr(or_1_out));
  RAM #(.addrWidth(24), .dataWidth(1), .bus("separate")) ram_12 (
    .addr(buffer_1_out), .din(or_20_out), .data(ram_12_data), .str(pull_resistor_1_node),
    .sel(decoder_1_out11), .clk(clock_1_out), .ld(not_2_out), .clr(or_1_out));
  RAM #(.addrWidth(24), .dataWidth(1), .bus("separate")) ram_13 (
    .addr(buffer_1_out), .din(or_20_out), .data(ram_13_data), .str(pull_resistor_1_node),
    .sel(decoder_1_out12), .clk(clock_1_out), .ld(not_2_out), .clr(or_1_out));
  RAM #(.addrWidth(24), .dataWidth(1), .bus("separate")) ram_14 (
    .addr(buffer_1_out), .din(or_20_out), .data(ram_14_data), .str(pull_resistor_1_node),
    .sel(decoder_1_out13), .clk(clock_1_out), .ld(not_2_out), .clr(or_1_out));
  RAM #(.addrWidth(24), .dataWidth(1), .bus("separate")) ram_15 (
    .addr(buffer_1_out), .din(or_20_out), .data(ram_15_data), .str(pull_resistor_1_node),
    .sel(decoder_1_out14), .clk(clock_1_out), .ld(not_2_out), .clr(or_1_out));
  RAM #(.addrWidth(24), .dataWidth(1), .bus("separate")) ram_16 (
    .addr(buffer_1_out), .din(or_20_out), .data(ram_16_data), .str(pull_resistor_1_node),
    .sel(decoder_1_out15), .clk(clock_1_out), .ld(not_2_out), .clr(or_1_out));
  Register #(.width(1), .trigger("high")) register_1 (
    .D(ram_1_data), .en(decoder_1_out0), .Q(register_1_q), .clk(clock_1_out), .clr(or_1_out));
  Register #(.width(1), .trigger("high")) register_2 (
    .D(ram_2_data), .en(decoder_1_out1), .Q(register_2_q), .clk(clock_1_out), .clr(or_1_out));
  Register #(.width(1), .trigger("high")) register_3 (
    .D(ram_3_data), .en(decoder_1_out2), .Q(register_3_q), .clk(clock_1_out), .clr(or_1_out));
  Register #(.width(1), .trigger("high")) register_4 (
    .D(ram_4_data), .en(decoder_1_out3), .Q(register_4_q), .clk(clock_1_out), .clr(or_1_out));
  Register #(.width(1), .trigger("high")) register_5 (
    .D(ram_5_data), .en(decoder_1_out4), .Q(register_5_q), .clk(clock_1_out), .clr(or_1_out));
  Register #(.width(1), .trigger("high")) register_6 (
    .D(ram_6_data), .en(decoder_1_out5), .Q(register_6_q), .clk(clock_1_out), .clr(or_1_out));
  Register #(.width(1), .trigger("high")) register_7 (
    .D(ram_7_data), .en(decoder_1_out6), .Q(register_7_q), .clk(clock_1_out), .clr(or_1_out));
  Register #(.width(1), .trigger("high")) register_8 (
    .D(ram_8_data), .en(decoder_1_out7), .Q(register_8_q), .clk(clock_1_out), .clr(or_1_out));
  Register #(.width(1), .trigger("high")) register_9 (
    .D(ram_9_data), .en(decoder_1_out8), .Q(register_9_q), .clk(clock_1_out), .clr(or_1_out));
  Register #(.width(1), .trigger("high")) register_10 (
    .D(ram_10_data), .en(decoder_1_out9), .Q(register_10_q), .clk(clock_1_out), .clr(or_1_out));
  Register #(.width(1), .trigger("high")) register_11 (
    .D(ram_11_data), .en(decoder_1_out10), .Q(register_11_q), .clk(clock_1_out), .clr(or_1_out));
  Register #(.width(1), .trigger("high")) register_12 (
    .D(ram_12_data), .en(decoder_1_out11), .Q(register_12_q), .clk(clock_1_out), .clr(or_1_out));
  Register #(.width(1), .trigger("high")) register_13 (
    .D(ram_13_data), .en(decoder_1_out12), .Q(register_13_q), .clk(clock_1_out), .clr(or_1_out));
  Register #(.width(1), .trigger("high")) register_14 (
    .D(ram_14_data), .en(decoder_1_out13), .Q(register_14_q), .clk(clock_1_out), .clr(or_1_out));
  Register #(.width(1), .trigger("high")) register_15 (
    .D(ram_15_data), .en(decoder_1_out14), .Q(register_15_q), .clk(clock_1_out), .clr(or_1_out));
  Register #(.width(1), .trigger("high")) register_16 (
    .D(ram_16_data), .en(decoder_1_out15), .Q(register_16_q), .clk(clock_1_out), .clr(or_1_out));
  RAM #(.addrWidth(24), .dataWidth(32), .bus("separate")) ram_17 (
    .addr(buffer_1_out), .din(Data_in), .data(ram_17_data), .str(pull_resistor_1_node), .sel(decoder_1_out0),
    .clk(clock_1_out), .ld(pull_resistor_2_node), .clr(or_1_out));
  RAM #(.addrWidth(24), .dataWidth(32), .bus("separate")) ram_18 (
    .addr(buffer_1_out), .din(Data_in), .data(ram_18_data), .str(pull_resistor_1_node), .sel(decoder_1_out1),
    .clk(clock_1_out), .ld(pull_resistor_2_node), .clr(or_1_out));
  RAM #(.addrWidth(24), .dataWidth(32), .bus("separate")) ram_19 (
    .addr(buffer_1_out), .din(Data_in), .data(ram_19_data), .str(pull_resistor_1_node), .sel(decoder_1_out2),
    .clk(clock_1_out), .ld(pull_resistor_2_node), .clr(or_1_out));
  RAM #(.addrWidth(24), .dataWidth(32), .bus("separate")) ram_20 (
    .addr(buffer_1_out), .din(Data_in), .data(ram_20_data), .str(pull_resistor_1_node), .sel(decoder_1_out3),
    .clk(clock_1_out), .ld(pull_resistor_2_node), .clr(or_1_out));
  RAM #(.addrWidth(24), .dataWidth(32), .bus("separate")) ram_21 (
    .addr(buffer_1_out), .din(Data_in), .data(ram_21_data), .str(pull_resistor_1_node), .sel(decoder_1_out4),
    .clk(clock_1_out), .ld(pull_resistor_2_node), .clr(or_1_out));
  RAM #(.addrWidth(24), .dataWidth(32), .bus("separate")) ram_22 (
    .addr(buffer_1_out), .din(Data_in), .data(ram_22_data), .str(pull_resistor_1_node), .sel(decoder_1_out5),
    .clk(clock_1_out), .ld(pull_resistor_2_node), .clr(or_1_out));
  RAM #(.addrWidth(24), .dataWidth(32), .bus("separate")) ram_23 (
    .addr(buffer_1_out), .din(Data_in), .data(ram_23_data), .str(pull_resistor_1_node), .sel(decoder_1_out6),
    .clk(clock_1_out), .ld(pull_resistor_2_node), .clr(or_1_out));
  RAM #(.addrWidth(24), .dataWidth(32), .bus("separate")) ram_24 (
    .addr(buffer_1_out), .din(Data_in), .data(ram_24_data), .str(pull_resistor_1_node), .sel(decoder_1_out7),
    .clk(clock_1_out), .ld(pull_resistor_2_node), .clr(or_1_out));
  RAM #(.addrWidth(24), .dataWidth(32), .bus("separate")) ram_25 (
    .addr(buffer_1_out), .din(Data_in), .data(ram_25_data), .str(pull_resistor_1_node), .sel(decoder_1_out8),
    .clk(clock_1_out), .ld(pull_resistor_2_node), .clr(or_1_out));
  RAM #(.addrWidth(24), .dataWidth(32), .bus("separate")) ram_26 (
    .addr(buffer_1_out), .din(Data_in), .data(ram_26_data), .str(pull_resistor_1_node), .sel(decoder_1_out9),
    .clk(clock_1_out), .ld(pull_resistor_2_node), .clr(or_1_out));
  RAM #(.addrWidth(24), .dataWidth(32), .bus("separate")) ram_27 (
    .addr(buffer_1_out), .din(Data_in), .data(ram_27_data), .str(pull_resistor_1_node),
    .sel(decoder_1_out10), .clk(clock_1_out), .ld(pull_resistor_2_node), .clr(or_1_out));
  RAM #(.addrWidth(24), .dataWidth(32), .bus("separate")) ram_28 (
    .addr(buffer_1_out), .din(Data_in), .data(ram_28_data), .str(pull_resistor_1_node),
    .sel(decoder_1_out11), .clk(clock_1_out), .ld(pull_resistor_2_node), .clr(or_1_out));
  RAM #(.addrWidth(24), .dataWidth(32), .bus("separate")) ram_29 (
    .addr(buffer_1_out), .din(Data_in), .data(ram_29_data), .str(pull_resistor_1_node),
    .sel(decoder_1_out12), .clk(clock_1_out), .ld(pull_resistor_2_node), .clr(or_1_out));
  RAM #(.addrWidth(24), .dataWidth(32), .bus("separate")) ram_30 (
    .addr(buffer_1_out), .din(Data_in), .data(ram_30_data), .str(pull_resistor_1_node),
    .sel(decoder_1_out13), .clk(clock_1_out), .ld(pull_resistor_2_node), .clr(or_1_out));
  RAM #(.addrWidth(24), .dataWidth(32), .bus("separate")) ram_31 (
    .addr(buffer_1_out), .din(Data_in), .data(ram_31_data), .str(pull_resistor_1_node),
    .sel(decoder_1_out14), .clk(clock_1_out), .ld(pull_resistor_2_node), .clr(or_1_out));
  RAM #(.addrWidth(24), .dataWidth(32), .bus("separate")) ram_32 (
    .addr(buffer_1_out), .din(Data_in), .data(ram_32_data), .str(pull_resistor_1_node),
    .sel(decoder_1_out15), .clk(clock_1_out), .ld(pull_resistor_2_node), .clr(or_1_out));
  Register #(.width(32), .trigger("high")) register_17 (
    .D(ram_17_data), .en(decoder_1_out0), .Q(register_17_q), .clk(clock_1_out), .clr(or_3_out));
  or or_3 (or_3_out, not_3_out, or_1_out);
  not not_3 (not_3_out, decoder_1_out0);
  Register #(.width(32), .trigger("high")) register_18 (
    .D(ram_18_data), .en(decoder_1_out1), .Q(register_18_q), .clk(clock_1_out), .clr(or_4_out));
  or or_4 (or_4_out, not_4_out, or_1_out);
  not not_4 (not_4_out, decoder_1_out1);
  Register #(.width(32), .trigger("high")) register_19 (
    .D(ram_19_data), .en(decoder_1_out2), .Q(register_19_q), .clk(clock_1_out), .clr(or_5_out));
  or or_5 (or_5_out, not_5_out, or_1_out);
  not not_5 (not_5_out, decoder_1_out2);
  Register #(.width(32), .trigger("high")) register_20 (
    .D(ram_20_data), .en(decoder_1_out3), .Q(register_20_q), .clk(clock_1_out), .clr(or_6_out));
  or or_6 (or_6_out, not_6_out, or_1_out);
  not not_6 (not_6_out, decoder_1_out3);
  Register #(.width(32), .trigger("high")) register_21 (
    .D(ram_21_data), .en(decoder_1_out4), .Q(register_21_q), .clk(clock_1_out), .clr(or_7_out));
  or or_7 (or_7_out, not_7_out, or_1_out);
  not not_7 (not_7_out, decoder_1_out4);
  Register #(.width(32), .trigger("high")) register_22 (
    .D(ram_22_data), .en(decoder_1_out5), .Q(register_22_q), .clk(clock_1_out), .clr(or_8_out));
  or or_8 (or_8_out, not_8_out, or_1_out);
  not not_8 (not_8_out, decoder_1_out5);
  Register #(.width(32), .trigger("high")) register_23 (
    .D(ram_23_data), .en(decoder_1_out6), .Q(register_23_q), .clk(clock_1_out), .clr(or_9_out));
  or or_9 (or_9_out, not_9_out, or_1_out);
  not not_9 (not_9_out, decoder_1_out6);
  Register #(.width(32), .trigger("high")) register_24 (
    .D(ram_24_data), .en(decoder_1_out7), .Q(register_24_q), .clk(clock_1_out), .clr(or_10_out));
  or or_10 (or_10_out, not_10_out, or_1_out);
  not not_10 (not_10_out, decoder_1_out7);
  Register #(.width(32), .trigger("high")) register_25 (
    .D(ram_25_data), .en(decoder_1_out8), .Q(register_25_q), .clk(clock_1_out), .clr(or_11_out));
  or or_11 (or_11_out, not_11_out, or_1_out);
  not not_11 (not_11_out, decoder_1_out8);
  Register #(.width(32), .trigger("high")) register_26 (
    .D(ram_26_data), .en(decoder_1_out9), .Q(register_26_q), .clk(clock_1_out), .clr(or_12_out));
  or or_12 (or_12_out, not_12_out, or_1_out);
  not not_12 (not_12_out, decoder_1_out9);
  Register #(.width(32), .trigger("high")) register_27 (
    .D(ram_27_data), .en(decoder_1_out10), .Q(register_27_q), .clk(clock_1_out), .clr(or_13_out));
  or or_13 (or_13_out, not_13_out, or_1_out);
  not not_13 (not_13_out, decoder_1_out10);
  Register #(.width(32), .trigger("high")) register_28 (
    .D(ram_28_data), .en(decoder_1_out11), .Q(register_28_q), .clk(clock_1_out), .clr(or_14_out));
  or or_14 (or_14_out, not_14_out, or_1_out);
  not not_14 (not_14_out, decoder_1_out11);
  Register #(.width(32), .trigger("high")) register_29 (
    .D(ram_29_data), .en(decoder_1_out12), .Q(register_29_q), .clk(clock_1_out), .clr(or_15_out));
  or or_15 (or_15_out, not_15_out, or_1_out);
  not not_15 (not_15_out, decoder_1_out12);
  Register #(.width(32), .trigger("high")) register_30 (
    .D(ram_30_data), .en(decoder_1_out13), .Q(register_30_q), .clk(clock_1_out), .clr(or_16_out));
  or or_16 (or_16_out, not_16_out, or_1_out);
  not not_16 (not_16_out, decoder_1_out13);
  Register #(.width(32), .trigger("high")) register_31 (
    .D(ram_31_data), .en(decoder_1_out14), .Q(register_31_q), .clk(clock_1_out), .clr(or_17_out));
  or or_17 (or_17_out, not_17_out, or_1_out);
  not not_17 (not_17_out, decoder_1_out14);
  Register #(.width(32), .trigger("high")) register_32 (
    .D(ram_32_data), .en(decoder_1_out15), .Q(register_32_q), .clk(clock_1_out), .clr(or_18_out));
  or or_18 (or_18_out, not_18_out, or_1_out);
  not not_18 (not_18_out, decoder_1_out15);
  assign Data_out = register_17_q | register_18_q | register_19_q | register_20_q | register_21_q | register_22_q | register_23_q | register_24_q | register_25_q | register_26_q | register_27_q | register_28_q | register_29_q | register_30_q | register_31_q | register_32_q;  // OR_Gate or_19, 32 bits wide
  or or_20 (or_20_out, Data_in[0], Data_in[1], Data_in[2], Data_in[3], Data_in[4], Data_in[5], Data_in[6], Data_in[7], Data_in[8], Data_in[9], Data_in[10], Data_in[11], Data_in[12], Data_in[13], Data_in[14], Data_in[15], Data_in[17], Data_in[18], Data_in[19], Data_in[20], Data_in[21], Data_in[22], Data_in[23], Data_in[24], Data_in[25], Data_in[26], Data_in[27], Data_in[28], Data_in[29], Data_in[30], Data_in[31], Data_in[16]);

  // Notes on the sheet:
  //   RAM: 1,073,741,760 Bytes
endmodule

module _2_GIG_RAM (
  input  Power,
  input  clear,
  input  write,
  input  [28:0] adress_in,
  input  [31:0] data_in,
  input  [23:0] preasa,
  input  ass,
  input  aw,
  output [31:0] data_out,
  output adress_contains_data,
  output [28:0] arc,
  output [28:0] a_out
);

  wire aw_out, clear_out, clock_1_out, n1gb_ram_1_address_contains_data, n1gb_ram_2_address_contains_data,
       not_1_out, not_2_out, not_3_out, not_4_out, not_5_out, not_6_out, or_1_out, or_2_out, or_3_out,
       write_out;
  wire [27:0] controlled_buffer_1_out, controlled_buffer_3_out;
  wire [31:0] controlled_buffer_2_out, controlled_buffer_4_out, n1gb_ram_1_data_out, n1gb_ram_2_data_out;

  Button u_aw (.out(aw_out));
  Button u_write (.out(write_out));
  Button u_clear (.out(clear_out));
  or or_1 (or_1_out, clear_out, clear);
  not not_1 (not_1_out, a_out[28]);
  Pull_Resistor pull_resistor_1 (.node(ass));
  or or_2 (or_2_out, aw_out, aw);
  or or_3 (or_3_out, write, write_out);
  assign controlled_buffer_1_out = not_1_out ? a_out[27:0] : 28'bz;  // Controlled_Buffer controlled_buffer_1
  assign controlled_buffer_2_out = not_1_out ? data_in : 32'bz;  // Controlled_Buffer controlled_buffer_2
  assign controlled_buffer_3_out = not_2_out ? a_out[27:0] : 28'bz;  // Controlled_Buffer controlled_buffer_3
  assign controlled_buffer_4_out = not_3_out ? data_in : 32'bz;  // Controlled_Buffer controlled_buffer_4
  not not_2 (not_2_out, not_1_out);
  not not_3 (not_3_out, not_1_out);
  Clock clock_1 (.out(clock_1_out));
  _1GB_RAM u_1gb_ram_1 (
    .Reset(or_1_out), .Data_in(controlled_buffer_2_out), .Address(controlled_buffer_1_out), .Write(or_3_out),
    .Address_Contains_Data(n1gb_ram_1_address_contains_data), .Data_out(n1gb_ram_1_data_out), .Power(Power));
  _1GB_RAM u_1gb_ram_2 (
    .Reset(or_1_out), .Data_in(controlled_buffer_4_out), .Address(controlled_buffer_3_out), .Write(or_3_out),
    .Address_Contains_Data(n1gb_ram_2_address_contains_data), .Data_out(n1gb_ram_2_data_out), .Power(Power));
  not not_4 (not_4_out, or_2_out);
  assign data_out = not_1_out ? n1gb_ram_1_data_out : 32'bz;  // Controlled_Buffer controlled_buffer_5
  assign adress_contains_data = not_1_out ? n1gb_ram_1_address_contains_data : 1'bz;  // Controlled_Buffer controlled_buffer_6
  not not_5 (not_5_out, not_1_out);
  not not_6 (not_6_out, not_1_out);
  assign data_out = not_5_out ? n1gb_ram_2_data_out : 32'bz;  // Controlled_Buffer controlled_buffer_7
  assign adress_contains_data = not_6_out ? n1gb_ram_2_address_contains_data : 1'bz;  // Controlled_Buffer controlled_buffer_8
  RAM #(.addrWidth(24), .dataWidth(29), .bus("separate")) ram_1 (
    .addr(preasa), .din(adress_in), .data(arc), .str(or_2_out), .clk(clock_1_out), .ld(not_4_out));  // open: sel, clr
  Multiplexer #(.width(29), .disabled(0), .enable("false")) multiplexer_1 (
    .in0(adress_in), .in1(arc), .out(a_out), .sel(ass));

  // Notes on the sheet:
  //   aw: pull=down
endmodule

module easy_2_GIG_RAM (
  input  Power,
  input  [28:0] a_in__optional,
  input  dec,
  input  inc,
  input  clear,
  input  write,
  input  m_adress__optional,
  input  [31:0] d_in,
  input  res,
  input  [23:0] preasa,
  input  ass,
  input  aw,
  output [28:0] a_out,
  output [28:0] arc,
  output [31:0] d_out,
  output acd,
  output fa,
  output la
);

  wire clock_1_out, or_1_out, or_2_out;
  wire [28:0] counter_1_q;

  Clock clock_1 (.out(clock_1_out));
  or or_1 (or_1_out, dec, m_adress__optional);
  or or_2 (or_2_out, inc, dec);
  Comparator #(.width(29)) comparator_1 (.a(counter_1_q), .b({29{1'b0}}), .eq(fa));  // open: gt, lt
  Comparator #(.width(29)) comparator_2 (.a(counter_1_q), .b({29{1'b1}}), .eq(la));  // open: gt, lt
  Counter #(.width(29), .max('h1fffffff)) counter_1 (
    .load(or_1_out), .D(a_in__optional), .count(or_2_out), .Q(counter_1_q), .clk(clock_1_out), .clr(res));  // open: carry
  _2_GIG_RAM u_2_gig_ram_1 (
    .clear(clear), .write(write), .data_in(d_in), .data_out(d_out), .adress_contains_data(acd),
    .adress_in(counter_1_q), .Power(Power), .preasa(preasa), .ass(ass), .aw(aw), .a_out(a_out), .arc(arc));

  // Notes on the sheet:
  //   res: pull=down
endmodule

module easy_2_GIG_RAM_test (
  input  [28:0] a,
  input  [31:0] d_in,
  input  [23:0] preasa,
  output [6:0] arc
);

  wire clock_1_out, easy_2_gig_ram_1_acd, easy_2_gig_ram_1_fa, easy_2_gig_ram_1_la, key_dec_1_ass,
       key_dec_1_aw, key_dec_1_d, key_dec_1_e, key_dec_1_i, key_dec_1_j, key_dec_1_power, key_dec_1_r,
       key_dec_1_w, keyboard_1_avail;
  wire [1:0] adder_2_out;
  wire [4:0] adder_1_out;
  wire [23:0] easy_2_gig_ram_1_a_out;
  wire [28:0] easy_2_gig_ram_1_arc;
  wire [28:24] easy_2_gig_ram_1_a_out_2;
  wire [31:0] easy_2_gig_ram_1_d_out;

  LED acd (.in(easy_2_gig_ram_1_acd));
  LED fa (.in(easy_2_gig_ram_1_fa));
  LED la (.in(easy_2_gig_ram_1_la));
  // Probe on adder_2_out
  // Probe on adder_1_out
  // Probe on easy_2_gig_ram_1_a_out
  // Probe on easy_2_gig_ram_1_d_out
  // Probe on easy_2_gig_ram_1_arc
  KEY_DEC key_dec_1 (
    .I(key_dec_1_i), .R(key_dec_1_r), .D(key_dec_1_d), .W(key_dec_1_w), .J(key_dec_1_j), .E(key_dec_1_e),
    .Power(key_dec_1_power), .ass(key_dec_1_ass), .aw(key_dec_1_aw), .ASCII(arc), .AV(keyboard_1_avail));
  easy_2_GIG_RAM easy_2_gig_ram_1 (
    .a_in__optional(a), .clear(key_dec_1_e), .write(key_dec_1_w), .m_adress__optional(key_dec_1_j),
    .d_in(d_in), .d_out(easy_2_gig_ram_1_d_out), .acd(easy_2_gig_ram_1_acd), .dec(key_dec_1_d),
    .inc(key_dec_1_i), .la(easy_2_gig_ram_1_la), .a_out({easy_2_gig_ram_1_a_out_2, easy_2_gig_ram_1_a_out}),
    .res(key_dec_1_r), .fa(easy_2_gig_ram_1_fa), .Power(key_dec_1_power), .preasa(preasa),
    .ass(key_dec_1_ass), .aw(key_dec_1_aw), .arc(easy_2_gig_ram_1_arc));
  Clock clock_1 (.out(clock_1_out));
  Keyboard keyboard_1 (.clk(clock_1_out), .avail(keyboard_1_avail), .data(arc));  // open: re, clr
  Adder #(.width(5)) adder_1 (
    .a({1'b0, easy_2_gig_ram_1_a_out_2[27:24]}), .b(5'b00001), .out(adder_1_out));  // open: cin, cout
  Adder #(.width(2)) adder_2 (
    .a(2'b01), .b({1'b0, easy_2_gig_ram_1_a_out_2[28]}), .out(adder_2_out));  // open: cin, cout

  // Notes on the sheet:
  //   preasa: pull=down
  //   a: pull=down
  //   d_in: pull=down
endmodule

module KEY_DEC (
  input  [6:0] ASCII,
  input  AV,
  output I,
  output R,
  output D,
  output W,
  output J,
  output E,
  output aw,
  output Power,
  output ass
);

  wire and_1_out, and_3_out, comparator_3_eq, comparator_4_eq, comparator_5_eq, comparator_6_eq,
       comparator_7_eq, comparator_8_eq, or_1_out;
  wire [6:0] shift_register_1_q0, shift_register_1_q1;

  Shift_Register #(.width(7), .length(2)) shift_register_1 (
    .shift(1'b1), .in(ASCII), .clk(AV), .clr(or_1_out), .q0(shift_register_1_q0), .q1(shift_register_1_q1));  // open: out, load, d0, d1
  Comparator #(.width(7), .mode("unsigned")) comparator_1 (
    .a(shift_register_1_q1), .b(7'b1001001), .eq(I));  // open: gt, lt
  Comparator #(.width(7), .mode("unsigned")) comparator_2 (
    .a(shift_register_1_q1), .b(7'b1010111), .eq(W));  // open: gt, lt
  Comparator #(.width(7), .mode("unsigned")) comparator_3 (
    .a(shift_register_1_q1), .b(7'b1010100), .eq(comparator_3_eq));  // open: gt, lt
  Comparator #(.width(7), .mode("unsigned")) comparator_4 (
    .a(shift_register_1_q0), .b(7'b1010000), .eq(comparator_4_eq));  // open: gt, lt
  and and_1 (and_1_out, comparator_5_eq, comparator_6_eq);
  Comparator #(.width(7), .mode("unsigned")) comparator_5 (
    .a(shift_register_1_q1), .b(7'b1000001), .eq(comparator_5_eq));  // open: gt, lt
  Comparator #(.width(7), .mode("unsigned")) comparator_6 (
    .a(shift_register_1_q0), .b(7'b1010011), .eq(comparator_6_eq));  // open: gt, lt
  Comparator #(.width(7), .mode("unsigned")) comparator_7 (
    .a(shift_register_1_q1), .b(7'b1000001), .eq(comparator_7_eq));  // open: gt, lt
  and and_2 (aw, comparator_7_eq, comparator_8_eq);
  Comparator #(.width(7), .mode("unsigned")) comparator_8 (
    .a(shift_register_1_q0), .b(7'b1010111), .eq(comparator_8_eq));  // open: gt, lt
  and and_3 (and_3_out, comparator_3_eq, comparator_4_eq);
  or or_1 (or_1_out, ass, W, I, D, J, E, aw, R, Power);
  T_Flip_Flop t_ff_1 (.clk(and_3_out), .T(and_3_out), .Q(Power));  // open: Qn, preset, reset, en
  T_Flip_Flop t_ff_2 (.clk(and_1_out), .T(and_1_out), .Q(ass));  // open: Qn, preset, reset, en
  Comparator #(.width(7), .mode("unsigned")) comparator_9 (
    .a(shift_register_1_q1), .b(7'b1010010), .eq(R));  // open: gt, lt
  Comparator #(.width(7), .mode("unsigned")) comparator_10 (
    .a(shift_register_1_q1), .b(7'b1000100), .eq(D));  // open: gt, lt
  Comparator #(.width(7), .mode("unsigned")) comparator_11 (
    .a(shift_register_1_q1), .b(7'b1001010), .eq(J));  // open: gt, lt
  Comparator #(.width(7), .mode("unsigned")) comparator_12 (
    .a(shift_register_1_q1), .b(7'b1000101), .eq(E));  // open: gt, lt

  // Notes on the sheet:
  //   ASCII: pull=down
endmodule

module manual_adress_2_GIG_RAM (
  input  [28:0] adress,
  input  [31:0] D
);

  wire erase_out, store_out;
  wire [1:0] adder_2_out;
  wire [4:0] adder_1_out;
  wire [31:0] n2_gig_ram_1_data_out;

  Button store (.out(store_out));
  Button erase (.out(erase_out));
  // Probe on adder_2_out
  // Probe on adder_1_out
  // Probe on adress[23:0]
  // Probe on n2_gig_ram_1_data_out
  Adder #(.width(5)) adder_1 (.a({1'b0, adress[27:24]}), .b(5'b00001), .out(adder_1_out));  // open: cin, cout
  Adder #(.width(2)) adder_2 (.a(2'b01), .b({1'b0, adress[28]}), .out(adder_2_out));  // open: cin, cout
  _2_GIG_RAM u_2_gig_ram_1 (
    .clear(erase_out), .write(store_out), .data_in(D), .data_out(n2_gig_ram_1_data_out), .adress_in(adress),
    .Power(1'b1), .preasa({24{1'b0}}));  // open: adress_contains_data, ass, aw, a_out, arc

  // Notes on the sheet:
  //   D: pull=down
endmodule
