// Logisim project 7.circ as structural Verilog: 1 circuit, main circuit WORM converter
module WORM_converter (
  input  store,
  input  carry,
  input  acd,
  input  new_punch_card,
  output store_2
);

  wire and_1_out, and_2_out, controlled_buffer_1_out, counter_1_q, not_1_out, t_ff_1_q;

  T_Flip_Flop t_ff_1 (
    .clk(counter_1_q), .T(counter_1_q), .Q(t_ff_1_q), .preset(controlled_buffer_1_out), .reset(new_punch_card));  // open: Qn, en
  assign controlled_buffer_1_out = not_1_out ? t_ff_1_q : 1'bz;  // Controlled_Buffer controlled_buffer_1
  not not_1 (not_1_out, new_punch_card);
  Counter #(.width(1), .max('h1)) counter_1 (
    .count(and_1_out), .Q(counter_1_q), .clk(and_1_out), .clr(new_punch_card));  // open: load, D, carry
  and and_1 (and_1_out, store, carry);
  and and_2 (and_2_out, store, ~t_ff_1_q);  // AND_Gate
  and and_3 (store_2, and_2_out, ~acd);  // AND_Gate
endmodule
