// Logisim project 8 bit RAM or 16 bit RAM.circ as structural Verilog: 6 circuits, main circuit 1 bit 8 loc ram
module _1_bit_8_loc_ram (
  input  d_in,
  input  write,
  input  [2:0] address,
  output data_out
);

  wire d_ff_1_q, d_ff_2_q, d_ff_3_q, d_ff_4_q, d_ff_5_q, d_ff_6_q, d_ff_7_q, d_ff_8_q, demultiplexer_1_out0,
       demultiplexer_1_out1, demultiplexer_1_out2, demultiplexer_1_out3, demultiplexer_1_out4,
       demultiplexer_1_out5, demultiplexer_1_out6, demultiplexer_1_out7;

  Demultiplexer #(.select(3), .disabled(0), .enable("false")) demultiplexer_1 (
    .out0(demultiplexer_1_out0), .out1(demultiplexer_1_out1), .out2(demultiplexer_1_out2),
    .out3(demultiplexer_1_out3), .out4(demultiplexer_1_out4), .out5(demultiplexer_1_out5),
    .out6(demultiplexer_1_out6), .out7(demultiplexer_1_out7), .in(write), .sel(address));
  D_Flip_Flop d_ff_1 (.clk(demultiplexer_1_out0), .D(d_in), .Q(d_ff_1_q));  // open: Qn, preset, en, reset
  D_Flip_Flop d_ff_2 (.clk(demultiplexer_1_out1), .D(d_in), .Q(d_ff_2_q));  // open: Qn, preset, en, reset
  D_Flip_Flop d_ff_3 (.clk(demultiplexer_1_out2), .D(d_in), .Q(d_ff_3_q));  // open: Qn, preset, en, reset
  D_Flip_Flop d_ff_4 (.D(d_in), .Q(d_ff_4_q));  // open: clk, Qn, preset, en, reset
  D_Flip_Flop d_ff_5 (.clk(demultiplexer_1_out4), .D(d_in), .Q(d_ff_5_q));  // open: Qn, preset, en, reset
  D_Flip_Flop d_ff_6 (.clk(demultiplexer_1_out5), .D(d_in), .Q(d_ff_6_q));  // open: Qn, preset, en, reset
  D_Flip_Flop d_ff_7 (.clk(demultiplexer_1_out6), .D(d_in), .Q(d_ff_7_q));  // open: Qn, preset, en, reset
  D_Flip_Flop d_ff_8 (.clk(demultiplexer_1_out7), .D(d_in), .Q(d_ff_8_q));  // open: Qn, preset, en, reset
  Multiplexer #(.select(3), .disabled(0), .enable("false")) multiplexer_1 (
    .in0(d_ff_1_q), .in1(d_ff_2_q), .in2(d_ff_3_q), .in3(d_ff_4_q), .in4(d_ff_5_q), .in5(d_ff_6_q),
    .in6(d_ff_7_q), .in7(d_ff_8_q), .out(data_out), .sel(address));
endmodule

module _1_bit_16_loc_ram (
  input  data_in,
  input  write,
  input  [3:0] adress,
  output data_out
);

  wire demultiplexer_1_out0, demultiplexer_1_out1, n1_bit_8_loc_ram_1_data_out, n1_bit_8_loc_ram_2_data_out;
  wire [2:0] demultiplexer_2_out0, demultiplexer_2_out1;

  // Probe on demultiplexer_2_out0
  // Probe on demultiplexer_2_out1
  Demultiplexer #(.disabled(0), .enable("false")) demultiplexer_1 (
    .out0(demultiplexer_1_out0), .out1(demultiplexer_1_out1), .in(write), .sel(adress[3]));
  Demultiplexer #(.width(3), .disabled(0), .enable("false")) demultiplexer_2 (
    .out0(demultiplexer_2_out0), .out1(demultiplexer_2_out1), .in(adress[2:0]), .sel(adress[3]));
  _1_bit_8_loc_ram u_1_bit_8_loc_ram_1 (
    .d_in(data_in), .write(demultiplexer_1_out0), .address(demultiplexer_2_out0),
    .data_out(n1_bit_8_loc_ram_1_data_out));
  _1_bit_8_loc_ram u_1_bit_8_loc_ram_2 (
    .d_in(data_in), .write(demultiplexer_1_out1), .address(demultiplexer_2_out1),
    .data_out(n1_bit_8_loc_ram_2_data_out));
  Multiplexer #(.disabled(0), .enable("false")) multiplexer_1 (
    .in0(n1_bit_8_loc_ram_1_data_out), .in1(n1_bit_8_loc_ram_2_data_out), .out(data_out), .sel(adress[3]));

  // Notes on the sheet:
  //   write: pull=down
endmodule

module _4_bit_16_loc_ram (
  input  write,
  input  [3:0] data_in,
  input  [3:0] adress,
  output [3:0] data_out
);

  _1_bit_16_loc_ram u_1_bit_16_loc_ram_1 (.data_in(data_in[0]), .write(write), .adress(adress), .data_out(data_out[0]));
  _1_bit_16_loc_ram u_1_bit_16_loc_ram_2 (.data_in(data_in[1]), .write(write), .adress(adress), .data_out(data_out[1]));
  _1_bit_16_loc_ram u_1_bit_16_loc_ram_3 (.data_in(data_in[2]), .write(write), .adress(adress), .data_out(data_out[2]));
  _1_bit_16_loc_ram u_1_bit_16_loc_ram_4 (.data_in(data_in[3]), .write(write), .adress(adress), .data_out(data_out[3]));
endmodule

module _8_bit_32_loc_ram (
  input  [4:0] adress_in,
  input  [7:0] data_in,
  input  write,
  output [7:0] data_out
);

  wire demultiplexer_2_out0, demultiplexer_2_out1;
  wire [3:0] demultiplexer_1_out0, demultiplexer_1_out1, n4_bit_16_loc_ram_1_data_out,
       n4_bit_16_loc_ram_2_data_out, n4_bit_16_loc_ram_3_data_out, n4_bit_16_loc_ram_4_data_out;

  Demultiplexer #(.width(4), .disabled(0), .enable("false")) demultiplexer_1 (
    .out0(demultiplexer_1_out0), .out1(demultiplexer_1_out1), .in(adress_in[3:0]), .sel(adress_in[4]));
  Demultiplexer #(.disabled(0), .enable("false")) demultiplexer_2 (
    .out0(demultiplexer_2_out0), .out1(demultiplexer_2_out1), .in(write), .sel(adress_in[4]));
  _4_bit_16_loc_ram u_4_bit_16_loc_ram_1 (
    .write(demultiplexer_2_out0), .data_in(data_in[3:0]), .adress(demultiplexer_1_out0),
    .data_out(n4_bit_16_loc_ram_1_data_out));
  _4_bit_16_loc_ram u_4_bit_16_loc_ram_2 (
    .write(demultiplexer_2_out0), .data_in(data_in[7:4]), .adress(demultiplexer_1_out0),
    .data_out(n4_bit_16_loc_ram_2_data_out));
  _4_bit_16_loc_ram u_4_bit_16_loc_ram_3 (
    .write(demultiplexer_2_out1), .data_in(data_in[3:0]), .adress(demultiplexer_1_out1),
    .data_out(n4_bit_16_loc_ram_3_data_out));
  _4_bit_16_loc_ram u_4_bit_16_loc_ram_4 (
    .write(demultiplexer_2_out1), .data_in(data_in[7:4]), .adress(demultiplexer_1_out1),
    .data_out(n4_bit_16_loc_ram_4_data_out));
  Multiplexer #(.width(8), .disabled(0), .enable("false")) multiplexer_1 (
    .in0({n4_bit_16_loc_ram_2_data_out, n4_bit_16_loc_ram_1_data_out}),
    .in1({n4_bit_16_loc_ram_4_data_out, n4_bit_16_loc_ram_3_data_out}), .out(data_out), .sel(adress_in[4]));
endmodule

module _8_bit_64_loc_ram (
  input  [7:0] write,
  input  write_2,
  input  [5:0] adress_in,
  output [7:0] data_out
);

  wire demultiplexer_2_out0, demultiplexer_2_out1;
  wire [4:0] demultiplexer_1_out0, demultiplexer_1_out1;
  wire [7:0] n8_bit_32_loc_ram_1_data_out, n8_bit_32_loc_ram_2_data_out;

  Demultiplexer #(.width(5), .disabled(0), .enable("false")) demultiplexer_1 (
    .out0(demultiplexer_1_out0), .out1(demultiplexer_1_out1), .in(adress_in[4:0]), .sel(adress_in[5]));
  Demultiplexer #(.disabled(0), .enable("false")) demultiplexer_2 (
    .out0(demultiplexer_2_out0), .out1(demultiplexer_2_out1), .in(write_2), .sel(adress_in[5]));
  _8_bit_32_loc_ram u_8_bit_32_loc_ram_1 (
    .adress_in(demultiplexer_1_out0), .data_in(write), .write(demultiplexer_2_out0),
    .data_out(n8_bit_32_loc_ram_1_data_out));
  _8_bit_32_loc_ram u_8_bit_32_loc_ram_2 (
    .adress_in(demultiplexer_1_out1), .data_in(write), .write(demultiplexer_2_out1),
    .data_out(n8_bit_32_loc_ram_2_data_out));
  Multiplexer #(.width(8), .disabled(0), .enable("false")) multiplexer_1 (
    .in0(n8_bit_32_loc_ram_1_data_out), .in1(n8_bit_32_loc_ram_2_data_out), .out(data_out), .sel(adress_in[5]));

  // Notes on the sheet:
  //   write_2: pull=down
endmodule

module _16_bit_64_loc_ram (
  input  [15:0] data_in,
  input  [5:0] adress_in,
  input  write,
  output [15:0] data_out
);

  _8_bit_64_loc_ram u_8_bit_64_loc_ram_1 (
    .write(data_in[7:0]), .write_2(write), .adress_in(adress_in), .data_out(data_out[7:0]));
  _8_bit_64_loc_ram u_8_bit_64_loc_ram_2 (
    .write(data_in[15:8]), .write_2(write), .adress_in(adress_in), .data_out(data_out[15:8]));
endmodule
