// Logisim project 8080.circ as structural Verilog: 2 circuits, main circuit RF
module RF (
  input  [7:0] A_in,
  input  [7:0] B_in,
  input  [7:0] C_in,
  input  [7:0] D_in,
  input  [7:0] E_in,
  input  [7:0] H_in,
  input  [7:0] L_in,
  input  en_A,
  input  en_B,
  input  en_C,
  input  en_D,
  input  en_E,
  input  en_H,
  input  en_L,
  input  res,
  output [7:0] A_in_2,
  output [7:0] B_in_2,
  output [7:0] C_in_2,
  output [7:0] D_in_2,
  output [7:0] E_in_2,
  output [7:0] H_in_2,
  output [7:0] L_in_2
);

  wire clock_1_out;

  Clock clock_1 (.out(clock_1_out));
  Register register_1 (.D(A_in), .en(en_A), .Q(A_in_2), .clk(clock_1_out), .clr(res));
  Register register_2 (.D(B_in), .en(en_B), .Q(B_in_2), .clk(clock_1_out), .clr(res));
  Register register_3 (.D(C_in), .en(en_C), .Q(C_in_2), .clk(clock_1_out), .clr(res));
  Register register_4 (.D(D_in), .en(en_D), .Q(D_in_2), .clk(clock_1_out), .clr(res));
  Register register_5 (.D(E_in), .en(en_E), .Q(E_in_2), .clk(clock_1_out), .clr(res));
  Register register_6 (.D(H_in), .en(en_H), .Q(H_in_2), .clk(clock_1_out), .clr(res));
  Register register_7 (.D(L_in), .en(en_L), .Q(L_in_2), .clk(clock_1_out), .clr(res));
endmodule

module ALU (
);

  wire [7:0] adder_1_out, subtractor_1_out;

  Adder adder_1 (.out(adder_1_out));  // open: a, b, cin, cout
  Subtractor subtractor_1 (.out(subtractor_1_out));  // open: a, b, bin, bout
  Multiplexer #(.select(3), .width(8), .disabled(0), .enable("false")) multiplexer_1 (
    .in0(adder_1_out), .in1(subtractor_1_out));  // open: in2, in3, in4, in5, in6, in7, out, sel
endmodule
