// Logisim project ASync Serial.circ as structural Verilog: 3 circuits, main circuit main
module Sender (
  input  [7:0] Pin,
  input  Pload,
  input  Sin,
  input  Trans,
  output Sout,
  output [7:0] Pout
);

  wire clock_1_out, counter_2_carry, d_ff_1_q, not_1_out, or_1_out, shift_register_1_q8;
  wire [1:0] counter_1_q;

  Pull_Resistor pull_resistor_1 (.node(Pin));
  Pull_Resistor pull_resistor_2 (.node(Pload));
  Shift_Register #(.length(9)) shift_register_1 (
    .shift(d_ff_1_q), .in(Sin), .clk(counter_1_q[1]), .load(Pload), .d0(Pin[7]), .q0(Pout[7]), .d1(Pin[6]),
    .q1(Pout[6]), .d2(Pin[5]), .q2(Pout[5]), .d3(Pin[4]), .q3(Pout[4]), .d4(Pin[3]), .q4(Pout[3]),
    .d5(Pin[2]), .q5(Pout[2]), .d6(Pin[1]), .q6(Pout[1]), .d7(Pin[0]), .q7(Pout[0]), .d8(1'b0),
    .q8(shift_register_1_q8));  // open: out, clr
  Pull_Resistor pull_resistor_3 (.node(Trans));
  Pull_Resistor pull_resistor_4 (.node(Sin));
  Counter #(.width(2), .max('h3)) counter_1 (.Q(counter_1_q), .clk(clock_1_out));  // open: load, D, count, carry, clr
  Clock clock_1 (.out(clock_1_out));
  D_Flip_Flop d_ff_1 (.Q(d_ff_1_q), .preset(Trans), .reset(counter_2_carry));  // open: clk, D, Qn, en
  not not_1 (not_1_out, or_1_out);
  or or_1 (or_1_out, Trans, d_ff_1_q);
  assign Sout = or_1_out ? shift_register_1_q8 : 1'bz;  // Controlled_Buffer controlled_buffer_1
  assign Sout = not_1_out ? counter_1_q[1] : 1'bz;  // Controlled_Buffer controlled_buffer_2
  Counter #(.width(4), .max('h8), .ongoal("stay")) counter_2 (
    .count(d_ff_1_q), .carry(counter_2_carry), .clk(counter_1_q[1]), .clr(Trans));  // open: load, D, Q
endmodule

module main (
  input  [7:0] SPin,
  input  SPload,
  input  Trans,
  input  [7:0] RPin,
  input  RPload,
  output [7:0] SPout,
  output [7:0] RPout
);

  wire reciver_1_sout, sender_1_sout;

  Sender sender_1 (.Pin(SPin), .Pload(SPload), .Sin(reciver_1_sout), .Trans(Trans), .Sout(sender_1_sout), .Pout(SPout));
  Reciver reciver_1 (.Pin(RPin), .Pload(RPload), .Sin(sender_1_sout), .Sout(reciver_1_sout), .Pout(RPout));
endmodule

module Reciver (
  input  [7:0] Pin,
  input  Pload,
  input  Sin,
  output Sout,
  output [7:0] Pout
);

  wire and_1_out, button_1_out, button_2_out, clock_1_out, clock_2_out, controlled_buffer_1_out,
       counter_1_carry, d_ff_1_q, multiplexer_1_out, multiplexer_2_out, not_1_out, not_2_out,
       pull_resistor_4_node, shift_register_2_out, t_ff_1_q, Toggle_out;

  Pull_Resistor pull_resistor_1 (.node(Pin));
  Pull_Resistor pull_resistor_2 (.node(Pload));
  Pull_Resistor pull_resistor_3 (.node(Sin));
  Button Toggle (.out(Toggle_out));
  Button button_1 (.out(button_1_out));
  Multiplexer #(.disabled(0), .enable("false")) multiplexer_1 (
    .in0(Sin), .in1(button_1_out), .out(multiplexer_1_out), .sel(t_ff_1_q));
  T_Flip_Flop t_ff_1 (.clk(Toggle_out), .T(Toggle_out), .Q(t_ff_1_q));  // open: Qn, preset, reset, en
  and and_1 (and_1_out, shift_register_2_out, ~multiplexer_1_out);  // AND_Gate
  Clock clock_1 (.out(clock_1_out));
  Shift_Register shift_register_1 (
    .shift(d_ff_1_q), .in(multiplexer_1_out), .clk(shift_register_2_out), .load(Pload), .d0(Pin[7]),
    .q0(Pout[7]), .d1(Pin[6]), .q1(Pout[6]), .d2(Pin[5]), .q2(Pout[5]), .d3(Pin[4]), .q3(Pout[4]),
    .d4(Pin[3]), .q4(Pout[3]), .d5(Pin[2]), .q5(Pout[2]), .d6(Pin[1]), .q6(Pout[1]), .d7(Pin[0]), .q7(Pout[0]));  // open: out, clr
  Multiplexer #(.disabled(0), .enable("false")) multiplexer_2 (
    .in0(multiplexer_1_out), .in1(shift_register_2_out), .out(multiplexer_2_out), .sel(d_ff_1_q));
  assign controlled_buffer_1_out = not_1_out ? d_ff_1_q : 1'bz;  // Controlled_Buffer controlled_buffer_1
  not not_1 (not_1_out, pull_resistor_4_node);
  Pull_Resistor pull_resistor_4 (.node(pull_resistor_4_node));
  not not_2 (not_2_out, clock_1_out);
  Shift_Register #(.length(32)) shift_register_2 (
    .in(multiplexer_2_out), .clk(clock_2_out), .out(shift_register_2_out));  // open: shift, load, clr, d0, q0, d1, q1, d2, q2, d3, q3, d4, q4, d5, q5, d6, q6, d7, q7, d8, q8, d9, q9, d10, q10, d11, q11, d12, q12, d13, q13, d14, q14, d15, q15, d16, q16, d17, q17, d18, q18, d19, q19, d20, q20, d21, q21, d22, q22, d23, q23, d24, q24, d25, q25, d26, q26, d27, q27, d28, q28, d29, q29, d30, q30, d31, q31
  Clock clock_2 (.out(clock_2_out));
  D_Flip_Flop d_ff_1 (
    .clk(not_2_out), .D(and_1_out), .Q(d_ff_1_q), .preset(controlled_buffer_1_out),
    .reset(pull_resistor_4_node));  // open: Qn, en
  Button button_2 (.out(button_2_out));
  or or_1 (pull_resistor_4_node, button_2_out, counter_1_carry);
  Counter #(.width(4), .max('h7)) counter_1 (
    .count(d_ff_1_q), .carry(counter_1_carry), .clk(shift_register_2_out), .clr(counter_1_carry));  // open: load, D, Q

  assign Sout = Pout[0];
endmodule
