// Logisim project But how Do It Know computer.circ as structural Verilog: 7 circuits, main circuit main
module main (
  input  [7:0] in_1,
  input  custom_en
);

  wire clock_1_out, control_section_1_acc_en, control_section_1_acc_set, control_section_1_bus_1,
       control_section_1_iar_en, control_section_1_iar_set, control_section_1_ir_set,
       control_section_1_mar_set, control_section_1_r0_en, control_section_1_r0_set, control_section_1_r1_en,
       control_section_1_r1_set, control_section_1_r2_en, control_section_1_r2_set, control_section_1_r3_en,
       control_section_1_r3_set, control_section_1_ram_en, control_section_1_ram_set,
       control_section_1_tmp_set, not_1_out, not_2_out;
  wire [2:0] control_section_1_alu_op;
  wire [7:0] alu_1_c, bus_1_1_out, controlled_buffer_1_out, controlled_buffer_2_out, IR_o, MAR_o, TMP_o;

  // Probe on controlled_buffer_1_out
  assign controlled_buffer_1_out = custom_en ? in_1 : 8'bz;  // Controlled_Buffer controlled_buffer_1
  R TMP (.i(controlled_buffer_1_out), .s(control_section_1_tmp_set), .e(1'b1), .o(TMP_o));
  ALU alu_1 (
    .a(TMP_o), .b(bus_1_1_out), .op(control_section_1_alu_op), .c(alu_1_c));  // open: carry_in, carry_out, a_larger, equal, zero
  R R0 (
    .i(controlled_buffer_1_out), .s(control_section_1_r0_set), .e(control_section_1_r0_en),
    .o(controlled_buffer_1_out));
  bus_1 bus_1_1 (.in(controlled_buffer_1_out), .bus_1(control_section_1_bus_1), .out(bus_1_1_out));
  R ACC (.i(alu_1_c), .s(control_section_1_acc_set), .e(control_section_1_acc_en), .o(controlled_buffer_1_out));
  R R1 (
    .i(controlled_buffer_1_out), .s(control_section_1_r1_set), .e(control_section_1_r1_en),
    .o(controlled_buffer_1_out));
  R R3 (
    .i(controlled_buffer_1_out), .s(control_section_1_r3_set), .e(control_section_1_r3_en),
    .o(controlled_buffer_1_out));
  R R2 (
    .i(controlled_buffer_1_out), .s(control_section_1_r2_set), .e(control_section_1_r2_en),
    .o(controlled_buffer_1_out));
  R IR (.i(controlled_buffer_1_out), .s(1'b1), .e(control_section_1_ir_set), .o(IR_o));
  assign controlled_buffer_2_out = not_1_out ? controlled_buffer_1_out : 8'bz;  // Controlled_Buffer controlled_buffer_2
  not not_1 (not_1_out, not_2_out);
  not not_2 (not_2_out, control_section_1_ram_set);
  Control_section control_section_1 (
    .R0_en(control_section_1_r0_en), .R1_en(control_section_1_r1_en), .R2_en(control_section_1_r2_en),
    .R3_en(control_section_1_r3_en), .ram_en(control_section_1_ram_en), .acc_en(control_section_1_acc_en),
    .bus_1(control_section_1_bus_1), .alu_op(control_section_1_alu_op), .R0_set(control_section_1_r0_set),
    .R1_set(control_section_1_r1_set), .R2_set(control_section_1_r2_set), .R3_set(control_section_1_r3_set),
    .ram_set(control_section_1_ram_set), .mar_set(control_section_1_mar_set),
    .acc_set(control_section_1_acc_set), .tmp_set(control_section_1_tmp_set), .ir_in(IR_o),
    .ir_set(control_section_1_ir_set), .iar_en(control_section_1_iar_en), .iar_set(control_section_1_iar_set));
  R MAR (.i(controlled_buffer_1_out), .s(control_section_1_mar_set), .e(1'b1), .o(MAR_o));
  Clock clock_1 (.out(clock_1_out));
  R IAR (
    .i(controlled_buffer_1_out), .s(control_section_1_iar_set), .e(control_section_1_iar_en),
    .o(controlled_buffer_1_out));
  RAM ram_1 (.addr(MAR_o), .data(controlled_buffer_2_out), .clk(clock_1_out), .ld(not_2_out));  // open: sel, clr
  assign controlled_buffer_1_out = control_section_1_ram_en ? controlled_buffer_2_out : 8'bz;  // Controlled_Buffer controlled_buffer_3
endmodule

// Z
module Zero (
  input  [7:0] bus_in,
  output zero
);

  nor nor_1 (zero, bus_in[0], bus_in[1], bus_in[2], bus_in[3], bus_in[4], bus_in[5], bus_in[6], bus_in[7]);
endmodule

module bus_1 (
  input  [7:0] in,
  input  bus_1,
  output [7:0] out
);

  wire not_1_out;

  Pull_Resistor pull_resistor_1 (.node(in));
  Pull_Resistor pull_resistor_2 (.node(bus_1));
  not not_1 (not_1_out, bus_1);
  or or_1 (out[0], in[0], bus_1);
  and and_1 (out[1], in[1], not_1_out);
  and and_2 (out[2], in[2], not_1_out);
  and and_3 (out[3], in[3], not_1_out);
  and and_4 (out[4], in[4], not_1_out);
  and and_5 (out[5], in[5], not_1_out);
  and and_6 (out[6], in[6], not_1_out);
  and and_7 (out[7], in[7], not_1_out);
endmodule

module ALU (
  input  [7:0] a,
  input  [7:0] b,
  input  carry_in,
  input  [2:0] op,
  output a_larger,
  output equal,
  output zero,
  output [7:0] c,
  output carry_out
);

  wire adder_1_cout, decoder_1_out0, decoder_1_out1, decoder_1_out2, decoder_1_out3, decoder_1_out4,
       decoder_1_out5, decoder_1_out6;
  wire [7:0] adder_1_out, and_1_out, not_1_out, or_1_out, shifter_1_out, shifter_2_out, xor_1_out;

  Pull_Resistor pull_resistor_1 (.node(carry_in));
  Pull_Resistor pull_resistor_2 (.node(op));
  Comparator #(.mode("unsigned")) comparator_1 (.a(a), .b(b), .gt(a_larger), .eq(equal));  // open: lt
  assign xor_1_out = a ^ b;  // XOR_Gate xor_1, 8 bits wide
  assign or_1_out = a | b;  // OR_Gate or_1, 8 bits wide
  assign and_1_out = a & b;  // AND_Gate and_1, 8 bits wide
  assign not_1_out = ~a;  // NOT_Gate not_1, 8 bits wide
  Shifter shifter_1 (.in(a), .\dist (3'b000), .out(shifter_1_out));
  Shifter #(.shift("lr")) shifter_2 (.in(a), .\dist (3'b000), .out(shifter_2_out));
  Adder adder_1 (.a(a), .b(b), .out(adder_1_out), .cin(carry_in), .cout(adder_1_cout));
  assign c = decoder_1_out6 ? xor_1_out : 8'bz;  // Controlled_Buffer controlled_buffer_1
  assign c = decoder_1_out5 ? or_1_out : 8'bz;  // Controlled_Buffer controlled_buffer_2
  assign c = decoder_1_out4 ? and_1_out : 8'bz;  // Controlled_Buffer controlled_buffer_3
  assign c = decoder_1_out3 ? not_1_out : 8'bz;  // Controlled_Buffer controlled_buffer_4
  assign c = decoder_1_out2 ? shifter_1_out : 8'bz;  // Controlled_Buffer controlled_buffer_5
  assign c = decoder_1_out1 ? shifter_2_out : 8'bz;  // Controlled_Buffer controlled_buffer_6
  assign c = decoder_1_out0 ? adder_1_out : 8'bz;  // Controlled_Buffer controlled_buffer_7
  Decoder #(.select(3), .disabled(0), .enable("false")) decoder_1 (
    .out0(decoder_1_out0), .out1(decoder_1_out1), .out2(decoder_1_out2), .out3(decoder_1_out3),
    .out4(decoder_1_out4), .out5(decoder_1_out5), .out6(decoder_1_out6), .sel(op));  // open: out7
  Pull_Resistor pull_resistor_3 (.node(c));
  and and_2 (carry_out, adder_1_cout, decoder_1_out0);
  Zero zero_1 (.bus_in(c), .zero(zero));
endmodule

module Stepper (
  input  clk,
  output out_2,
  output out_3,
  output out_4,
  output out_5,
  output out_6,
  output out_7
);

  wire comparator_7_eq;
  wire [2:0] counter_1_q;

  Counter #(.width(3), .max('h7)) counter_1 (
    .Q(counter_1_q), .clk(clk), .clr(comparator_7_eq));  // open: load, D, count, carry
  Comparator #(.width(3), .mode("unsigned")) comparator_1 (.a(counter_1_q), .b(3'b001), .eq(out_2));  // open: gt, lt
  Comparator #(.width(3), .mode("unsigned")) comparator_2 (.a(counter_1_q), .b(3'b010), .eq(out_3));  // open: gt, lt
  Comparator #(.width(3), .mode("unsigned")) comparator_3 (.a(counter_1_q), .b(3'b011), .eq(out_4));  // open: gt, lt
  Comparator #(.width(3), .mode("unsigned")) comparator_4 (.a(counter_1_q), .b(3'b100), .eq(out_5));  // open: gt, lt
  Comparator #(.width(3), .mode("unsigned")) comparator_5 (.a(counter_1_q), .b(3'b101), .eq(out_6));  // open: gt, lt
  Comparator #(.width(3), .mode("unsigned")) comparator_6 (.a(counter_1_q), .b(3'b110), .eq(out_7));  // open: gt, lt
  Comparator #(.width(3), .mode("unsigned")) comparator_7 (
    .a(counter_1_q), .b(3'b111), .eq(comparator_7_eq));  // open: gt, lt
endmodule

module R (
  input  [7:0] i,
  input  s,
  input  e,
  output [7:0] o
);

  wire clock_1_out;
  wire [7:0] register_1_q;

  Pull_Resistor pull_resistor_1 (.node(s));
  Pull_Resistor pull_resistor_2 (.node(e));
  Clock clock_1 (.out(clock_1_out));
  Register register_1 (.D(i), .en(s), .Q(register_1_q), .clk(clock_1_out));  // open: clr
  assign o = e ? register_1_q : 8'bz;  // Controlled_Buffer controlled_buffer_1
endmodule

// Control Section
module Control_section (
  input  [7:0] ir_in,
  output R0_en,
  output R0_set,
  output R1_en,
  output R1_set,
  output R2_en,
  output R2_set,
  output R3_en,
  output R3_set,
  output ram_en,
  output ram_set,
  output acc_en,
  output mar_set,
  output bus_1,
  output acc_set,
  output [2:0] alu_op,
  output tmp_set,
  output ir_set,
  output iar_en,
  output iar_set
);

  wire clock_1_out, pull_resistor_1_node, pull_resistor_2_node, pull_resistor_3_node, pull_resistor_4_node,
       pull_resistor_6_node, pull_resistor_8_node, pull_resistor_9_node, pull_resistor_10_node,
       pull_resistor_12_node, pull_resistor_13_node, pull_resistor_14_node, pull_resistor_15_node,
       pull_resistor_19_node, pull_resistor_20_node;

  and R0 (R0_en, clock_1_out, pull_resistor_1_node);
  and R1 (R1_en, clock_1_out, pull_resistor_3_node);
  and R2 (R2_en, clock_1_out, pull_resistor_4_node);
  and R3 (R3_en, clock_1_out, pull_resistor_2_node);
  and RAM (ram_en, clock_1_out, pull_resistor_6_node);
  and ACC (acc_en, clock_1_out, pull_resistor_8_node);
  Clock clock_1 (.out(clock_1_out));
  Pull_Resistor pull_resistor_1 (.node(pull_resistor_1_node));
  Pull_Resistor pull_resistor_2 (.node(pull_resistor_2_node));
  Pull_Resistor pull_resistor_3 (.node(pull_resistor_3_node));
  Pull_Resistor pull_resistor_4 (.node(pull_resistor_4_node));
  Pull_Resistor pull_resistor_5 (.node(bus_1));
  Pull_Resistor pull_resistor_6 (.node(pull_resistor_6_node));
  Pull_Resistor pull_resistor_7 (.node(alu_op));
  Pull_Resistor pull_resistor_8 (.node(pull_resistor_8_node));
  Stepper stepper_1 (.clk(clock_1_out));  // open: out_2, out_3, out_4, out_5, out_6, out_7
  Pull_Resistor pull_resistor_9 (.node(pull_resistor_9_node));
  Pull_Resistor pull_resistor_10 (.node(pull_resistor_10_node));
  Pull_Resistor pull_resistor_11 (.node(ir_in));
  Pull_Resistor pull_resistor_12 (.node(pull_resistor_12_node));
  Pull_Resistor pull_resistor_13 (.node(pull_resistor_13_node));
  Pull_Resistor pull_resistor_14 (.node(pull_resistor_14_node));
  Pull_Resistor pull_resistor_15 (.node(pull_resistor_15_node));
  Pull_Resistor pull_resistor_16 (.node(ir_set));
  Pull_Resistor pull_resistor_17 (.node(iar_en));
  Pull_Resistor pull_resistor_18 (.node(iar_set));
  Pull_Resistor pull_resistor_19 (.node(pull_resistor_19_node));
  Pull_Resistor pull_resistor_20 (.node(pull_resistor_20_node));
  and R0_2 (R0_set, clock_1_out, pull_resistor_20_node);
  and R1_2 (R1_set, clock_1_out, pull_resistor_19_node);
  and R2_2 (R2_set, clock_1_out, pull_resistor_12_node);
  and R3_2 (R3_set, clock_1_out, pull_resistor_15_node);
  and RAM_2 (ram_set, clock_1_out, pull_resistor_13_node);
  and MAR (mar_set, clock_1_out, pull_resistor_14_node);
  and ACC_2 (acc_set, clock_1_out, pull_resistor_10_node);
  and TMP (tmp_set, clock_1_out, pull_resistor_9_node);
endmodule
