// Logisim project CA devices.circ as structural Verilog: 3 circuits, main circuit Register File
module Register_File (
  input  write_enable,
  input  [4:0] Read_Sel0,
  input  [4:0] Read_Sel1,
  input  [4:0] Wrie_Sel,
  input  [31:0] in_5,
  output [31:0] out_6,
  output [31:0] out_7
);

  _32_register_file u_32_register_file_1 (
    .in_1(Read_Sel0), .in_2(Read_Sel1), .in_3(Wrie_Sel), .in_4(in_5), .Write(write_enable), .out_6(out_6),
    .out_7(out_7));

  // Notes on the sheet:
  //   Write Data
  //   Read Data0
  //   Read Data1
endmodule

module Instruction_Memory (
  input  [31:0] in_1,
  output [31:0] out_2
);

  RAM #(.dataWidth(32)) ram_1 (.addr(in_1[9:2]), .data(out_2));  // open: sel, clk, ld, clr
endmodule

module Data_Memory (
  input  mem_write,
  input  [23:0] a_in,
  input  [31:0] d_in,
  input  read_enable,
  output [31:0] d_out
);

  wire and_1_out, clock_1_out, not_1_out, not_2_out, not_3_out, or_1_out;
  wire [31:0] ram_1_data;

  not not_1 (not_1_out, mem_write);
  Clock clock_1 (.out(clock_1_out));
  not not_2 (not_2_out, mem_write);
  and and_1 (and_1_out, not_2_out, read_enable);
  or or_1 (or_1_out, not_1_out, clock_1_out);
  RAM #(.addrWidth(24), .dataWidth(32)) ram_1 (
    .addr(a_in), .data(ram_1_data), .clk(or_1_out), .ld(and_1_out));  // open: sel, clr
  not not_3 (not_3_out, and_1_out);
  assign d_out = and_1_out ? ram_1_data : 32'bz;  // Controlled_Buffer controlled_buffer_1
  assign ram_1_data = not_3_out ? d_in : 32'bz;  // Controlled_Buffer controlled_buffer_2

  // Notes on the sheet:
  //   mem write
  //   Address
  //   Write Data
  //   read enable
  //   Read Data
endmodule
