// Logisim project CombinedRAM2.circ as structural Verilog: 3 circuits, main circuit main
module main (
  input  RESET
);

  wire clock_1_out, clock_2_out, clock_3_out, clock_4_out, clock_5_out, Decoder_load_a, Decoder_load_p,
       Decoder_ram_store, not_1_out, not_2_out, Phase_Control_execute, Phase_Control_loada,
       Phase_Control_loadb;
  wire [15:0] A_q, counter_1_q, Decoder_data_out, INA, Instruction_B_q, multiplexer_1_out, P_q, ram_1_data;

  Counter #(.width(16), .max('hffff)) counter_1 (
    .count(not_1_out), .Q(counter_1_q), .clk(clock_1_out), .clr(RESET));  // open: load, D, carry
  Clock clock_1 (.out(clock_1_out));
  Multiplexer #(.width(16), .disabled(0), .enable("false")) multiplexer_1 (
    .in0(P_q), .in1(counter_1_q), .out(multiplexer_1_out), .sel(not_1_out));
  not not_1 (not_1_out, Phase_Control_execute);
  Phase_Control Phase_Control (
    .RESET(RESET), .Data_In(INA), .EXECUTE(Phase_Control_execute), .LOADB(Phase_Control_loadb),
    .LOADA(Phase_Control_loada));
  Clock clock_2 (.out(clock_2_out));
  not not_2 (not_2_out, Decoder_ram_store);
  RAM #(.addrWidth(16), .dataWidth(16), .bus("separate")) ram_1 (
    .addr(multiplexer_1_out), .din(A_q), .data(ram_1_data), .str(Decoder_ram_store), .clk(clock_2_out),
    .ld(not_2_out));  // open: sel, clr
  Register #(.width(16)) Instruction_A (
    .D(ram_1_data), .en(Phase_Control_loada), .Q(INA), .clk(clock_3_out));  // open: clr
  Register #(.width(16)) Instruction_B (
    .D(ram_1_data), .en(Phase_Control_loadb), .Q(Instruction_B_q), .clk(clock_3_out));  // open: clr
  Clock clock_3 (.out(clock_3_out));
  Ins_Decoder Decoder (
    .Data_In(ram_1_data), .Instruction_A(INA), .Data_Out(Decoder_data_out), .Load_A(Decoder_load_a),
    .RAM_Store(Decoder_ram_store), .Load_P(Decoder_load_p), .Execute(Phase_Control_execute),
    .Instruction_B(Instruction_B_q));
  Register #(.width(16)) P (.D(A_q), .en(Decoder_load_p), .Q(P_q), .clk(clock_4_out));  // open: clr
  Clock clock_4 (.out(clock_4_out));
  Register #(.width(16)) A (.D(Decoder_data_out), .en(Decoder_load_a), .Q(A_q), .clk(clock_5_out));  // open: clr
  Clock clock_5 (.out(clock_5_out));

  // Notes on the sheet:
  //   Instructions:
  //   0x0000: Load A
  //   0x0001: Store to RAM
  //   Load B
  //   0x80000000 to 0x8000FFFF: Immediate Load A
  //   0x0002: Set Pointer (P)
  //   Load A
  //   Execute
endmodule

module Ins_Decoder (
  input  [15:0] Data_In,
  input  [15:0] Instruction_B,
  input  [15:0] Instruction_A,
  input  Execute,
  output [15:0] Data_Out,
  output Load_A,
  output RAM_Store,
  output Load_P
);

  wire decoder_1_out0, decoder_1_out1, decoder_1_out2, or_1_out;

  Decoder #(.select(2), .disabled(0), .enable("false")) decoder_1 (
    .out0(decoder_1_out0), .out1(decoder_1_out1), .out2(decoder_1_out2), .sel(Instruction_A[1:0]));  // open: out3
  Multiplexer #(.width(16), .disabled(0), .enable("false")) multiplexer_1 (
    .in0(Data_In), .in1(Instruction_B), .out(Data_Out), .sel(Instruction_A[15]));
  or or_1 (or_1_out, Instruction_A[15], decoder_1_out0);
  and and_1 (Load_A, or_1_out, Execute);
  and and_2 (RAM_Store, decoder_1_out1, Execute);
  and and_3 (Load_P, decoder_1_out2, Execute);
endmodule

module Phase_Control (
  input  RESET,
  input  [15:0] Data_In,
  output EXECUTE,
  output LOADB,
  output LOADA
);

  wire clock_1_out, LONG, not_1_out, not_2_out, or_1_out, SHORT;

  or or_1 (or_1_out, SHORT, LOADB);
  Clock clock_1 (.out(clock_1_out));
  D_Flip_Flop #(.trigger("falling")) d_ff_1 (
    .clk(clock_1_out), .D(or_1_out), .Q(EXECUTE), .reset(RESET));  // open: Qn, preset, en
  D_Flip_Flop #(.trigger("falling")) d_ff_2 (
    .clk(clock_1_out), .D(LONG), .Q(LOADB), .en(not_1_out), .reset(RESET));  // open: Qn, preset
  not not_1 (not_1_out, EXECUTE);
  nor nor_1 (LOADA, LOADB, EXECUTE);
  not not_2 (not_2_out, Data_In[15]);
  and and_1 (LONG, LOADA, Data_In[15]);
  and and_2 (SHORT, LOADA, not_2_out);
endmodule
