// Logisim project Flash card machine.circ as structural Verilog: 2 circuits, main circuit main
module main (
  input  [23:0] problem,
  input  [1:0] op,
  input  [31:0] a,
  input  [31:0] b,
  input  [31:0] geuss
);

  wire clock_1_out, clock_2_out, clock_3_out, not_1_out, not_2_out, not_3_out,
       op_decoder_cpu_checker_1_right, store_out;
  wire [1:0] ram_1_data;
  wire [31:0] ram_2_data, ram_3_data;

  Button store (.out(store_out));
  LED right (.in(op_decoder_cpu_checker_1_right));
  op_decoder_cpu_checker op_decoder_cpu_checker_1 (
    .op(ram_1_data), .a(ram_2_data), .b(ram_3_data), .guess(geuss), .right(op_decoder_cpu_checker_1_right));
  Clock clock_1 (.out(clock_1_out));
  not not_1 (not_1_out, store_out);
  Clock clock_2 (.out(clock_2_out));
  not not_2 (not_2_out, store_out);
  Clock clock_3 (.out(clock_3_out));
  not not_3 (not_3_out, store_out);
  RAM #(.addrWidth(24), .dataWidth(2), .bus("separate")) ram_1 (
    .addr(problem), .din(op), .data(ram_1_data), .str(store_out), .clk(clock_1_out), .ld(not_1_out));  // open: sel, clr
  RAM #(.addrWidth(24), .dataWidth(32), .bus("separate")) ram_2 (
    .addr(problem), .din(a), .data(ram_2_data), .str(store_out), .clk(clock_2_out), .ld(not_2_out));  // open: sel, clr
  RAM #(.addrWidth(24), .dataWidth(32), .bus("separate")) ram_3 (
    .addr(problem), .din(b), .data(ram_3_data), .str(store_out), .clk(clock_3_out), .ld(not_3_out));  // open: sel, clr
endmodule

module op_decoder_cpu_checker (
  input  [1:0] op,
  input  [31:0] a,
  input  [31:0] b,
  input  [31:0] guess,
  output right
);

  wire decoder_1_out0, decoder_1_out1, decoder_1_out2, decoder_1_out3;
  wire [31:0] adder_1_out, controlled_buffer_1_out, controlled_buffer_2_out, controlled_buffer_3_out,
       controlled_buffer_4_out, controlled_buffer_5_out, controlled_buffer_6_out, controlled_buffer_7_out,
       controlled_buffer_8_out, subtractor_1_out;

  Decoder #(.select(2), .disabled(0), .enable("false")) decoder_1 (
    .out0(decoder_1_out0), .out1(decoder_1_out1), .out2(decoder_1_out2), .out3(decoder_1_out3), .sel(op));
  assign controlled_buffer_1_out = decoder_1_out0 ? a : 32'bz;  // Controlled_Buffer controlled_buffer_1
  Adder #(.width(32)) adder_1 (
    .a(controlled_buffer_1_out), .b(controlled_buffer_2_out), .out(adder_1_out));  // open: cin, cout
  assign controlled_buffer_2_out = decoder_1_out0 ? b : 32'bz;  // Controlled_Buffer controlled_buffer_2
  assign controlled_buffer_3_out = decoder_1_out1 ? a : 32'bz;  // Controlled_Buffer controlled_buffer_3
  Subtractor #(.width(32)) subtractor_1 (
    .a(controlled_buffer_3_out), .b(controlled_buffer_4_out), .out(subtractor_1_out));  // open: bin, bout
  assign controlled_buffer_4_out = decoder_1_out1 ? b : 32'bz;  // Controlled_Buffer controlled_buffer_4
  assign controlled_buffer_5_out = decoder_1_out2 ? a : 32'bz;  // Controlled_Buffer controlled_buffer_5
  Multiplier #(.width(32)) multiplier_1 (
    .a(controlled_buffer_5_out), .b(controlled_buffer_6_out), .out(adder_1_out));  // open: cin, cout
  assign controlled_buffer_6_out = decoder_1_out2 ? b : 32'bz;  // Controlled_Buffer controlled_buffer_6
  assign controlled_buffer_7_out = decoder_1_out3 ? a : 32'bz;  // Controlled_Buffer controlled_buffer_7
  Divider #(.width(32)) divider_1 (
    .a(controlled_buffer_7_out), .b(controlled_buffer_8_out), .out(adder_1_out));  // open: upper, rem
  assign controlled_buffer_8_out = decoder_1_out3 ? b : 32'bz;  // Controlled_Buffer controlled_buffer_8
  assign adder_1_out = decoder_1_out1 ? subtractor_1_out : 32'bz;  // Controlled_Buffer controlled_buffer_9
  Comparator #(.width(32), .mode("unsigned")) comparator_1 (.a(adder_1_out), .b(guess), .eq(right));  // open: gt, lt
endmodule
