// Logisim project CPU2.circ as structural Verilog: 15 circuits, main circuit Counter
module Counter (
  input  in_1,
  input  in_2,
  output out_3,
  output out_4,
  output out_5,
  output out_6,
  output out_7,
  output out_8,
  output out_9,
  output out_10,
  output out_11,
  output out_12,
  output out_13,
  output out_14,
  output out_15,
  output out_16,
  output out_17,
  output out_18,
  output out_19,
  output out_20,
  output out_21
);

  wire comparator_2_eq, comparator_3_eq, comparator_4_eq, comparator_5_eq, comparator_6_eq, comparator_7_eq,
       comparator_8_eq, comparator_9_eq, comparator_10_eq, comparator_11_eq, comparator_12_eq,
       comparator_13_eq, comparator_14_eq, comparator_15_eq, comparator_16_eq, comparator_17_eq,
       comparator_18_eq, comparator_19_eq;
  wire [7:0] counter_1_q;

  decoder decoder_1 ();  // open: ins, read, write
  Counter_part #(.max('h17)) counter_1 (.Q(counter_1_q), .clk(in_1), .clr(in_2));  // open: load, D, count, carry
  Comparator comparator_1 (.a(8'h17), .b(counter_1_q), .eq(out_5));  // open: gt, lt
  Comparator comparator_2 (.a(counter_1_q), .b({8{1'b0}}), .eq(comparator_2_eq));  // open: gt, lt
  Comparator comparator_3 (.a(counter_1_q), .b(8'h1), .eq(comparator_3_eq));  // open: gt, lt
  Comparator comparator_4 (.a(counter_1_q), .b(8'h2), .eq(comparator_4_eq));  // open: gt, lt
  Comparator comparator_5 (.a(counter_1_q), .b(8'h4), .eq(comparator_5_eq));  // open: gt, lt
  Comparator comparator_6 (.a(counter_1_q), .b(8'h5), .eq(comparator_6_eq));  // open: gt, lt
  Comparator comparator_7 (.a(counter_1_q), .b(8'h6), .eq(comparator_7_eq));  // open: gt, lt
  Comparator comparator_8 (.a(counter_1_q), .b(8'h8), .eq(comparator_8_eq));  // open: gt, lt
  Comparator comparator_9 (.a(counter_1_q), .b(8'h9), .eq(comparator_9_eq));  // open: gt, lt
  Comparator comparator_10 (.a(counter_1_q), .b(8'ha), .eq(comparator_10_eq));  // open: gt, lt
  Comparator comparator_11 (.a(counter_1_q), .b(8'hc), .eq(comparator_11_eq));  // open: gt, lt
  Comparator comparator_12 (.a(counter_1_q), .b(8'hd), .eq(comparator_12_eq));  // open: gt, lt
  Comparator comparator_13 (.a(counter_1_q), .b(8'he), .eq(comparator_13_eq));  // open: gt, lt
  Comparator comparator_14 (.a(counter_1_q), .b(8'h10), .eq(comparator_14_eq));  // open: gt, lt
  Comparator comparator_15 (.a(counter_1_q), .b(8'h11), .eq(comparator_15_eq));  // open: gt, lt
  Comparator comparator_16 (.a(counter_1_q), .b(8'h12), .eq(comparator_16_eq));  // open: gt, lt
  Comparator comparator_17 (.a(counter_1_q), .b(8'h14), .eq(comparator_17_eq));  // open: gt, lt
  Comparator comparator_18 (.a(counter_1_q), .b(8'h15), .eq(comparator_18_eq));  // open: gt, lt
  Comparator comparator_19 (.a(counter_1_q), .b(8'h16), .eq(comparator_19_eq));  // open: gt, lt
  and and_1 (out_3, in_1, comparator_2_eq);
  and and_2 (out_4, in_1, comparator_3_eq);
  and and_3 (out_6, in_1, comparator_4_eq);
  and and_4 (out_7, in_1, comparator_5_eq);
  and and_5 (out_8, in_1, comparator_6_eq);
  and and_6 (out_9, in_1, comparator_7_eq);
  and and_7 (out_10, in_1, comparator_8_eq);
  and and_8 (out_11, in_1, comparator_9_eq);
  and and_9 (out_12, in_1, comparator_10_eq);
  and and_10 (out_13, in_1, comparator_11_eq);
  and and_11 (out_14, in_1, comparator_12_eq);
  and and_12 (out_15, in_1, comparator_13_eq);
  and and_13 (out_16, in_1, comparator_14_eq);
  and and_14 (out_17, in_1, comparator_15_eq);
  and and_15 (out_18, in_1, comparator_16_eq);
  and and_16 (out_19, in_1, comparator_17_eq);
  and and_17 (out_20, in_1, comparator_18_eq);
  and and_18 (out_21, in_1, comparator_19_eq);
endmodule

module Interpolator (
  input  [6:0] in_1,
  input  in_2,
  output [7:0] out_3,
  output [7:0] out_4,
  output out_5,
  output [7:0] out_6,
  output out_7,
  output [7:0] out_8,
  output [7:0] out_9,
  output [7:0] out_10
);

  wire and_3_out, clock_1_out, clock_2_out, comparator_1_eq, counter_1_out_3, counter_1_out_4,
       counter_1_out_5, counter_1_out_6, counter_1_out_7, counter_1_out_8, counter_1_out_9, counter_1_out_10,
       counter_1_out_11, counter_1_out_12, counter_1_out_13, counter_1_out_14, counter_1_out_15,
       counter_1_out_16, counter_1_out_17, counter_1_out_18, counter_1_out_19, counter_1_out_20,
       counter_1_out_21, s_r_ff_1_q, s_r_ff_1_qn;
  wire [3:0] counter_2_q;
  wire [6:0] register_1_q, register_2_q, register_3_q, register_4_q, register_5_q, register_6_q,
       register_7_q, register_8_q, register_9_q, register_10_q, register_11_q, register_12_q, register_13_q,
       register_14_q, register_15_q, register_16_q, register_17_q, register_18_q, subtractor_1_out,
       subtractor_2_out, subtractor_3_out, subtractor_4_out, subtractor_5_out, subtractor_6_out,
       subtractor_7_out, subtractor_8_out, subtractor_9_out, subtractor_10_out, subtractor_11_out,
       subtractor_12_out, subtractor_13_out, subtractor_14_out, subtractor_15_out;
  wire [7:0] adder_1_out, adder_3_out, adder_5_out, adder_7_out, adder_9_out, bit_extender_1_out,
       bit_extender_2_out, bit_extender_3_out, bit_extender_4_out, bit_extender_5_out, bit_extender_6_out,
       bit_extender_7_out, bit_extender_8_out, bit_extender_9_out, bit_extender_10_out, bit_extender_11_out,
       bit_extender_12_out, bit_extender_13_out, bit_extender_14_out, bit_extender_15_out,
       bit_extender_16_out, bit_extender_17_out, bit_extender_18_out, multiplier_1_out, multiplier_2_out,
       multiplier_3_out, multiplier_4_out, multiplier_5_out, multiplier_6_out, multiplier_7_out,
       multiplier_8_out, multiplier_9_out, multiplier_10_out;
  wire [23:0] rom_1_data;

  S_R_Flip_Flop s_r_ff_1 (
    .Q(s_r_ff_1_q), .Qn(s_r_ff_1_qn), .preset(in_2), .reset(counter_1_out_5));  // open: S, clk, R, en
  Clock clock_1 (.out(clock_1_out));
  and and_1 (out_7, counter_1_out_5, comparator_1_eq);
  and and_2 (out_5, s_r_ff_1_q, clock_1_out, ~in_2);  // AND_Gate
  Counter counter_1 (
    .in_1(out_5), .out_5(counter_1_out_5), .out_3(counter_1_out_3), .out_4(counter_1_out_4),
    .out_6(counter_1_out_6), .out_7(counter_1_out_7), .out_8(counter_1_out_8), .out_9(counter_1_out_9),
    .out_10(counter_1_out_10), .out_11(counter_1_out_11), .out_12(counter_1_out_12),
    .out_13(counter_1_out_13), .out_14(counter_1_out_14), .out_15(counter_1_out_15),
    .out_16(counter_1_out_16), .out_17(counter_1_out_17), .out_18(counter_1_out_18),
    .out_19(counter_1_out_19), .out_20(counter_1_out_20), .out_21(counter_1_out_21), .in_2(s_r_ff_1_qn));
  Register #(.width(7)) register_1 (.D(in_1), .Q(register_1_q), .clk(counter_1_out_3));  // open: en, clr
  Register #(.width(7)) register_2 (.D(in_1), .Q(register_2_q), .clk(counter_1_out_4));  // open: en, clr
  Register #(.width(7)) register_3 (.D(in_1), .Q(register_3_q), .clk(counter_1_out_6));  // open: en, clr
  Register #(.width(7)) register_4 (.D(in_1), .Q(register_4_q), .clk(counter_1_out_7));  // open: en, clr
  Register #(.width(7)) register_5 (.D(in_1), .Q(register_5_q), .clk(counter_1_out_8));  // open: en, clr
  Register #(.width(7)) register_6 (.D(in_1), .Q(register_6_q), .clk(counter_1_out_9));  // open: en, clr
  Register #(.width(7)) register_7 (.D(in_1), .Q(register_7_q), .clk(counter_1_out_10));  // open: en, clr
  Register #(.width(7)) register_8 (.D(in_1), .Q(register_8_q), .clk(counter_1_out_11));  // open: en, clr
  Register #(.width(7)) register_9 (.D(in_1), .Q(register_9_q), .clk(counter_1_out_12));  // open: en, clr
  Register #(.width(7)) register_10 (.D(in_1), .Q(register_10_q), .clk(counter_1_out_13));  // open: en, clr
  Register #(.width(7)) register_11 (.D(in_1), .Q(register_11_q), .clk(counter_1_out_14));  // open: en, clr
  Register #(.width(7)) register_12 (.D(in_1), .Q(register_12_q), .clk(counter_1_out_15));  // open: en, clr
  Register #(.width(7)) register_13 (.D(in_1), .Q(register_13_q), .clk(counter_1_out_16));  // open: en, clr
  Register #(.width(7)) register_14 (.D(in_1), .Q(register_14_q), .clk(counter_1_out_17));  // open: en, clr
  Register #(.width(7)) register_15 (.D(in_1), .Q(register_15_q), .clk(counter_1_out_18));  // open: en, clr
  Register #(.width(7)) register_16 (.D(in_1), .Q(register_16_q), .clk(counter_1_out_19));  // open: en, clr
  Register #(.width(7)) register_17 (.D(in_1), .Q(register_17_q), .clk(counter_1_out_20));  // open: en, clr
  Register #(.width(7)) register_18 (.D(in_1), .Q(register_18_q), .clk(counter_1_out_21));  // open: en, clr
  Subtractor #(.width(7)) subtractor_1 (.a(register_1_q), .b(7'b0110000), .out(subtractor_1_out));  // open: bin, bout
  Subtractor #(.width(7)) subtractor_2 (.a(register_2_q), .b(7'b0110000), .out(subtractor_2_out));  // open: bin, bout
  Subtractor #(.width(7)) subtractor_3 (.a(register_3_q), .b(7'b0110000), .out(subtractor_3_out));  // open: bin, bout
  assign bit_extender_1_out = {{1{1'b0}}, register_4_q};  // Bit_Extender bit_extender_1
  and and_3 (and_3_out, clock_2_out, ~comparator_1_eq);  // AND_Gate
  assign bit_extender_2_out = {{1{1'b0}}, register_5_q};  // Bit_Extender bit_extender_2
  Clock clock_2 (.out(clock_2_out));
  assign bit_extender_3_out = {{1{1'b0}}, register_6_q};  // Bit_Extender bit_extender_3
  Subtractor #(.width(7)) subtractor_4 (.a(register_7_q), .b(7'b0110000), .out(subtractor_4_out));  // open: bin, bout
  Subtractor #(.width(7)) subtractor_5 (.a(register_8_q), .b(7'b0110000), .out(subtractor_5_out));  // open: bin, bout
  Subtractor #(.width(7)) subtractor_6 (.a(register_9_q), .b(7'b0110000), .out(subtractor_6_out));  // open: bin, bout
  Subtractor #(.width(7)) subtractor_7 (.a(register_10_q), .b(7'b0110000), .out(subtractor_7_out));  // open: bin, bout
  Subtractor #(.width(7)) subtractor_8 (.a(register_11_q), .b(7'b0110000), .out(subtractor_8_out));  // open: bin, bout
  Subtractor #(.width(7)) subtractor_9 (.a(register_12_q), .b(7'b0110000), .out(subtractor_9_out));  // open: bin, bout
  Subtractor #(.width(7)) subtractor_10 (
    .a(register_13_q), .b(7'b0110000), .out(subtractor_10_out));  // open: bin, bout
  Subtractor #(.width(7)) subtractor_11 (
    .a(register_14_q), .b(7'b0110000), .out(subtractor_11_out));  // open: bin, bout
  Subtractor #(.width(7)) subtractor_12 (
    .a(register_15_q), .b(7'b0110000), .out(subtractor_12_out));  // open: bin, bout
  Subtractor #(.width(7)) subtractor_13 (
    .a(register_16_q), .b(7'b0110000), .out(subtractor_13_out));  // open: bin, bout
  Subtractor #(.width(7)) subtractor_14 (
    .a(register_17_q), .b(7'b0110000), .out(subtractor_14_out));  // open: bin, bout
  Subtractor #(.width(7)) subtractor_15 (
    .a(register_18_q), .b(7'b0110000), .out(subtractor_15_out));  // open: bin, bout
  assign bit_extender_4_out = {{1{1'b0}}, subtractor_1_out};  // Bit_Extender bit_extender_4
  Multiplier multiplier_1 (.a(bit_extender_4_out), .b(8'h64), .out(multiplier_1_out));  // open: cin, cout
  assign bit_extender_5_out = {{1{1'b0}}, subtractor_2_out};  // Bit_Extender bit_extender_5
  Multiplier multiplier_2 (.a(bit_extender_5_out), .b(8'ha), .out(multiplier_2_out));  // open: cin, cout
  assign bit_extender_6_out = {{1{1'b0}}, subtractor_3_out};  // Bit_Extender bit_extender_6
  Counter_part #(.width(4), .max('hb)) counter_2 (
    .Q(counter_2_q), .clk(and_3_out));  // open: load, D, count, carry, clr
  Comparator #(.width(24)) comparator_1 (
    .a(rom_1_data), .b({bit_extender_1_out, bit_extender_2_out, bit_extender_3_out}), .eq(comparator_1_eq));  // open: gt, lt
  assign bit_extender_7_out = {{1{1'b0}}, subtractor_4_out};  // Bit_Extender bit_extender_7
  Multiplier multiplier_3 (.a(bit_extender_7_out), .b(8'h64), .out(multiplier_3_out));  // open: cin, cout
  Multiplier multiplier_4 (.a(bit_extender_8_out), .b(8'ha), .out(multiplier_4_out));  // open: cin, cout
  assign bit_extender_8_out = {{1{1'b0}}, subtractor_5_out};  // Bit_Extender bit_extender_8
  assign bit_extender_9_out = {{1{1'b0}}, subtractor_6_out};  // Bit_Extender bit_extender_9
  assign bit_extender_10_out = {{1{1'b0}}, subtractor_7_out};  // Bit_Extender bit_extender_10
  Multiplier multiplier_5 (.a(bit_extender_10_out), .b(8'h64), .out(multiplier_5_out));  // open: cin, cout
  Multiplier multiplier_6 (.a(bit_extender_11_out), .b(8'ha), .out(multiplier_6_out));  // open: cin, cout
  assign bit_extender_11_out = {{1{1'b0}}, subtractor_8_out};  // Bit_Extender bit_extender_11
  assign bit_extender_12_out = {{1{1'b0}}, subtractor_9_out};  // Bit_Extender bit_extender_12
  Multiplier multiplier_7 (.a(bit_extender_13_out), .b(8'h64), .out(multiplier_7_out));  // open: cin, cout
  assign bit_extender_13_out = {{1{1'b0}}, subtractor_10_out};  // Bit_Extender bit_extender_13
  Multiplier multiplier_8 (.a(bit_extender_14_out), .b(8'ha), .out(multiplier_8_out));  // open: cin, cout
  assign bit_extender_14_out = {{1{1'b0}}, subtractor_11_out};  // Bit_Extender bit_extender_14
  assign bit_extender_15_out = {{1{1'b0}}, subtractor_12_out};  // Bit_Extender bit_extender_15
  Multiplier multiplier_9 (.a(bit_extender_16_out), .b(8'h64), .out(multiplier_9_out));  // open: cin, cout
  assign bit_extender_16_out = {{1{1'b0}}, subtractor_13_out};  // Bit_Extender bit_extender_16
  Multiplier multiplier_10 (.a(bit_extender_17_out), .b(8'ha), .out(multiplier_10_out));  // open: cin, cout
  assign bit_extender_17_out = {{1{1'b0}}, subtractor_14_out};  // Bit_Extender bit_extender_17
  assign bit_extender_18_out = {{1{1'b0}}, subtractor_15_out};  // Bit_Extender bit_extender_18
  Adder adder_1 (.a(multiplier_1_out), .b(multiplier_2_out), .out(adder_1_out));  // open: cin, cout
  Adder adder_2 (.a(adder_1_out), .b(bit_extender_6_out), .out(out_3));  // open: cin, cout
  assign out_4 = {{4{1'b0}}, counter_2_q};  // Bit_Extender bit_extender_19
  Adder adder_3 (.a(multiplier_3_out), .b(multiplier_4_out), .out(adder_3_out));  // open: cin, cout
  Adder adder_4 (.a(adder_3_out), .b(bit_extender_9_out), .out(out_6));  // open: cin, cout
  Adder adder_5 (.a(multiplier_5_out), .b(multiplier_6_out), .out(adder_5_out));  // open: cin, cout
  Adder adder_6 (.a(adder_5_out), .b(bit_extender_12_out), .out(out_8));  // open: cin, cout
  Adder adder_7 (.a(multiplier_7_out), .b(multiplier_8_out), .out(adder_7_out));  // open: cin, cout
  Adder adder_8 (.a(adder_7_out), .b(bit_extender_15_out), .out(out_9));  // open: cin, cout
  Adder adder_9 (.a(multiplier_9_out), .b(multiplier_10_out), .out(adder_9_out));  // open: cin, cout
  Adder adder_10 (.a(adder_9_out), .b(bit_extender_18_out), .out(out_10));  // open: cin, cout
  ROM #(.addrWidth(4), .dataWidth(24)) rom_1 (.addr(counter_2_q), .data(rom_1_data));  // open: sel

  // Notes on the sheet:
  //   contents of rom_1 (hex, n*v repeats v):
  //   575254 4a4d50 535450 4f5450 494e50 57544f 575449 4c4441 434f4d 484748 4c4f57 434c4b
endmodule

// Instruction
module Instruction_Cache (
  input  [6:0] in_1,
  input  in_2,
  input  [7:0] in_3,
  input  in_4,
  output out_5,
  output [7:0] out_6,
  output [7:0] out_7,
  output [7:0] out_8,
  output [7:0] out_9,
  output [7:0] out_10,
  output [6:0] out_11,
  output out_12,
  output out_13
);

  wire and_1_out, and_2_out, and_3_out, and_4_out, and_5_out, and_6_out, and_7_out, and_8_out, clock_1_out,
       clock_2_out, comparator_1_eq, comparator_2_eq, comparator_3_eq, comparator_4_eq, comparator_5_eq,
       comparator_6_eq, comparator_7_eq, comparator_8_eq, interpolator_1_out_7, s_r_ff_1_q, s_r_ff_1_qn,
       s_r_ff_2_qn;
  wire [1:0] driver_1_out_4;
  wire [2:0] counter_1_q;
  wire [7:0] adder_1_out, bit_extender_2_out, interpolator_1_out_3, interpolator_1_out_4,
       interpolator_1_out_6, interpolator_1_out_8, interpolator_1_out_9, interpolator_1_out_10,
       multiplexer_1_out, multiplier_1_out, ram_1_data, register_1_q;
  wire [8:0] adder_2_out, bit_extender_1_out, bit_extender_3_out, counter_2_q, driver_1_out_8,
       multiplexer_2_out, multiplier_2_out;

  Interpolator interpolator_1 (
    .in_1(in_1), .out_5(out_5), .in_2(and_1_out), .out_3(interpolator_1_out_3), .out_4(interpolator_1_out_4),
    .out_6(interpolator_1_out_6), .out_8(interpolator_1_out_8), .out_9(interpolator_1_out_9),
    .out_10(interpolator_1_out_10), .out_7(interpolator_1_out_7));
  and and_1 (and_1_out, in_2, ~driver_1_out_4[1]);  // AND_Gate
  S_R_Flip_Flop s_r_ff_1 (
    .Q(s_r_ff_1_q), .Qn(s_r_ff_1_qn), .preset(interpolator_1_out_7), .reset(comparator_1_eq));  // open: S, clk, R, en
  Clock clock_1 (.out(clock_1_out));
  and and_2 (and_2_out, clock_1_out, s_r_ff_1_q);
  Multiplier multiplier_1 (.a(8'h6), .b(interpolator_1_out_3), .out(multiplier_1_out));  // open: cin, cout
  Multiplexer #(.select(3), .width(8), .enable("false")) multiplexer_1 (
    .in0(8'h1), .in1(interpolator_1_out_4), .in2(interpolator_1_out_6), .in3(interpolator_1_out_8),
    .in4(interpolator_1_out_9), .in5(interpolator_1_out_10), .out(multiplexer_1_out), .sel(counter_1_q));  // open: in6, in7
  Counter_part #(.width(3), .max('h6)) counter_1 (
    .Q(counter_1_q), .clk(and_2_out), .clr(s_r_ff_1_qn));  // open: load, D, count, carry
  Adder adder_1 (.a(multiplier_1_out), .b(bit_extender_2_out), .out(adder_1_out));  // open: cin, cout
  assign bit_extender_1_out = {{1{1'b0}}, adder_1_out};  // Bit_Extender bit_extender_1
  Register register_1 (.D(interpolator_1_out_3), .Q(register_1_q), .clk(comparator_2_eq));  // open: en, clr
  assign bit_extender_2_out = {{5{1'b0}}, counter_1_q};  // Bit_Extender bit_extender_2
  Comparator #(.width(3)) comparator_1 (.a(counter_1_q), .b(3'b110), .eq(comparator_1_eq));  // open: gt, lt
  Comparator #(.width(3)) comparator_2 (.a(counter_1_q), .b(3'b001), .eq(comparator_2_eq));  // open: gt, lt
  Multiplexer #(.select(2), .width(9), .enable("false")) multiplexer_2 (
    .in0(bit_extender_1_out), .in1(driver_1_out_8), .in2(adder_2_out), .out(multiplexer_2_out),
    .sel(driver_1_out_4));  // open: in3
  Driver driver_1 (
    .in_1(register_1_q), .in_2(ram_1_data), .in_3(comparator_1_eq), .out_4(driver_1_out_4[0]),
    .out_8(driver_1_out_8), .out_5(out_11), .out_6(out_12), .out_7(out_13));
  RAM #(.addrWidth(9), .bus("separate")) ram_1 (
    .addr(multiplexer_2_out), .din(multiplexer_1_out), .data(ram_1_data), .clk(and_2_out));  // open: str, sel, ld, clr
  assign bit_extender_3_out = {{1{1'b0}}, in_3};  // Bit_Extender bit_extender_3
  Counter_part #(.width(9), .max('h6)) counter_2 (
    .Q(counter_2_q), .clk(and_3_out), .clr(s_r_ff_2_qn));  // open: load, D, count, carry
  and and_3 (and_3_out, driver_1_out_4[1], clock_2_out);
  Clock clock_2 (.out(clock_2_out));
  S_R_Flip_Flop s_r_ff_2 (
    .Q(driver_1_out_4[1]), .Qn(s_r_ff_2_qn), .preset(in_4), .reset(comparator_3_eq));  // open: S, clk, R, en
  Comparator #(.width(9)) comparator_3 (.a(9'h6), .b(counter_2_q), .eq(comparator_3_eq));  // open: gt, lt
  Multiplier #(.width(9)) multiplier_2 (.a(9'h6), .b(bit_extender_3_out), .out(multiplier_2_out));  // open: cin, cout
  Adder #(.width(9)) adder_2 (.a(multiplier_2_out), .b(counter_2_q), .out(adder_2_out));  // open: cin, cout
  Comparator #(.width(9)) comparator_4 (.a(9'h1), .b(counter_2_q), .eq(comparator_4_eq));  // open: gt, lt
  Comparator #(.width(9)) comparator_5 (.a(9'h2), .b(counter_2_q), .eq(comparator_5_eq));  // open: gt, lt
  Comparator #(.width(9)) comparator_6 (.a(9'h3), .b(counter_2_q), .eq(comparator_6_eq));  // open: gt, lt
  Comparator #(.width(9)) comparator_7 (.a(9'h4), .b(counter_2_q), .eq(comparator_7_eq));  // open: gt, lt
  Comparator #(.width(9)) comparator_8 (.a(9'h5), .b(counter_2_q), .eq(comparator_8_eq));  // open: gt, lt
  Register register_2 (.D(ram_1_data), .Q(out_6), .clk(and_4_out));  // open: en, clr
  and and_4 (and_4_out, comparator_4_eq, and_3_out);
  Register register_3 (.D(ram_1_data), .Q(out_7), .clk(and_5_out));  // open: en, clr
  and and_5 (and_5_out, comparator_5_eq, and_3_out);
  Register register_4 (.D(ram_1_data), .Q(out_8), .clk(and_6_out));  // open: en, clr
  and and_6 (and_6_out, comparator_6_eq, and_3_out);
  Register register_5 (.D(ram_1_data), .Q(out_9), .clk(and_7_out));  // open: en, clr
  and and_7 (and_7_out, comparator_7_eq, and_3_out);
  Register register_6 (.D(ram_1_data), .Q(out_10), .clk(and_8_out));  // open: en, clr
  and and_8 (and_8_out, comparator_8_eq, and_3_out);
endmodule

module Driver (
  input  [7:0] in_1,
  input  [7:0] in_2,
  input  in_3,
  output out_4,
  output [6:0] out_5,
  output out_6,
  output out_7,
  output [8:0] out_8
);

  wire and_1_out, and_2_out, and_3_out, and_4_out, and_5_out, and_6_out, and_7_out, and_8_out,
       bit_extender_2_out, clock_1_out, clock_2_out, comparator_1_gt, comparator_2_eq, comparator_3_eq,
       comparator_4_eq, comparator_5_eq, comparator_6_eq, comparator_7_eq, comparator_8_eq, comparator_9_eq,
       comparator_10_eq, or_1_out, s_r_ff_1_qn, s_r_ff_2_q, s_r_ff_2_qn;
  wire [3:0] counter_1_q, counter_2_q, subtractor_1_out;
  wire [4:0] counter_3_q;
  wire [6:0] decoder_1_out_2, decoder_1_out_3, decoder_1_out_4, decoder_2_out_2, decoder_2_out_3,
       decoder_2_out_4, decoder_3_out_2, decoder_3_out_3, decoder_3_out_4, decoder_4_out_2, decoder_4_out_3,
       decoder_4_out_4, decoder_5_out_2, decoder_5_out_3, decoder_5_out_4, multiplexer_2_out,
       text_dec_1_out_2, text_dec_1_out_3, text_dec_1_out_4;
  wire [7:0] bit_extender_5_out, demultiplexer_1_out0, multiplexer_1_out, register_1_q, register_2_q,
       register_3_q, register_4_q, register_5_q, register_6_q, subtractor_2_out;
  wire [8:0] adder_2_out, bit_extender_1_out, bit_extender_3_out, bit_extender_4_out, multiplier_1_out;

  and and_1 (and_1_out, and_8_out, ~bit_extender_2_out);  // AND_Gate
  and and_2 (and_2_out, out_4, s_r_ff_2_qn, clock_1_out);
  or or_1 (or_1_out, comparator_9_eq, and_1_out);
  Clock clock_1 (.out(clock_1_out));
  S_R_Flip_Flop s_r_ff_1 (.Q(out_4), .Qn(s_r_ff_1_qn), .preset(in_3), .reset(or_1_out));  // open: S, clk, R, en
  Counter_part #(.width(4), .max('h8)) counter_1 (
    .Q(counter_1_q), .clk(and_2_out), .clr(s_r_ff_1_qn));  // open: load, D, count, carry
  Comparator comparator_1 (.a(8'h5), .b(in_1), .gt(comparator_1_gt));  // open: eq, lt
  Demultiplexer #(.width(8), .enable("false")) demultiplexer_1 (
    .out0(demultiplexer_1_out0), .in(in_1), .sel(comparator_1_gt));  // open: out1
  Comparator #(.width(4)) comparator_2 (.a(4'b0001), .b(counter_1_q), .eq(comparator_2_eq));  // open: gt, lt
  and and_3 (and_3_out, comparator_2_eq, and_2_out);
  Comparator #(.width(4)) comparator_3 (.a(4'b0010), .b(counter_1_q), .eq(comparator_3_eq));  // open: gt, lt
  and and_4 (and_4_out, comparator_3_eq, and_2_out);
  Comparator #(.width(4)) comparator_4 (.a(4'b0011), .b(counter_1_q), .eq(comparator_4_eq));  // open: gt, lt
  and and_5 (and_5_out, comparator_4_eq, and_2_out);
  Comparator #(.width(4)) comparator_5 (.a(4'b0100), .b(counter_1_q), .eq(comparator_5_eq));  // open: gt, lt
  and and_6 (and_6_out, comparator_5_eq, and_2_out);
  Comparator #(.width(4)) comparator_6 (.a(4'b0101), .b(counter_1_q), .eq(comparator_6_eq));  // open: gt, lt
  and and_7 (and_7_out, comparator_6_eq, and_2_out);
  Comparator #(.width(4)) comparator_7 (.a(4'b0110), .b(counter_1_q), .eq(comparator_7_eq));  // open: gt, lt
  and and_8 (and_8_out, comparator_7_eq, and_2_out);
  Comparator #(.width(4)) comparator_8 (.a(4'b0111), .b(counter_1_q), .eq(comparator_8_eq));  // open: gt, lt
  Subtractor #(.width(4)) subtractor_1 (.a(counter_1_q), .b(4'b0001), .out(subtractor_1_out));  // open: bin, bout
  assign bit_extender_1_out = {{5{1'b0}}, subtractor_1_out};  // Bit_Extender bit_extender_1
  Subtractor subtractor_2 (.a(demultiplexer_1_out0), .b(8'h5), .out(subtractor_2_out));  // open: bin, bout
  Bit_Extender #(.out_width(1)) bit_extender_2 (.in(register_1_q), .out(bit_extender_2_out));
  Register register_1 (.D(in_2), .Q(register_1_q), .clk(and_3_out));  // open: en, clr
  Text_Dec text_dec_1 (
    .in_1(register_2_q), .out_2(text_dec_1_out_2), .out_3(text_dec_1_out_3), .out_4(text_dec_1_out_4));
  Register register_2 (.D(in_2), .Q(register_2_q), .clk(and_4_out));  // open: en, clr
  Decoder decoder_1 (.in_1(register_3_q), .out_2(decoder_1_out_2), .out_3(decoder_1_out_3), .out_4(decoder_1_out_4));
  Register register_3 (.D(in_2), .Q(register_3_q), .clk(and_5_out));  // open: en, clr
  Decoder decoder_2 (.in_1(register_4_q), .out_2(decoder_2_out_2), .out_3(decoder_2_out_3), .out_4(decoder_2_out_4));
  Register register_4 (.D(in_2), .Q(register_4_q), .clk(and_6_out));  // open: en, clr
  Decoder decoder_3 (.in_1(register_5_q), .out_2(decoder_3_out_2), .out_3(decoder_3_out_3), .out_4(decoder_3_out_4));
  Register register_5 (.D(in_2), .Q(register_5_q), .clk(and_7_out));  // open: en, clr
  Decoder decoder_4 (.in_1(register_6_q), .out_2(decoder_4_out_2), .out_3(decoder_4_out_3), .out_4(decoder_4_out_4));
  Register register_6 (.D(in_2), .Q(register_6_q), .clk(and_8_out));  // open: en, clr
  Adder #(.width(9)) adder_1 (.a(multiplier_1_out), .b(bit_extender_1_out), .out(out_8));  // open: cin, cout
  Counter_part #(.width(4), .max('ha)) counter_2 (
    .Q(counter_2_q), .clk(comparator_10_eq), .clr(s_r_ff_1_qn));  // open: load, D, count, carry
  assign bit_extender_3_out = {{1{1'b0}}, multiplexer_1_out};  // Bit_Extender bit_extender_3
  Multiplexer #(.width(8), .enable("false")) multiplexer_1 (
    .in0(subtractor_2_out), .in1({8{1'b0}}), .out(multiplexer_1_out), .sel(comparator_1_gt));
  Decoder decoder_5 (
    .in_1(bit_extender_5_out), .out_2(decoder_5_out_2), .out_3(decoder_5_out_3), .out_4(decoder_5_out_4));
  S_R_Flip_Flop s_r_ff_2 (
    .Q(s_r_ff_2_q), .Qn(s_r_ff_2_qn), .preset(comparator_8_eq), .reset(comparator_10_eq));  // open: S, clk, R, en
  and and_9 (out_6, s_r_ff_2_q, clock_2_out);
  Clock clock_2 (.out(clock_2_out));
  assign bit_extender_4_out = {{5{1'b0}}, counter_2_q};  // Bit_Extender bit_extender_4
  Adder #(.width(9)) adder_2 (.a(bit_extender_4_out), .b(bit_extender_3_out), .out(adder_2_out));  // open: cin, cout
  Multiplexer #(.select(5), .width(7), .enable("false")) multiplexer_2 (
    .in0(decoder_5_out_4), .in1(decoder_5_out_3), .in2(decoder_5_out_2), .in3(7'b0100000),
    .in4(text_dec_1_out_4), .in5(text_dec_1_out_3), .in6(text_dec_1_out_2), .in7(7'b0100000),
    .in8(decoder_1_out_4), .in9(decoder_1_out_3), .in10(decoder_1_out_2), .in11(7'b0100000),
    .in12(decoder_2_out_4), .in13(decoder_2_out_3), .in14(decoder_2_out_2), .in15(7'b0100000),
    .in16(decoder_3_out_4), .in17(decoder_3_out_3), .in18(decoder_3_out_2), .in19(7'b0100000),
    .in20(decoder_4_out_4), .in21(decoder_4_out_3), .in22(decoder_4_out_2), .out(multiplexer_2_out),
    .sel(counter_3_q));  // open: in23, in24, in25, in26, in27, in28, in29, in30, in31
  Counter_part #(.width(5), .max('h17)) counter_3 (
    .Q(counter_3_q), .clk(out_6), .clr(s_r_ff_2_qn));  // open: load, D, count, carry
  Comparator #(.width(9)) comparator_9 (.a(bit_extender_4_out), .b(9'ha), .eq(comparator_9_eq));  // open: gt, lt
  Multiplier #(.width(9)) multiplier_1 (.a(9'h6), .b(adder_2_out), .out(multiplier_1_out));  // open: cin, cout
  Multiplexer #(.width(7), .enable("false")) multiplexer_3 (
    .in0(7'b0100000), .in1(multiplexer_2_out), .out(out_5), .sel(bit_extender_2_out));
  Comparator #(.width(5)) comparator_10 (.a(counter_3_q), .b(5'b10111), .eq(comparator_10_eq));  // open: gt, lt
  Bit_Extender #(.in_width(9), .out_width(8)) bit_extender_5 (.in(adder_2_out), .out(bit_extender_5_out));

  assign out_7 = in_3;
endmodule

module Decoder (
  input  [7:0] in_1,
  output [6:0] out_2,
  output [6:0] out_3,
  output [6:0] out_4
);

  wire comparator_1_eq;
  wire [6:0] bit_extender_1_out, bit_extender_2_out, bit_extender_3_out;
  wire [7:0] adder_1_out, adder_2_out, adder_3_out, divider_1_out, divider_2_out, divider_3_out,
       divider_4_out, multiplier_1_out, multiplier_2_out, subtractor_1_out, subtractor_2_out;

  Divider divider_1 (.a(in_1), .b(8'h64), .out(divider_1_out));  // open: upper, rem
  Multiplier multiplier_1 (.a(divider_1_out), .b(8'h64), .out(multiplier_1_out));  // open: cin, cout
  Divider divider_2 (.a(subtractor_1_out), .b(8'ha), .out(divider_2_out));  // open: upper, rem
  Subtractor subtractor_1 (.a(in_1), .b(multiplier_1_out), .out(subtractor_1_out));  // open: bin, bout
  Multiplier multiplier_2 (.a(divider_2_out), .b(8'ha), .out(multiplier_2_out));  // open: cin, cout
  Subtractor subtractor_2 (.a(subtractor_1_out), .b(multiplier_2_out), .out(subtractor_2_out));  // open: bin, bout
  Divider divider_3 (.a(multiplier_2_out), .b(8'ha), .out(divider_3_out));  // open: upper, rem
  Divider divider_4 (.a(multiplier_1_out), .b(8'h64), .out(divider_4_out));  // open: upper, rem
  Comparator comparator_1 (.a(in_1), .b(8'hb0), .eq(comparator_1_eq));  // open: gt, lt
  Adder adder_1 (.a(8'h30), .b(subtractor_2_out), .out(adder_1_out));  // open: cin, cout
  Bit_Extender #(.out_width(7)) bit_extender_1 (.in(adder_1_out), .out(bit_extender_1_out));
  Bit_Extender #(.out_width(7)) bit_extender_2 (.in(adder_2_out), .out(bit_extender_2_out));
  Adder adder_2 (.a(8'h30), .b(divider_3_out), .out(adder_2_out));  // open: cin, cout
  Adder adder_3 (.a(8'h30), .b(divider_4_out), .out(adder_3_out));  // open: cin, cout
  Bit_Extender #(.out_width(7)) bit_extender_3 (.in(adder_3_out), .out(bit_extender_3_out));
  Multiplexer #(.width(7), .enable("false")) multiplexer_1 (
    .in0(bit_extender_1_out), .in1(7'b0100000), .out(out_2), .sel(comparator_1_eq));
  Multiplexer #(.width(7), .enable("false")) multiplexer_2 (
    .in0(bit_extender_2_out), .in1(7'b0100000), .out(out_3), .sel(comparator_1_eq));
  Multiplexer #(.width(7), .enable("false")) multiplexer_3 (
    .in0(bit_extender_3_out), .in1(7'b0100000), .out(out_4), .sel(comparator_1_eq));
endmodule

module Text_Dec (
  input  [7:0] in_1,
  output [6:0] out_2,
  output [6:0] out_3,
  output [6:0] out_4
);

  wire [3:0] bit_extender_1_out;
  wire [23:0] divider_1_out, divider_2_out, divider_3_out, divider_4_out, multiplier_1_out, multiplier_2_out,
       rom_1_data, subtractor_1_out, subtractor_2_out;

  Bit_Extender #(.out_width(4)) bit_extender_1 (.in(in_1), .out(bit_extender_1_out));
  ROM #(.addrWidth(4), .dataWidth(24)) rom_1 (.addr(bit_extender_1_out), .data(rom_1_data));  // open: sel
  Divider #(.width(24)) divider_1 (.a(rom_1_data), .b(24'h10000), .out(divider_1_out));  // open: upper, rem
  Multiplier #(.width(24)) multiplier_1 (.a(divider_1_out), .b(24'h10000), .out(multiplier_1_out));  // open: cin, cout
  Subtractor #(.width(24)) subtractor_1 (
    .a(rom_1_data), .b(multiplier_1_out), .out(subtractor_1_out));  // open: bin, bout
  Divider #(.width(24)) divider_2 (.a(subtractor_1_out), .b(24'h100), .out(divider_2_out));  // open: upper, rem
  Multiplier #(.width(24)) multiplier_2 (.a(divider_2_out), .b(24'h100), .out(multiplier_2_out));  // open: cin, cout
  Subtractor #(.width(24)) subtractor_2 (
    .a(subtractor_1_out), .b(multiplier_2_out), .out(subtractor_2_out));  // open: bin, bout
  Divider #(.width(24)) divider_3 (.a(multiplier_2_out), .b(24'h100), .out(divider_3_out));  // open: upper, rem
  Divider #(.width(24)) divider_4 (.a(multiplier_1_out), .b(24'h10000), .out(divider_4_out));  // open: upper, rem
  Bit_Extender #(.in_width(24), .out_width(7)) bit_extender_2 (.in(subtractor_2_out), .out(out_2));
  Bit_Extender #(.in_width(24), .out_width(7)) bit_extender_3 (.in(divider_3_out), .out(out_3));
  Bit_Extender #(.in_width(24), .out_width(7)) bit_extender_4 (.in(divider_4_out), .out(out_4));

  // Notes on the sheet:
  //   contents of rom_1 (hex, n*v repeats v):
  //   575254 4a4d50 535450 4f5450 494e50 57544f 575449 4c4441 434f4d 484748 4c4f57 434c4b
endmodule

module CPU (
  input  reset,
  input  execute,
  input  [6:0] keyboard_in,
  input  load,
  input  [7:0] in_0,
  input  [7:0] in_1,
  input  [7:0] in_2,
  input  [7:0] in_3,
  input  [7:0] in_4,
  input  [7:0] in_5,
  input  [7:0] in_6,
  input  [7:0] in_7,
  output keyboard_clock,
  output display_clear,
  output display_clock,
  output [7:0] out_0,
  output [6:0] display_out,
  output [7:0] out_1,
  output [7:0] out_2,
  output [7:0] out_3,
  output [7:0] out_4,
  output [7:0] out_5,
  output [7:0] out_6,
  output [7:0] out_7
);

  wire control_unit_1_out_12, control_unit_1_out_14, control_unit_1_out_17;
  wire [7:0] control_unit_1_out_10, control_unit_1_out_11, control_unit_1_out_13, control_unit_1_out_15,
       control_unit_1_out_16, instruction_cache_1_out_6, instruction_cache_1_out_7,
       instruction_cache_1_out_8, instruction_cache_1_out_9, instruction_cache_1_out_10, port_1_out_21,
       ram_1_data;

  Instruction_Cache instruction_cache_1 (
    .in_2(load), .in_3(control_unit_1_out_11), .in_4(control_unit_1_out_12), .out_5(keyboard_clock),
    .out_11(display_out), .out_12(display_clock), .out_13(display_clear), .in_1(keyboard_in),
    .out_6(instruction_cache_1_out_6), .out_7(instruction_cache_1_out_7), .out_8(instruction_cache_1_out_8),
    .out_9(instruction_cache_1_out_9), .out_10(instruction_cache_1_out_10));
  Control_unit control_unit_1 (
    .out_11(control_unit_1_out_11), .out_12(control_unit_1_out_12), .in_3(instruction_cache_1_out_6),
    .in_4(instruction_cache_1_out_7), .in_5(instruction_cache_1_out_8), .in_6(instruction_cache_1_out_9),
    .in_7(instruction_cache_1_out_10), .out_10(control_unit_1_out_10), .out_13(control_unit_1_out_13),
    .in_1(execute), .out_14(control_unit_1_out_14), .in_2(reset), .out_15(control_unit_1_out_15),
    .out_16(control_unit_1_out_16), .out_17(control_unit_1_out_17), .in_9(port_1_out_21), .in_8(ram_1_data));
  Port port_1 (
    .in_1(control_unit_1_out_15), .in_2(control_unit_1_out_16), .in_3(control_unit_1_out_17),
    .out_21(port_1_out_21), .out_12(out_0), .out_13(out_1), .out_14(out_2), .out_15(out_3), .out_16(out_4),
    .out_17(out_5), .out_18(out_6), .out_19(out_7), .in_4(in_0), .in_5(in_1), .in_6(in_2), .in_7(in_3),
    .in_8(in_4), .in_9(in_5), .in_10(in_6), .in_11(in_7));  // open: out_20
  RAM #(.bus("separate")) ram_1 (
    .addr(control_unit_1_out_13), .din(control_unit_1_out_10), .data(ram_1_data), .clk(control_unit_1_out_14));  // open: str, sel, ld, clr
endmodule

module Port (
  input  [7:0] in_1,
  input  [7:0] in_2,
  input  in_3,
  input  [7:0] in_4,
  input  [7:0] in_5,
  input  [7:0] in_6,
  input  [7:0] in_7,
  input  [7:0] in_8,
  input  [7:0] in_9,
  input  [7:0] in_10,
  input  [7:0] in_11,
  output [7:0] out_12,
  output [7:0] out_13,
  output [7:0] out_14,
  output [7:0] out_15,
  output [7:0] out_16,
  output [7:0] out_17,
  output [7:0] out_18,
  output [7:0] out_19,
  output [7:0] out_20,
  output [7:0] out_21
);

  wire and_1_out, and_2_out, and_3_out, and_4_out, and_5_out, and_6_out, and_7_out, and_8_out,
       comparator_1_eq, comparator_2_eq, comparator_3_eq, comparator_4_eq, comparator_5_eq, comparator_6_eq,
       comparator_7_eq, comparator_8_eq;
  wire [2:0] bit_extender_1_out;

  Comparator comparator_1 (.a(in_1), .b({8{1'b0}}), .eq(comparator_1_eq));  // open: gt, lt
  Comparator comparator_2 (.a(in_1), .b(8'h1), .eq(comparator_2_eq));  // open: gt, lt
  Comparator comparator_3 (.a(in_1), .b(8'h2), .eq(comparator_3_eq));  // open: gt, lt
  Comparator comparator_4 (.a(in_1), .b(8'h3), .eq(comparator_4_eq));  // open: gt, lt
  Comparator comparator_5 (.a(in_1), .b(8'h4), .eq(comparator_5_eq));  // open: gt, lt
  Comparator comparator_6 (.a(in_1), .b(8'h5), .eq(comparator_6_eq));  // open: gt, lt
  Comparator comparator_7 (.a(in_1), .b(8'h6), .eq(comparator_7_eq));  // open: gt, lt
  Comparator comparator_8 (.a(in_1), .b(8'h7), .eq(comparator_8_eq));  // open: gt, lt
  Bit_Extender #(.out_width(3)) bit_extender_1 (.in(in_1), .out(bit_extender_1_out));
  Multiplexer #(.select(3), .width(8), .enable("false")) multiplexer_1 (
    .in0(out_12), .in1(out_13), .in2(out_14), .in3(out_15), .in4(out_16), .in5(out_17), .in6(out_18),
    .in7(out_19), .out(out_20), .sel(bit_extender_1_out));
  Multiplexer #(.select(3), .width(8), .enable("false")) multiplexer_2 (
    .in0(in_4), .in1(in_5), .in2(in_6), .in3(in_7), .in4(in_8), .in5(in_9), .in6(in_10), .in7(in_11),
    .out(out_21), .sel(bit_extender_1_out));
  Register register_1 (.D(in_2), .Q(out_12), .clk(and_1_out));  // open: en, clr
  and and_1 (and_1_out, comparator_1_eq, in_3);
  Register register_2 (.D(in_2), .Q(out_13), .clk(and_2_out));  // open: en, clr
  and and_2 (and_2_out, comparator_2_eq, in_3);
  Register register_3 (.D(in_2), .Q(out_14), .clk(and_3_out));  // open: en, clr
  and and_3 (and_3_out, comparator_3_eq, in_3);
  Register register_4 (.D(in_2), .Q(out_15), .clk(and_4_out));  // open: en, clr
  and and_4 (and_4_out, comparator_4_eq, in_3);
  Register register_5 (.D(in_2), .Q(out_16), .clk(and_5_out));  // open: en, clr
  and and_5 (and_5_out, comparator_5_eq, in_3);
  Register register_6 (.D(in_2), .Q(out_17), .clk(and_6_out));  // open: en, clr
  and and_6 (and_6_out, comparator_6_eq, in_3);
  Register register_7 (.D(in_2), .Q(out_18), .clk(and_7_out));  // open: en, clr
  and and_7 (and_7_out, comparator_7_eq, in_3);
  Register register_8 (.D(in_2), .Q(out_19), .clk(and_8_out));  // open: en, clr
  and and_8 (and_8_out, comparator_8_eq, in_3);
  Pull_Resistor pull_resistor_1 (.node(in_10));
  Pull_Resistor pull_resistor_2 (.node(in_9));
  Pull_Resistor pull_resistor_3 (.node(in_11));
  Pull_Resistor pull_resistor_4 (.node(in_8));
  Pull_Resistor pull_resistor_5 (.node(in_5));
  Pull_Resistor pull_resistor_6 (.node(in_6));
  Pull_Resistor pull_resistor_7 (.node(in_7));
  Pull_Resistor pull_resistor_8 (.node(in_4));
endmodule

// Conrtol
module Control_unit (
  input  in_1,
  input  in_2,
  input  [7:0] in_3,
  input  [7:0] in_4,
  input  [7:0] in_5,
  input  [7:0] in_6,
  input  [7:0] in_7,
  input  [7:0] in_8,
  input  [7:0] in_9,
  output [7:0] out_10,
  output [7:0] out_11,
  output out_12,
  output [7:0] out_13,
  output out_14,
  output [7:0] out_15,
  output [7:0] out_16,
  output out_17
);

  wire and_1_out, and_2_out, and_3_out, clock_1_out, comparator_1_eq, comparator_2_eq, comparator_2_gt,
       comparator_2_lt, comparator_3_eq, comparator_4_eq, comparator_5_gt, multiplexer_2_out, or_1_out,
       or_2_out, s_r_ff_1_q, s_r_ff_1_qn;
  wire [1:0] bit_extender_1_out;
  wire [7:0] adder_1_out, alu_1_out_4, counter_1_q, multiplexer_1_out, multiplexer_3_out, multiplier_1_out,
       register_1_q, register_2_q, subtractor_1_out;
  wire [19:0] rom_1_data;

  and and_1 (and_1_out, rom_1_data[6], or_1_out);
  or or_1 (or_1_out, rom_1_data[11], multiplexer_2_out, and_2_out);
  Comparator comparator_1 (.a(in_5), .b(in_9), .eq(comparator_1_eq));  // open: gt, lt
  Register register_1 (.D(in_8), .Q(register_1_q), .clk(rom_1_data[12]));  // open: en, clr
  S_R_Flip_Flop s_r_ff_1 (.Q(s_r_ff_1_q), .Qn(s_r_ff_1_qn), .preset(in_1), .reset(or_2_out));  // open: S, clk, R, en
  or or_2 (or_2_out, rom_1_data[10], in_2);
  counter2 counter2_1 (
    .in_1(comparator_4_eq), .in_2(s_r_ff_1_qn), .in_3(and_1_out), .in_4(multiplexer_1_out), .out_5(out_11));
  Counter_part #(.max('hd)) counter_1 (
    .Q(counter_1_q), .clk(and_3_out), .clr(s_r_ff_1_qn));  // open: load, D, count, carry
  Multiplexer #(.width(8), .enable("false")) multiplexer_1 (
    .in0(in_4), .in1(in_6), .out(multiplexer_1_out), .sel(rom_1_data[5]));
  and and_2 (and_2_out, comparator_1_eq, rom_1_data[13]);
  ALU alu_1 (.in_1(in_7), .in_2(register_1_q), .in_3(in_8), .out_4(alu_1_out_4));
  Register register_2 (.D(alu_1_out_4), .Q(register_2_q), .clk(rom_1_data[13]));  // open: en, clr
  Comparator comparator_2 (
    .a(register_1_q), .b(in_8), .gt(comparator_2_gt), .eq(comparator_2_eq), .lt(comparator_2_lt));
  Bit_Extender #(.out_width(2)) bit_extender_1 (.in(in_7), .out(bit_extender_1_out));
  Clock clock_1 (.out(clock_1_out));
  and and_3 (and_3_out, ~in_1, clock_1_out, s_r_ff_1_q);  // AND_Gate
  Comparator comparator_3 (.a(counter_1_q), .b({8{1'b0}}), .eq(comparator_3_eq));  // open: gt, lt
  and and_4 (out_12, comparator_3_eq, s_r_ff_1_q);
  Comparator comparator_4 (.a(counter_1_q), .b(8'hd), .eq(comparator_4_eq));  // open: gt, lt
  Comparator comparator_5 (.a(counter_1_q), .b(8'h4), .gt(comparator_5_gt));  // open: eq, lt
  Multiplexer #(.select(2), .enable("false")) multiplexer_2 (
    .in0(1'b0), .in1(comparator_2_gt), .in2(comparator_2_eq), .in3(comparator_2_lt), .out(multiplexer_2_out),
    .sel(bit_extender_1_out));
  Subtractor subtractor_1 (.a(counter_1_q), .b(8'h5), .out(subtractor_1_out));  // open: bin, bout
  Multiplexer #(.width(8), .enable("false")) multiplexer_3 (
    .in0({8{1'b0}}), .in1(subtractor_1_out), .out(multiplexer_3_out), .sel(comparator_5_gt));
  Adder adder_1 (.a(multiplexer_3_out), .b(multiplier_1_out), .out(adder_1_out));  // open: cin, cout
  Multiplier multiplier_1 (.a(in_3), .b(8'h8), .out(multiplier_1_out));  // open: cin, cout
  ROM #(.dataWidth(20)) rom_1 (
    .addr(adder_1_out), .data({rom_1_data[19:10], out_17, rom_1_data[8:5], out_14, rom_1_data[3:0]}));  // open: sel
  Multiplexer #(.select(2), .width(8), .enable("false")) multiplexer_4 (
    .in0(in_5), .in1(in_9), .in2(register_2_q), .out(out_10), .sel(rom_1_data[1:0]));  // open: in3
  Multiplexer #(.select(2), .width(8), .enable("false")) multiplexer_5 (
    .in0(in_4), .in1(in_5), .in2(in_6), .out(out_13), .sel(rom_1_data[3:2]));  // open: in3
  Multiplexer #(.width(8), .enable("false")) multiplexer_6 (
    .in0(in_4), .out(out_15), .sel(rom_1_data[7]));  // open: in1
  Multiplexer #(.width(8), .enable("false")) multiplexer_7 (.in0(in_5), .in1(in_8), .out(out_16), .sel(rom_1_data[8]));

  // Notes on the sheet:
  //   contents of rom_1 (hex, n*v repeats v):
  //   0 10 7*0 840 7*0 400 7*0 200 7*0 2160 7*0 104 304 6*0 5 15 6*0 1000 4 2004 a 1a 0 0 0 1000 4 64
endmodule

module counter2 (
  input  in_1,
  input  in_2,
  input  in_3,
  input  [7:0] in_4,
  output [7:0] out_5
);

  wire and_1_out, and_2_out, or_1_out, or_2_out, or_3_out, or_4_out, or_5_out, or_6_out, or_7_out, or_8_out,
       s_r_ff_1_q, s_r_ff_2_q, s_r_ff_2_qn, t_ff_1_qn, t_ff_2_qn, t_ff_3_qn, t_ff_4_qn, t_ff_5_qn, t_ff_6_qn,
       t_ff_7_qn;
  wire [7:0] multiplexer_1_out, multiplexer_2_out, not_1_out;

  S_R_Flip_Flop s_r_ff_1 (.Q(s_r_ff_1_q), .preset(in_1), .reset(s_r_ff_2_qn));  // open: S, clk, R, Qn, en
  S_R_Flip_Flop s_r_ff_2 (.Q(s_r_ff_2_q), .Qn(s_r_ff_2_qn), .preset(in_3), .reset(and_1_out));  // open: S, clk, R, en
  and and_1 (and_1_out, ~in_1, s_r_ff_1_q);  // AND_Gate
  Multiplexer #(.width(8), .enable("false")) multiplexer_1 (
    .in0({8{1'b0}}), .in1(not_1_out), .out(multiplexer_1_out), .sel(in_3));
  assign not_1_out = ~in_4;  // NOT_Gate not_1, 8 bits wide
  Multiplexer #(.width(8), .enable("false")) multiplexer_2 (
    .in0({8{1'b0}}), .in1(in_4), .out(multiplexer_2_out), .sel(in_3));
  and and_2 (and_2_out, in_1, ~s_r_ff_2_q);  // AND_Gate
  T_Flip_Flop t_ff_1 (
    .clk(t_ff_2_qn), .T(t_ff_2_qn), .Q(out_5[1]), .Qn(t_ff_1_qn), .preset(multiplexer_2_out[1]),
    .reset(or_1_out));  // open: en
  T_Flip_Flop t_ff_2 (
    .clk(and_2_out), .T(and_2_out), .Q(out_5[0]), .Qn(t_ff_2_qn), .preset(multiplexer_2_out[0]),
    .reset(or_2_out));  // open: en
  or or_1 (or_1_out, multiplexer_1_out[1], in_2);
  or or_2 (or_2_out, multiplexer_1_out[0], in_2);
  T_Flip_Flop t_ff_3 (
    .clk(t_ff_1_qn), .T(t_ff_1_qn), .Q(out_5[2]), .Qn(t_ff_3_qn), .preset(multiplexer_2_out[2]),
    .reset(or_3_out));  // open: en
  or or_3 (or_3_out, multiplexer_1_out[2], in_2);
  or or_4 (or_4_out, multiplexer_1_out[3], in_2);
  T_Flip_Flop t_ff_4 (
    .clk(t_ff_3_qn), .T(t_ff_3_qn), .Q(out_5[3]), .Qn(t_ff_4_qn), .preset(multiplexer_2_out[3]),
    .reset(or_4_out));  // open: en
  T_Flip_Flop t_ff_5 (
    .clk(t_ff_4_qn), .T(t_ff_4_qn), .Q(out_5[4]), .Qn(t_ff_5_qn), .preset(multiplexer_2_out[4]),
    .reset(or_5_out));  // open: en
  or or_5 (or_5_out, multiplexer_1_out[4], in_2);
  T_Flip_Flop t_ff_6 (
    .clk(t_ff_5_qn), .T(t_ff_5_qn), .Q(out_5[5]), .Qn(t_ff_6_qn), .preset(multiplexer_2_out[5]),
    .reset(or_7_out));  // open: en
  T_Flip_Flop t_ff_7 (
    .clk(t_ff_6_qn), .T(t_ff_6_qn), .Q(out_5[6]), .Qn(t_ff_7_qn), .preset(multiplexer_2_out[6]),
    .reset(or_6_out));  // open: en
  or or_6 (or_6_out, multiplexer_1_out[6], in_2);
  or or_7 (or_7_out, multiplexer_1_out[5], in_2);
  T_Flip_Flop t_ff_8 (
    .clk(t_ff_7_qn), .T(t_ff_7_qn), .Q(out_5[7]), .preset(multiplexer_2_out[7]), .reset(or_8_out));  // open: Qn, en
  or or_8 (or_8_out, multiplexer_1_out[7], in_2);
endmodule

module counter3 (
  input  in_1,
  output [7:0] out_2
);

  wire and_1_out, clock_1_out, s_r_ff_1_q, s_r_ff_1_qn;
  wire [7:0] counter_1_q;

  Counter_part #(.max('h8)) counter_1 (
    .Q(counter_1_q), .clk(and_1_out), .clr(s_r_ff_1_qn));  // open: load, D, count, carry
  and and_1 (and_1_out, s_r_ff_1_q, clock_1_out);
  S_R_Flip_Flop s_r_ff_1 (.Q(s_r_ff_1_q), .Qn(s_r_ff_1_qn), .preset(in_1), .reset(out_2[7]));  // open: S, clk, R, en
  Clock clock_1 (.out(clock_1_out));
  Comparator comparator_1 (.a(counter_1_q), .b(8'h1), .eq(out_2[0]));  // open: gt, lt
  Comparator comparator_2 (.a(counter_1_q), .b(8'h2), .eq(out_2[1]));  // open: gt, lt
  Comparator comparator_3 (.a(counter_1_q), .b(8'h3), .eq(out_2[2]));  // open: gt, lt
  Comparator comparator_4 (.a(counter_1_q), .b(8'h4), .eq(out_2[3]));  // open: gt, lt
  Comparator comparator_5 (.a(counter_1_q), .b(8'h5), .eq(out_2[4]));  // open: gt, lt
  Comparator comparator_6 (.a(counter_1_q), .b(8'h6), .eq(out_2[5]));  // open: gt, lt
  Comparator comparator_7 (.a(counter_1_q), .b(8'h7), .eq(out_2[6]));  // open: gt, lt
  Comparator comparator_8 (.a(counter_1_q), .b(8'h8), .eq(out_2[7]));  // open: gt, lt
endmodule

module ALU (
  input  [7:0] in_1,
  input  [7:0] in_2,
  input  [7:0] in_3,
  output [7:0] out_4
);

  wire [3:0] bit_extender_1_out;
  wire [7:0] adder_1_out, and_1_out, divider_1_out, multiplier_1_out, nand_1_out, nor_1_out, not_1_out,
       or_1_out, subtractor_1_out, xnor_1_out, xor_1_out;

  Bit_Extender #(.out_width(4)) bit_extender_1 (.in(in_1), .out(bit_extender_1_out));
  Adder adder_1 (.a(in_2), .b(in_3), .out(adder_1_out));  // open: cin, cout
  Subtractor subtractor_1 (.a(in_2), .b(in_3), .out(subtractor_1_out));  // open: bin, bout
  Multiplier multiplier_1 (.a(in_2), .b(in_3), .out(multiplier_1_out));  // open: cin, cout
  Divider divider_1 (.a(in_2), .b(in_3), .out(divider_1_out));  // open: upper, rem
  assign and_1_out = in_2 & in_3;  // AND_Gate and_1, 8 bits wide
  assign nand_1_out = ~(in_2 & in_3);  // NAND_Gate nand_1, 8 bits wide
  assign or_1_out = in_2 | in_3;  // OR_Gate or_1, 8 bits wide
  assign nor_1_out = ~(in_2 | in_3);  // NOR_Gate nor_1, 8 bits wide
  assign xor_1_out = in_2 ^ in_3;  // XOR_Gate xor_1, 8 bits wide
  assign xnor_1_out = ~(in_2 ^ in_3);  // XNOR_Gate xnor_1, 8 bits wide
  assign not_1_out = ~in_2;  // NOT_Gate not_1, 8 bits wide
  Multiplexer #(.select(4), .width(8), .enable("false")) multiplexer_1 (
    .in0(adder_1_out), .in1(subtractor_1_out), .in2(multiplier_1_out), .in3(divider_1_out), .in4(and_1_out),
    .in5(nand_1_out), .in6(or_1_out), .in7(nor_1_out), .in8(xor_1_out), .in9(xnor_1_out), .in10(not_1_out),
    .out(out_4), .sel(bit_extender_1_out));  // open: in11, in12, in13, in14, in15
endmodule

module Main (
);

  wire Cl_out, cpu_1_display_clear, cpu_1_display_clock, cpu_1_keyboard_clock, Ex_out, Ld_out, Rs_out;
  wire [6:0] cpu_1_display_out, keyboard_1_data;
  wire [7:0] cpu_1_out_0, cpu_1_out_1, cpu_1_out_2, ext_ram_1_data_out;

  TTY #(.rows(10), .cols(23)) tty_1 (
    .data(cpu_1_display_out), .clk(cpu_1_display_clock), .clr(cpu_1_display_clear));  // open: we
  Keyboard #(.buflen(23)) keyboard_1 (
    .clk(cpu_1_keyboard_clock), .clr(Cl_out), .data(keyboard_1_data));  // open: re, avail
  Button Ld (.out(Ld_out));
  Button Cl (.out(Cl_out));
  CPU cpu_1 (
    .reset(Rs_out), .execute(Ex_out), .keyboard_in(keyboard_1_data), .keyboard_clock(cpu_1_keyboard_clock),
    .load(Ld_out), .display_clear(cpu_1_display_clear), .display_clock(cpu_1_display_clock),
    .display_out(cpu_1_display_out), .out_0(cpu_1_out_0), .out_1(cpu_1_out_1), .out_2(cpu_1_out_2),
    .in_0(ext_ram_1_data_out));  // open: out_3, out_4, out_5, out_6, out_7, in_1, in_2, in_3, in_4, in_5, in_6, in_7
  Button Ex (.out(Ex_out));
  Button Rs (.out(Rs_out));
  ext_ram ext_ram_1 (.addr(cpu_1_out_1), .data_in(cpu_1_out_2), .ins(cpu_1_out_0), .data_out(ext_ram_1_data_out));
endmodule

module ext_ram (
  input  [7:0] addr,
  input  [7:0] data_in,
  input  [7:0] ins,
  output [7:0] data_out
);

  wire clock_1_out, decoder_1_read, decoder_1_write;

  Clock clock_1 (.out(clock_1_out));
  decoder decoder_1 (.ins(ins), .read(decoder_1_read), .write(decoder_1_write));
  RAM #(.bus("separate")) ram_1 (
    .addr(addr), .din(data_in), .data(data_out), .str(decoder_1_write), .clk(clock_1_out), .ld(decoder_1_read));  // open: sel, clr
endmodule

module decoder (
  input  [7:0] ins,
  output read,
  output write
);

  Comparator comparator_1 (.a(ins), .b(8'h1), .eq(read));  // open: gt, lt
  Comparator comparator_2 (.a(ins), .b(8'h2), .eq(write));  // open: gt, lt
endmodule
