// Logisim project KT8.circ as structural Verilog: 5 circuits, main circuit main
module main (
);

  wire clock_1_out, cpu_1_reset_k_d, cpu_1_w_nr, not_1_out, or_1_out, Reset_out, RKD_out, sel_gen_1_d_sel,
       sel_gen_1_k_sel, sel_gen_1_mem_sel;
  wire [3:0] cpu_1_address, pull_resistor_1_node, pull_resistor_1_node_2, rom_1_data, rom_1_data_2;
  wire [6:0] bit_extender_2_out, keyboard_1_data;
  wire [7:0] bit_extender_1_out, cpu_1_code_address, cpu_1_ram_out;

  Hex_Digit_Display hex_digit_display_1 (.value(cpu_1_code_address[7:4]));  // open: dp
  Hex_Digit_Display hex_digit_display_2 (.value(cpu_1_code_address[3:0]));  // open: dp
  cpu cpu_1 (
    .Reset(Reset_out), .Instruction({rom_1_data_2, rom_1_data}),
    .RAM_in({pull_resistor_1_node_2, pull_resistor_1_node}), .Clock(clock_1_out),
    .Code_address(cpu_1_code_address), .Address(cpu_1_address), .RAM_out(cpu_1_ram_out), .W_nR(cpu_1_w_nr),
    .Reset_K_D(cpu_1_reset_k_d));
  Button Reset (.out(Reset_out));
  Hex_Digit_Display hex_digit_display_3 (.value(rom_1_data_2));  // open: dp
  Hex_Digit_Display hex_digit_display_4 (.value(rom_1_data));  // open: dp
  sel_gen sel_gen_1 (
    .Address(cpu_1_address), .mem_sel(sel_gen_1_mem_sel), .k_sel(sel_gen_1_k_sel), .d_sel(sel_gen_1_d_sel));
  ROM rom_1 (.addr(cpu_1_code_address), .data({rom_1_data_2, rom_1_data}));  // open: sel
  Hex_Digit_Display hex_digit_display_5 (.value(cpu_1_address));  // open: dp
  Clock clock_1 (.out(clock_1_out));
  Hex_Digit_Display hex_digit_display_6 (.value(cpu_1_ram_out[7:4]));  // open: dp
  Pull_Resistor pull_resistor_1 (.node({pull_resistor_1_node_2, pull_resistor_1_node}));
  or or_1 (or_1_out, cpu_1_reset_k_d, RKD_out);
  Button RKD (.out(RKD_out));
  Hex_Digit_Display hex_digit_display_7 (.value(cpu_1_ram_out[3:0]));  // open: dp
  Hex_Digit_Display hex_digit_display_8 (.value(pull_resistor_1_node_2));  // open: dp
  LED Mem (.in(sel_gen_1_mem_sel));
  Hex_Digit_Display hex_digit_display_9 (.value(pull_resistor_1_node));  // open: dp
  RAM #(.addrWidth(4), .bus("separate")) ram_1 (
    .addr(cpu_1_address), .din(cpu_1_ram_out), .data({pull_resistor_1_node_2, pull_resistor_1_node}),
    .str(cpu_1_w_nr), .sel(sel_gen_1_mem_sel), .clk(clock_1_out), .ld(not_1_out));  // open: clr
  not not_1 (not_1_out, cpu_1_w_nr);
  Keyboard keyboard_1 (.clk(clock_1_out), .re(sel_gen_1_k_sel), .clr(or_1_out), .data(keyboard_1_data));  // open: avail
  assign {pull_resistor_1_node_2, pull_resistor_1_node} = sel_gen_1_k_sel ? bit_extender_1_out : 8'bz;  // Controlled_Buffer controlled_buffer_1
  LED Kyb (.in(sel_gen_1_k_sel));
  LED Dsp (.in(sel_gen_1_d_sel));
  assign bit_extender_1_out = {{1{1'b0}}, keyboard_1_data};  // Bit_Extender bit_extender_1
  LED W_nR (.in(cpu_1_w_nr));
  Bit_Extender #(.out_width(7)) bit_extender_2 (.in(cpu_1_ram_out), .out(bit_extender_2_out));
  TTY tty_1 (.data(bit_extender_2_out), .clk(clock_1_out), .we(sel_gen_1_d_sel), .clr(or_1_out));

  // Notes on the sheet:
  //   Code addr
  //   Instruction
  //   contents of rom_1 (hex, n*v repeats v):
  //   0 4c 20 a3 b1
  //   Addr
  //   Data out
  //   Data in
endmodule

// CPU
module cpu (
  input  Reset,
  input  [7:0] Instruction,
  input  [7:0] RAM_in,
  input  Clock,
  output [7:0] Code_address,
  output [3:0] Address,
  output [7:0] RAM_out,
  output W_nR,
  output Reset_K_D
);

  wire and_1_out, and_2_out, and_3_out, and_4_out, and_5_out, decoder_1_out0, decoder_1_out1, decoder_1_out3,
       decoder_1_out4, decoder_1_out5, decoder_1_out6, decoder_1_out7, decoder_1_out8, decoder_1_out9,
       decoder_1_out10, decoder_1_out11, decoder_2_out0, decoder_2_out1, not_1_out, or_1_out, or_2_out,
       or_3_out, or_4_out, zero_1_zero;
  wire [7:0] adder_1_out, alu_1_r, bit_extender_1_out, multiplexer_1_out, multiplexer_2_out, register_1_q,
       register_2_q, subtractor_1_out;

  and and_1 (and_1_out, Clock, ~decoder_2_out1);  // AND_Gate
  Decoder #(.select(4), .disabled(0), .enable("false")) decoder_1 (
    .out0(decoder_1_out0), .out1(decoder_1_out1), .out2(W_nR), .out3(decoder_1_out3), .out4(decoder_1_out4),
    .out5(decoder_1_out5), .out6(decoder_1_out6), .out7(decoder_1_out7), .out8(decoder_1_out8),
    .out9(decoder_1_out9), .out10(decoder_1_out10), .out11(decoder_1_out11), .out12(Reset_K_D),
    .sel(Instruction[7:4]));  // open: out13, out14, out15
  Decoder #(.select(4), .disabled(0)) decoder_2 (
    .out0(decoder_2_out0), .out1(decoder_2_out1), .sel(Instruction[3:0]), .en(decoder_1_out11));  // open: out2, out3, out4, out5, out6, out7, out8, out9, out10, out11, out12, out13, out14, out15
  zero zero_1 (.In(RAM_out), .Zero(zero_1_zero));
  assign bit_extender_1_out = {{4{1'b0}}, Instruction[3:0]};  // Bit_Extender bit_extender_1
  and and_2 (and_2_out, decoder_1_out7, zero_1_zero);
  and and_3 (and_3_out, decoder_1_out8, zero_1_zero);
  and and_4 (and_4_out, decoder_1_out9, ~zero_1_zero);  // AND_Gate
  and and_5 (and_5_out, decoder_1_out10, ~zero_1_zero);  // AND_Gate
  Register register_1 (.D(RAM_in), .en(decoder_1_out0), .Q(register_1_q), .clk(and_1_out));  // open: clr
  Register register_2 (.D(multiplexer_1_out), .en(decoder_1_out1), .Q(register_2_q), .clk(and_1_out));  // open: clr
  Multiplexer #(.width(8), .disabled(0), .enable("false")) multiplexer_1 (
    .in0(RAM_in), .in1(bit_extender_1_out), .out(multiplexer_1_out), .sel(decoder_1_out3));
  Register register_3 (.D(alu_1_r), .en(decoder_1_out4), .Q(RAM_out), .clk(and_1_out));  // open: clr
  or or_1 (or_1_out, decoder_1_out5, and_2_out, and_4_out);
  or or_2 (or_2_out, decoder_1_out6, and_3_out, and_5_out);
  alu alu_1 (.A(register_1_q), .B(register_2_q), .Op(Instruction[3:0]), .R(alu_1_r));
  or or_3 (or_3_out, or_1_out, or_2_out);
  Adder adder_1 (.a(Code_address), .b(bit_extender_1_out), .out(adder_1_out));  // open: cin, cout
  Subtractor subtractor_1 (.a(Code_address), .b(bit_extender_1_out), .out(subtractor_1_out));  // open: bin, bout
  Counter counter_1 (
    .load(or_3_out), .D(multiplexer_2_out), .count(not_1_out), .Q(Code_address), .clk(and_1_out),
    .clr(or_4_out));  // open: carry
  not not_1 (not_1_out, or_3_out);
  or or_4 (or_4_out, decoder_2_out0, Reset);
  Multiplexer #(.width(8), .disabled(0), .enable("false")) multiplexer_2 (
    .in0(adder_1_out), .in1(subtractor_1_out), .out(multiplexer_2_out), .sel(or_2_out));

  assign Address = Instruction[3:0];

  // Notes on the sheet:
  //   Clock: pull=down
endmodule

// ALU
module alu (
  input  [7:0] A,
  input  [7:0] B,
  input  [3:0] Op,
  output [7:0] R
);

  wire [7:0] adder_1_out, adder_2_out, and_1_out, not_1_out, not_2_out, or_1_out, shifter_1_out,
       shifter_2_out, subtractor_1_out, subtractor_2_out, xor_1_out;

  Adder adder_1 (.a(A), .b(B), .out(adder_1_out));  // open: cin, cout
  Subtractor subtractor_1 (.a(A), .b(B), .out(subtractor_1_out));  // open: bin, bout
  assign and_1_out = A & B;  // AND_Gate and_1, 8 bits wide
  assign or_1_out = A | B;  // OR_Gate or_1, 8 bits wide
  assign xor_1_out = A ^ B;  // XOR_Gate xor_1, 8 bits wide
  assign not_1_out = ~A;  // NOT_Gate not_1, 8 bits wide
  assign not_2_out = ~B;  // NOT_Gate not_2, 8 bits wide
  Shifter shifter_1 (.in(A), .\dist (3'b001), .out(shifter_1_out));
  Shifter #(.shift("lr")) shifter_2 (.in(A), .\dist (3'b001), .out(shifter_2_out));
  Adder adder_2 (.a(A), .b(8'h1), .out(adder_2_out));  // open: cin, cout
  Subtractor subtractor_2 (.a(A), .b(8'h1), .out(subtractor_2_out));  // open: bin, bout
  Multiplexer #(.select(4), .width(8), .disabled(0), .enable("false")) multiplexer_1 (
    .in0(adder_1_out), .in1(subtractor_1_out), .in2(and_1_out), .in3(or_1_out), .in4(xor_1_out),
    .in5(not_1_out), .in6(not_2_out), .in7(A), .in8(B), .in9(shifter_1_out), .in10(shifter_2_out),
    .in11({8{1'b0}}), .in12(adder_2_out), .in13(subtractor_2_out), .out(R), .sel(Op));  // open: in14, in15
endmodule

// SG
module sel_gen (
  input  [3:0] Address,
  output mem_sel,
  output k_sel,
  output d_sel
);

  wire comparator_1_eq, comparator_1_gt, not_1_out;

  Comparator #(.width(4), .mode("unsigned")) comparator_1 (
    .a(Address), .b(4'b1110), .gt(comparator_1_gt), .eq(comparator_1_eq));  // open: lt
  nor nor_1 (mem_sel, comparator_1_gt, comparator_1_eq);
  not not_1 (not_1_out, mem_sel);
  Pull_Resistor pull_resistor_1 (.node(mem_sel));
  and and_1 (k_sel, not_1_out, ~Address[0]);  // AND_Gate
  and and_2 (d_sel, not_1_out, Address[0]);
  Pull_Resistor pull_resistor_2 (.node(k_sel));
  Pull_Resistor pull_resistor_3 (.node(d_sel));
endmodule

// Z?
module zero (
  input  [7:0] In,
  output Zero
);

  nor nor_1 (Zero, In[0], In[1], In[2], In[3], In[4], In[5], In[6], In[7]);
endmodule
