// Logisim project ME Serial V2.1.circ as structural Verilog: 2 circuits, main circuit main
module main (
  input  [15:0] address,
  input  [7:0] Data_out,
  input  IO_Memory,
  input  nR_W,
  input  [7:0] in_5,
  input  in_6,
  output [7:0] Data_In,
  output [7:0] out_8
);

  wire and_1_out, and_2_out, comparator_1_eq, me_serial_adapter_1_bit_ready_out,
       me_serial_adapter_1_s_data_out, me_serial_adapter_2_bit_ready_out, me_serial_adapter_2_s_data_out;
  wire [7:0] me_serial_adapter_1_data_out;

  Comparator #(.width(16), .mode("unsigned")) comparator_1 (
    .a(address), .b({16{1'b0}}), .eq(comparator_1_eq));  // open: gt, lt
  and and_1 (and_1_out, nR_W, IO_Memory, comparator_1_eq);
  assign Data_In = and_2_out ? me_serial_adapter_1_data_out : 8'bz;  // Controlled_Buffer controlled_buffer_1
  and and_2 (and_2_out, comparator_1_eq, IO_Memory);
  ME_serial_adapter me_serial_adapter_1 (
    .Data_in(Data_out), .Bit_Ready_in(me_serial_adapter_2_bit_ready_out),
    .S_Data_in(me_serial_adapter_2_s_data_out), .Write(and_1_out),
    .Bit_Ready_out(me_serial_adapter_1_bit_ready_out), .S_Data_out(me_serial_adapter_1_s_data_out),
    .Data_out(me_serial_adapter_1_data_out));
  ME_serial_adapter me_serial_adapter_2 (
    .Data_in(in_5), .Bit_Ready_in(me_serial_adapter_1_bit_ready_out),
    .S_Data_in(me_serial_adapter_1_s_data_out), .Write(in_6),
    .Bit_Ready_out(me_serial_adapter_2_bit_ready_out), .S_Data_out(me_serial_adapter_2_s_data_out),
    .Data_out(out_8));
endmodule

module ME_serial_adapter (
  input  [7:0] Data_in,
  input  Bit_Ready_in,
  input  S_Data_in,
  input  Write,
  output Bit_Ready_out,
  output S_Data_out,
  output [7:0] Data_out
);

  wire clock_1_out, clock_2_out, counter_1_carry, one_shot_1_out, or_1_out, t_ff_1_q;

  one_shot one_shot_1 (.in(Write), .out(one_shot_1_out));
  Shift_Register shift_register_1 (
    .in(S_Data_in), .clk(or_1_out), .out(S_Data_out), .load(Write), .d0(Data_in[7]), .q0(Data_out[7]),
    .d1(Data_in[6]), .q1(Data_out[6]), .d2(Data_in[5]), .q2(Data_out[5]), .d3(Data_in[4]), .q3(Data_out[4]),
    .d4(Data_in[3]), .q4(Data_out[3]), .d5(Data_in[2]), .q5(Data_out[2]), .d6(Data_in[1]), .q6(Data_out[1]),
    .d7(Data_in[0]), .q7(Data_out[0]));  // open: shift, clr
  or or_1 (or_1_out, Bit_Ready_in, Bit_Ready_out, Write);
  T_Flip_Flop t_ff_1 (
    .clk(one_shot_1_out), .T(one_shot_1_out), .Q(t_ff_1_q), .reset(counter_1_carry));  // open: Qn, preset, en
  Counter #(.max('h8)) counter_1 (
    .count(t_ff_1_q), .carry(counter_1_carry), .clk(clock_1_out), .clr(counter_1_carry));  // open: load, D, Q
  Clock clock_1 (.out(clock_1_out));
  Clock clock_2 (.out(clock_2_out));
  and and_1 (Bit_Ready_out, t_ff_1_q, clock_2_out);
endmodule
