// Logisim project ME Serial V5.circ as structural Verilog: 1 circuit, main circuit main
module main (
  input  [7:0] Data_In,
  input  [7:0] Data_In_2,
  input  Load,
  input  Load_2,
  input  Error,
  input  Bit_Ready,
  input  Error_2,
  input  RTT,
  input  Bit_Ready_2,
  input  Trans,
  input  Dir,
  output [7:0] Data_Out,
  output [7:0] Data_Out_2,
  output RTT_2
);

  wire and_1_out, and_2_out, and_3_out, and_4_out, and_5_out, and_6_out, or_1_out, or_2_out,
       pull_resistor_1_node, shift_register_1_out;

  and and_1 (and_1_out, Bit_Ready_2, Dir);
  and and_2 (and_2_out, Bit_Ready, ~Dir);  // AND_Gate
  or or_1 (or_1_out, and_1_out, Load, and_2_out);
  and and_3 (and_3_out, Error, Trans);
  Pull_Resistor pull_resistor_1 (.node(pull_resistor_1_node));
  Shift_Register shift_register_1 (
    .shift(Trans), .in(pull_resistor_1_node), .clk(or_1_out), .out(shift_register_1_out), .load(Load),
    .clr(and_3_out), .d0(Data_In[7]), .q0(Data_Out[7]), .d1(Data_In[6]), .q1(Data_Out[6]), .d2(Data_In[5]),
    .q2(Data_Out[5]), .d3(Data_In[4]), .q3(Data_Out[4]), .d4(Data_In[3]), .q4(Data_Out[3]), .d5(Data_In[2]),
    .q5(Data_Out[2]), .d6(Data_In[1]), .q6(Data_Out[1]), .d7(Data_In[0]), .q7(Data_Out[0]));
  Pull_Resistor pull_resistor_2 (.node(shift_register_1_out));
  and and_4 (and_4_out, Bit_Ready_2, Dir);
  or or_2 (or_2_out, and_4_out, Load_2, and_5_out);
  and and_5 (and_5_out, Bit_Ready, ~Dir);  // AND_Gate
  and and_6 (and_6_out, Error_2, Trans);
  Shift_Register shift_register_2 (
    .shift(Trans), .in(shift_register_1_out), .clk(or_2_out), .out(pull_resistor_1_node), .load(Load_2),
    .clr(and_6_out), .d0(Data_In_2[7]), .q0(Data_Out_2[7]), .d1(Data_In_2[6]), .q1(Data_Out_2[6]),
    .d2(Data_In_2[5]), .q2(Data_Out_2[5]), .d3(Data_In_2[4]), .q3(Data_Out_2[4]), .d4(Data_In_2[3]),
    .q4(Data_Out_2[3]), .d5(Data_In_2[2]), .q5(Data_Out_2[2]), .d6(Data_In_2[1]), .q6(Data_Out_2[1]),
    .d7(Data_In_2[0]), .q7(Data_Out_2[0]));

  assign RTT_2 = RTT;
endmodule
