// Logisim project PLG.circ as structural Verilog: 1 circuit, main circuit PLG
module PLG (
  input  a,
  input  b,
  input  OR,
  input  AND,
  input  NAND,
  input  NOR,
  input  XOR,
  input  NXOR,
  input  sel,
  output out
);

  wire and_1_out, and_2_out, and_3_out, and_4_out, multiplexer_1_out, multiplexer_2_out, multiplexer_3_out,
       multiplexer_4_out, multiplexer_5_out, nand_1_out, nor_1_out, or_1_out, or_2_out, or_3_out, xnor_1_out,
       xor_1_out;

  Pull_Resistor pull_resistor_1 (.node(a));
  Pull_Resistor pull_resistor_2 (.node(NXOR));
  Pull_Resistor pull_resistor_3 (.node(b));
  Pull_Resistor pull_resistor_4 (.node(OR));
  Pull_Resistor pull_resistor_5 (.node(AND));
  Pull_Resistor pull_resistor_6 (.node(NAND));
  Pull_Resistor pull_resistor_7 (.node(NOR));
  Pull_Resistor pull_resistor_8 (.node(XOR));
  and and_1 (and_1_out, a, b);
  or or_1 (or_1_out, a, b);
  and and_2 (and_2_out, ~OR, AND);  // AND_Gate
  nor nor_1 (nor_1_out, a, b);
  nand nand_1 (nand_1_out, a, b);
  and and_3 (and_3_out, ~NOR, NAND);  // AND_Gate
  and and_4 (and_4_out, ~XOR, NXOR);  // AND_Gate
  xnor xnor_1 (xnor_1_out, a, b);
  xor xor_1 (xor_1_out, a, b);
  Multiplexer #(.disabled(0), .enable("false")) multiplexer_1 (
    .in0(or_1_out), .in1(and_1_out), .out(multiplexer_1_out), .sel(and_2_out));
  Multiplexer #(.disabled(0), .enable("false")) multiplexer_2 (
    .in0(nor_1_out), .in1(nand_1_out), .out(multiplexer_2_out), .sel(and_3_out));
  Multiplexer #(.disabled(0), .enable("false")) multiplexer_3 (
    .in0(multiplexer_1_out), .in1(multiplexer_2_out), .out(multiplexer_3_out), .sel(or_2_out));
  or or_2 (or_2_out, NAND, NOR);
  Multiplexer #(.disabled(0), .enable("false")) multiplexer_4 (
    .in0(xor_1_out), .in1(xnor_1_out), .out(multiplexer_4_out), .sel(and_4_out));
  Multiplexer #(.disabled(0), .enable("false")) multiplexer_5 (
    .in0(multiplexer_3_out), .in1(multiplexer_4_out), .out(multiplexer_5_out), .sel(or_3_out));
  or or_3 (or_3_out, XOR, NXOR);
  assign out = sel ? multiplexer_5_out : 1'bz;  // Controlled_Buffer controlled_buffer_1
endmodule
