// Logisim project RAM 3.circ as structural Verilog: 2 circuits, main circuit main
module main (
  input  [23:0] RAM_1_adress,
  input  [23:0] RAM_2_adress,
  input  [23:0] RAM_3_adress,
  input  [31:0] RAM_1_data_in,
  input  [31:0] RAM_2_data_in,
  input  [31:0] RAM_3_data_in,
  input  RAM_1_write,
  input  RAM_2_write,
  input  RAM_3_write,
  output [31:0] RAM_1_data_out,
  output [31:0] RAM_2_data_out,
  output [31:0] RAM_3_data_out
);

  wire clock_1_out, not_1_out, not_2_out, not_3_out;
  wire [31:0] ram_1_data, ram_2_data, ram_3_data;

  not not_1 (not_1_out, RAM_1_write);
  not not_2 (not_2_out, RAM_2_write);
  not not_3 (not_3_out, RAM_3_write);
  Clock clock_1 (.out(clock_1_out));
  RAM #(.addrWidth(24), .dataWidth(32), .bus("separate")) ram_1 (
    .addr(RAM_1_adress), .din(RAM_1_data_in), .data(ram_1_data), .str(RAM_1_write), .clk(clock_1_out),
    .ld(not_1_out));  // open: sel, clr
  RAM #(.addrWidth(24), .dataWidth(32), .bus("separate")) ram_2 (
    .addr(RAM_2_adress), .din(RAM_2_data_in), .data(ram_2_data), .str(RAM_2_write), .clk(clock_1_out),
    .ld(not_2_out));  // open: sel, clr
  Multiplexer #(.width(32), .enable("false")) multiplexer_1 (
    .in0(ram_2_data), .in1(RAM_2_data_in), .out(RAM_2_data_out), .sel(RAM_2_write));
  RAM #(.addrWidth(24), .dataWidth(32), .bus("separate")) ram_3 (
    .addr(RAM_3_adress), .din(RAM_3_data_in), .data(ram_3_data), .str(RAM_3_write), .clk(clock_1_out),
    .ld(not_3_out));  // open: sel, clr
  Multiplexer #(.width(32), .enable("false")) multiplexer_2 (
    .in0(ram_3_data), .in1(RAM_3_data_in), .out(RAM_3_data_out), .sel(RAM_3_write));
  Multiplexer #(.width(32), .enable("false")) multiplexer_3 (
    .in0(ram_1_data), .in1(RAM_1_data_in), .out(RAM_1_data_out), .sel(RAM_1_write));

  // Notes on the sheet:
  //   RAM_2_adress: pull=down
  //   RAM_1_data_out: pull=down
  //   RAM_3_adress: pull=down
  //   RAM_3_data_out: pull=down
  //   RAM_1_adress: pull=down
  //   RAM_2_data_out: pull=down
endmodule

module test (
  input  [23:0] RAM_1_adress,
  input  [23:0] RAM_2_adress,
  input  [23:0] RAM_3_adress,
  input  [31:0] RAM_1_data_in,
  input  [31:0] RAM_2_data_in,
  input  [31:0] RAM_3_data_in,
  output [31:0] RAM_1_data_out,
  output [31:0] RAM_2_data_out,
  output [31:0] RAM_3_data_out
);

  wire RAM_1_write_out, RAM_2_write_out, RAM_3_write_out;

  Button RAM_1_write (.out(RAM_1_write_out));
  Button RAM_2_write (.out(RAM_2_write_out));
  Button RAM_3_write (.out(RAM_3_write_out));
  main main_1 (
    .RAM_1_adress(RAM_1_adress), .RAM_2_adress(RAM_2_adress), .RAM_3_adress(RAM_3_adress),
    .RAM_1_data_in(RAM_1_data_in), .RAM_2_data_in(RAM_2_data_in), .RAM_3_data_in(RAM_3_data_in),
    .RAM_1_write(RAM_1_write_out), .RAM_2_write(RAM_2_write_out), .RAM_3_write(RAM_3_write_out),
    .RAM_1_data_out(RAM_1_data_out), .RAM_2_data_out(RAM_2_data_out), .RAM_3_data_out(RAM_3_data_out));

  // Notes on the sheet:
  //   RAM_2_adress: pull=down
  //   RAM_1_data_out: pull=down
  //   RAM_3_adress: pull=down
  //   RAM_1_adress: pull=down
  //   RAM_3_data_out: pull=down
  //   RAM_2_data_out: pull=down
endmodule
