// Logisim project ROM.circ as structural Verilog: 1 circuit, main circuit main
module main (
);

  wire and_1_out, clock_1_out, clock_2_out, d_ff_1_q, d_ff_2_q, d_ff_2_qn, Digital_logic_is_fun_out,
       Hello__World_out, not_1_out, or_1_out, or_2_out, or_3_out, or_4_out, or_5_out, This_is_a_ROM_test_out,
       Whats_the_MSB_for_this_letter_out;
  wire [6:0] rom_1_data;
  wire [23:0] counter_1_q, multiplexer_1_out, multiplexer_2_out;

  TTY tty_1 (.data(rom_1_data), .clk(clock_2_out), .we(or_5_out), .clr(or_2_out));
  // Probe on multiplexer_1_out
  Multiplexer #(.width(24), .disabled(0), .enable("false")) multiplexer_1 (
    .in0(24'h10), .in1(24'h28), .out(multiplexer_1_out), .sel(This_is_a_ROM_test_out));
  Button Hello__World (.out(Hello__World_out));
  Button Digital_logic_is_fun (.out(Digital_logic_is_fun_out));
  Button This_is_a_ROM_test (.out(This_is_a_ROM_test_out));
  Button Whats_the_MSB_for_this_letter (.out(Whats_the_MSB_for_this_letter_out));
  or or_1 (or_1_out, Digital_logic_is_fun_out, This_is_a_ROM_test_out, Whats_the_MSB_for_this_letter_out);
  Multiplexer #(.width(24), .disabled(0), .enable("false")) multiplexer_2 (
    .in0(multiplexer_1_out), .in1(24'h3e), .out(multiplexer_2_out), .sel(Whats_the_MSB_for_this_letter_out));
  // Probe on multiplexer_2_out
  Counter #(.width(24), .max('hffffff)) counter_1 (
    .load(or_1_out), .D(multiplexer_2_out), .count(or_5_out), .Q(counter_1_q), .clk(clock_1_out),
    .clr(Hello__World_out));  // open: carry
  Clock clock_1 (.out(clock_1_out));
  D_Flip_Flop d_ff_1 (.Q(d_ff_1_q), .preset(or_3_out), .reset(not_1_out));  // open: clk, D, Qn, en
  or or_2 (or_2_out, Hello__World_out, Digital_logic_is_fun_out, This_is_a_ROM_test_out, Whats_the_MSB_for_this_letter_out);
  or or_3 (or_3_out, Hello__World_out, d_ff_2_q);
  ROM #(.addrWidth(24), .dataWidth(7)) rom_1 (.addr(counter_1_q), .data(rom_1_data));  // open: sel
  Clock clock_2 (.out(clock_2_out));
  not not_1 (not_1_out, or_4_out);
  or or_4 (or_4_out, rom_1_data[0], rom_1_data[1], rom_1_data[2], rom_1_data[3], rom_1_data[4], rom_1_data[5], rom_1_data[6]);
  D_Flip_Flop #(.trigger("falling")) d_ff_2 (
    .clk(or_1_out), .D(d_ff_2_qn), .Q(d_ff_2_q), .Qn(d_ff_2_qn), .reset(not_1_out));  // open: preset, en
  and and_1 (and_1_out, d_ff_1_q, ~Hello__World_out);  // AND_Gate
  or or_5 (or_5_out, and_1_out, d_ff_2_q);

  // Notes on the sheet:
  //   contents of rom_1 (hex, n*v repeats v):
  //   48 65 6c 6c 6f 2c 20 57 6f 72 6c 64 21 0 0 0 44 69 67 69 74 61 6c 20 6c 6f 67 69 63 20 69 73 20 66
  //   75 6e 2e 0 0 0 54 68 69 73 20 69 73 20 61 20 52 4f 4d 20 74 65 73 74 2e 0 0 0 57 68 61 74 27 73 20
  //   74 68 65 20 4d 53 42 20 66 6f 72 20 74 68 69 73 20 6c 65 74 74 65 72 3f
endmodule
