// Logisim project SPI.circ as structural Verilog: 1 circuit, main circuit main
module main (
  input  MLD,
  input  [7:0] MDATAOUT,
  input  S1LD,
  input  [7:0] S1DATAOUT,
  input  S2LD,
  input  [7:0] S2DATAOUT,
  input  res,
  input  sel,
  output [7:0] MDATAIN,
  output [7:0] S1DATAIN,
  output [7:0] S2DATAIN
);

  wire and_1_out, and_2_out, and_3_out, and_4_out, clock_1_out, controlled_buffer_1_out,
       controlled_buffer_2_out, controlled_buffer_3_out, counter_1_carry, d_ff_1_q, d_ff_1_qn, not_1_out,
       one_shot_1_out, or_1_out, or_2_out, or_3_out, or_4_out, or_5_out, or_6_out, shift_register_1_out,
       shift_register_2_out, shift_register_3_out, START_out;

  one_shot one_shot_1 (.in(START_out), .out(one_shot_1_out));
  Button START (.out(START_out));
  Clock clock_1 (.out(clock_1_out));
  DotMatrix #(.inputtype("row"), .matrixcols(8), .matrixrows(3)) dotmatrix_1 (
    .row0(MDATAIN), .row1(S1DATAIN), .row2(S2DATAIN));
  or or_1 (or_1_out, d_ff_1_q, one_shot_1_out);
  LED SPIBUSY (.in(or_3_out));
  or or_2 (or_2_out, MLD, S1LD, S2LD);
  or or_3 (or_3_out, or_2_out, d_ff_1_q);
  D_Flip_Flop d_ff_1 (
    .clk(clock_1_out), .D(or_1_out), .Q(d_ff_1_q), .Qn(d_ff_1_qn), .en(1'b1), .reset(counter_1_carry));  // open: preset
  Counter #(.width(3), .max('h7)) counter_1 (
    .count(d_ff_1_q), .carry(counter_1_carry), .clk(clock_1_out), .clr(d_ff_1_qn));  // open: load, D, Q
  and and_1 (and_1_out, d_ff_1_q, clock_1_out);
  Shift_Register shift_register_1 (
    .shift(d_ff_1_q), .in(controlled_buffer_3_out), .clk(or_4_out), .out(shift_register_1_out), .load(MLD),
    .clr(res), .d0(MDATAOUT[7]), .q0(MDATAIN[7]), .d1(MDATAOUT[6]), .q1(MDATAIN[6]), .d2(MDATAOUT[5]),
    .q2(MDATAIN[5]), .d3(MDATAOUT[4]), .q3(MDATAIN[4]), .d4(MDATAOUT[3]), .q4(MDATAIN[3]), .d5(MDATAOUT[2]),
    .q5(MDATAIN[2]), .d6(MDATAOUT[1]), .q6(MDATAIN[1]), .d7(MDATAOUT[0]), .q7(MDATAIN[0]));
  and and_2 (and_2_out, clock_1_out, MLD);
  or or_4 (or_4_out, and_2_out, and_1_out);
  and and_3 (and_3_out, clock_1_out, S1LD);
  or or_5 (or_5_out, and_3_out, and_1_out);
  and and_4 (and_4_out, clock_1_out, S2LD);
  or or_6 (or_6_out, and_4_out, and_1_out);
  not not_1 (not_1_out, sel);
  assign controlled_buffer_1_out = not_1_out ? not_1_out : 1'bz;  // Controlled_Buffer controlled_buffer_1
  Pull_Resistor pull_resistor_1 (.node(controlled_buffer_1_out));
  assign controlled_buffer_2_out = sel ? sel : 1'bz;  // Controlled_Buffer controlled_buffer_2
  Pull_Resistor pull_resistor_2 (.node(controlled_buffer_2_out));
  Shift_Register shift_register_2 (
    .shift(controlled_buffer_1_out), .in(shift_register_1_out), .clk(or_5_out), .out(shift_register_2_out),
    .load(S1LD), .clr(res), .d0(S1DATAOUT[7]), .q0(S1DATAIN[7]), .d1(S1DATAOUT[6]), .q1(S1DATAIN[6]),
    .d2(S1DATAOUT[5]), .q2(S1DATAIN[5]), .d3(S1DATAOUT[4]), .q3(S1DATAIN[4]), .d4(S1DATAOUT[3]),
    .q4(S1DATAIN[3]), .d5(S1DATAOUT[2]), .q5(S1DATAIN[2]), .d6(S1DATAOUT[1]), .q6(S1DATAIN[1]),
    .d7(S1DATAOUT[0]), .q7(S1DATAIN[0]));
  assign controlled_buffer_3_out = controlled_buffer_1_out ? shift_register_2_out : 1'bz;  // Controlled_Buffer controlled_buffer_3
  Shift_Register shift_register_3 (
    .shift(controlled_buffer_2_out), .in(shift_register_1_out), .clk(or_6_out), .out(shift_register_3_out),
    .load(S2LD), .clr(res), .d0(S2DATAOUT[7]), .q0(S2DATAIN[7]), .d1(S2DATAOUT[6]), .q1(S2DATAIN[6]),
    .d2(S2DATAOUT[5]), .q2(S2DATAIN[5]), .d3(S2DATAOUT[4]), .q3(S2DATAIN[4]), .d4(S2DATAOUT[3]),
    .q4(S2DATAIN[3]), .d5(S2DATAOUT[2]), .q5(S2DATAIN[2]), .d6(S2DATAOUT[1]), .q6(S2DATAIN[1]),
    .d7(S2DATAOUT[0]), .q7(S2DATAIN[0]));
  assign controlled_buffer_3_out = controlled_buffer_2_out ? shift_register_3_out : 1'bz;  // Controlled_Buffer controlled_buffer_4
endmodule
