// Logisim project TK16X3.circ as structural Verilog: 8 circuits, main circuit main
module main (
  input  RESET
);

  wire alu_1_store_r, clock_1_out, clock_2_out, Decode_call, Decode_en_alu, Decode_i____r, Decode_jump,
       Decode_m___r, Decode_r___m, Decode_ret, Fetch_execute, Fetch_inc_pc, not_1_out, or_1_out;
  wire [4:0] Decode_a, Decode_alu_op, Decode_b, Decode_r;
  wire [14:0] Decode_imm, multiplexer_1_out, PC_out;
  wire [15:0] alu_1_r_value, multiplexer_2_out, multiplexer_3_out, n32_to_16x2_1__16_1, n32_to_16x2_1__16_2,
       ram_1_data;
  wire [15:15] Decode_imm_2;
  wire [31:0] Fetch_ins, n16_to_32x1_1__32, registerfile_1_p7, registerfile_1_p8;

  PC PC (
    .ADDRESS({Decode_imm_2[15], Decode_imm}), .OUT(PC_out), .RET(Decode_ret), .CALL(Decode_call),
    .JUMP(Decode_jump), .INC(Fetch_inc_pc), .RESET(RESET));
  Multiplexer #(.width(15), .disabled(0), .enable("false")) multiplexer_1 (
    .in0(PC_out), .in1(Decode_imm), .out(multiplexer_1_out), .sel(Decode_m___r));
  not not_1 (not_1_out, Decode_r___m);
  Clock clock_1 (.out(clock_1_out));
  RAM #(.addrWidth(15), .dataWidth(16), .bus("separate")) ram_1 (
    .addr(multiplexer_1_out), .din(n32_to_16x2_1__16_1), .data(ram_1_data), .str(Decode_r___m),
    .clk(clock_1_out), .ld(not_1_out));  // open: sel, clr
  Ins_Fetch Fetch (
    .RESET(RESET), .Data_In(ram_1_data), .INC_PC(Fetch_inc_pc), .EXECUTE(Fetch_execute), .Ins(Fetch_ins));
  // Probe on Fetch_ins
  Decoder Decode (
    .EXECUTE(Fetch_execute), .INS(Fetch_ins), .JUMP(Decode_jump), .RET(Decode_ret), .CALL(Decode_call),
    .IMM({Decode_imm_2[15], Decode_imm}), .A(Decode_a), .B(Decode_b), .R(Decode_r), .ALU_OP(Decode_alu_op),
    .En_alu(Decode_en_alu), .M___R(Decode_m___r), .R___M(Decode_r___m), .I____R(Decode_i____r));
  Clock clock_2 (.out(clock_2_out));
  Multiplexer #(.width(16), .disabled(0), .enable("false")) multiplexer_2 (
    .in0(multiplexer_3_out), .in1(ram_1_data), .out(multiplexer_2_out), .sel(Decode_m___r));
  _16_to_32x1 u_16_to_32x1_1 (._16(multiplexer_2_out), ._32(n16_to_32x1_1__32));
  Multiplexer #(.width(16), .disabled(0), .enable("false")) multiplexer_3 (
    .in0(alu_1_r_value), .in1({Decode_imm_2[15], Decode_imm}), .out(multiplexer_3_out), .sel(Decode_i____r));
  or or_1 (or_1_out, alu_1_store_r, Decode_i____r, Decode_m___r);
  // RegisterFile registerfile_1: pin names not known; wires that end beside it: n16_to_32x1_1__32, clock_2_out, or_1_out, Decode_r, Decode_a, Decode_b, registerfile_1_p7, registerfile_1_p8
  _32_to_16x2 u_32_to_16x2_1 (
    ._32_2(registerfile_1_p8), ._32_1(registerfile_1_p7), ._16_2(n32_to_16x2_1__16_2),
    ._16_1(n32_to_16x2_1__16_1));
  ALU alu_1 (
    .b(n32_to_16x2_1__16_2), .a(n32_to_16x2_1__16_1), .ins(Decode_alu_op), .En(Decode_en_alu),
    .R_Value(alu_1_r_value), .Store_R(alu_1_store_r));
endmodule

module Ins_Fetch (
  input  RESET,
  input  [15:0] Data_In,
  output EXECUTE,
  output [31:0] Ins,
  output INC_PC
);

  wire clock_1_out, clock_2_out, d_ff_2_q, LONG, nor_1_out, not_1_out, not_2_out, or_1_out, SHORT;

  or or_1 (or_1_out, SHORT, d_ff_2_q);
  Clock clock_1 (.out(clock_1_out));
  D_Flip_Flop #(.trigger("falling")) d_ff_1 (
    .clk(clock_1_out), .D(or_1_out), .Q(EXECUTE), .reset(RESET));  // open: Qn, preset, en
  D_Flip_Flop #(.trigger("falling")) d_ff_2 (
    .clk(clock_1_out), .D(LONG), .Q(d_ff_2_q), .en(not_1_out), .reset(RESET));  // open: Qn, preset
  not not_1 (not_1_out, EXECUTE);
  nor nor_1 (nor_1_out, d_ff_2_q, EXECUTE);
  not not_2 (not_2_out, Data_In[15]);
  and and_1 (LONG, nor_1_out, Data_In[15]);
  and and_2 (SHORT, nor_1_out, not_2_out);
  or or_2 (INC_PC, d_ff_2_q, nor_1_out);
  Register #(.width(16)) InsB (.D(Data_In), .en(d_ff_2_q), .Q(Ins[15:0]), .clk(clock_2_out), .clr(nor_1_out));
  Register #(.width(16)) InsA (.D(Data_In), .en(nor_1_out), .Q(Ins[31:16]), .clk(clock_2_out));  // open: clr
  Clock clock_2 (.out(clock_2_out));
endmodule

module PC (
  input  RET,
  input  CALL,
  input  JUMP,
  input  [15:0] ADDRESS,
  input  RESET,
  input  INC,
  output [14:0] OUT
);

  wire and_1_out, clock_1_out, clock_2_out, clock_3_out, not_1_out, not_2_out, or_1_out, or_2_out;
  wire [3:0] counter_2_q;
  wire [14:0] multiplexer_1_out, ram_1_data, register_1_q;

  not not_1 (not_1_out, or_1_out);
  Multiplexer #(.width(15), .enable("false")) multiplexer_1 (
    .in0(ADDRESS[14:0]), .in1(ram_1_data), .out(multiplexer_1_out), .sel(RET));
  and and_1 (and_1_out, not_1_out, INC);
  or or_1 (or_1_out, RET, CALL, JUMP);
  Counter #(.width(15), .max('h7fff)) counter_1 (
    .load(or_1_out), .D(multiplexer_1_out), .count(and_1_out), .Q(OUT), .clk(clock_1_out), .clr(RESET));  // open: carry
  Clock clock_1 (.out(clock_1_out));
  Counter #(.width(4), .max('hf)) counter_2 (
    .load(RET), .count(or_2_out), .Q(counter_2_q), .clk(clock_2_out), .clr(RESET));  // open: D, carry
  or or_2 (or_2_out, CALL, RET);
  Clock clock_2 (.out(clock_2_out));
  Register #(.width(15)) register_1 (.D(OUT), .en(CALL), .Q(register_1_q), .clk(clock_3_out));  // open: clr
  not not_2 (not_2_out, clock_3_out);
  Clock clock_3 (.out(clock_3_out));
  RAM #(.addrWidth(4), .dataWidth(15), .bus("separate")) ram_1 (
    .addr(counter_2_q), .din(register_1_q), .data(ram_1_data), .str(CALL), .clk(not_2_out));  // open: sel, ld, clr
endmodule

module Decoder (
  input  EXECUTE,
  input  [31:0] INS,
  output JUMP,
  output RET,
  output CALL,
  output [15:0] IMM,
  output [4:0] A,
  output [4:0] B,
  output [4:0] R,
  output [4:0] ALU_OP,
  output En_alu,
  output M___R,
  output R___M,
  output I____R
);

  wire comparator_1_gt, decoder_1_out1, decoder_1_out2, decoder_1_out3;

  and and_1 (JUMP, decoder_1_out1, EXECUTE);
  and and_2 (RET, decoder_1_out2, EXECUTE);
  and and_3 (CALL, decoder_1_out3, EXECUTE);
  Decoder_part #(.select(5)) decoder_1 (
    .out1(decoder_1_out1), .out2(decoder_1_out2), .out3(decoder_1_out3), .out4(M___R), .out5(R___M),
    .out6(I____R), .sel(INS[30:26]));  // open: out0, out7, out8, out9, out10, out11, out12, out13, out14, out15, out16, out17, out18, out19, out20, out21, out22, out23, out24, out25, out26, out27, out28, out29, out30, out31, en
  Comparator #(.width(5)) comparator_1 (.a(5'b01101), .b(INS[25:21]), .gt(comparator_1_gt), .lt(En_alu));  // open: eq

  assign A = INS[4:0];
  assign ALU_OP = INS[25:21];
  assign B = INS[9:5];
  assign IMM = INS[15:0];
  assign R = INS[20:16];
endmodule

module ALU (
  input  [15:0] b,
  input  [15:0] a,
  input  [4:0] ins,
  input  En,
  output [15:0] R_Value,
  output Store_R
);

  wire decoder_1_out1, decoder_1_out2, decoder_1_out3, decoder_1_out4, decoder_1_out5, decoder_1_out6,
       decoder_1_out7, decoder_1_out8, decoder_1_out9, decoder_1_out10, decoder_1_out11, decoder_1_out12,
       or_2_out, or_3_out, or_4_out;
  wire [15:0] adder_1_out, and_1_out, divider_1_out, multiplier_1_out, negator_1_out, or_1_out,
       shifter_1_out, shifter_2_out, subtractor_1_out;

  Shifter #(.width(16)) shifter_1 (.in(a), .\dist (b[3:0]), .out(shifter_1_out));
  assign R_Value = decoder_1_out9 ? shifter_1_out : 16'bz;  // Controlled_Buffer controlled_buffer_1
  Shifter #(.width(16), .shift("lr")) shifter_2 (.in(a), .\dist (b[3:0]), .out(shifter_2_out));
  assign R_Value = decoder_1_out10 ? shifter_2_out : 16'bz;  // Controlled_Buffer controlled_buffer_2
  Adder #(.width(16)) adder_1 (.a(a), .b(b), .out(adder_1_out));  // open: cin, cout
  assign R_Value = decoder_1_out1 ? adder_1_out : 16'bz;  // Controlled_Buffer controlled_buffer_3
  Subtractor #(.width(16)) subtractor_1 (.a(a), .b(b), .out(subtractor_1_out));  // open: bin, bout
  assign R_Value = decoder_1_out2 ? subtractor_1_out : 16'bz;  // Controlled_Buffer controlled_buffer_4
  assign R_Value = decoder_1_out3 ? multiplier_1_out : 16'bz;  // Controlled_Buffer controlled_buffer_5
  Multiplier #(.width(16)) multiplier_1 (.a(a), .b(b), .out(multiplier_1_out));  // open: cin, cout
  assign R_Value = decoder_1_out4 ? divider_1_out : 16'bz;  // Controlled_Buffer controlled_buffer_6
  Divider #(.width(16)) divider_1 (.a(a), .b(b), .out(divider_1_out));  // open: upper, rem
  Negator #(.width(16)) negator_1 (.in(a), .out(negator_1_out));
  assign R_Value = decoder_1_out5 ? negator_1_out : 16'bz;  // Controlled_Buffer controlled_buffer_7
  assign and_1_out = a & b;  // AND_Gate and_1, 16 bits wide
  assign R_Value = decoder_1_out6 ? and_1_out : 16'bz;  // Controlled_Buffer controlled_buffer_8
  assign R_Value = decoder_1_out7 ? or_1_out : 16'bz;  // Controlled_Buffer controlled_buffer_9
  assign or_1_out = a | b;  // OR_Gate or_1, 16 bits wide
  assign R_Value = decoder_1_out8 ? ~a : 16'bz;  // Controlled_Inverter controlled_inverter_1
  assign R_Value = decoder_1_out11 ? a : 16'bz;  // Controlled_Buffer controlled_buffer_10
  assign R_Value = decoder_1_out12 ? b : 16'bz;  // Controlled_Buffer controlled_buffer_11
  Decoder_part #(.select(5), .disabled(0)) decoder_1 (
    .out1(decoder_1_out1), .out2(decoder_1_out2), .out3(decoder_1_out3), .out4(decoder_1_out4),
    .out5(decoder_1_out5), .out6(decoder_1_out6), .out7(decoder_1_out7), .out8(decoder_1_out8),
    .out9(decoder_1_out9), .out10(decoder_1_out10), .out11(decoder_1_out11), .out12(decoder_1_out12),
    .sel(ins), .en(En));  // open: out0, out13, out14, out15, out16, out17, out18, out19, out20, out21, out22, out23, out24, out25, out26, out27, out28, out29, out30, out31
  or or_2 (or_2_out, decoder_1_out1, decoder_1_out2, decoder_1_out3, decoder_1_out4);
  or or_3 (or_3_out, decoder_1_out5, decoder_1_out6, decoder_1_out7, decoder_1_out8);
  or or_4 (or_4_out, decoder_1_out9, decoder_1_out10, decoder_1_out11, decoder_1_out12);
  or or_5 (Store_R, or_2_out, or_3_out, or_4_out);
endmodule

module _32_to_16x2 (
  input  [31:0] _32_2,
  input  [31:0] _32_1,
  output [15:0] _16_2,
  output [15:0] _16_1
);


  assign _16_1 = _32_1[15:0];
  assign _16_2 = _32_2[15:0];
endmodule

module _16_to_32x1 (
  input  [15:0] _16,
  output [31:0] _32
);


  assign _32[15:0] = _16;
endmodule

module ALU_test (
  input  in_1
);

  wire RAM_Push_out;
  wire [4:0] PC_q;
  wire [15:0] alu_1_r_value;

  Button RAM_Push (.out(RAM_Push_out));
  Counter #(.width(5), .max('hd)) PC (.count(RAM_Push_out), .Q(PC_q), .clk(RAM_Push_out));  // open: load, D, carry, clr
  ALU alu_1 (.b(16'h8), .a(16'h8), .ins(PC_q), .En(in_1), .R_Value(alu_1_r_value));  // open: Store_R
  // Probe on alu_1_r_value
endmodule
