// Logisim project TK8.circ as structural Verilog: 3 circuits, main circuit main
module main (
  input  in_1,
  input  [21:0] in_2
);

  wire button_1_out, button_2_out, keyboard_1_avail, q238_1_disp_clock_out, q238_1_key_clock_out;
  wire [6:0] keyboard_1_data, q238_1_ascii_out;

  Keyboard keyboard_1 (.clk(q238_1_key_clock_out), .avail(keyboard_1_avail), .data(keyboard_1_data));  // open: re, clr
  Button button_1 (.out(button_1_out));
  Button button_2 (.out(button_2_out));
  q238 q238_1 (
    .reset(button_1_out), .ascii_in(keyboard_1_data), .av_in(keyboard_1_avail), .instruction_in(in_2),
    .store(in_1), .count(button_2_out), .key_clock_out(q238_1_key_clock_out), .ascii_out(q238_1_ascii_out),
    .disp_clock_out(q238_1_disp_clock_out));
  TTY tty_1 (.data(q238_1_ascii_out), .clk(q238_1_disp_clock_out));  // open: we, clr
endmodule

module q238 (
  input  reset,
  input  [6:0] ascii_in,
  input  av_in,
  input  [21:0] instruction_in,
  input  store,
  input  count,
  output key_clock_out,
  output [6:0] ascii_out,
  output disp_clock_out
);

  wire and_1_out, nor_1_out, not_1_out, not_2_out, or_1_out, or_2_out, or_4_out, or_5_out, or_6_out;
  wire [6:0] and_2_out, and_3_out, and_4_out;
  wire [15:0] ins_dec_1_a_out, multiplexer_1_out, or_3_out, pull_resistor_1_node, Register_R_q;
  wire [21:0] ram_1_data;
  wire [23:0] Program_Counter_q;
  wire [31:0] ins_dec_1_high_bits, ins_dec_1_low_bits;

  and and_1 (and_1_out, disp_clock_out, ~store);  // AND_Gate
  Clock clock_1 (.out(disp_clock_out));
  or or_1 (or_1_out, ins_dec_1_low_bits[0], reset);
  or or_2 (or_2_out, count, nor_1_out);
  nor nor_1 (nor_1_out, reset, and_1_out);
  not not_1 (not_1_out, nor_1_out);
  Counter #(.width(24), .max('hffffff)) Program_Counter (
    .count(or_2_out), .Q(Program_Counter_q), .clk(or_2_out), .clr(or_1_out));  // open: load, D, carry
  assign or_3_out = Register_R_q | {{9{1'b0}}, and_2_out};  // OR_Gate or_3, 16 bits wide
  assign key_clock_out = av_in ? disp_clock_out : 1'bz;  // Controlled_Buffer controlled_buffer_1
  or or_4 (or_4_out, ins_dec_1_low_bits[3], ins_dec_1_low_bits[5]);
  RAM #(.addrWidth(24), .dataWidth(22), .bus("separate")) ram_1 (
    .addr(Program_Counter_q), .din(instruction_in), .data(ram_1_data), .str(store), .clk(or_2_out),
    .ld(not_2_out));  // open: sel, clr
  not not_2 (not_2_out, store);
  Pull_Resistor pull_resistor_1 (.node(pull_resistor_1_node));
  RAM #(.addrWidth(16), .dataWidth(16), .bus("separate")) ram_2 (
    .addr(ins_dec_1_a_out), .din(or_3_out), .data(pull_resistor_1_node), .str(or_4_out), .clk(not_1_out),
    .ld(or_5_out));  // open: sel, clr
  or or_5 (or_5_out, ins_dec_1_low_bits[1], ins_dec_1_low_bits[6], ins_dec_1_low_bits[2]);
  assign and_2_out = ascii_in & {7{ins_dec_1_low_bits[5]}};  // AND_Gate and_2, 7 bits wide
  Register #(.width(16)) Register_A (.en(ins_dec_1_low_bits[1]), .clk(nor_1_out));  // open: D, Q, clr
  Multiplexer #(.width(16), .disabled(0), .enable("false")) multiplexer_1 (
    .in0(pull_resistor_1_node), .in1(ins_dec_1_a_out), .out(multiplexer_1_out), .sel(ins_dec_1_low_bits[4]));
  or or_6 (or_6_out, ins_dec_1_low_bits[4], ins_dec_1_low_bits[2]);
  Register #(.width(16)) Register_B (.D(multiplexer_1_out), .en(or_6_out), .clk(nor_1_out));  // open: Q, clr
  Register #(.width(16)) Register_R (.en(ins_dec_1_low_bits[3]), .Q(Register_R_q), .clk(nor_1_out));  // open: D, clr
  assign and_3_out = {7{ins_dec_1_low_bits[7]}} & ascii_in;  // AND_Gate and_3, 7 bits wide
  assign and_4_out = pull_resistor_1_node[6:0] & {7{ins_dec_1_low_bits[6]}};  // AND_Gate and_4, 7 bits wide
  assign ascii_out = and_4_out | and_3_out;  // OR_Gate or_7, 7 bits wide
  ins_dec ins_dec_1 (
    .ins_in(ram_1_data), .a_out(ins_dec_1_a_out), .low_bits(ins_dec_1_low_bits),
    .high_bits(ins_dec_1_high_bits));

  // Notes on the sheet:
  //   RESET
  //   Program Memory
endmodule

module ins_dec (
  input  [21:0] ins_in,
  output [15:0] a_out,
  output [31:0] low_bits,
  output [31:0] high_bits
);

  wire decoder_1_out0, decoder_1_out1, decoder_1_out2, decoder_1_out3;

  Decoder #(.select(2), .enable("false")) decoder_1 (
    .out0(decoder_1_out0), .out1(decoder_1_out1), .out2(decoder_1_out2), .out3(decoder_1_out3),
    .sel(ins_in[21:20]));
  Decoder #(.select(4), .disabled(0)) decoder_2 (
    .out0(low_bits[0]), .out1(low_bits[1]), .out2(low_bits[2]), .out3(low_bits[3]), .out4(low_bits[4]),
    .out5(low_bits[5]), .out6(low_bits[6]), .out7(low_bits[7]), .out8(low_bits[8]), .out9(low_bits[9]),
    .out10(low_bits[10]), .out11(low_bits[11]), .out12(low_bits[12]), .out13(low_bits[13]),
    .out14(low_bits[14]), .out15(low_bits[15]), .sel(ins_in[19:16]), .en(decoder_1_out0));
  Decoder #(.select(4), .disabled(0)) decoder_3 (
    .out0(high_bits[0]), .out1(high_bits[1]), .out2(high_bits[2]), .out3(high_bits[3]), .out4(high_bits[4]),
    .out5(high_bits[5]), .out6(high_bits[6]), .out7(high_bits[7]), .out8(high_bits[8]), .out9(high_bits[9]),
    .out10(high_bits[10]), .out11(high_bits[11]), .out12(high_bits[12]), .out13(high_bits[13]),
    .out14(high_bits[14]), .out15(high_bits[15]), .sel(ins_in[19:16]), .en(decoder_1_out2));
  Decoder #(.select(4), .disabled(0)) decoder_4 (
    .out0(high_bits[16]), .out1(high_bits[17]), .out2(high_bits[18]), .out3(high_bits[19]),
    .out4(high_bits[20]), .out5(high_bits[21]), .out6(high_bits[22]), .out7(high_bits[23]),
    .out8(high_bits[24]), .out9(high_bits[25]), .out10(high_bits[26]), .out11(high_bits[27]),
    .out12(high_bits[28]), .out13(high_bits[29]), .out14(high_bits[30]), .out15(high_bits[31]),
    .sel(ins_in[19:16]), .en(decoder_1_out3));
  Decoder #(.select(4), .disabled(0)) decoder_5 (
    .out0(low_bits[16]), .out1(low_bits[17]), .out2(low_bits[18]), .out3(low_bits[19]), .out4(low_bits[20]),
    .out5(low_bits[21]), .out6(low_bits[22]), .out7(low_bits[23]), .out8(low_bits[24]), .out9(low_bits[25]),
    .out10(low_bits[26]), .out11(low_bits[27]), .out12(low_bits[28]), .out13(low_bits[29]),
    .out14(low_bits[30]), .out15(low_bits[31]), .sel(ins_in[19:16]), .en(decoder_1_out1));

  assign a_out = ins_in[15:0];
endmodule
