// Logisim project TKStack5.circ as structural Verilog: 4 circuits, main circuit main
module main (
  input  RESET
);

  wire and_1_out, and_2_out, clock_1_out, clock_2_out, clock_3_out, clock_4_out, Decoder_alu_en,
       Decoder_pointer, not_1_out, not_2_out, not_3_out, not_4_out, Phase_Control_execute,
       Phase_Control_loada, Phase_Control_loadb, Stack_ALU_write;
  wire [2:0] Decoder_alu_op, Decoder_segment;
  wire [15:0] counter_1_q, Decoder_data_out, INA, Instruction_B_q, multiplexer_1_out, multiplexer_2_out,
       ram_1_data, ram_2_data, Stack_ALU_top;

  Counter #(.width(16), .max('hffff)) counter_1 (
    .count(not_1_out), .Q(counter_1_q), .clk(clock_1_out), .clr(RESET));  // open: load, D, carry
  Clock clock_1 (.out(clock_1_out));
  Multiplexer #(.width(16), .disabled(0), .enable("false")) multiplexer_1 (
    .in0(ram_2_data), .in1(counter_1_q), .out(multiplexer_1_out), .sel(not_1_out));
  not not_1 (not_1_out, Phase_Control_execute);
  Phase_Control Phase_Control (
    .RESET(RESET), .Data_In(INA), .EXECUTE(Phase_Control_execute), .LOADB(Phase_Control_loadb),
    .LOADA(Phase_Control_loada));
  Clock clock_2 (.out(clock_2_out));
  not not_2 (not_2_out, and_1_out);
  RAM #(.addrWidth(16), .dataWidth(16), .bus("separate")) ram_1 (
    .addr(multiplexer_1_out), .din(Stack_ALU_top), .data(ram_1_data), .str(and_1_out), .clk(clock_2_out),
    .ld(not_2_out));  // open: sel, clr
  Register #(.width(16)) Instruction_A (
    .D(ram_1_data), .en(Phase_Control_loada), .Q(INA), .clk(clock_3_out));  // open: clr
  Register #(.width(16)) Instruction_B (
    .D(ram_1_data), .en(Phase_Control_loadb), .Q(Instruction_B_q), .clk(clock_3_out));  // open: clr
  Clock clock_3 (.out(clock_3_out));
  and and_1 (and_1_out, not_3_out, Stack_ALU_write);
  not not_3 (not_3_out, Decoder_pointer);
  Ins_Decoder Decoder (
    .Data_In(ram_1_data), .Instruction_A(INA), .Data_Out(Decoder_data_out), .Instruction_B(Instruction_B_q),
    .ALU_OP(Decoder_alu_op), .ALU_EN(Decoder_alu_en), .SEGMENT(Decoder_segment), .POINTER(Decoder_pointer));
  Multiplexer #(.width(16), .enable("false")) multiplexer_2 (
    .in0(Decoder_data_out), .in1(ram_2_data), .out(multiplexer_2_out), .sel(Decoder_pointer));
  Clock clock_4 (.out(clock_4_out));
  and and_2 (and_2_out, Stack_ALU_write, Decoder_pointer);
  Stack_ALU Stack_ALU (
    .PUSHIN(multiplexer_2_out), .OP(Decoder_alu_op), .ENABLE(Decoder_alu_en), .RESET(RESET),
    .WRITE(Stack_ALU_write), .TOP(Stack_ALU_top));  // open: TOP_1
  RAM #(.addrWidth(3), .dataWidth(16), .bus("separate")) ram_2 (
    .addr(Decoder_segment), .din(Stack_ALU_top), .data(ram_2_data), .str(and_2_out), .clk(clock_4_out),
    .ld(not_4_out));  // open: sel, clr
  not not_4 (not_4_out, and_2_out);

  // Other names for the same wires on the sheet: RST = RESET

  // Notes on the sheet:
  //   Main RAM
  //   Load B
  //   Load A
  //   Execute
  //   Pointers
endmodule

module Ins_Decoder (
  input  [15:0] Data_In,
  input  [15:0] Instruction_B,
  input  [15:0] Instruction_A,
  output [15:0] Data_Out,
  output [2:0] ALU_OP,
  output ALU_EN,
  output [2:0] SEGMENT,
  output POINTER
);

  Multiplexer #(.width(16), .disabled(0), .enable("false")) multiplexer_1 (
    .in0(Data_In), .in1(Instruction_B), .out(Data_Out), .sel(Instruction_A[15]));

  assign ALU_EN = Instruction_A[3];
  assign ALU_OP = Instruction_A[2:0];
  assign POINTER = Instruction_A[7];
  assign SEGMENT = Instruction_A[6:4];
endmodule

module Phase_Control (
  input  RESET,
  input  [15:0] Data_In,
  output EXECUTE,
  output LOADB,
  output LOADA
);

  wire clock_1_out, LONG, not_1_out, not_2_out, or_1_out, SHORT;

  or or_1 (or_1_out, SHORT, LOADB);
  Clock clock_1 (.out(clock_1_out));
  D_Flip_Flop #(.trigger("falling")) d_ff_1 (
    .clk(clock_1_out), .D(or_1_out), .Q(EXECUTE), .reset(RESET));  // open: Qn, preset, en
  D_Flip_Flop #(.trigger("falling")) d_ff_2 (
    .clk(clock_1_out), .D(LONG), .Q(LOADB), .en(not_1_out), .reset(RESET));  // open: Qn, preset
  not not_1 (not_1_out, EXECUTE);
  nor nor_1 (LOADA, LOADB, EXECUTE);
  not not_2 (not_2_out, Data_In[15]);
  and and_1 (LONG, LOADA, Data_In[15]);
  and and_2 (SHORT, LOADA, not_2_out);
endmodule

module rty789 (
  input  [15:0] addr,
  input  [15:0] ponter_addr,
  input  pointer_not_used,
  input  [7:0] Pointer,
  input  [31:0] data,
  output [31:0] data_out
);

  wire and_1_out, and_2_out, and_3_out, change_to_from_pointer_out, clock_1_out, clock_2_out, d_ff_1_q,
       d_ff_1_qn, not_1_out, not_2_out, or_1_out, store_out, t_ff_1_q, t_ff_1_qn;
  wire [7:0] ram_1_data, sel;
  wire [15:0] multiplexer_1_out, ram_3_data, register_1_q;

  and and_1 (and_1_out, store_out, ~pointer_not_used);  // AND_Gate
  Button store (.out(store_out));
  Button change_to_from_pointer (.out(change_to_from_pointer_out));
  LED at_pointer (.in(t_ff_1_q));
  LED not_at_pointer (.in(t_ff_1_qn));
  Multiplexer #(.width(16), .disabled(0), .enable("false")) multiplexer_1 (
    .in0(addr), .in1(register_1_q), .out(multiplexer_1_out), .sel(t_ff_1_q));
  T_Flip_Flop t_ff_1 (
    .clk(change_to_from_pointer_out), .T(change_to_from_pointer_out), .Q(t_ff_1_q), .Qn(t_ff_1_qn));  // open: preset, reset, en
  not not_1 (not_1_out, store_out);
  RAM #(.addrWidth(16), .bus("separate")) ram_1 (
    .addr(multiplexer_1_out), .din(Pointer), .data(ram_1_data), .str(and_1_out), .clk(and_1_out),
    .ld(not_1_out));  // open: sel, clr
  RAM #(.addrWidth(16), .dataWidth(32), .bus("separate")) ram_2 (
    .addr(multiplexer_1_out), .din(data), .data(data_out), .str(store_out), .clk(store_out), .ld(not_1_out));  // open: sel, clr
  or or_1 (or_1_out, and_1_out, and_3_out);
  D_Flip_Flop d_ff_1 (.clk(clock_1_out), .D(and_2_out), .Q(d_ff_1_q), .Qn(d_ff_1_qn));  // open: preset, en, reset
  Clock clock_1 (.out(clock_1_out));
  and and_2 (and_2_out, d_ff_1_qn, or_1_out);
  and and_3 (and_3_out, and_1_out, d_ff_1_q);
  Register #(.width(16)) register_1 (.D(ram_3_data), .en(t_ff_1_q), .Q(register_1_q), .clk(t_ff_1_q));  // open: clr
  Multiplexer #(.width(8), .disabled(0), .enable("false")) multiplexer_2 (
    .in0(ram_1_data), .in1(Pointer), .out(sel), .sel(and_3_out));
  Clock clock_2 (.out(clock_2_out));
  RAM #(.dataWidth(16), .bus("separate")) ram_3 (
    .addr(sel), .din(ponter_addr), .data(ram_3_data), .str(and_3_out), .clk(clock_2_out), .ld(not_2_out));  // open: sel, clr
  not not_2 (not_2_out, and_3_out);

  // Other names for the same wires on the sheet: dat[31:0] = data; point[7:0] = Pointer

  // Notes on the sheet:
  //   Pointer: pull=down
  //   Pointer RAM
  //   Main RAM
  //   Pointers
endmodule
