// Logisim project TKStackALU.circ as structural Verilog: 2 circuits, main circuit Stack ALU
module stack (
  input  [15:0] IN,
  input  POP,
  input  PUSH,
  input  RESET,
  output [15:0] OUT
);

  wire clock_1_out, clock_2_out, not_1_out, or_1_out;
  wire [11:0] counter_1_q;
  wire [15:0] register_1_q;

  or or_1 (or_1_out, POP, PUSH);
  Register #(.width(16)) register_1 (.D(IN), .en(or_1_out), .Q(register_1_q), .clk(clock_1_out), .clr(RESET));
  Clock clock_1 (.out(clock_1_out));
  Clock clock_2 (.out(clock_2_out));
  Counter #(.width(12), .max('hfff)) counter_1 (
    .load(POP), .count(or_1_out), .Q(counter_1_q), .clk(clock_2_out), .clr(RESET));  // open: D, carry
  not not_1 (not_1_out, clock_2_out);
  RAM #(.addrWidth(12), .dataWidth(16), .bus("separate")) ram_1 (
    .addr(counter_1_q), .din(register_1_q), .data(OUT), .str(PUSH), .sel(1'b1), .clk(not_1_out), .clr(RESET));  // open: ld
endmodule

module Stack_ALU (
  input  [15:0] PUSHIN,
  input  [2:0] OP,
  input  ENABLE,
  input  RESET,
  output WRITE,
  output [15:0] TOP_1,
  output [15:0] TOP
);

  wire clock_1_out, decoder_1_out0, decoder_1_out1, decoder_1_out3, decoder_1_out4, or_1_out;
  wire [15:0] adder_1_out, and_1_out, multiplexer_1_out, negator_1_out, not_1_out, or_2_out;

  Decoder #(.select(3), .disabled(0)) decoder_1 (
    .out0(decoder_1_out0), .out1(decoder_1_out1), .out2(WRITE), .out3(decoder_1_out3), .out4(decoder_1_out4),
    .sel(OP), .en(ENABLE));  // open: out5, out6, out7
  or or_1 (or_1_out, decoder_1_out1, WRITE, decoder_1_out3, decoder_1_out4);
  stack stack_1 (.IN(TOP), .POP(or_1_out), .PUSH(decoder_1_out0), .RESET(RESET), .OUT(TOP_1));
  assign and_1_out = TOP_1 & TOP;  // AND_Gate and_1, 16 bits wide
  assign or_2_out = TOP_1 | TOP;  // OR_Gate or_2, 16 bits wide
  assign not_1_out = ~TOP;  // NOT_Gate not_1, 16 bits wide
  Negator #(.width(16)) negator_1 (.in(TOP), .out(negator_1_out));
  Adder #(.width(16)) adder_1 (.a(TOP_1), .b(TOP), .out(adder_1_out));  // open: cin, cout
  Multiplexer #(.select(3), .width(16), .enable("false")) multiplexer_1 (
    .in0(PUSHIN), .in1(TOP_1), .in2(adder_1_out), .in3(and_1_out), .in4(or_2_out), .in5(not_1_out),
    .in6(negator_1_out), .out(multiplexer_1_out), .sel(OP));  // open: in7
  Clock clock_1 (.out(clock_1_out));
  Register #(.width(16)) u_Top (.D(multiplexer_1_out), .en(ENABLE), .Q(TOP), .clk(clock_1_out), .clr(RESET));

  // Notes on the sheet:
  //   0- PUSH
  //   1- POP
  //   2 - ADD
  //   3 - AND
  //   4 - OR
  //   5 - NOT
  //   6 - INV
  //   7 - NOP
  //   Stack
endmodule
