// Logisim project TKStackPointers.circ as structural Verilog: 1 circuit, main circuit main
module main (
  input  [15:0] addr,
  input  [15:0] ponter_addr,
  input  pointer_not_used,
  input  [7:0] Pointer,
  input  [31:0] data,
  output [31:0] data_out
);

  wire and_1_out, and_2_out, and_3_out, change_to_from_pointer_out, clock_1_out, clock_2_out, d_ff_1_q,
       d_ff_1_qn, not_1_out, not_2_out, or_1_out, store_out, t_ff_1_q, t_ff_1_qn;
  wire [7:0] ram_1_data, sel;
  wire [15:0] multiplexer_1_out, ram_3_data, register_1_q;

  and and_1 (and_1_out, store_out, ~pointer_not_used);  // AND_Gate
  Button store (.out(store_out));
  Button change_to_from_pointer (.out(change_to_from_pointer_out));
  LED at_pointer (.in(t_ff_1_q));
  LED not_at_pointer (.in(t_ff_1_qn));
  Multiplexer #(.width(16), .disabled(0), .enable("false")) multiplexer_1 (
    .in0(addr), .in1(register_1_q), .out(multiplexer_1_out), .sel(t_ff_1_q));
  T_Flip_Flop t_ff_1 (
    .clk(change_to_from_pointer_out), .T(change_to_from_pointer_out), .Q(t_ff_1_q), .Qn(t_ff_1_qn));  // open: preset, reset, en
  not not_1 (not_1_out, store_out);
  RAM #(.addrWidth(16), .bus("separate")) ram_1 (
    .addr(multiplexer_1_out), .din(Pointer), .data(ram_1_data), .str(and_1_out), .clk(and_1_out),
    .ld(not_1_out));  // open: sel, clr
  RAM #(.addrWidth(16), .dataWidth(32), .bus("separate")) ram_2 (
    .addr(multiplexer_1_out), .din(data), .data(data_out), .str(store_out), .clk(store_out), .ld(not_1_out));  // open: sel, clr
  or or_1 (or_1_out, and_1_out, and_3_out);
  Clock clock_1 (.out(clock_1_out));
  D_Flip_Flop d_ff_1 (.clk(clock_1_out), .D(and_2_out), .Q(d_ff_1_q), .Qn(d_ff_1_qn));  // open: preset, en, reset
  and and_2 (and_2_out, d_ff_1_qn, or_1_out);
  and and_3 (and_3_out, and_1_out, d_ff_1_q);
  Register #(.width(16)) register_1 (.D(ram_3_data), .en(t_ff_1_q), .Q(register_1_q), .clk(t_ff_1_q));  // open: clr
  Multiplexer #(.width(8), .disabled(0), .enable("false")) multiplexer_2 (
    .in0(ram_1_data), .in1(Pointer), .out(sel), .sel(and_3_out));
  Clock clock_2 (.out(clock_2_out));
  RAM #(.dataWidth(16), .bus("separate")) ram_3 (
    .addr(sel), .din(ponter_addr), .data(ram_3_data), .str(and_3_out), .clk(clock_2_out), .ld(not_2_out));  // open: sel, clr
  not not_2 (not_2_out, and_3_out);

  // Other names for the same wires on the sheet: dat[31:0] = data; point[7:0] = Pointer

  // Notes on the sheet:
  //   Pointer: pull=down
  //   Pointer RAM
  //   Main RAM
  //   Pointers
endmodule
