// Logisim project TelePad test.circ as structural Verilog: 5 circuits, main circuit test
module main (
  input  toggle_write_protection,
  input  [15:0] Time,
  input  Same_time,
  input  [15:0] Dim,
  input  Same_dim,
  input  [31:0] X,
  input  [31:0] Y,
  input  [31:0] Z,
  input  [15:0] Chosen_pad,
  input  same_loc,
  input  Store,
  input  teleport,
  output [15:0] Dim_2,
  output [15:0] Time_2,
  output [15:0] loc_X,
  output [15:0] loc_Y,
  output [15:0] loc_Z,
  output Write_protection_stat
);

  wire clock_1_out, not_1_out, not_2_out, ram_1_data;

  time_dim_manager time_dim_manager_1 (
    .Time(Time), .Same_time(Same_time), .Dim(Dim), .Same_dim(Same_dim), .Chosen_pad(Chosen_pad),
    .Teleport(teleport), .Store(Store), .toggle_Write_protect(toggle_write_protection), .Dim_2(Time_2),
    .Dim_3(Dim_2));
  TelePad_reg telepad_reg_1 (
    .Write_protect_adress(toggle_write_protection), .same_loc(same_loc), .X(X), .Y(Y), .Z(Z),
    .Chosen_pad(Chosen_pad), .Teleport(teleport), .Store(Store), .loc_X(loc_X), .loc_Y(loc_Y), .loc_Z(loc_Z));
  not not_1 (not_1_out, Write_protection_stat);
  Clock clock_1 (.out(clock_1_out));
  not not_2 (not_2_out, toggle_write_protection);
  RAM #(.addrWidth(16), .dataWidth(1), .bus("separate")) ram_1 (
    .addr(Chosen_pad), .din(not_1_out), .data(ram_1_data), .str(toggle_write_protection), .clk(clock_1_out),
    .ld(not_2_out));  // open: sel, clr
  Multiplexer #(.enable("false")) multiplexer_1 (
    .in0(ram_1_data), .in1(Write_protection_stat), .out(Write_protection_stat), .sel(toggle_write_protection));
endmodule

module TelePad_reg (
  input  Write_protect_adress,
  input  same_loc,
  input  [31:0] X,
  input  [31:0] Y,
  input  [31:0] Z,
  input  [15:0] Chosen_pad,
  input  Teleport,
  input  Store,
  output [15:0] loc_X,
  output [15:0] loc_Y,
  output [15:0] loc_Z
);

  wire and_1_out, and_2_out, clock_1_out, clock_2_out, clock_3_out, multiplexer_1_out, not_1_out, not_2_out,
       not_3_out, not_4_out, not_5_out, not_6_out, ram_1_data, ram_5_data;
  wire [31:0] ram_2_data, ram_3_data, ram_4_data;

  not not_1 (not_1_out, and_1_out);
  RAM #(.addrWidth(16), .dataWidth(1), .bus("separate")) ram_1 (
    .addr(Chosen_pad), .din(same_loc), .data(ram_1_data), .str(and_1_out), .ld(not_1_out));  // open: sel, clk, clr
  and and_1 (and_1_out, Store, ~multiplexer_1_out);  // AND_Gate
  and and_2 (and_2_out, Teleport, ~ram_1_data);  // AND_Gate
  Clock clock_1 (.out(clock_1_out));
  Clock clock_2 (.out(clock_2_out));
  not not_2 (not_2_out, and_1_out);
  RAM #(.addrWidth(16), .dataWidth(32), .bus("separate")) ram_2 (
    .addr(Chosen_pad), .din(X), .data(ram_2_data), .str(and_1_out), .clk(clock_1_out), .ld(not_2_out));  // open: sel, clr
  Register #(.width(16)) u_X (.D(ram_2_data[15:0]), .en(and_2_out), .Q(loc_X), .clk(clock_2_out));  // open: clr
  not not_3 (not_3_out, and_1_out);
  RAM #(.addrWidth(16), .dataWidth(32), .bus("separate")) ram_3 (
    .addr(Chosen_pad), .din(Y), .data(ram_3_data), .str(and_1_out), .clk(clock_1_out), .ld(not_3_out));  // open: sel, clr
  Register #(.width(16)) u_Y (.D(ram_3_data[15:0]), .en(and_2_out), .Q(loc_Y), .clk(clock_2_out));  // open: clr
  RAM #(.addrWidth(16), .dataWidth(32), .bus("separate")) ram_4 (
    .addr(Chosen_pad), .din(Z), .data(ram_4_data), .str(and_1_out), .clk(clock_1_out), .ld(not_4_out));  // open: sel, clr
  not not_4 (not_4_out, and_1_out);
  not not_5 (not_5_out, multiplexer_1_out);
  Register #(.width(16)) u_Z (.D(ram_4_data[15:0]), .en(and_2_out), .Q(loc_Z), .clk(clock_2_out));  // open: clr
  Clock clock_3 (.out(clock_3_out));
  not not_6 (not_6_out, Write_protect_adress);
  RAM #(.addrWidth(16), .dataWidth(1), .bus("separate")) ram_5 (
    .addr(Chosen_pad), .din(not_5_out), .data(ram_5_data), .str(Write_protect_adress), .clk(clock_3_out),
    .ld(not_6_out));  // open: sel, clr
  Multiplexer #(.enable("false")) multiplexer_1 (
    .in0(ram_5_data), .in1(multiplexer_1_out), .out(multiplexer_1_out), .sel(Write_protect_adress));
  // Pins of 16 and 32 bits meet at ram_3_data
  // Pins of 16 and 32 bits meet at ram_2_data
  // Pins of 16 and 32 bits meet at ram_4_data
endmodule

module time_dim_manager (
  input  [15:0] Time,
  input  Same_time,
  input  [15:0] Dim,
  input  Same_dim,
  input  [15:0] Chosen_pad,
  input  Teleport,
  input  Store,
  input  toggle_Write_protect,
  output [15:0] Dim_2,
  output [15:0] Dim_3
);

  wire and_1_out, and_2_out, and_3_out, clock_1_out, clock_2_out, clock_3_out, clock_4_out, clock_5_out,
       clock_6_out, multiplexer_1_out, not_1_out, not_2_out, not_3_out, not_4_out, not_5_out, ram_1_data;
  wire [1:0] ram_2_data;
  wire [15:0] ram_3_data, ram_4_data;

  not not_1 (not_1_out, multiplexer_1_out);
  Clock clock_1 (.out(clock_1_out));
  not not_2 (not_2_out, toggle_Write_protect);
  Clock clock_2 (.out(clock_2_out));
  RAM #(.addrWidth(16), .dataWidth(1), .bus("separate")) ram_1 (
    .addr(Chosen_pad), .din(not_1_out), .data(ram_1_data), .str(toggle_Write_protect), .clk(clock_1_out),
    .ld(not_2_out));  // open: sel, clr
  Multiplexer #(.enable("false")) multiplexer_1 (
    .in0(ram_1_data), .in1(multiplexer_1_out), .out(multiplexer_1_out), .sel(toggle_Write_protect));
  RAM #(.addrWidth(16), .dataWidth(2), .bus("separate")) ram_2 (
    .addr(Chosen_pad), .din({Same_dim, Same_time}), .data(ram_2_data), .str(and_1_out), .clk(clock_2_out),
    .ld(not_3_out));  // open: sel, clr
  not not_3 (not_3_out, and_1_out);
  and and_1 (and_1_out, Store, ~multiplexer_1_out);  // AND_Gate
  Clock clock_3 (.out(clock_3_out));
  not not_4 (not_4_out, Store);
  Clock clock_4 (.out(clock_4_out));
  not not_5 (not_5_out, Store);
  RAM #(.addrWidth(16), .dataWidth(16), .bus("separate")) ram_3 (
    .addr(Chosen_pad), .din(Time), .data(ram_3_data), .str(Store), .clk(clock_3_out), .ld(not_4_out));  // open: sel, clr
  RAM #(.addrWidth(16), .dataWidth(16), .bus("separate")) ram_4 (
    .addr(Chosen_pad), .din(Dim), .data(ram_4_data), .clk(clock_4_out), .ld(not_5_out));  // open: str, sel, clr
  Clock clock_5 (.out(clock_5_out));
  and and_2 (and_2_out, Teleport, ~ram_2_data[1]);  // AND_Gate
  Register #(.width(16)) T (.D(ram_3_data), .en(and_3_out), .Q(Dim_2), .clk(clock_6_out));  // open: clr
  Clock clock_6 (.out(clock_6_out));
  and and_3 (and_3_out, Teleport, ~ram_2_data[0]);  // AND_Gate
  Register #(.width(16)) D (.D(ram_4_data), .en(and_2_out), .Q(Dim_3), .clk(clock_5_out));  // open: clr
endmodule

module test (
  input  [15:0] Time,
  input  Same_time,
  input  [15:0] Dim,
  input  Same_dim,
  input  [31:0] X,
  input  [31:0] Y,
  input  [31:0] Z,
  input  [15:0] Chosen_pad,
  input  same_loc,
  output [15:0] Dim_2,
  output [15:0] Time_2,
  output [15:0] loc_X,
  output [15:0] loc_Y,
  output [15:0] loc_Z
);

  wire main_1_write_protection_stat, Store_out, Teleport_out, toggle_write_protection_out;

  Button toggle_write_protection (.out(toggle_write_protection_out));
  Button Store (.out(Store_out));
  Button Teleport (.out(Teleport_out));
  LED Write_protection_stat (.in(main_1_write_protection_stat));
  main main_1 (
    .toggle_write_protection(toggle_write_protection_out), .Time(Time), .Same_time(Same_time), .Dim(Dim),
    .Same_dim(Same_dim), .X(X), .Y(Y), .Z(Z), .Chosen_pad(Chosen_pad), .same_loc(same_loc),
    .Store(Store_out), .teleport(Teleport_out), .Dim_2(Dim_2), .Time_2(Time_2), .loc_X(loc_X), .loc_Y(loc_Y),
    .loc_Z(loc_Z), .Write_protection_stat(main_1_write_protection_stat));
endmodule

module lock_mamager (
  input  [15:0] _16_1,
  input  [15:0] _16_2,
  input  [15:0] _16_3,
  input  [15:0] _16_4,
  input  [15:0] _16_5,
  input  _1,
  input  _2,
  input  [15:0] _16_6,
  input  _3,
  input  _4,
  input  [15:0] _16_7,
  input  _5,
  input  _6,
  input  [15:0] _16_8,
  input  _7,
  input  _8,
  input  [15:0] _16_9,
  input  _9,
  input  _0,
  input  [15:0] _16_0,
  output [15:0] _16_1_2,
  output [15:0] _16_2_2,
  output [15:0] _16_3_2,
  output [15:0] _16_4_2,
  output [15:0] _16_5_2,
  output [15:0] _16_6_2,
  output [15:0] _16_7_2,
  output [15:0] _16_8_2,
  output [15:0] _16_9_2,
  output [15:0] _16_0_2
);

  wire and_1_out, and_2_out, clock_1_out, clock_2_out, counter_1_q, decoder_1_out0, decoder_1_out1, or_1_out,
       or_2_out;
  wire [3:0] D_2_q, D_q, priority_encoder_1_out, rom_1_data;
  wire [15:0] multiplexer_1_out;

  Multiplexer #(.select(4), .width(16)) multiplexer_1 (
    .in0(_16_1), .in1(_16_2), .in2(_16_3), .in3(_16_4), .in4(_16_5), .in5(_16_6), .in6(_16_7), .in7(_16_8),
    .in8(_16_9), .in9(_16_0), .out(multiplexer_1_out), .sel(D_2_q));  // open: in10, in11, in12, in13, in14, in15, en
  Counter #(.width(1), .max('h1)) counter_1 (
    .count(or_2_out), .Q(counter_1_q), .clk(or_2_out));  // open: load, D, carry, clr
  Decoder #(.disabled(0), .enable("false")) decoder_1 (.out0(decoder_1_out0), .out1(decoder_1_out1), .sel(counter_1_q));
  or or_1 (or_1_out, _1, _2, _3, _4, _5, _6, _7, _8, _9, _0);
  Priority_Encoder #(.select(4)) priority_encoder_1 (
    .in0(_1), .in1(_2), .in2(_3), .in3(_4), .in4(_5), .in5(_6), .in6(_7), .in7(_8), .in8(_9), .in9(_0),
    .out(priority_encoder_1_out));  // open: in10, in11, in12, in13, in14, in15, gs, en_out, en_in
  and and_1 (and_1_out, or_1_out, decoder_1_out0);
  and and_2 (and_2_out, or_1_out, decoder_1_out1);
  ROM #(.addrWidth(4), .dataWidth(4)) rom_1 (.addr(priority_encoder_1_out), .data(rom_1_data), .sel(or_1_out));
  or or_2 (or_2_out, and_1_out, and_2_out);
  Register #(.width(4)) D (.D(rom_1_data), .en(and_1_out), .Q(D_q), .clk(clock_1_out));  // open: clr
  Clock clock_1 (.out(clock_1_out));
  Clock clock_2 (.out(clock_2_out));
  Demultiplexer #(.select(4), .width(16)) demultiplexer_1 (
    .out0(_16_1_2), .out1(_16_2_2), .out2(_16_3_2), .out3(_16_4_2), .out4(_16_5_2), .out5(_16_6_2),
    .out6(_16_7_2), .out7(_16_8_2), .out8(_16_9_2), .out9(_16_0_2), .in(multiplexer_1_out), .sel(D_q));  // open: out10, out11, out12, out13, out14, out15, en
  Register #(.width(4)) D_2 (.D(rom_1_data), .en(and_2_out), .Q(D_2_q), .clk(clock_2_out));  // open: clr

  // Notes on the sheet:
  //   contents of rom_1 (hex, n*v repeats v):
  //   1 2 3 4 5 6 7 8 9 0 a b c d e f
endmodule
