// Logisim project WIP 1.circ as structural Verilog: 2 circuits, main circuit 6345
module test (
);

  wire clock_1_out, clock_2_out, keyboard_1_avail, n6345_1_disp_clock_en, res_out;
  wire [6:0] keyboard_1_data, n6345_1_ascii_out;

  Keyboard #(.buflen(199)) keyboard_1 (
    .clk(clock_1_out), .avail(keyboard_1_avail), .data(keyboard_1_data));  // open: re, clr
  Clock clock_1 (.out(clock_1_out));
  Button res (.out(res_out));
  _6345 u_6345_1 (
    .reset(res_out), .ASCII_in(keyboard_1_data), .av_in(keyboard_1_avail), .ASCII_out(n6345_1_ascii_out),
    .disp_clock_en(n6345_1_disp_clock_en));
  TTY #(.cols(36)) tty_1 (.data(n6345_1_ascii_out), .clk(clock_2_out), .we(n6345_1_disp_clock_en), .clr(res_out));
  Clock clock_2 (.out(clock_2_out));
endmodule

module _6345 (
  input  reset,
  input  [6:0] ASCII_in,
  input  av_in,
  output [6:0] ASCII_out,
  output disp_clock_en
);

  wire and_1_out, clock_1_out, clock_2_out, not_1_out;
  wire [6:0] ram_1_data;
  wire [23:0] counter_1_q;

  Counter #(.width(24), .max('hffffff)) counter_1 (
    .count(and_1_out), .Q(counter_1_q), .clk(clock_1_out), .clr(reset));  // open: load, D, carry
  Clock clock_1 (.out(clock_1_out));
  and and_1 (and_1_out, disp_clock_en, ~reset);  // AND_Gate
  Clock clock_2 (.out(clock_2_out));
  not not_1 (not_1_out, av_in);
  RAM #(.addrWidth(24), .dataWidth(7), .bus("separate")) ram_1 (
    .addr(counter_1_q), .din(ASCII_in), .data(ram_1_data), .str(av_in), .clk(clock_2_out), .ld(not_1_out));  // open: sel, clr
  Multiplexer #(.width(7), .disabled(0), .enable("false")) multiplexer_1 (
    .in0(ram_1_data), .in1(ASCII_in), .out(ASCII_out), .sel(av_in));
  or or_1 (disp_clock_en, ASCII_out[0], ASCII_out[1], ASCII_out[2], ASCII_out[3], ASCII_out[4], ASCII_out[5], ASCII_out[6]);

  // Notes on the sheet:
  //   reset: pull=down
endmodule
