// Logisim project WIP.circ as structural Verilog: 2 circuits, main circuit main
module main (
  input  [31:0] A,
  input  [31:0] B,
  input  add,
  input  sub,
  input  mult,
  input  div,
  output [31:0] out,
  output carry_borrow,
  output [31:0] carry_remainder
);

  wire carr, multiplexer_5_out, not_1_out, subtractor_1_bout;
  wire [31:0] adder_1_out, divider_1_out, divider_1_rem, multiplexer_1_out, multiplexer_2_out,
       multiplexer_3_out, multiplexer_7_out, multiplier_1_cout, multiplier_1_out, subtractor_1_out;

  Adder #(.width(32)) adder_1 (.a(A), .b(B), .out(adder_1_out), .cout(carr));  // open: cin
  Multiplexer #(.width(32), .disabled(0), .enable("false")) multiplexer_1 (
    .in0(adder_1_out), .in1({32{1'b0}}), .out(multiplexer_1_out), .sel(not_1_out));
  not not_1 (not_1_out, add);
  Subtractor #(.width(32)) subtractor_1 (.a(A), .b(B), .out(subtractor_1_out), .bout(subtractor_1_bout));  // open: bin
  Multiplier #(.width(32)) multiplier_1 (.a(A), .b(B), .out(multiplier_1_out), .cout(multiplier_1_cout));  // open: cin
  Divider #(.width(32)) divider_1 (.a(A), .b(B), .out(divider_1_out), .rem(divider_1_rem));  // open: upper
  Multiplexer #(.width(32), .disabled(0), .enable("false")) multiplexer_2 (
    .in0(multiplexer_1_out), .in1(subtractor_1_out), .out(multiplexer_2_out), .sel(sub));
  Multiplexer #(.width(32), .disabled(0), .enable("false")) multiplexer_3 (
    .in0(multiplexer_2_out), .in1(multiplier_1_out), .out(multiplexer_3_out), .sel(mult));
  Multiplexer #(.width(32), .disabled(0), .enable("false")) multiplexer_4 (
    .in0(multiplexer_3_out), .in1(divider_1_out), .out(out), .sel(div));
  Multiplexer #(.disabled(0), .enable("false")) multiplexer_5 (
    .in0(1'b0), .in1(carr), .out(multiplexer_5_out), .sel(add));
  Multiplexer #(.disabled(0), .enable("false")) multiplexer_6 (
    .in0(multiplexer_5_out), .in1(subtractor_1_bout), .out(carry_borrow), .sel(sub));
  Multiplexer #(.width(32), .disabled(0), .enable("false")) multiplexer_7 (
    .in0({32{1'b0}}), .in1(multiplier_1_cout), .out(multiplexer_7_out), .sel(mult));
  Multiplexer #(.width(32), .disabled(0), .enable("false")) multiplexer_8 (
    .in0(multiplexer_7_out), .in1(divider_1_rem), .out(carry_remainder), .sel(div));

  // Other names for the same wires on the sheet: _1 = add; _2 = sub; _3 = mult; _4 = div

  // Notes on the sheet:
  //   div: pull=down
  //   carry_borrow: pull=down
  //   sub: pull=down
  //   carry_remainder: pull=down
  //   mult: pull=down
endmodule

module g (
  input  [31:0] A,
  input  [31:0] B,
  input  add,
  input  sub,
  input  mult,
  input  div,
  output [31:0] out,
  output carry_borow,
  output [31:0] carry_remainder
);

  main main_1 (
    .A(A), .B(B), .add(add), .sub(sub), .mult(mult), .div(div), .out(out), .carry_borrow(carry_borow),
    .carry_remainder(carry_remainder));

  // Notes on the sheet:
  //   sub: pull=down
  //   add: pull=down
  //   div: pull=down
  //   mult: pull=down
endmodule
