// Logisim project a-track machine.circ as structural Verilog: 2 circuits, main circuit a-track
module a_track (
  input  [31:0] new_pass,
  input  [31:0] user_pass,
  input  [23:0] loc,
  input  [31:0] in,
  input  set,
  input  store,
  input  load,
  output [31:0] out
);

  wire and_1_out, clock_1_out, clock_2_out, clock_3_out, comparator_1_eq, comparator_2_eq;
  wire [31:0] multiplier_1_cout, multiplier_1_out, multiplier_2_cout, multiplier_2_out, multiplier_3_cout,
       multiplier_3_out, multiplier_4_cout, multiplier_4_out, multiplier_5_cout, multiplier_5_out,
       multiplier_6_cout, multiplier_6_out, register_1_q, register_2_q;

  Multiplier #(.width(32)) multiplier_1 (
    .a(new_pass), .b(new_pass), .out(multiplier_1_out), .cout(multiplier_1_cout));  // open: cin
  Register #(.width(32)) register_1 (
    .D(multiplier_3_cout), .en(set), .Q(register_1_q), .clk(clock_1_out));  // open: clr
  Clock clock_1 (.out(clock_1_out));
  Multiplier #(.width(32)) multiplier_2 (
    .a(multiplier_1_out), .b(multiplier_1_out), .out(multiplier_2_out), .cin(multiplier_1_cout),
    .cout(multiplier_2_cout));
  Register #(.width(32)) register_2 (.D(multiplier_3_out), .en(set), .Q(register_2_q), .clk(clock_2_out));  // open: clr
  Clock clock_2 (.out(clock_2_out));
  Clock clock_3 (.out(clock_3_out));
  Multiplier #(.width(32)) multiplier_3 (
    .a(multiplier_2_out), .b(multiplier_2_out), .out(multiplier_3_out), .cin(multiplier_2_cout),
    .cout(multiplier_3_cout));
  Comparator #(.width(32), .mode("unsigned")) comparator_1 (
    .a(multiplier_6_out), .b(register_2_q), .eq(comparator_1_eq));  // open: gt, lt
  Comparator #(.width(32), .mode("unsigned")) comparator_2 (
    .a(register_1_q), .b(multiplier_6_cout), .eq(comparator_2_eq));  // open: gt, lt
  RAM #(.addrWidth(24), .dataWidth(32), .bus("separate")) ram_1 (
    .addr(loc), .din(in), .data(out), .str(store), .sel(and_1_out), .clk(clock_3_out), .ld(load));  // open: clr
  Multiplier #(.width(32)) multiplier_4 (
    .a(user_pass), .b(user_pass), .out(multiplier_4_out), .cout(multiplier_4_cout));  // open: cin
  and and_1 (and_1_out, comparator_1_eq, comparator_2_eq);
  Multiplier #(.width(32)) multiplier_5 (
    .a(multiplier_4_out), .b(multiplier_4_out), .out(multiplier_5_out), .cin(multiplier_4_cout),
    .cout(multiplier_5_cout));
  Multiplier #(.width(32)) multiplier_6 (
    .a(multiplier_5_out), .b(multiplier_5_out), .out(multiplier_6_out), .cin(multiplier_5_cout),
    .cout(multiplier_6_cout));
endmodule

module main (
  input  [31:0] new_pass,
  input  [31:0] user_pass,
  input  [23:0] loc,
  input  [31:0] in,
  output [31:0] out
);

  wire not_1_out, set_out, store_out;

  Button set (.out(set_out));
  Button store (.out(store_out));
  not not_1 (not_1_out, store_out);
  a_track Peter ();  // open: store, load, out, in, loc, set, user_pass, new_pass
  a_track Charlie ();  // open: store, load, out, in, loc, set, user_pass, new_pass
endmodule
