// Logisim project acd gen.circ as structural Verilog: 1 circuit, main circuit main
module main (
  input  [31:0] d_in,
  input  acd_load,
  input  write,
  output out
);

  wire clock_1_out, multiplexer_1_out;
  wire [0:0] or_1_out;
  wire [28:0] counter_1_q;
  wire [31:0] n2_gig_ram_1_data_out;

  Counter #(.width(29), .max('h1fffffff)) counter_1 (
    .count(or_1_out[0]), .Q(counter_1_q), .clk(clock_1_out));  // open: load, D, carry, clr
  Clock clock_1 (.out(clock_1_out));
  // Probe on counter_1_q
  _2_GIG_RAM u_2_gig_ram_1 (
    .clear(1'b0), .write(write), .data_in(d_in), .data_out(n2_gig_ram_1_data_out), .adress_in(counter_1_q),
    .Power(1'b1), .ass(1'b0));  // open: adress_contains_data, preasa, aw, a_out, arc
  // Probe on n2_gig_ram_1_data_out
  or or_1 (or_1_out[0], n2_gig_ram_1_data_out[0], n2_gig_ram_1_data_out[1], n2_gig_ram_1_data_out[2], n2_gig_ram_1_data_out[3], n2_gig_ram_1_data_out[4], n2_gig_ram_1_data_out[5], n2_gig_ram_1_data_out[6], n2_gig_ram_1_data_out[7], n2_gig_ram_1_data_out[8], n2_gig_ram_1_data_out[9], n2_gig_ram_1_data_out[10], n2_gig_ram_1_data_out[11], n2_gig_ram_1_data_out[12], n2_gig_ram_1_data_out[13], n2_gig_ram_1_data_out[14], n2_gig_ram_1_data_out[15], n2_gig_ram_1_data_out[17], n2_gig_ram_1_data_out[18], n2_gig_ram_1_data_out[19], n2_gig_ram_1_data_out[20], n2_gig_ram_1_data_out[21], n2_gig_ram_1_data_out[22], n2_gig_ram_1_data_out[23], n2_gig_ram_1_data_out[24], n2_gig_ram_1_data_out[25], n2_gig_ram_1_data_out[26], n2_gig_ram_1_data_out[27], n2_gig_ram_1_data_out[28], n2_gig_ram_1_data_out[29], n2_gig_ram_1_data_out[30], n2_gig_ram_1_data_out[31], n2_gig_ram_1_data_out[16]);
  // Probe on {{31{1'b0}}, or_1_out[0]}
  Multiplexer #(.disabled(0), .enable("false")) multiplexer_1 (
    .in0(or_1_out[0]), .in1(1'b0), .out(multiplexer_1_out), .sel(acd_load));
  _2_GIG_RAM u_2_gig_ram_2 (
    .clear(1'b0), .write(multiplexer_1_out), .data_in({{31{1'b0}}, or_1_out[0]}), .adress_contains_data(out),
    .adress_in(counter_1_q), .Power(1'b1), .ass(1'b0));  // open: data_out, preasa, aw, a_out, arc
endmodule
