// Logisim project adv reg.circ as structural Verilog: 1 circuit, main circuit 4 rf
module _4_rf (
  input  [4:0] r_sel,
  input  [31:0] d_out,
  input  [31:0] d_in,
  input  r_w,
  input  [1:0] select_rf
);

  wire clock_1_out, demultiplexer_1_out0, demultiplexer_1_out1, demultiplexer_1_out2, demultiplexer_1_out3,
       registerfile_3_p1;
  wire [4:0] demultiplexer_2_out0, demultiplexer_2_out1, demultiplexer_2_out2, demultiplexer_2_out3;
  wire [31:0] demultiplexer_3_out0, demultiplexer_3_out1, demultiplexer_3_out2, demultiplexer_3_out3,
       registerfile_1_p5, registerfile_2_p2, registerfile_3_p4, registerfile_4_p2;

  Demultiplexer #(.select(2), .disabled(0), .enable("false")) demultiplexer_1 (
    .out0(demultiplexer_1_out0), .out1(demultiplexer_1_out1), .out2(demultiplexer_1_out2),
    .out3(demultiplexer_1_out3), .in(r_w), .sel(select_rf));
  Demultiplexer #(.select(2), .width(5), .disabled(0), .enable("false")) demultiplexer_2 (
    .out0(demultiplexer_2_out0), .out1(demultiplexer_2_out1), .out2(demultiplexer_2_out2),
    .out3(demultiplexer_2_out3), .in(r_sel));  // open: sel
  Demultiplexer #(.select(2), .width(32), .disabled(0), .enable("false")) demultiplexer_3 (
    .out0(demultiplexer_3_out0), .out1(demultiplexer_3_out1), .out2(demultiplexer_3_out2),
    .out3(demultiplexer_3_out3), .in(d_in), .sel(select_rf));
  Clock clock_1 (.out(clock_1_out));
  // RegisterFile registerfile_1: pin names not known; wires that end beside it: demultiplexer_3_out0, clock_1_out, demultiplexer_1_out0, demultiplexer_2_out0, registerfile_1_p5, demultiplexer_3_out1, clock_1_out, demultiplexer_1_out1
  // RegisterFile registerfile_2: pin names not known; wires that end beside it: demultiplexer_2_out1, registerfile_2_p2, demultiplexer_3_out2, clock_1_out, demultiplexer_1_out2
  // RegisterFile registerfile_3: pin names not known; wires that end beside it: registerfile_3_p1, registerfile_3_p1, demultiplexer_2_out2, registerfile_3_p4, demultiplexer_3_out3, clock_1_out, demultiplexer_1_out3
  // RegisterFile registerfile_4: pin names not known; wires that end beside it: demultiplexer_2_out3, registerfile_4_p2
  Multiplexer #(.select(2), .width(32), .disabled(0), .enable("false")) multiplexer_1 (
    .in0(registerfile_1_p5), .in1(registerfile_2_p2), .in2(registerfile_3_p4), .in3(registerfile_4_p2),
    .out(d_out), .sel(select_rf));
endmodule
