// Logisim project auto text editor.circ as structural Verilog: 2 circuits, main circuit main
module main (
  input  [23:0] in_1,
  input  load_chars
);

  wire button_1_out, jmp_out, keyboard_1_avail, n457984578_1_disp_clock_out, n457984578_1_key_clock_out,
       res_out;
  wire [6:0] keyboard_1_data, n457984578_1_ascii_out;

  Keyboard keyboard_1 (
    .clk(n457984578_1_key_clock_out), .avail(keyboard_1_avail), .data(keyboard_1_data));  // open: re, clr
  Button jmp (.out(jmp_out));
  Button res (.out(res_out));
  _457984578 u_457984578_1 (
    .jump_in(jmp_out), .ASCII_in(keyboard_1_data), .a_in(in_1), .res_in(res_out), .R_W_in(load_chars),
    .avalible_in(keyboard_1_avail), .key_clock_out(n457984578_1_key_clock_out),
    .ASCII_out(n457984578_1_ascii_out), .disp_clock_out(n457984578_1_disp_clock_out));
  Button button_1 (.out(button_1_out));
  TTY #(.cols(40)) tty_1 (
    .data(n457984578_1_ascii_out), .clk(n457984578_1_disp_clock_out), .clr(button_1_out));  // open: we
endmodule

module _457984578 (
  input  jump_in,
  input  [6:0] ASCII_in,
  input  [23:0] a_in,
  input  res_in,
  input  R_W_in,
  input  avalible_in,
  output key_clock_out,
  output [6:0] ASCII_out,
  output disp_clock_out
);

  wire and_1_out, and_2_out, and_3_out, and_4_out, clock_1_out, not_1_out, not_2_out, or_1_out, or_3_out,
       or_4_out;
  wire [6:0] and_5_out, and_6_out, or_2_out, ram_1_data;
  wire [6:6] not_3_out;
  wire [23:0] counter_1_q;

  and and_1 (and_1_out, or_4_out, R_W_in);
  Clock clock_1 (.out(clock_1_out));
  assign disp_clock_out = not_1_out ? ~and_2_out : 1'bz;  // Controlled_Inverter controlled_inverter_1
  not not_1 (not_1_out, R_W_in);
  and and_2 (and_2_out, clock_1_out, ~res_in);  // AND_Gate
  not not_2 (not_2_out, disp_clock_out);
  assign disp_clock_out = R_W_in ? and_2_out : 1'bz;  // Controlled_Buffer controlled_buffer_1
  or or_1 (or_1_out, and_1_out, and_3_out);
  assign key_clock_out = and_4_out ? disp_clock_out : 1'bz;  // Controlled_Buffer controlled_buffer_2
  and and_3 (and_3_out, or_3_out, not_2_out);
  Counter #(.width(24), .max('hffffff)) counter_1 (
    .load(jump_in), .D(a_in), .count(or_1_out), .Q(counter_1_q), .clk(disp_clock_out), .clr(res_in));  // open: carry
  and and_4 (and_4_out, avalible_in, or_4_out);
  assign or_2_out = and_5_out | and_6_out;  // OR_Gate or_2, 7 bits wide
  assign and_5_out = ASCII_in & {7{R_W_in}};  // AND_Gate and_5, 7 bits wide
  assign and_6_out = {7{not_3_out[6]}} & ram_1_data;  // AND_Gate and_6, 7 bits wide
  RAM #(.addrWidth(24), .dataWidth(7), .bus("separate")) ram_1 (
    .addr(counter_1_q), .din(ASCII_in), .data(ram_1_data), .str(R_W_in), .clk(disp_clock_out),
    .ld(not_3_out[6]));  // open: sel, clr
  not not_3 (not_3_out[6], R_W_in);
  or or_3 (or_3_out, or_2_out[0], or_2_out[1], or_2_out[2], or_2_out[3], or_2_out[4], or_2_out[5], or_2_out[6]);
  Multiplexer #(.width(7), .disabled(0), .enable("false")) multiplexer_1 (
    .in0(ram_1_data), .in1(ASCII_in), .out(ASCII_out), .sel(R_W_in));
  or or_4 (or_4_out, and_5_out[0], and_5_out[1], and_5_out[2], and_5_out[3], and_5_out[4], and_5_out[5], and_5_out[6]);
endmodule
