// Logisim project calculator.circ as structural Verilog: 2 circuits, main circuit main
module main (
  input  [31:0] in_1
);

  wire and_1_out, button_2_out, button_3_out, button_4_out, button_5_out, button_out, C_out, d_ff_1_q,
       d_ff_1_qn, d_ff_2_q, d_ff_2_qn, d_ff_3_q, d_ff_4_q, d_ff_5_q, d_ff_6_q, not_1_out, not_2_out,
       not_3_out, not_4_out, not_5_out, not_6_out, not_7_out, not_8_out, not_9_out, not_10_out, not_11_out,
       not_12_out, not_13_out, not_14_out, not_15_out, not_16_out, not_17_out, not_18_out, not_19_out,
       not_20_out, not_21_out, not_22_out, not_23_out, or_1_out, or_4_out, or_5_out, or_6_out, or_7_out,
       or_8_out, or_9_out, or_10_out, or_11_out, or_12_out, or_14_out, or_15_out, renderer_1_a, renderer_1_b,
       renderer_1_c, renderer_1_d, renderer_1_e, renderer_1_f, renderer_1_g, renderer_2_a, renderer_2_b,
       renderer_2_c, renderer_2_d, renderer_2_e, renderer_2_f, renderer_2_g, renderer_3_a, renderer_3_b,
       renderer_3_c, renderer_3_d, renderer_3_e, renderer_3_f, renderer_3_g, renderer_4_a, renderer_4_b,
       renderer_4_c, renderer_4_d, renderer_4_e, renderer_4_f, renderer_4_g, renderer_5_a, renderer_5_b,
       renderer_5_c, renderer_5_d, renderer_5_e, renderer_5_f, renderer_5_g, renderer_6_a, renderer_6_b,
       renderer_6_c, renderer_6_d, renderer_6_e, renderer_6_f, renderer_6_g, renderer_7_a, renderer_7_b,
       renderer_7_c, renderer_7_d, renderer_7_e, renderer_7_f, renderer_7_g, renderer_8_a, renderer_8_b,
       renderer_8_c, renderer_8_d, renderer_8_e, renderer_8_f, renderer_8_g;
  wire [1:0] or_3_out, register_5_q, register_6_q, register_17_q, register_18_q;
  wire [3:0] multiplexer_1_out_2, multiplexer_1_out_3, multiplexer_1_out_4, multiplexer_1_out_5, or_2_out_2,
       or_2_out_3, or_13_out, register_7_q, register_8_q, register_9_q, register_10_q, register_11_q,
       register_12_q, register_13_q, register_14_q, register_15_q, register_16_q, shift_register_1_q0,
       shift_register_1_q1, shift_register_1_q2, shift_register_1_q3, shift_register_1_q4,
       shift_register_1_q5, shift_register_1_q6, shift_register_1_q7, shift_register_2_q0,
       shift_register_2_q1, shift_register_2_q2, shift_register_2_q3, shift_register_2_q4,
       shift_register_2_q5, shift_register_2_q6, shift_register_2_q7;
  wire [9:0] _7_out;
  wire [15:0] multiplexer_1_out;
  wire [31:0] adder_1_out, divider_1_out, multiplier_1_out, or_2_out, register_1_q, register_2_q,
       register_3_q, register_4_q, renderer_2_carry_out, renderer_3_carry_out, renderer_4_carry_out,
       renderer_5_carry_out, renderer_6_carry_out, renderer_7_carry_out, renderer_8_carry_out,
       subtractor_1_out;

  _7_Segment_Display u_7_segment_display_1 (
    .g(renderer_1_g), .f(renderer_1_f), .a(renderer_1_a), .b(renderer_1_b), .e(renderer_1_e),
    .d(renderer_1_d), .c(renderer_1_c));  // open: dp
  _7_Segment_Display u_7_segment_display_2 (
    .g(renderer_2_g), .f(renderer_2_f), .a(renderer_2_a), .b(renderer_2_b), .e(renderer_2_e),
    .d(renderer_2_d), .c(renderer_2_c));  // open: dp
  renderer renderer_1 (
    .E(renderer_1_e), .D(renderer_1_d), .C(renderer_1_c), .B(renderer_1_b), .A(renderer_1_a),
    .F(renderer_1_f), .G(renderer_1_g), .Value(or_2_out[31:28]), .Carry_In(renderer_2_carry_out));  // open: Carry_Out
  or or_1 (or_1_out, _7_out[9], _7_out[8], _7_out[7], _7_out[6], _7_out[5], _7_out[4], _7_out[3], _7_out[2], _7_out[1], _7_out[1]);
  D_Flip_Flop d_ff_1 (.Q(d_ff_1_q), .Qn(d_ff_1_qn), .preset(or_12_out), .reset(C_out));  // open: clk, D, en
  _7_Segment_Display u_7_segment_display_3 (
    .g(renderer_3_g), .f(renderer_3_f), .a(renderer_3_a), .b(renderer_3_b), .e(renderer_3_e),
    .d(renderer_3_d), .c(renderer_3_c));  // open: dp
  renderer renderer_2 (
    .Carry_Out(renderer_2_carry_out), .E(renderer_2_e), .D(renderer_2_d), .C(renderer_2_c), .B(renderer_2_b),
    .A(renderer_2_a), .F(renderer_2_f), .G(renderer_2_g), .Value(or_2_out[27:24]),
    .Carry_In(renderer_3_carry_out));
  Button _1 (.out(_7_out[2]));
  Button _2 (.out(_7_out[6]));
  Button _4 (.out(_7_out[1]));
  Button _5 (.out(_7_out[5]));
  Button _8 (.out(_7_out[4]));
  Button _7 (.out(_7_out[0]));
  Button _0 (.out(_7_out[3]));
  Register #(.width(32), .trigger("high")) register_1 (
    .D({shift_register_2_q7, shift_register_2_q6, shift_register_2_q5, shift_register_2_q4, shift_register_2_q3, shift_register_2_q2, shift_register_2_q1, shift_register_2_q0}),
    .en(d_ff_2_qn), .Q(register_1_q), .clk(d_ff_2_qn), .clr(not_1_out));
  not not_1 (not_1_out, d_ff_2_qn);
  Adder #(.width(32)) adder_1 (.a(register_2_q), .b(register_3_q), .out(adder_1_out));  // open: cin, cout
  Subtractor #(.width(32)) subtractor_1 (
    .a(register_2_q), .b(register_3_q), .out(subtractor_1_out));  // open: bin, bout
  Multiplier #(.width(32)) multiplier_1 (
    .a(register_2_q), .b(register_3_q), .out(multiplier_1_out));  // open: cin, cout
  Divider #(.width(32)) divider_1 (.a(register_2_q), .b(register_3_q), .out(divider_1_out));  // open: upper, rem
  Register #(.width(32), .trigger("high")) register_2 (
    .D({shift_register_2_q7, shift_register_2_q6, shift_register_2_q5, shift_register_2_q4, shift_register_2_q3, shift_register_2_q2, shift_register_2_q1, shift_register_2_q0}),
    .en(d_ff_1_qn), .Q(register_2_q), .clk(not_2_out), .clr(C_out));
  Register #(.width(32), .trigger("high")) register_3 (
    .D({shift_register_2_q7, shift_register_2_q6, shift_register_2_q5, shift_register_2_q4, shift_register_2_q3, shift_register_2_q2, shift_register_2_q1, shift_register_2_q0}),
    .en(d_ff_1_q), .Q(register_3_q), .clk(not_2_out), .clr(C_out));
  not not_2 (not_2_out, or_1_out);
  _7_Segment_Display u_7_segment_display_4 (
    .g(renderer_4_g), .f(renderer_4_f), .a(renderer_4_a), .b(renderer_4_b), .e(renderer_4_e),
    .d(renderer_4_d), .c(renderer_4_c));  // open: dp
  renderer renderer_3 (
    .Carry_Out(renderer_3_carry_out), .E(renderer_3_e), .D(renderer_3_d), .C(renderer_3_c), .B(renderer_3_b),
    .A(renderer_3_a), .F(renderer_3_f), .G(renderer_3_g), .Value(or_2_out_3), .Carry_In(renderer_4_carry_out));
  Button _3 (.out(_7_out[9]));
  Button _6 (.out(_7_out[8]));
  Button _9 (.out(_7_out[7]));
  Button C (.out(C_out));
  assign {or_2_out[31:24], or_2_out_3, or_2_out[19:16], or_2_out_2, or_2_out[11:0]} = register_1_q | register_4_q;  // OR_Gate or_2, 32 bits wide
  D_Flip_Flop d_ff_2 (.Q(d_ff_2_q), .Qn(d_ff_2_qn), .preset(button_5_out), .reset(C_out));  // open: clk, D, en
  Register #(.width(32), .trigger("high")) register_4 (
    .D({shift_register_1_q0, shift_register_1_q1, shift_register_1_q2, shift_register_1_q3, shift_register_1_q4, shift_register_1_q5, shift_register_1_q6, shift_register_1_q7}),
    .en(d_ff_2_q), .Q(register_4_q), .clk(d_ff_2_q), .clr(not_3_out));
  not not_3 (not_3_out, d_ff_2_q);
  Multiplexer #(.select(2), .width(32), .enable("false")) multiplexer_1 (
    .in0(adder_1_out), .in1(subtractor_1_out), .in2(multiplier_1_out), .in3(divider_1_out),
    .out({multiplexer_1_out_5, multiplexer_1_out_4, multiplexer_1_out_3, multiplexer_1_out_2, multiplexer_1_out}),
    .sel(or_3_out));
  assign or_3_out = register_17_q | register_18_q | register_5_q | register_6_q;  // OR_Gate or_3, 2 bits wide
  _7_Segment_Display u_7_segment_display_5 (
    .g(renderer_5_g), .f(renderer_5_f), .a(renderer_5_a), .b(renderer_5_b), .e(renderer_5_e),
    .d(renderer_5_d), .c(renderer_5_c));  // open: dp
  renderer renderer_4 (
    .Carry_Out(renderer_4_carry_out), .E(renderer_4_e), .D(renderer_4_d), .C(renderer_4_c), .B(renderer_4_b),
    .A(renderer_4_a), .F(renderer_4_f), .G(renderer_4_g), .Value(or_2_out[19:16]),
    .Carry_In(renderer_5_carry_out));
  Button button (.out(button_out));
  Button button_2 (.out(button_2_out));
  Button button_3 (.out(button_3_out));
  Button button_4 (.out(button_4_out));
  or or_4 (or_4_out, button_4_out, button_2_out, button_out);
  or or_5 (or_5_out, button_3_out, button_2_out, button_out);
  not not_4 (not_4_out, button_4_out);
  not not_5 (not_5_out, button_3_out);
  or or_6 (or_6_out, not_4_out, or_5_out);
  or or_7 (or_7_out, not_5_out, or_4_out);
  not not_6 (not_6_out, or_6_out);
  not not_7 (not_7_out, or_7_out);
  _7_Segment_Display u_7_segment_display_6 (
    .g(renderer_6_g), .f(renderer_6_f), .a(renderer_6_a), .b(renderer_6_b), .e(renderer_6_e),
    .d(renderer_6_d), .c(renderer_6_c));  // open: dp
  renderer renderer_5 (
    .Carry_Out(renderer_5_carry_out), .E(renderer_5_e), .D(renderer_5_d), .C(renderer_5_c), .B(renderer_5_b),
    .A(renderer_5_a), .F(renderer_5_f), .G(renderer_5_g), .Value(or_2_out_2), .Carry_In(renderer_6_carry_out));
  Button button_5 (.out(button_5_out));
  or or_8 (or_8_out, button_4_out, button_3_out, button_2_out);
  or or_9 (or_9_out, button_4_out, button_3_out, button_out);
  not not_8 (not_8_out, button_out);
  not not_9 (not_9_out, button_2_out);
  or or_10 (or_10_out, not_9_out, or_9_out);
  or or_11 (or_11_out, not_8_out, or_8_out);
  not not_10 (not_10_out, or_11_out);
  not not_11 (not_11_out, or_10_out);
  _7_Segment_Display u_7_segment_display_7 (
    .g(renderer_7_g), .f(renderer_7_f), .a(renderer_7_a), .b(renderer_7_b), .e(renderer_7_e),
    .d(renderer_7_d), .c(renderer_7_c));  // open: dp
  renderer renderer_6 (
    .Carry_Out(renderer_6_carry_out), .E(renderer_6_e), .D(renderer_6_d), .C(renderer_6_c), .B(renderer_6_b),
    .A(renderer_6_a), .F(renderer_6_f), .G(renderer_6_g), .Value(or_2_out[11:8]),
    .Carry_In(renderer_7_carry_out));
  D_Flip_Flop d_ff_3 (.Q(d_ff_3_q), .preset(not_10_out), .reset(C_out));  // open: clk, D, Qn, en
  D_Flip_Flop d_ff_4 (.Q(d_ff_4_q), .preset(not_7_out), .reset(C_out));  // open: clk, D, Qn, en
  _7_Segment_Display u_7_segment_display_8 (
    .g(renderer_8_g), .f(renderer_8_f), .a(renderer_8_a), .b(renderer_8_b), .e(renderer_8_e),
    .d(renderer_8_d), .c(renderer_8_c));  // open: dp
  renderer renderer_7 (
    .Carry_Out(renderer_7_carry_out), .E(renderer_7_e), .D(renderer_7_d), .C(renderer_7_c), .B(renderer_7_b),
    .A(renderer_7_a), .F(renderer_7_f), .G(renderer_7_g), .Value(or_2_out[7:4]),
    .Carry_In(renderer_8_carry_out));
  Register #(.width(2)) register_5 (.D(2'b00), .en(d_ff_3_q), .Q(register_5_q), .clk(d_ff_3_q), .clr(C_out));
  Register #(.width(2)) register_6 (.D(2'b10), .en(d_ff_4_q), .Q(register_6_q), .clk(d_ff_4_q), .clr(C_out));
  renderer renderer_8 (
    .Carry_Out(renderer_8_carry_out), .E(renderer_8_e), .D(renderer_8_d), .C(renderer_8_c), .B(renderer_8_b),
    .A(renderer_8_a), .F(renderer_8_f), .G(renderer_8_g), .Value(or_2_out[3:0]), .Carry_In(in_1));
  or or_12 (or_12_out, button_out, button_2_out, button_3_out, button_4_out);
  D_Flip_Flop d_ff_5 (.Q(d_ff_5_q), .preset(not_11_out), .reset(C_out));  // open: clk, D, Qn, en
  D_Flip_Flop d_ff_6 (.Q(d_ff_6_q), .preset(not_6_out), .reset(C_out));  // open: clk, D, Qn, en
  Register #(.width(4), .trigger("high")) register_7 (
    .D(4'b0000), .Q(register_7_q), .clk(_7_out[3]), .clr(not_12_out));  // open: en
  not not_12 (not_12_out, _7_out[3]);
  Register #(.width(4), .trigger("high")) register_8 (
    .D(4'b0001), .Q(register_8_q), .clk(_7_out[2]), .clr(not_13_out));  // open: en
  not not_13 (not_13_out, _7_out[2]);
  Register #(.width(4), .trigger("high")) register_9 (
    .D(4'b0010), .Q(register_9_q), .clk(_7_out[6]), .clr(not_14_out));  // open: en
  not not_14 (not_14_out, _7_out[6]);
  Register #(.width(4), .trigger("high")) register_10 (
    .D(4'b0011), .Q(register_10_q), .clk(_7_out[9]), .clr(not_15_out));  // open: en
  not not_15 (not_15_out, _7_out[9]);
  Register #(.width(4), .trigger("high")) register_11 (
    .D(4'b0100), .Q(register_11_q), .clk(_7_out[1]), .clr(not_16_out));  // open: en
  not not_16 (not_16_out, _7_out[1]);
  Register #(.width(4), .trigger("high")) register_12 (
    .D(4'b0101), .Q(register_12_q), .clk(_7_out[5]), .clr(not_17_out));  // open: en
  not not_17 (not_17_out, _7_out[5]);
  Register #(.width(4), .trigger("high")) register_13 (
    .D(4'b0110), .Q(register_13_q), .clk(_7_out[8]), .clr(not_18_out));  // open: en
  not not_18 (not_18_out, _7_out[8]);
  Register #(.width(4), .trigger("high")) register_14 (
    .D(4'b0111), .Q(register_14_q), .clk(_7_out[0]), .clr(not_19_out));  // open: en
  not not_19 (not_19_out, _7_out[0]);
  Register #(.width(4), .trigger("high")) register_15 (
    .D(4'b1000), .Q(register_15_q), .clk(_7_out[4]), .clr(not_20_out));  // open: en
  not not_20 (not_20_out, _7_out[4]);
  Register #(.width(4), .trigger("high")) register_16 (
    .D(4'b1001), .Q(register_16_q), .clk(_7_out[7]), .clr(not_21_out));  // open: en
  not not_21 (not_21_out, _7_out[7]);
  Register #(.width(2)) register_17 (.D(2'b01), .en(d_ff_5_q), .Q(register_17_q), .clk(d_ff_5_q), .clr(C_out));
  Register #(.width(2)) register_18 (.D(2'b11), .en(d_ff_6_q), .Q(register_18_q), .clk(d_ff_6_q), .clr(C_out));
  and and_1 (and_1_out, not_21_out, not_20_out, not_19_out, not_18_out, not_17_out, not_16_out, not_15_out, not_14_out, not_13_out, not_12_out);
  not not_22 (not_22_out, and_1_out);
  assign or_13_out = register_16_q | register_15_q | register_14_q | register_13_q | register_12_q | register_11_q | register_10_q | register_9_q | register_8_q | register_7_q;  // OR_Gate or_13, 4 bits wide
  or or_14 (or_14_out, button_5_out, not_22_out);
  not not_23 (not_23_out, or_14_out);
  Shift_Register #(.width(4)) shift_register_1 (
    .clk(button_5_out), .load(button_5_out), .clr(C_out), .d0(multiplexer_1_out_5), .q0(shift_register_1_q0),
    .d1(multiplexer_1_out_4), .q1(shift_register_1_q1), .d2(multiplexer_1_out_3), .q2(shift_register_1_q2),
    .d3(multiplexer_1_out_2), .q3(shift_register_1_q3), .d4(multiplexer_1_out[15:12]),
    .q4(shift_register_1_q4), .d5(multiplexer_1_out[11:8]), .q5(shift_register_1_q5),
    .d6(multiplexer_1_out[7:4]), .q6(shift_register_1_q6), .d7(multiplexer_1_out[3:0]),
    .q7(shift_register_1_q7));  // open: shift, in, out
  Shift_Register #(.width(4)) shift_register_2 (
    .in(or_13_out), .clk(not_23_out), .clr(or_15_out), .q0(shift_register_2_q0), .q1(shift_register_2_q1),
    .q2(shift_register_2_q2), .q3(shift_register_2_q3), .q4(shift_register_2_q4), .q5(shift_register_2_q5),
    .q6(shift_register_2_q6), .q7(shift_register_2_q7));  // open: shift, out, load, d0, d1, d2, d3, d4, d5, d6, d7
  or or_15 (or_15_out, C_out, button_5_out, or_12_out);
endmodule

module renderer (
  input  [31:0] Carry_In,
  input  [3:0] Value,
  output A,
  output F,
  output G,
  output B,
  output E,
  output C,
  output D,
  output [31:0] Carry_Out
);

  wire comparator_1_eq, comparator_1_gt, comparator_1_lt, decoder_1_out10, decoder_1_out11, decoder_1_out12,
       decoder_1_out13, decoder_1_out14, decoder_1_out15, decoder_2_out0, decoder_2_out1, decoder_2_out2,
       decoder_2_out3, decoder_2_out4, decoder_2_out5, decoder_2_out6, decoder_2_out7, decoder_2_out8,
       decoder_2_out9, not_1_out, not_2_out, not_3_out, not_4_out, not_5_out, not_6_out, not_7_out,
       not_8_out, or_1_out, or_2_out;
  wire [3:0] bit_extender_3_out, or_3_out, or_4_out, register_1_q, register_2_q, register_3_q, register_4_q,
       register_5_q, register_6_q, register_7_q, register_8_q;
  wire [31:0] adder_1_out, bit_extender_2_out;

  or u_F (F, decoder_2_out0, decoder_2_out4, decoder_2_out5, decoder_2_out6, decoder_2_out7, decoder_2_out8, decoder_2_out9);
  or or_1 (or_1_out, decoder_1_out15, decoder_1_out14, decoder_1_out13, decoder_1_out12, decoder_1_out11, decoder_1_out10);
  assign Carry_Out = {{31{1'b0}}, or_1_out};  // Bit_Extender bit_extender_1
  Decoder #(.select(4), .enable("false")) decoder_1 (
    .out10(decoder_1_out10), .out11(decoder_1_out11), .out12(decoder_1_out12), .out13(decoder_1_out13),
    .out14(decoder_1_out14), .out15(decoder_1_out15), .sel(register_4_q));  // open: out0, out1, out2, out3, out4, out5, out6, out7, out8, out9
  assign bit_extender_2_out = {{28{1'b0}}, Value};  // Bit_Extender bit_extender_2
  or u_G (G, decoder_2_out2, decoder_2_out3, decoder_2_out4, decoder_2_out5, decoder_2_out6, decoder_2_out8, decoder_2_out9);
  Register #(.width(4), .trigger("high")) register_1 (
    .D(4'b0000), .en(decoder_1_out10), .Q(register_1_q), .clk(decoder_1_out10), .clr(not_1_out));
  not not_1 (not_1_out, decoder_1_out10);
  Adder #(.width(32)) adder_1 (.a(bit_extender_2_out), .b(Carry_In), .out(adder_1_out));  // open: cin, cout
  or u_E (E, decoder_2_out0, decoder_2_out2, decoder_2_out6, decoder_2_out8);
  Register #(.width(4), .trigger("high")) register_2 (
    .D(4'b0001), .en(decoder_1_out11), .Q(register_2_q), .clk(decoder_1_out11), .clr(not_2_out));
  not not_2 (not_2_out, decoder_1_out11);
  or or_2 (or_2_out, comparator_1_gt, comparator_1_eq);
  Bit_Extender #(.in_width(32), .out_width(4)) bit_extender_3 (.in(adder_1_out), .out(bit_extender_3_out));
  not not_3 (not_3_out, comparator_1_lt);
  Comparator #(.width(32), .mode("unsigned")) comparator_1 (
    .a(adder_1_out), .b(32'ha), .gt(comparator_1_gt), .eq(comparator_1_eq), .lt(comparator_1_lt));
  Register #(.width(4), .trigger("high")) register_3 (
    .D(4'b0010), .en(decoder_1_out12), .Q(register_3_q), .clk(decoder_1_out12), .clr(not_4_out));
  not not_4 (not_4_out, decoder_1_out12);
  not not_5 (not_5_out, decoder_1_out13);
  Register #(.width(4), .trigger("high")) register_4 (
    .D(bit_extender_3_out), .en(or_2_out), .Q(register_4_q), .clk(or_2_out), .clr(not_6_out));
  not not_6 (not_6_out, or_2_out);
  Register #(.width(4), .trigger("high")) register_5 (
    .D(bit_extender_3_out), .en(comparator_1_lt), .Q(register_5_q), .clk(comparator_1_lt), .clr(not_3_out));
  _7_Segment_Display u_7_segment_display_1 (.g(G), .f(F), .a(A), .b(B), .e(E), .d(D), .c(C));  // open: dp
  or u_D (D, decoder_2_out0, decoder_2_out2, decoder_2_out3, decoder_2_out5, decoder_2_out6, decoder_2_out8, decoder_2_out9);
  Register #(.width(4), .trigger("high")) register_6 (
    .D(4'b0011), .en(decoder_1_out13), .Q(register_6_q), .clk(decoder_1_out13), .clr(not_5_out));
  Register #(.width(4), .trigger("high")) register_7 (
    .D(4'b0100), .en(decoder_1_out14), .Q(register_7_q), .clk(decoder_1_out14), .clr(not_7_out));
  not not_7 (not_7_out, decoder_1_out14);
  or u_C (C, decoder_2_out0, decoder_2_out1, decoder_2_out3, decoder_2_out4, decoder_2_out5, decoder_2_out6, decoder_2_out7, decoder_2_out8, decoder_2_out9);
  Register #(.width(4), .trigger("high")) register_8 (
    .D(4'b0101), .en(decoder_1_out15), .Q(register_8_q), .clk(decoder_1_out15), .clr(not_8_out));
  not not_8 (not_8_out, decoder_1_out15);
  or u_B (B, decoder_2_out0, decoder_2_out1, decoder_2_out2, decoder_2_out3, decoder_2_out4, decoder_2_out7, decoder_2_out8, decoder_2_out9);
  or u_A (A, decoder_2_out9, decoder_2_out8, decoder_2_out7, decoder_2_out6, decoder_2_out5, decoder_2_out3, decoder_2_out2, decoder_2_out0);
  Decoder #(.select(4), .enable("false")) decoder_2 (
    .out0(decoder_2_out0), .out1(decoder_2_out1), .out2(decoder_2_out2), .out3(decoder_2_out3),
    .out4(decoder_2_out4), .out5(decoder_2_out5), .out6(decoder_2_out6), .out7(decoder_2_out7),
    .out8(decoder_2_out8), .out9(decoder_2_out9), .sel(or_3_out));  // open: out10, out11, out12, out13, out14, out15
  assign or_3_out = or_4_out | register_5_q;  // OR_Gate or_3, 4 bits wide
  assign or_4_out = register_1_q | register_2_q | register_3_q | register_6_q | register_7_q | register_8_q;  // OR_Gate or_4, 4 bits wide
endmodule
