// Logisim project ck text editor.circ as structural Verilog: 1 circuit, main circuit main
module main (
);

  wire and_1_out, button_1_out, button_2_out, button_3_out, clock_1_out, keyboard_1_avail, not_1_out,
       or_1_out, or_2_out, or_3_out, or_4_out, or_5_out;
  wire [6:0] keyboard_1_data, multiplexer_1_out, ram_1_data;
  wire [23:0] counter_1_q;

  Clock clock_1 (.out(clock_1_out));
  and and_1 (and_1_out, clock_1_out, ~or_2_out);  // AND_Gate
  Keyboard keyboard_1 (.clk(and_1_out), .avail(keyboard_1_avail), .data(keyboard_1_data));  // open: re, clr
  Button button_1 (.out(button_1_out));
  or or_1 (or_1_out, or_5_out, keyboard_1_avail);
  Button button_2 (.out(button_2_out));
  or or_2 (or_2_out, button_2_out, button_1_out);
  Counter #(.width(24), .max('hffffff)) counter_1 (
    .count(or_1_out), .Q(counter_1_q), .clk(and_1_out), .clr(or_2_out));  // open: load, D, carry
  Button button_3 (.out(button_3_out));
  or or_3 (or_3_out, button_2_out, button_3_out);
  RAM #(.addrWidth(24), .dataWidth(7), .bus("separate")) ram_1 (
    .addr(counter_1_q), .din(keyboard_1_data), .data(ram_1_data), .str(keyboard_1_avail), .clk(and_1_out),
    .ld(not_1_out), .clr(button_2_out));  // open: sel
  not not_1 (not_1_out, keyboard_1_avail);
  or or_4 (or_4_out, keyboard_1_avail, or_5_out);
  Multiplexer #(.width(7), .disabled(0), .enable("false")) multiplexer_1 (
    .in0(ram_1_data), .in1(keyboard_1_data), .out(multiplexer_1_out), .sel(keyboard_1_avail));
  TTY tty_1 (.data(multiplexer_1_out), .clk(and_1_out), .we(or_4_out), .clr(or_3_out));
  or or_5 (or_5_out, ram_1_data[0], ram_1_data[1], ram_1_data[2], ram_1_data[3], ram_1_data[4], ram_1_data[5], ram_1_data[6]);

  // Notes on the sheet:
  //   LOAD
  //   RESET
  //   CLEAR
endmodule
