// Logisim project comp(new).circ as structural Verilog: 1 circuit, main circuit main
module main (
  input  [15:0] addr,
  input  jmp,
  input  msel,
  input  str,
  input  aen,
  input  ben,
  input  ren,
  input  a_s
);

  wire and_1_out, clock_1_out, not_1_out;
  wire [7:0] adder_1_out, multiplexer_1_out, multiplexer_2_out, ram_1_data, register_1_q, register_2_q,
       register_3_q, subtractor_1_out;
  wire [15:0] counter_1_q;
  wire [23:0] rom_1_data;

  Clock clock_1 (.out(clock_1_out));
  Counter #(.width(16), .max('hffff)) counter_1 (
    .load(jmp), .D(addr), .count(and_1_out), .Q(counter_1_q), .clk(clock_1_out));  // open: carry, clr
  and and_1 (and_1_out, 1'b1, ~jmp);  // AND_Gate
  ROM #(.addrWidth(16), .dataWidth(24)) rom_1 (.addr(counter_1_q), .data(rom_1_data));  // open: sel
  Register register_1 (.D(ram_1_data), .en(aen), .Q(register_1_q), .clk(clock_1_out));  // open: clr
  Register register_2 (.D(ram_1_data), .en(ben), .Q(register_2_q), .clk(clock_1_out));  // open: clr
  Multiplexer #(.width(8), .disabled(0), .enable("false")) multiplexer_1 (
    .in0(rom_1_data[7:0]), .in1(register_3_q), .out(multiplexer_1_out), .sel(msel));
  not not_1 (not_1_out, str);
  RAM #(.addrWidth(16), .bus("separate")) ram_1 (
    .addr(rom_1_data[15:0]), .din(multiplexer_1_out), .data(ram_1_data), .str(str), .clk(clock_1_out),
    .ld(not_1_out));  // open: sel, clr
  Adder adder_1 (.a(register_1_q), .b(register_2_q), .out(adder_1_out));  // open: cin, cout
  Subtractor subtractor_1 (.a(register_1_q), .b(register_2_q), .out(subtractor_1_out));  // open: bin, bout
  Multiplexer #(.width(8), .disabled(0), .enable("false")) multiplexer_2 (
    .in0(adder_1_out), .in1(subtractor_1_out), .out(multiplexer_2_out), .sel(a_s));
  Register register_3 (.D(multiplexer_2_out), .en(ren), .Q(register_3_q), .clk(clock_1_out));  // open: clr
endmodule
