// Logisim project comp.circ as structural Verilog: 2 circuits, main circuit main
module main (
  input  res,
  input  Takeover,
  input  [15:0] addr_code,
  input  [23:0] code,
  input  writec,
  input  [31:0] data_in,
  input  [15:0] addr_data,
  input  writed
);

  wire clock_1_out, clock_2_out, multiplexer_4_out, not_1_out, not_2_out, not_3_out, proc_1_data_st;
  wire [15:0] multiplexer_1_out, multiplexer_2_out, proc_1_addrc, proc_1_addrd;
  wire [23:0] ram_1_data;
  wire [31:0] multiplexer_3_out, proc_1_acc, proc_1_data_in, ram_2_data;

  // Probe on ram_2_data
  // Probe on proc_1_acc
  Multiplexer #(.width(16), .disabled(0), .enable("false")) multiplexer_1 (
    .in0(addr_data), .in1(proc_1_addrd), .out(multiplexer_1_out), .sel(not_1_out));
  not not_1 (not_1_out, Takeover);
  Clock clock_1 (.out(clock_1_out));
  not not_2 (not_2_out, writec);
  Clock clock_2 (.out(clock_2_out));
  not not_3 (not_3_out, multiplexer_4_out);
  RAM #(.addrWidth(16), .dataWidth(24), .bus("separate")) ram_1 (
    .addr(multiplexer_2_out), .din(code), .data(ram_1_data), .str(writec), .clk(clock_1_out), .ld(not_2_out));  // open: sel, clr
  RAM #(.addrWidth(16), .dataWidth(32), .bus("separate")) ram_2 (
    .addr(multiplexer_1_out), .din(multiplexer_3_out), .data(ram_2_data), .str(multiplexer_4_out),
    .clk(clock_2_out), .ld(not_3_out));  // open: sel, clr
  Multiplexer #(.width(16), .disabled(0), .enable("false")) multiplexer_2 (
    .in0(proc_1_addrc), .in1(addr_code), .out(multiplexer_2_out), .sel(Takeover));
  Multiplexer #(.width(32), .disabled(0), .enable("false")) multiplexer_3 (
    .in0(proc_1_data_in), .in1(data_in), .out(multiplexer_3_out), .sel(Takeover));
  Multiplexer #(.disabled(0), .enable("false")) multiplexer_4 (
    .in0(proc_1_data_st), .in1(writed), .out(multiplexer_4_out), .sel(Takeover));
  proc proc_1 (
    .cin(ram_1_data), .Data_in(proc_1_data_in), .Data_out(ram_2_data), .acc(proc_1_acc),
    .data_st(proc_1_data_st), .addrc(proc_1_addrc), .addrd(proc_1_addrd), .res(res));

  // Notes on the sheet:
  //   1h - ld
  //   2h - str
  //   3h - add
  //   4h - sub
  //   5h - jmp
  //   6h - jmpz
  //   7h - jmpnz
  //   8h - imm
endmodule

// CPU
module proc (
  input  res,
  input  [23:0] cin,
  input  [31:0] Data_out,
  output [31:0] acc,
  output data_st,
  output [31:0] Data_in,
  output [15:0] addrc,
  output [15:0] addrd
);

  wire and_1_out, and_2_out, clock_1_out, clock_2_out, comparator_1_eq, comparator_2_eq, comparator_5_gt,
       comparator_6_lt, comparator_7_eq, comparator_9_eq, comparator_10_eq, comparator_11_eq,
       comparator_12_eq, comparator_13_gt, comparator_14_eq, d_ff_1_q, d_ff_1_qn, not_1_out, not_2_out,
       not_3_out, not_4_out, not_5_out, or_1_out, or_2_out, or_3_out, or_4_out, or_5_out, or_6_out;
  wire [7:0] controlled_buffer_3_out;
  wire [31:0] adder_1_out, bit_extender_1_out, buffer_1_out, controlled_buffer_1_out,
       controlled_buffer_2_out, multiplexer_1_out, multiplexer_2_out;

  not not_1 (not_1_out, res);
  assign bit_extender_1_out = {{16{1'b0}}, cin[15:0]};  // Bit_Extender bit_extender_1
  Comparator #(.mode("unsigned")) comparator_1 (
    .a(controlled_buffer_3_out), .b(8'h6), .eq(comparator_1_eq));  // open: gt, lt
  not not_2 (not_2_out, comparator_11_eq);
  or or_1 (or_1_out, comparator_10_eq, or_5_out, res);
  Clock clock_1 (.out(clock_1_out));
  not not_3 (not_3_out, or_1_out);
  Multiplexer #(.width(32), .disabled(0), .enable("false")) multiplexer_1 (
    .in0(Data_out), .in1(bit_extender_1_out), .out(multiplexer_1_out), .sel(comparator_13_gt));
  or or_2 (or_2_out, comparator_12_eq, and_1_out, and_2_out);
  and and_1 (and_1_out, comparator_1_eq, d_ff_1_qn);
  assign controlled_buffer_1_out = not_2_out ? multiplexer_1_out : 32'bz;  // Controlled_Buffer controlled_buffer_1
  assign controlled_buffer_1_out = not_2_out ? ~multiplexer_1_out : 32'bz;  // Controlled_Inverter controlled_inverter_1
  Counter #(.width(16), .max('hffff)) counter_1 (
    .load(or_2_out), .D(cin[15:0]), .count(not_3_out), .Q(addrc), .clk(clock_1_out), .clr(res));  // open: carry
  Comparator #(.mode("unsigned")) comparator_2 (
    .a(controlled_buffer_3_out), .b(8'h7), .eq(comparator_2_eq));  // open: gt, lt
  or or_3 (or_3_out, res, comparator_10_eq);
  and and_2 (and_2_out, comparator_2_eq, ~d_ff_1_qn);  // AND_Gate
  or or_4 (or_4_out, comparator_11_eq, comparator_9_eq);
  assign controlled_buffer_2_out = or_4_out ? adder_1_out : 32'bz;  // Controlled_Buffer controlled_buffer_2
  Adder #(.width(32)) adder_1 (
    .a(controlled_buffer_1_out), .b(acc), .out(adder_1_out), .cin(comparator_11_eq));  // open: cout
  assign buffer_1_out = controlled_buffer_2_out;  // Buffer buffer_1, 32 bits wide
  Multiplexer #(.width(32), .disabled(0), .enable("false")) multiplexer_2 (
    .in0(multiplexer_1_out), .in1(controlled_buffer_2_out), .out(multiplexer_2_out), .sel(not_4_out));
  not not_4 (not_4_out, or_6_out);
  Register #(.width(32)) register_1 (.D(multiplexer_2_out), .en(not_5_out), .Q(acc), .clk(clock_1_out), .clr(or_3_out));
  Comparator #(.mode("unsigned")) comparator_3 ();  // open: a, b, gt, eq, lt
  Comparator #(.mode("unsigned")) comparator_4 ();  // open: a, b, gt, eq, lt
  Clock clock_2 (.out(clock_2_out));
  not not_5 (not_5_out, comparator_10_eq);
  D_Flip_Flop d_ff_1 (
    .clk(clock_2_out), .D(comparator_14_eq), .Q(d_ff_1_q), .Qn(d_ff_1_qn));  // open: preset, en, reset
  assign controlled_buffer_3_out = not_1_out ? cin[23:16] : 8'bz;  // Controlled_Buffer controlled_buffer_3
  Pull_Resistor pull_resistor_1 (.node(controlled_buffer_3_out));
  Pull_Resistor pull_resistor_2 (.node(buffer_1_out));
  Comparator #(.mode("unsigned")) comparator_5 (
    .a(controlled_buffer_3_out), .b(8'h8), .gt(comparator_5_gt));  // open: eq, lt
  Comparator #(.mode("unsigned")) comparator_6 (
    .a(controlled_buffer_3_out), .b(8'h1), .lt(comparator_6_lt));  // open: gt, eq
  Comparator #(.mode("unsigned")) comparator_7 (
    .a(controlled_buffer_3_out), .b(8'h1), .eq(comparator_7_eq));  // open: gt, lt
  Comparator #(.mode("unsigned")) comparator_8 (.a(controlled_buffer_3_out), .b(8'h2), .eq(data_st));  // open: gt, lt
  Comparator #(.mode("unsigned")) comparator_9 (
    .a(controlled_buffer_3_out), .b(8'h3), .eq(comparator_9_eq));  // open: gt, lt
  Comparator #(.mode("unsigned")) comparator_10 (
    .a(controlled_buffer_3_out), .b(8'h5), .eq(comparator_10_eq));  // open: gt, lt
  Comparator #(.mode("unsigned")) comparator_11 (
    .a(controlled_buffer_3_out), .b(8'h4), .eq(comparator_11_eq));  // open: gt, lt
  Comparator #(.mode("unsigned")) comparator_12 (
    .a(controlled_buffer_3_out), .b(8'h5), .eq(comparator_12_eq));  // open: gt, lt
  Comparator #(.mode("unsigned")) comparator_13 (
    .a(controlled_buffer_3_out), .b(8'h8), .gt(comparator_13_gt));  // open: eq, lt
  or or_5 (or_5_out, comparator_5_gt, comparator_6_lt);
  or or_6 (or_6_out, comparator_7_eq, comparator_13_gt);
  Comparator #(.width(32), .mode("unsigned")) comparator_14 (
    .a(buffer_1_out), .b({32{1'b0}}), .eq(comparator_14_eq));  // open: gt, lt

  assign addrd = cin[15:0];
  assign Data_in = acc;
endmodule
