// Logisim project comp_v2.circ as structural Verilog: 2 circuits, main circuit main
module main (
  input  Takeover,
  input  [15:0] addr_code,
  input  [31:0] code,
  input  writec,
  input  execute
);

  wire multiplexer_2_out, not_1_out, proc_1_data_st;
  wire [15:0] multiplexer_3_out, proc_1_addrc;
  wire [31:0] multiplexer_1_out, proc_1_acc, proc_1_data_in, ram_1_data;

  // Probe on ram_1_data
  // Probe on proc_1_acc
  Multiplexer #(.width(32), .enable("false")) multiplexer_1 (
    .in0(proc_1_data_in), .in1(code), .out(multiplexer_1_out), .sel(Takeover));
  Multiplexer #(.enable("false")) multiplexer_2 (
    .in0(proc_1_data_st), .in1(writec), .out(multiplexer_2_out), .sel(Takeover));
  Clock clock_1 ();  // open: out
  not not_1 (not_1_out, multiplexer_2_out);
  RAM #(.addrWidth(16), .dataWidth(32), .bus("separate")) ram_1 (
    .addr(multiplexer_3_out), .din(multiplexer_1_out), .data(ram_1_data), .str(multiplexer_2_out),
    .ld(not_1_out));  // open: sel, clk, clr
  Multiplexer #(.width(16), .disabled(0), .enable("false")) multiplexer_3 (
    .in0(proc_1_addrc), .in1(addr_code), .out(multiplexer_3_out), .sel(Takeover));
  proc proc_1 (
    .cin(ram_1_data), .Data_in(proc_1_data_in), .Execute(execute), .acc(proc_1_acc),
    .data_st(proc_1_data_st), .addrc(proc_1_addrc));

  // Notes on the sheet:
  //   1h - ld
  //   2h - str
  //   3h - add
  //   4h - sub
  //   5h - jmp
  //   6h - imm
endmodule

// CPU
module proc (
  input  Execute,
  input  [31:0] cin,
  output [31:0] acc,
  output data_st,
  output [31:0] Data_in,
  output [15:0] addrc
);

  wire and_1_out, clock_1_out, clock_2_out, clock_3_out, comparator_1_gt, comparator_2_lt, comparator_3_eq,
       comparator_5_eq, comparator_6_eq, comparator_7_eq, comparator_8_eq, counter_2_q, not_1_out, not_2_out,
       not_3_out, not_4_out, not_5_out, or_1_out, or_2_out, or_3_out, or_4_out, or_5_out;
  wire [7:0] controlled_buffer_3_out, register_2_q;
  wire [15:0] counter_1_q;
  wire [23:0] bit_extender_2_out;
  wire [31:0] adder_1_out, bit_extender_1_out, controlled_buffer_1_out, controlled_buffer_2_out,
       multiplexer_1_out, multiplexer_3_out;

  not not_1 (not_1_out, Execute);
  assign bit_extender_1_out = {{16{1'b0}}, bit_extender_2_out[15:0]};  // Bit_Extender bit_extender_1
  and and_1 (and_1_out, counter_2_q, Execute);
  or or_1 (or_1_out, not_1_out, not_1_out);
  not not_2 (not_2_out, comparator_6_eq);
  or or_2 (or_2_out, or_4_out, comparator_7_eq, not_1_out);
  Clock clock_1 (.out(clock_1_out));
  not not_3 (not_3_out, or_2_out);
  Multiplexer #(.width(32), .disabled(0), .enable("false")) multiplexer_1 (
    .in0(cin), .in1(bit_extender_1_out), .out(multiplexer_1_out), .sel(comparator_8_eq));
  assign controlled_buffer_1_out = not_2_out ? multiplexer_1_out : 32'bz;  // Controlled_Buffer controlled_buffer_1
  assign controlled_buffer_1_out = not_2_out ? ~multiplexer_1_out : 32'bz;  // Controlled_Inverter controlled_inverter_1
  Counter #(.width(16), .max('hffff)) counter_1 (
    .load(comparator_7_eq), .D(bit_extender_2_out[15:0]), .count(not_3_out), .Q(counter_1_q),
    .clk(clock_1_out), .clr(or_1_out));  // open: carry
  Counter #(.width(1), .max('h1)) counter_2 (
    .count(clock_1_out), .Q(counter_2_q), .clk(clock_2_out), .clr(clock_2_out));  // open: load, D, carry
  Clock clock_2 (.out(clock_2_out));
  not not_4 (not_4_out, Execute);
  or or_3 (or_3_out, comparator_6_eq, comparator_5_eq);
  assign controlled_buffer_2_out = or_3_out ? adder_1_out : 32'bz;  // Controlled_Buffer controlled_buffer_2
  Adder #(.width(32)) adder_1 (
    .a(controlled_buffer_1_out), .b(acc), .out(adder_1_out), .cin(comparator_6_eq));  // open: cout
  Multiplexer #(.width(16), .enable("false")) multiplexer_2 (
    .in0(counter_1_q), .in1(bit_extender_2_out[15:0]), .out(addrc), .sel(Execute));
  Multiplexer #(.width(32), .disabled(0), .enable("false")) multiplexer_3 (
    .in0(multiplexer_1_out), .in1(controlled_buffer_2_out), .out(multiplexer_3_out), .sel(not_5_out));
  not not_5 (not_5_out, or_5_out);
  Register #(.width(32)) register_1 (.D(multiplexer_3_out), .Q(acc), .clk(clock_1_out), .clr(not_1_out));  // open: en
  Bit_Extender #(.in_width(32), .out_width(24)) bit_extender_2 (.in(cin), .out(bit_extender_2_out));
  Register register_2 (
    .D(bit_extender_2_out[23:16]), .en(not_4_out), .Q(register_2_q), .clk(clock_3_out));  // open: clr
  Clock clock_3 (.out(clock_3_out));
  assign controlled_buffer_3_out = and_1_out ? register_2_q : 8'bz;  // Controlled_Buffer controlled_buffer_3
  Pull_Resistor pull_resistor_1 (.node(controlled_buffer_3_out));
  Comparator #(.mode("unsigned")) comparator_1 (
    .a(controlled_buffer_3_out), .b(8'h6), .gt(comparator_1_gt));  // open: eq, lt
  Comparator #(.mode("unsigned")) comparator_2 (
    .a(controlled_buffer_3_out), .b(8'h1), .lt(comparator_2_lt));  // open: gt, eq
  Comparator #(.mode("unsigned")) comparator_3 (
    .a(controlled_buffer_3_out), .b(8'h1), .eq(comparator_3_eq));  // open: gt, lt
  Comparator #(.mode("unsigned")) comparator_4 (.a(controlled_buffer_3_out), .b(8'h2), .eq(data_st));  // open: gt, lt
  Comparator #(.mode("unsigned")) comparator_5 (
    .a(controlled_buffer_3_out), .b(8'h3), .eq(comparator_5_eq));  // open: gt, lt
  Comparator #(.mode("unsigned")) comparator_6 (
    .a(controlled_buffer_3_out), .b(8'h4), .eq(comparator_6_eq));  // open: gt, lt
  Comparator #(.mode("unsigned")) comparator_7 (
    .a(controlled_buffer_3_out), .b(8'h5), .eq(comparator_7_eq));  // open: gt, lt
  Comparator #(.mode("unsigned")) comparator_8 (
    .a(controlled_buffer_3_out), .b(8'h6), .eq(comparator_8_eq));  // open: gt, lt
  or or_4 (or_4_out, comparator_1_gt, comparator_2_lt);
  or or_5 (or_5_out, comparator_3_eq, comparator_8_eq);

  assign Data_in = acc;
endmodule
