// Logisim project cpu.circ as structural Verilog: 2 circuits, main circuit main
module main (
  input  [7:0] Opcode,
  input  [7:0] Addr,
  input  str,
  input  clk,
  input  m_a,
  input  prog,
  input  reset
);

  wire adder_1_cout, and_1_out, and_2_out, and_3_out, and_4_out, clock_1_out, comparator_1_eq,
       multiplexer_1_out, multiplexer_2_out, nor_1_out, not_1_out, not_2_out, not_3_out, subtractor_1_bout;
  wire [1:0] multiplexer_5_out, register_2_q;
  wire [7:0] adder_1_out, counter_1_q, multiplexer_3_out, multiplexer_4_out, pull_resistor_4_node,
       ram_2_data, register_1_q, subtractor_1_out;
  wire [15:0] pull_resistor_1_node;

  Clock clock_1 (.out(clock_1_out));
  Counter counter_1 (.Q(counter_1_q), .clk(multiplexer_1_out), .clr(reset));  // open: load, D, count, carry
  Multiplexer #(.disabled(0), .enable("false")) multiplexer_1 (
    .in0(and_3_out), .in1(multiplexer_2_out), .out(multiplexer_1_out), .sel(prog));
  Multiplexer #(.disabled(0), .enable("false")) multiplexer_2 (
    .in0(clk), .in1(clock_1_out), .out(multiplexer_2_out), .sel(m_a));
  not not_1 (not_1_out, str);
  and and_1 (and_1_out, multiplexer_2_out, prog);
  Pull_Resistor pull_resistor_1 (.node(pull_resistor_1_node));
  RAM #(.dataWidth(16), .bus("separate")) ram_1 (
    .addr(counter_1_q), .din({Opcode, Addr}), .data(pull_resistor_1_node), .str(str), .clk(and_1_out),
    .ld(not_1_out));  // open: sel, clr
  and and_2 (and_2_out, multiplexer_2_out, ~prog);  // AND_Gate
  and and_3 (and_3_out, and_2_out, ~comparator_1_eq);  // AND_Gate
  nor nor_1 (nor_1_out, pull_resistor_1_node[14], pull_resistor_1_node[15], comparator_1_eq);
  not not_2 (not_2_out, pull_resistor_1_node[14]);
  Multiplexer #(.select(2), .width(8), .disabled(0), .enable("false")) multiplexer_3 (
    .in0(ram_2_data), .in1(pull_resistor_1_node[7:0]), .in2(register_1_q), .out(multiplexer_3_out),
    .sel(pull_resistor_1_node[9:8]));  // open: in3
  Multiplexer #(.select(2), .width(8), .disabled(0), .enable("false")) multiplexer_4 (
    .in0(ram_2_data), .in1(pull_resistor_1_node[7:0]), .in2(register_1_q), .out(multiplexer_4_out),
    .sel(pull_resistor_1_node[11:10]));  // open: in3
  RAM #(.bus("separate")) ram_2 (
    .addr(pull_resistor_1_node[7:0]), .din(register_1_q), .data(ram_2_data), .str(pull_resistor_1_node[14]),
    .clk(and_3_out), .ld(not_2_out));  // open: sel, clr
  Pull_Resistor pull_resistor_2 (.node(multiplexer_3_out));
  Pull_Resistor pull_resistor_3 (.node(multiplexer_4_out));
  Comparator #(.width(2), .mode("unsigned")) comparator_1 (
    .a(pull_resistor_1_node[13:12]), .b(2'b11), .eq(comparator_1_eq));  // open: gt, lt
  Adder adder_1 (.a(multiplexer_3_out), .b(multiplexer_4_out), .out(adder_1_out), .cout(adder_1_cout));  // open: cin
  Subtractor subtractor_1 (
    .a(multiplexer_3_out), .b(multiplexer_4_out), .out(subtractor_1_out), .bout(subtractor_1_bout));  // open: bin
  Multiplexer #(.disabled(0), .enable("false")) multiplexer_5 (
    .in0(adder_1_cout), .in1(subtractor_1_bout), .out(multiplexer_5_out[0]), .sel(pull_resistor_1_node[12]));
  Pull_Resistor pull_resistor_4 (.node(pull_resistor_4_node));
  Zero zero_1 (.In(pull_resistor_4_node), .Zero(multiplexer_5_out[1]));
  Register register_1 (.D(pull_resistor_4_node), .en(nor_1_out), .Q(register_1_q), .clk(and_3_out), .clr(reset));
  Multiplexer #(.select(2), .width(8), .disabled(0), .enable("false")) multiplexer_6 (
    .in0(adder_1_out), .in1(subtractor_1_out), .in2(multiplexer_3_out), .out(pull_resistor_4_node),
    .sel(pull_resistor_1_node[13:12]));  // open: in3
  not not_3 (not_3_out, pull_resistor_1_node[13]);
  Register #(.width(2)) register_2 (
    .D(multiplexer_5_out), .en(and_4_out), .Q(register_2_q), .clk(and_3_out), .clr(reset));
  and and_4 (and_4_out, nor_1_out, not_3_out);
endmodule

// Z
module Zero (
  input  [7:0] In,
  output Zero
);

  nor nor_1 (Zero, In[0], In[1], In[2], In[3], In[4], In[5], In[6], In[7]);
endmodule
