// Logisim project cpu 4.circ as structural Verilog
module CPU (
  input  [4:0] instr,
  input  [7:0] addr_imm,
  input  [7:0] Din,
  output [7:0] Addr,
  output [7:0] Dout,
  output nR_W
);

  wire ins_dec_1_p2, ins_dec_1_p3, ins_dec_1_p4, ins_dec_1_p5;
  wire [1:0] ins_dec_1_p6;
  wire [7:0] multiplexer_1_out, multiplexer_2_out, P_q;

  // ins_dec ins_dec_1: pin names not known; wires that end beside it: instr, ins_dec_1_p2, ins_dec_1_p3, ins_dec_1_p4, ins_dec_1_p5, ins_dec_1_p6, nR_W
  Multiplexer #(.width(8), .disabled(0), .enable("false")) multiplexer_1 (
    .in0(Din), .in1(Din), .out(multiplexer_1_out), .sel(ins_dec_1_p2));
  Multiplexer #(.width(8), .disabled(0), .enable("false")) multiplexer_2 (
    .in0(Din), .in1(Dout), .out(multiplexer_2_out), .sel(ins_dec_1_p4));
  Register A (.D(multiplexer_1_out), .en(ins_dec_1_p3), .Q(Dout));  // open: clk, clr
  Register P (.D(multiplexer_2_out), .en(ins_dec_1_p5), .Q(P_q));  // open: clk, clr
  Multiplexer #(.select(2), .width(8), .disabled(0), .enable("false")) multiplexer_3 (
    .in0(addr_imm), .in1(P_q), .out(Addr), .sel(ins_dec_1_p6));  // open: in2, in3
endmodule

module ALU (
  input  [7:0] A,
  input  [7:0] B,
  input  [1:0] Op,
  output [7:0] R
);

  wire [7:0] adder_1_out, adder_2_out, subtractor_1_out, undriven;

  Adder adder_1 (.a(A), .b(B), .out(adder_1_out));  // open: cin, cout
  Subtractor subtractor_1 (.a(A), .b(B), .out(subtractor_1_out));  // open: bin, bout
  Adder adder_2 (.a(A), .b(8'h1), .out(adder_2_out));  // open: cin, cout
  Subtractor subtractor_2 (.a(A), .b(8'h1));  // open: out, bin, bout
  Multiplexer #(.select(2), .width(8), .disabled(0), .enable("false")) multiplexer_1 (
    .in0(adder_1_out), .in1(subtractor_1_out), .in2(adder_2_out), .in3(undriven), .out(R), .sel(Op));
endmodule

module ins_dec (
  input  [4:0] instruction,
  output a_mux_sel,
  output a_en,
  output p_mux_sel,
  output p_en,
  output [1:0] addr_select,
  output nR_W,
  output IO
);

  wire decoder_1_out0, decoder_1_out2, decoder_1_out3, decoder_1_out5, decoder_1_out6, decoder_1_out7,
       decoder_1_out8, or_1_out, or_2_out;

  Decoder #(.select(5), .enable("false")) decoder_1 (
    .out0(decoder_1_out0), .out1(a_mux_sel), .out2(decoder_1_out2), .out3(decoder_1_out3), .out4(p_mux_sel),
    .out5(decoder_1_out5), .out6(decoder_1_out6), .out7(decoder_1_out7), .out8(decoder_1_out8),
    .sel(instruction));  // open: out9, out10, out11, out12, out13, out14, out15, out16, out17, out18, out19, out20, out21, out22, out23, out24, out25, out26, out27, out28, out29, out30, out31
  or or_1 (or_1_out, decoder_1_out0, a_mux_sel, decoder_1_out2, decoder_1_out3);
  or or_2 (or_2_out, decoder_1_out5, decoder_1_out6);
  or or_3 (nR_W, decoder_1_out3, decoder_1_out6, decoder_1_out8);
  or or_4 (IO, decoder_1_out7, decoder_1_out8);
  or or_5 (p_en, p_mux_sel, decoder_1_out2);
  Priority_Encoder #(.select(2)) priority_encoder_1 (
    .in0(or_1_out), .in1(or_2_out), .out(addr_select));  // open: in2, in3, gs, en_out, en_in
  or or_6 (a_en, decoder_1_out0, decoder_1_out5, a_mux_sel, decoder_1_out7);
  Pull_Resistor pull_resistor_1 (.node(addr_select));
endmodule
