// Logisim project cpu.circ as structural Verilog: 4 circuits, main circuit main
module main (
  input  clk,
  input  res,
  output [3:0] out_3,
  output [3:0] out_4
);

  wire ins_dec_1_a_register_source, ins_dec_1_flag_enable, ins_dec_1_jump, ins_dec_1_memory_store,
       ins_dec_1_write_enable, ins_dec_1_write_register_source, not_1_out;
  wire [1:0] alu_1_carry, ins_dec_1_alu_op, ins_dec_1_lod_i__sto_reg, ins_dec_1_write_data_source,
       multiplexer_2_out, multiplexer_3_out, register_1_q, rom_1_data, rom_1_data_2;
  wire [3:0] alu_1_r, counter_1_q, multiplexer_1_out, ram_1_data;
  wire [4:0] rom_1_data_3;

  Counter #(.width(4), .max('hf)) counter_1 (
    .load(ins_dec_1_jump), .D({rom_1_data_2, rom_1_data}), .Q(counter_1_q), .clk(clk), .clr(res));  // open: count, carry
  ROM #(.addrWidth(4), .dataWidth(9)) rom_1 (
    .addr(counter_1_q), .data({rom_1_data_3, rom_1_data_2, rom_1_data}));  // open: sel
  ins_dec ins_dec_1 (
    .Ins(rom_1_data_3), .Flags(register_1_q), .Write_data_source(ins_dec_1_write_data_source),
    .Write_register_source(ins_dec_1_write_register_source), .LOD_I__STO_reg(ins_dec_1_lod_i__sto_reg),
    .Write_enable(ins_dec_1_write_enable), .A_register_source(ins_dec_1_a_register_source),
    .Memory_store(ins_dec_1_memory_store), .Flag_enable(ins_dec_1_flag_enable), .ALU_op(ins_dec_1_alu_op),
    .Jump(ins_dec_1_jump));
  Multiplexer #(.select(2), .width(4), .disabled(0), .enable("false")) multiplexer_1 (
    .in0(ram_1_data), .in1({rom_1_data_2, rom_1_data}), .in2(alu_1_r), .out(multiplexer_1_out),
    .sel(ins_dec_1_write_data_source));  // open: in3
  Multiplexer #(.width(2), .disabled(0), .enable("false")) multiplexer_2 (
    .in0(ins_dec_1_lod_i__sto_reg), .in1(rom_1_data_2), .out(multiplexer_2_out),
    .sel(ins_dec_1_write_register_source));
  Multiplexer #(.width(2), .disabled(0), .enable("false")) multiplexer_3 (
    .in0(rom_1_data_2), .in1(ins_dec_1_lod_i__sto_reg), .out(multiplexer_3_out),
    .sel(ins_dec_1_a_register_source));
  Reg_file reg_file_1 (
    .Data_in(multiplexer_1_out), .Wreg(multiplexer_2_out), .we(ins_dec_1_write_enable),
    .Areg(multiplexer_3_out), .Breg(rom_1_data), .clk(clk), .res(res), .Aout(out_3), .Bout(out_4));
  ALU alu_1 (.A(out_3), .B(out_4), .in_3(ins_dec_1_alu_op), .Carry(alu_1_carry[0]), .Zero(alu_1_carry[1]), .R(alu_1_r));
  Register #(.width(2)) register_1 (
    .D(alu_1_carry), .en(ins_dec_1_flag_enable), .Q(register_1_q), .clk(clk), .clr(res));
  not not_1 (not_1_out, ins_dec_1_memory_store);
  RAM #(.addrWidth(4), .dataWidth(4), .bus("separate")) ram_1 (
    .addr({rom_1_data_2, rom_1_data}), .din(out_3), .data(ram_1_data), .str(ins_dec_1_memory_store),
    .clk(clk), .ld(not_1_out));  // open: sel, clr

  // Notes on the sheet:
  //   contents of rom_1 (hex, n*v repeats v):
  //   0 11 c1 82
endmodule

module Reg_file (
  input  [3:0] Data_in,
  input  [1:0] Wreg,
  input  we,
  input  [1:0] Areg,
  input  [1:0] Breg,
  input  clk,
  input  res,
  output [3:0] Aout,
  output [3:0] Bout
);

  wire decoder_1_out0, decoder_1_out1, decoder_1_out2, decoder_1_out3;
  wire [3:0] register_1_q, register_2_q, register_3_q, register_4_q;

  Decoder #(.select(2), .disabled(0)) decoder_1 (
    .out0(decoder_1_out0), .out1(decoder_1_out1), .out2(decoder_1_out2), .out3(decoder_1_out3), .sel(Wreg),
    .en(we));
  Register #(.width(4)) register_1 (.D(Data_in), .en(decoder_1_out0), .Q(register_1_q), .clk(clk), .clr(res));
  Register #(.width(4)) register_2 (.D(Data_in), .en(decoder_1_out1), .Q(register_2_q), .clk(clk), .clr(res));
  Register #(.width(4)) register_3 (.D(Data_in), .en(decoder_1_out2), .Q(register_3_q), .clk(clk), .clr(res));
  Register #(.width(4)) register_4 (.D(Data_in), .en(decoder_1_out3), .Q(register_4_q), .clk(clk), .clr(res));
  Multiplexer #(.select(2), .width(4), .disabled(0), .enable("false")) multiplexer_1 (
    .in0(register_1_q), .in1(register_2_q), .in2(register_3_q), .in3(register_4_q), .out(Aout), .sel(Areg));
  Multiplexer #(.select(2), .width(4), .disabled(0), .enable("false")) multiplexer_2 (
    .in0(register_1_q), .in1(register_2_q), .in2(register_3_q), .in3(register_4_q), .out(Bout), .sel(Breg));
endmodule

module ins_dec (
  input  [4:0] Ins,
  input  [1:0] Flags,
  output [1:0] Write_data_source,
  output Write_register_source,
  output [1:0] LOD_I__STO_reg,
  output Write_enable,
  output A_register_source,
  output Memory_store,
  output Flag_enable,
  output [1:0] ALU_op,
  output Jump
);

  wire decoder_1_out0, decoder_1_out1, decoder_1_out2, decoder_1_out3, decoder_1_out4, decoder_1_out5,
       decoder_1_out6, decoder_1_out7, decoder_1_out8, decoder_1_out9, decoder_1_out10, decoder_1_out11,
       decoder_1_out12, decoder_1_out13, decoder_1_out14, decoder_1_out15, decoder_1_out16, or_1_out,
       or_2_out, or_3_out, or_4_out, or_5_out, or_6_out, or_9_out, or_10_out;

  Decoder #(.select(5), .disabled(0), .enable("false")) decoder_1 (
    .out0(decoder_1_out0), .out1(decoder_1_out1), .out2(decoder_1_out2), .out3(decoder_1_out3),
    .out4(decoder_1_out4), .out5(decoder_1_out5), .out6(decoder_1_out6), .out7(decoder_1_out7),
    .out8(decoder_1_out8), .out9(decoder_1_out9), .out10(decoder_1_out10), .out11(decoder_1_out11),
    .out12(decoder_1_out12), .out13(decoder_1_out13), .out14(decoder_1_out14), .out15(decoder_1_out15),
    .out16(decoder_1_out16), .sel(Ins));  // open: out17, out18, out19, out20, out21, out22, out23, out24, out25, out26, out27, out28, out29, out30, out31
  or or_1 (or_1_out, decoder_1_out0, decoder_1_out8, decoder_1_out4);
  or or_2 (or_2_out, decoder_1_out1, decoder_1_out9, decoder_1_out5);
  or or_3 (or_3_out, decoder_1_out2, decoder_1_out10, decoder_1_out6);
  or or_4 (or_4_out, decoder_1_out3, decoder_1_out11, decoder_1_out7);
  or or_5 (or_5_out, decoder_1_out0, decoder_1_out1, decoder_1_out2, decoder_1_out3);
  or or_6 (or_6_out, decoder_1_out4, decoder_1_out5, decoder_1_out6, decoder_1_out7);
  or or_7 (Memory_store, decoder_1_out8, decoder_1_out9, decoder_1_out10, decoder_1_out11);
  or or_8 (A_register_source, decoder_1_out12, decoder_1_out13, decoder_1_out14, decoder_1_out15, decoder_1_out16);
  or or_9 (or_9_out, decoder_1_out12, decoder_1_out13, decoder_1_out14, decoder_1_out15);
  Priority_Encoder #(.select(2)) priority_encoder_1 (
    .in0(or_5_out), .in1(or_6_out), .in2(or_9_out), .out(Write_data_source));  // open: in3, gs, en_out, en_in
  Priority_Encoder #(.select(2)) priority_encoder_2 (
    .in0(or_1_out), .in1(or_2_out), .in2(or_3_out), .in3(or_4_out), .out(LOD_I__STO_reg));  // open: gs, en_out, en_in
  Priority_Encoder #(.select(2)) priority_encoder_3 (
    .in0(decoder_1_out12), .in1(decoder_1_out13), .in2(decoder_1_out14), .in3(or_10_out), .out(ALU_op));  // open: gs, en_out, en_in
  or or_10 (or_10_out, decoder_1_out15, decoder_1_out16);
  Pull_Resistor pull_resistor_1 (.node(LOD_I__STO_reg));
  Pull_Resistor pull_resistor_2 (.node(Write_data_source));
  or or_11 (Write_enable, or_5_out, or_9_out, or_6_out);
  Pull_Resistor pull_resistor_3 (.node(ALU_op));

  assign Flag_enable = A_register_source;
  assign Write_register_source = A_register_source;
endmodule

module ALU (
  input  [3:0] A,
  input  [3:0] B,
  input  [1:0] in_3,
  output Carry,
  output Zero,
  output [3:0] R
);

  wire adder_1_cout, multiplexer_1_out, subtractor_1_bout;
  wire [3:0] adder_1_out, and_1_out, or_1_out, subtractor_1_out;

  Adder #(.width(4)) adder_1 (.a(A), .b(B), .out(adder_1_out), .cout(adder_1_cout));  // open: cin
  Subtractor #(.width(4)) subtractor_1 (.a(A), .b(B), .out(subtractor_1_out), .bout(subtractor_1_bout));  // open: bin
  assign and_1_out = A & B;  // AND_Gate and_1, 4 bits wide
  assign or_1_out = A | B;  // OR_Gate or_1, 4 bits wide
  Multiplexer #(.disabled(0), .enable("false")) multiplexer_1 (
    .in0(adder_1_cout), .in1(subtractor_1_bout), .out(multiplexer_1_out), .sel(in_3[0]));
  Multiplexer #(.disabled(0), .enable("false")) multiplexer_2 (
    .in0(multiplexer_1_out), .in1(1'b0), .out(Carry), .sel(in_3[1]));
  Multiplexer #(.select(2), .width(4), .disabled(0), .enable("false")) multiplexer_3 (
    .in0(adder_1_out), .in1(subtractor_1_out), .in2(and_1_out), .in3(or_1_out), .out(R), .sel(in_3));
  nor nor_1 (Zero, R[0], R[1], R[2], R[3]);
endmodule
