// Logisim project cpu.circ as structural Verilog: 6 circuits, main circuit main
module main (
);

  wire clock_1_out, cpu_1_ld, cpu_1_phase, cpu_1_str, rst_out;
  wire [3:0] cpu_1_addr;
  wire [7:0] cpu_1_a, cpu_1_b, cpu_1_din, ram_1_data;

  Button rst (.out(rst_out));
  Clock clock_1 (.out(clock_1_out));
  RAM #(.addrWidth(4), .bus("separate")) ram_1 (
    .addr(cpu_1_addr), .din(cpu_1_din), .data(ram_1_data), .str(cpu_1_str), .clk(cpu_1_str), .ld(cpu_1_ld));  // open: sel, clr
  cpu cpu_1 (
    .din(cpu_1_din), .addr(cpu_1_addr), .dout(ram_1_data), .ld(cpu_1_ld), .str(cpu_1_str), .rst(rst_out),
    .clk(clock_1_out), .phase(cpu_1_phase), .a(cpu_1_a), .b(cpu_1_b));
  // Probe on cpu_1_phase
  // Probe on cpu_1_a
  // Probe on cpu_1_b
endmodule

module decoder (
  input  [3:0] opcode,
  input  en,
  output loada,
  output loadb,
  output str,
  output add,
  output sub,
  output jmp,
  output jn,
  output hlt
);

  wire [3:0] controlled_buffer_1_out;

  assign controlled_buffer_1_out = en ? opcode : 4'bz;  // Controlled_Buffer controlled_buffer_1
  Comparator #(.width(4)) comparator_1 (.a(controlled_buffer_1_out), .b(4'b0000), .eq(loada));  // open: gt, lt
  Comparator #(.width(4)) comparator_2 (.a(controlled_buffer_1_out), .b(4'b0001), .eq(loadb));  // open: gt, lt
  Comparator #(.width(4)) comparator_3 (.a(controlled_buffer_1_out), .b(4'b0010), .eq(str));  // open: gt, lt
  Comparator #(.width(4)) comparator_4 (.a(controlled_buffer_1_out), .b(4'b0011), .eq(add));  // open: gt, lt
  Comparator #(.width(4)) comparator_5 (.a(controlled_buffer_1_out), .b(4'b0100), .eq(sub));  // open: gt, lt
  Comparator #(.width(4)) comparator_6 (.a(controlled_buffer_1_out), .b(4'b0101), .eq(jmp));  // open: gt, lt
  Comparator #(.width(4)) comparator_7 (.a(controlled_buffer_1_out), .b(4'b0110), .eq(jn));  // open: gt, lt
  Comparator #(.width(4)) comparator_8 (.a(controlled_buffer_1_out), .b(4'b0111), .eq(hlt));  // open: gt, lt
endmodule

module cu (
  input  [7:0] ALU_out,
  input  [7:0] Data,
  input  clk,
  input  rst,
  input  zero,
  input  overflow,
  input  neg,
  output [7:0] A_data_in,
  output [3:0] Address,
  output ALU_op,
  output aen,
  output ben,
  output ld,
  output clk_2,
  output str,
  output phase
);

  wire and_1_out, and_3_out, and_4_out, d_ff_3_q, decoder_1_out0, decoder_1_out1, decoder_2_add,
       decoder_2_hlt, decoder_2_jmp, decoder_2_jn, decoder_2_loada, decoder_2_loadb, or_3_out, or_4_out;
  wire [3:0] counter_2_q, register_1_q;
  wire [7:4] register_1_q_2;

  or or_1 (aen, and_1_out, decoder_2_add);
  and and_1 (and_1_out, decoder_2_loada, decoder_1_out1);
  and and_2 (ben, decoder_2_loadb, decoder_1_out1);
  D_Flip_Flop d_ff_1 (.clk(decoder_1_out1), .D(zero));  // open: Q, Qn, preset, en, reset
  D_Flip_Flop d_ff_2 (.clk(decoder_1_out1), .D(overflow));  // open: Q, Qn, preset, en, reset
  D_Flip_Flop d_ff_3 (.clk(decoder_1_out1), .D(neg), .Q(d_ff_3_q));  // open: Qn, preset, en, reset
  Counter #(.width(1), .max('h1)) counter_1 (.Q(phase), .clk(clk_2));  // open: load, D, count, carry, clr
  Decoder #(.disabled(0), .enable("false")) decoder_1 (.out0(decoder_1_out0), .out1(decoder_1_out1), .sel(phase));
  and and_3 (and_3_out, decoder_1_out1, ~or_3_out);  // AND_Gate
  Counter #(.width(4), .max('hf)) counter_2 (
    .load(or_3_out), .D(Address), .count(and_3_out), .Q(counter_2_q), .clk(clk_2), .clr(rst));  // open: carry
  Multiplexer #(.width(4), .disabled(0), .enable("false")) multiplexer_1 (
    .in0(counter_2_q), .in1(register_1_q), .out(Address), .sel(decoder_1_out1));
  Multiplexer #(.width(8), .disabled(0), .enable("false")) multiplexer_2 (
    .in0(Data), .in1(ALU_out), .out(A_data_in), .sel(or_4_out));
  or or_2 (ld, decoder_2_loada, decoder_2_loadb, decoder_1_out0);
  Register register_1 (.D(Data), .en(decoder_1_out0), .Q({register_1_q_2, register_1_q}), .clk(clk_2), .clr(rst));
  decoder decoder_2 (
    .opcode(register_1_q_2), .en(decoder_1_out1), .loada(decoder_2_loada), .loadb(decoder_2_loadb),
    .str(str), .add(decoder_2_add), .sub(ALU_op), .jmp(decoder_2_jmp), .jn(decoder_2_jn), .hlt(decoder_2_hlt));
  or or_3 (or_3_out, decoder_2_jmp, and_4_out);
  and and_4 (and_4_out, decoder_2_jn, d_ff_3_q);
  or or_4 (or_4_out, decoder_2_add, ALU_op);
  Pull_Resistor pull_resistor_1 (.node(decoder_2_loadb));
  Pull_Resistor pull_resistor_2 (.node(str));
  Pull_Resistor pull_resistor_3 (.node(decoder_2_loada));
  Pull_Resistor pull_resistor_4 (.node(decoder_2_jn));
  Pull_Resistor pull_resistor_5 (.node(ALU_op));
  Pull_Resistor pull_resistor_6 (.node(decoder_2_add));
  Pull_Resistor pull_resistor_7 (.node(decoder_2_jmp));
  Pull_Resistor pull_resistor_8 (.node(decoder_2_hlt));
  and and_5 (clk_2, clk, ~decoder_2_hlt);  // AND_Gate
endmodule

module cpu (
  input  [7:0] dout,
  input  rst,
  input  clk,
  output [7:0] din,
  output [3:0] addr,
  output ld,
  output str,
  output phase,
  output [7:0] a,
  output [7:0] b
);

  wire alu_1_neg, alu_1_overflow, alu_1_zero, cu_1_aen, cu_1_alu_op, cu_1_ben, cu_1_clk_2;
  wire [7:0] alu_1_r, cu_1_a_data_in;

  Register register_1 (.D(cu_1_a_data_in), .en(cu_1_aen), .Q(a), .clk(cu_1_clk_2), .clr(rst));
  alu alu_1 (
    .A(a), .B(b), .Op(cu_1_alu_op), .R(alu_1_r), .zero(alu_1_zero), .overflow(alu_1_overflow), .neg(alu_1_neg));
  Register register_2 (.D(dout), .en(cu_1_ben), .Q(b), .clk(cu_1_clk_2), .clr(rst));
  cu cu_1 (
    .ALU_out(alu_1_r), .Address(addr), .rst(rst), .A_data_in(cu_1_a_data_in), .Data(dout), .ld(ld),
    .str(str), .aen(cu_1_aen), .ben(cu_1_ben), .clk(clk), .phase(phase), .ALU_op(cu_1_alu_op),
    .zero(alu_1_zero), .clk_2(cu_1_clk_2), .overflow(alu_1_overflow), .neg(alu_1_neg));

  assign din = a;
endmodule

module alu (
  input  [7:0] A,
  input  [7:0] B,
  input  Op,
  output [7:0] R,
  output zero,
  output overflow,
  output neg
);

  wire [7:0] adder_1_out, subtractor_1_out;

  Adder adder_1 (.a(A), .b(B), .out(adder_1_out), .cout(overflow));  // open: cin
  Subtractor subtractor_1 (.a(A), .b(B), .out(subtractor_1_out));  // open: bin, bout
  Multiplexer #(.width(8), .disabled(0), .enable("false")) multiplexer_1 (
    .in0(adder_1_out), .in1(subtractor_1_out), .out({neg, R[6:0]}), .sel(Op));
  zero zero_1 (.in_1({neg, R[6:0]}), .zero(zero));

  assign R[7] = neg;
endmodule

module zero (
  input  [7:0] in_1,
  output zero
);

  nor nor_1 (zero, in_1[0], in_1[1], in_1[2], in_1[3], in_1[4], in_1[5], in_1[6], in_1[7]);
endmodule
