// Logisim project cpu.circ as structural Verilog: 2 circuits, main circuit main
module main (
);

  wire adder_1_cout, and_1_out, and_2_out, and_3_out, and_4_out, and_5_out, and_6_out, button_1_out,
       clock_1_out, decoder_1_out0, decoder_1_out1, decoder_1_out2, decoder_1_out3, decoder_1_out4,
       decoder_1_out5, decoder_1_out6, decoder_1_out7, decoder_1_out8, decoder_1_out9, decoder_1_out10,
       decoder_1_out11, decoder_1_out12, not_1_out, not_2_out, not_3_out, or_1_out, or_2_out, or_3_out,
       or_4_out, or_5_out, or_6_out, or_7_out, or_8_out, subtractor_1_bout;
  wire [1:0] multiplexer_2_out, register_3_q;
  wire [3:0] adder_1_out, counter_1_q, multiplexer_1_out, multiplexer_3_out, ram_1_data, ram_1_data_2,
       ram_2_data, register_1_q, register_2_q, register_4_q, subtractor_1_out;

  Button button_1 (.out(button_1_out));
  Counter #(.width(4), .max('hf)) counter_1 (
    .load(or_8_out), .D(ram_1_data), .count(not_1_out), .Q(counter_1_q), .clk(and_2_out), .clr(and_1_out));  // open: carry
  not not_1 (not_1_out, or_8_out);
  and and_1 (and_1_out, or_1_out, ~decoder_1_out12);  // AND_Gate
  Clock clock_1 (.out(clock_1_out));
  and and_2 (and_2_out, clock_1_out, ~or_1_out);  // AND_Gate
  or or_1 (or_1_out, button_1_out, decoder_1_out12);
  not not_2 (not_2_out, 1'b0);
  Decoder #(.select(4), .disabled(0), .enable("false")) decoder_1 (
    .out0(decoder_1_out0), .out1(decoder_1_out1), .out2(decoder_1_out2), .out3(decoder_1_out3),
    .out4(decoder_1_out4), .out5(decoder_1_out5), .out6(decoder_1_out6), .out7(decoder_1_out7),
    .out8(decoder_1_out8), .out9(decoder_1_out9), .out10(decoder_1_out10), .out11(decoder_1_out11),
    .out12(decoder_1_out12), .sel(ram_1_data_2));  // open: out13, out14, out15
  RAM #(.addrWidth(4), .bus("separate")) ram_1 (
    .addr(counter_1_q), .din({8{1'b0}}), .data({ram_1_data_2, ram_1_data}), .str(1'b0), .clk(and_2_out),
    .ld(not_2_out));  // open: sel, clr
  and and_3 (and_3_out, decoder_1_out8, register_3_q[0]);
  and and_4 (and_4_out, decoder_1_out9, ~register_3_q[0]);  // AND_Gate
  and and_5 (and_5_out, decoder_1_out10, register_3_q[1]);
  and and_6 (and_6_out, decoder_1_out11, ~register_3_q[1]);  // AND_Gate
  not not_3 (not_3_out, decoder_1_out6);
  or or_2 (or_2_out, decoder_1_out0, decoder_1_out2);
  or or_3 (or_3_out, decoder_1_out1, decoder_1_out3);
  or or_4 (or_4_out, decoder_1_out2, decoder_1_out3);
  or or_5 (or_5_out, decoder_1_out4, decoder_1_out5);
  RAM #(.addrWidth(4), .dataWidth(4), .bus("separate")) ram_2 (
    .addr(ram_1_data), .din(register_4_q), .data(ram_2_data), .str(decoder_1_out6), .clk(and_2_out),
    .ld(not_3_out));  // open: sel, clr
  or or_6 (or_6_out, and_3_out, and_4_out);
  or or_7 (or_7_out, and_5_out, and_6_out);
  Multiplexer #(.width(4), .disabled(0), .enable("false")) multiplexer_1 (
    .in0(ram_2_data), .in1(ram_1_data), .out(multiplexer_1_out), .sel(or_4_out));
  or or_8 (or_8_out, or_6_out, or_7_out, decoder_1_out7);
  Register #(.width(4)) register_1 (
    .D(multiplexer_1_out), .en(or_2_out), .Q(register_1_q), .clk(and_2_out), .clr(or_1_out));
  Register #(.width(4)) register_2 (
    .D(multiplexer_1_out), .en(or_3_out), .Q(register_2_q), .clk(and_2_out), .clr(or_1_out));
  Multiplexer #(.disabled(0), .enable("false")) multiplexer_2 (
    .in0(adder_1_cout), .in1(subtractor_1_bout), .out(multiplexer_2_out[0]), .sel(decoder_1_out5));
  Register #(.width(2)) register_3 (
    .D(multiplexer_2_out), .en(or_5_out), .Q(register_3_q), .clk(and_2_out), .clr(or_1_out));
  Adder #(.width(4)) adder_1 (.a(register_1_q), .b(register_2_q), .out(adder_1_out), .cout(adder_1_cout));  // open: cin
  Multiplexer #(.width(4), .disabled(0), .enable("false")) multiplexer_3 (
    .in0(adder_1_out), .in1(subtractor_1_out), .out(multiplexer_3_out), .sel(decoder_1_out5));
  Subtractor #(.width(4)) subtractor_1 (
    .a(register_1_q), .b(register_2_q), .out(subtractor_1_out), .bout(subtractor_1_bout));  // open: bin
  zero zero_1 (.in(multiplexer_3_out), .zero(multiplexer_2_out[1]));
  Register #(.width(4)) register_4 (
    .D(multiplexer_3_out), .en(or_5_out), .Q(register_4_q), .clk(and_2_out), .clr(or_1_out));
endmodule

// Z
module zero (
  input  [3:0] in,
  output zero
);

  nor nor_1 (zero, in[0], in[1], in[2], in[3]);
endmodule
