// Logisim project cpu67.circ as structural Verilog: 2 circuits, main circuit main
module main (
  input  [15:0] Addr,
  input  [7:0] Data,
  input  Write,
  input  Takeover,
  input  [15:0] Addr_2,
  input  [7:0] Data_2,
  input  Write_2,
  input  Takeover_2
);

  wire and_1_out, and_2_out, button_1_out, clock_1_out, comparator_1_eq, comparator_2_eq, comparator_3_eq,
       comparator_4_eq, comparator_5_eq, multiplexer_4_out, not_1_out, not_2_out, or_1_out, or_2_out;
  wire [7:0] adder_1_out, inverter_1_out, multiplexer_3_out, multiplexer_5_out, pull_resistor_1_node,
       ram_1_data, register_1_q;
  wire [15:0] counter_1_q, multiplexer_1_out, multiplexer_2_out;

  and and_1 (and_1_out, clock_1_out, ~or_1_out);  // AND_Gate
  Clock clock_1 (.out(clock_1_out));
  Button button_1 (.out(button_1_out));
  // Probe on ram_1_data
  // Probe on pull_resistor_1_node
  and and_2 (and_2_out, and_1_out, ~Takeover_2);  // AND_Gate
  or or_1 (or_1_out, button_1_out, comparator_5_eq);
  Counter #(.width(16), .max('hffff)) counter_1 (
    .Q(counter_1_q), .clk(and_2_out), .clr(button_1_out));  // open: load, D, count, carry
  Multiplexer #(.width(16), .disabled(0), .enable("false")) multiplexer_1 (
    .in0(counter_1_q), .in1(Addr), .out(multiplexer_1_out), .sel(Takeover));
  Multiplexer #(.width(16), .disabled(0), .enable("false")) multiplexer_2 (
    .in0(counter_1_q), .in1(Addr_2), .out(multiplexer_2_out), .sel(Takeover_2));
  Multiplexer #(.width(8), .disabled(0), .enable("false")) multiplexer_3 (
    .in0(register_1_q), .in1(Data_2), .out(multiplexer_3_out), .sel(Takeover_2));
  Multiplexer #(.disabled(0), .enable("false")) multiplexer_4 (
    .in0(comparator_2_eq), .in1(Write_2), .out(multiplexer_4_out), .sel(Takeover_2));
  not not_1 (not_1_out, Write);
  not not_2 (not_2_out, multiplexer_4_out);
  RAM #(.addrWidth(16), .bus("separate")) ram_1 (
    .addr(multiplexer_1_out), .din(Data), .data(ram_1_data), .str(Write), .ld(not_1_out));  // open: sel, clk, clr
  Pull_Resistor pull_resistor_1 (.node(pull_resistor_1_node));
  RAM #(.addrWidth(16), .bus("separate")) ram_2 (
    .addr(multiplexer_2_out), .din(multiplexer_3_out), .data(pull_resistor_1_node), .str(multiplexer_4_out),
    .clk(and_1_out), .ld(not_2_out));  // open: sel, clr
  Inverter inverter_1 (.In(pull_resistor_1_node), .Invert(ram_1_data[0]), .Out(inverter_1_out));
  Comparator comparator_1 (.a(ram_1_data), .b(8'h10), .eq(comparator_1_eq));  // open: gt, lt
  Comparator comparator_2 (.a(ram_1_data), .b(8'h11), .eq(comparator_2_eq));  // open: gt, lt
  Comparator comparator_3 (.a(ram_1_data), .b(8'h20), .eq(comparator_3_eq));  // open: gt, lt
  Comparator comparator_4 (.a(ram_1_data), .b(8'h21), .eq(comparator_4_eq));  // open: gt, lt
  Comparator comparator_5 (.a(ram_1_data), .b({8{1'b1}}), .eq(comparator_5_eq));  // open: gt, lt
  Adder adder_1 (.a(inverter_1_out), .b(register_1_q), .out(adder_1_out));  // open: cin, cout
  Multiplexer #(.width(8), .disabled(0), .enable("false")) multiplexer_5 (
    .in0(adder_1_out), .in1(pull_resistor_1_node), .out(multiplexer_5_out), .sel(comparator_1_eq));
  Register register_1 (.D(multiplexer_5_out), .en(or_2_out), .Q(register_1_q), .clk(and_2_out), .clr(or_1_out));
  or or_2 (or_2_out, comparator_1_eq, comparator_3_eq, comparator_4_eq);
endmodule

module Inverter (
  input  [7:0] In,
  input  Invert,
  output [7:0] Out
);

  xor xor_1 (Out[0], In[0], Invert);
  xor xor_2 (Out[1], In[1], Invert);
  xor xor_3 (Out[2], In[2], Invert);
  xor xor_4 (Out[3], In[3], Invert);
  xor xor_5 (Out[4], In[4], Invert);
  xor xor_6 (Out[5], In[5], Invert);
  xor xor_7 (Out[6], In[6], Invert);
  xor xor_8 (Out[7], In[7], Invert);
endmodule
