// Logisim project cpu87.circ as structural Verilog: 2 circuits, main circuit main
module main (
);

  ROM_RAM rom_ram_1 ();  // open: addr, str, out_3
endmodule

module ROM_RAM (
  input  [15:0] addr,
  input  str,
  output out_3
);

  wire clock_1_out, decoder_1_out0, decoder_1_out1, decoder_1_out2, not_1_out, not_2_out;
  wire [7:0] undriven;
  wire [15:0] rom_1_data;

  Clock clock_1 (.out(clock_1_out));
  Decoder #(.select(4), .disabled(0), .enable("false")) decoder_1 (
    .out0(decoder_1_out0), .out1(decoder_1_out1), .out2(decoder_1_out2), .sel(addr[15:12]));  // open: out3, out4, out5, out6, out7, out8, out9, out10, out11, out12, out13, out14, out15
  not not_1 (not_1_out, str);
  not not_2 (not_2_out, str);
  ROM #(.addrWidth(12), .dataWidth(16)) rom_1 (.addr(addr[11:0]), .data(rom_1_data), .sel(decoder_1_out0));
  RAM #(.addrWidth(12), .bus("separate")) ram_1 (
    .addr(addr[11:0]), .din(undriven), .data(rom_1_data[7:0]), .str(str), .sel(decoder_1_out1),
    .clk(clock_1_out), .ld(not_1_out));  // open: clr
  RAM #(.addrWidth(12), .bus("separate")) ram_2 (
    .addr(addr[11:0]), .din(undriven), .data(rom_1_data[7:0]), .str(str), .sel(decoder_1_out2),
    .clk(clock_1_out), .ld(not_2_out));  // open: clr
  // Pins of 8 and 16 bits meet at rom_1_data
endmodule
