// Digital circuit ALU.dig as structural Verilog
module ALU (
  input  AO,
  input  [7:0] B,
  input  [7:0] A,
  output [7:0] R
);

  wire [7:0] add_1_s, sub_1_s;

  Add #(.Bits(8)) add_1 (.a(A), .b(B), .c_i(1'b0), .s(add_1_s));  // open: c_o
  Sub #(.Bits(8)) sub_1 (.a(A), .b(B), .c_i(1'b0), .s(sub_1_s));  // open: c_o
  Multiplexer #(.Bits(8)) multiplexer_1 (.sel(AO), .in_0(add_1_s), .in_1(sub_1_s), .out(R));
endmodule
