// Digital circuit CPU.dig as structural Verilog
module CPU (
  input  clk
);

  wire and_1_out, button_1_out, control_1_ao, control_1_halt, control_1_lar, control_1_lb, control_1_lir,
       control_1_lmar, control_1_lo, control_1_pa, control_1_par, control_1_pcc, control_1_pira,
       control_1_pm, control_1_ppca;
  wire [3:0] counter_1_out, driver_1_out, register_1_q, register_1_q_2, register_2_q;
  wire [7:0] alu_1_r, Out_q, register_3_q, register_4_q, rom_1_d;
  wire [7:4] driver_1_out_2;

  and and_1 (and_1_out, clk, ~control_1_halt);  // And
  Button button_1 (.out(button_1_out));
  Register #(.Bits(8)) register_1 (
    .D({driver_1_out_2, driver_1_out}), .C(and_1_out), .en(control_1_lir), .Q({register_1_q_2, register_1_q}));
  // Probe PC on counter_1_out
  Counter #(.Bits(4)) counter_1 (.en(control_1_pcc), .C(button_1_out), .out(counter_1_out));  // open: clr, ovf
  ROM #(.isProgramMemory("true"), .Bits(8), .Addr_Bits(4)) rom_1 (.A(register_2_q), .sel(1'b1), .D(rom_1_d));
  // Probe Bus on {driver_1_out_2, driver_1_out}
  Register #(.Bits(4)) register_2 (.D(driver_1_out), .C(and_1_out), .en(control_1_lmar), .Q(register_2_q));
  assign {driver_1_out_2, driver_1_out} = control_1_pira ? {4'b0000, register_1_q} : 8'bz;  // Driver driver_1
  Control control_1 (
    .clr(button_1_out), .C(and_1_out), .op(register_1_q_2), .LO(control_1_lo), .PA(control_1_pa),
    .AO(control_1_ao), .LB(control_1_lb), .PAR(control_1_par), .LAR(control_1_lar), .PIRA(control_1_pira),
    .LIR(control_1_lir), .PM(control_1_pm), .LMAR(control_1_lmar), .PPCA(control_1_ppca),
    .PCC(control_1_pcc), .HALT(control_1_halt));
  // Probe A on register_3_q
  // Probe B on register_4_q
  assign {driver_1_out_2, driver_1_out} = control_1_ppca ? {4'b0000, counter_1_out} : 8'bz;  // Driver driver_2
  assign {driver_1_out_2, driver_1_out} = control_1_pm ? rom_1_d : 8'bz;  // Driver driver_3
  PullDown #(.Bits(8)) pulldown_1 (.out({driver_1_out_2, driver_1_out}));
  // Probe MAR on register_2_q
  Register #(.Bits(8)) register_3 (
    .D({driver_1_out_2, driver_1_out}), .C(and_1_out), .en(control_1_lar), .Q(register_3_q));
  Register #(.Bits(8)) register_4 (
    .D({driver_1_out_2, driver_1_out}), .C(and_1_out), .en(control_1_lb), .Q(register_4_q));
  ALU alu_1 (.AO(control_1_ao), .B(register_4_q), .A(register_3_q), .R(alu_1_r));
  assign {driver_1_out_2, driver_1_out} = control_1_pa ? alu_1_r : 8'bz;  // Driver driver_4
  // Probe IR on {register_1_q_2, register_1_q}
  assign {driver_1_out_2, driver_1_out} = control_1_par ? register_3_q : 8'bz;  // Driver driver_5
  Register #(.Bits(8)) Out (.D({driver_1_out_2, driver_1_out}), .C(and_1_out), .en(control_1_lo), .Q(Out_q));
  // Probe ROM out on rom_1_d
  Seven_Seg_Hex seven_seg_hex_1 (.d(Out_q[7:4]), .dp(1'b0));
  Seven_Seg_Hex seven_seg_hex_2 (.d(Out_q[3:0]), .dp(1'b0));

  // Notes on the sheet:
  //   clk: Hz: 500000
  //   contents of rom_1 (hex, n*v repeats v):
  //   5,16,27,30,40,b,1
endmodule
