// Digital circuit Control.dig as structural Verilog
module Control (
  input  clr,
  input  C,
  input  [3:0] op,
  output LO,
  output PA,
  output AO,
  output LB,
  output PAR,
  output LAR,
  output PIRA,
  output LIR,
  output PM,
  output LMAR,
  output PPCA,
  output PCC,
  output HALT
);

  wire comparator_1_eq, decoder_1_out_0, decoder_1_out_1, decoder_2_out_0, decoder_2_out_1, decoder_2_out_2,
       decoder_2_out_3, driver_1_out, driver_2_out, driver_3_out, driver_4_out, or_1_out, t_ff_1_q;
  wire [1:0] counter_1_out;

  T_FF t_ff_1 (.T(or_1_out), .Q(t_ff_1_q));  // open: C, nQ
  Decoder decoder_1 (.sel(t_ff_1_q), .out_0(decoder_1_out_0), .out_1(decoder_1_out_1));
  or or_1 (or_1_out, clr, comparator_1_eq);
  Comparator #(.Bits(2)) comparator_1 (.a(counter_1_out), .b(2'b11), .eq(comparator_1_eq));  // open: gt, lt
  Decoder #(.Selector_Bits(3)) decoder_2 (
    .sel(op[2:0]), .out_0(decoder_2_out_0), .out_1(decoder_2_out_1), .out_2(decoder_2_out_2),
    .out_3(decoder_2_out_3), .out_4(HALT));  // open: out_5, out_6, out_7
  Counter #(.Bits(2)) counter_1 (.en(C), .C(or_1_out), .out(counter_1_out));  // open: clr, ovf
  assign driver_1_out = decoder_1_out_1 ? decoder_2_out_0 : 1'bz;  // Driver driver_1
  assign driver_2_out = decoder_1_out_1 ? decoder_2_out_1 : 1'bz;  // Driver driver_2
  assign driver_3_out = decoder_1_out_1 ? decoder_2_out_2 : 1'bz;  // Driver driver_3
  assign driver_4_out = decoder_1_out_1 ? decoder_2_out_3 : 1'bz;  // Driver driver_4
  ROM #(.Bits(12)) rom_1 (
    .A(counter_1_out), .sel(decoder_1_out_0), .D({PCC, PPCA, LMAR, PM, LIR, PIRA, LAR, PAR, AO, PA, LB, LO}));
  ROM #(.Bits(12)) rom_2 (
    .A(counter_1_out), .sel(driver_1_out), .D({PCC, PPCA, LMAR, PM, LIR, PIRA, LAR, PAR, AO, PA, LB, LO}));
  ROM #(.Bits(12)) rom_3 (
    .A(counter_1_out), .sel(driver_2_out), .D({PCC, PPCA, LMAR, PM, LIR, PIRA, LAR, PAR, AO, PA, LB, LO}));
  ROM #(.Bits(12)) rom_4 (
    .A(counter_1_out), .sel(driver_3_out), .D({PCC, PPCA, LMAR, PM, LIR, PIRA, LAR, PAR, AO, PA, LB, LO}));
  ROM #(.Bits(12)) rom_5 (
    .A(counter_1_out), .sel(driver_4_out), .D({PCC, PPCA, LMAR, PM, LIR, PIRA, LAR, PAR, AO, PA, LB, LO}));
  PullDown #(.Bits(12)) pulldown_1 (.out({PCC, PPCA, LMAR, PM, LIR, PIRA, LAR, PAR, AO, PA, LB, LO}));

  // Notes on the sheet:
  //   contents of rom_1 (hex, n*v repeats v):
  //   600,800,180
  //   contents of rom_2 (hex, n*v repeats v):
  //   240,120
  //   contents of rom_3 (hex, n*v repeats v):
  //   240,102,24
  //   contents of rom_4 (hex, n*v repeats v):
  //   240,102,2c
  //   contents of rom_5 (hex, n*v repeats v):
  //   11
endmodule
