// Digital circuit main.dig as structural Verilog
module main (
);

  wire not_1_out, undriven;

  RAMDualPort #(.Bits(32), .Addr_Bits(32)) ramdualport_1 (.str(not_1_out), .ld(undriven));  // open: A, Din, C, D
  cpu cpu_1 ();  // open: clk
  not not_1 (not_1_out, undriven);
endmodule
