// Digital circuit elevator controller.dig as structural Verilog
module elevator_controller (
  input  clk
);

  wire _1, _2, _3, and_1_out, button_1_out, C1_b, C2_b, C3_b, CG_b, comparator_1_eq, D, D1_b, D2_b, D3_b,
       diodeforward_1_out, diodeforward_2_out, diodeforward_9_out, diodeforward_10_out, diodeforward_11_out,
       diodeforward_12_out, G, nor_1_out, not_1_out, or_1_out, or_2_out, or_3_out, or_4_out, or_5_out,
       or_6_out, relay_1_p4, relay_2_p4, relay_3_p3, relay_6_p4, relay_7_p1, rs_ff_1_q, U, U1_b, U2_b, UG_b;
  wire [1:0] floor_sel_1_f;

  Button button_1 (.out(button_1_out));
  or or_1 (or_1_out, U, D);
  not not_1 (not_1_out, or_1_out);
  Comparator #(.Bits(2)) comparator_1 (.a(floor_sel_1_f), .b(2'b00), .eq(comparator_1_eq));  // open: gt, lt
  Seven_Seg_Hex seven_seg_hex_1 (.d({2'b00, floor_sel_1_f}), .dp(1'b0));
  and and_1 (and_1_out, button_1_out, or_1_out);
  RS_FF rs_ff_1 (.S(not_1_out), .C(clk), .R(comparator_1_eq), .Q(rs_ff_1_q));  // open: nQ
  floor_sel floor_sel_1 (.M(and_1_out), .D(D), .F(floor_sel_1_f));
  Decoder #(.Selector_Bits(2)) decoder_1 (.sel(floor_sel_1_f), .out_0(G), .out_1(_1), .out_2(_2), .out_3(_3));
  or or_2 (or_2_out, D, or_3_out, nor_1_out);
  or or_3 (or_3_out, D1_b, D2_b, D3_b);
  or or_4 (or_4_out, UG_b, U1_b, U2_b);
  or or_5 (or_5_out, U, or_4_out, nor_1_out);
  // Relay #(.relayNormallyClosed("true")) relay_1: pin names not known; wires that end beside it: or_3_out, or_5_out, 1'b0, relay_1_p4
  // Relay #(.relayNormallyClosed("true")) relay_2: pin names not known; wires that end beside it: or_4_out, or_2_out, 1'b0, relay_2_p4
  Switch U2 (.A(relay_1_p4), .B(U2_b));
  Switch U1 (.A(relay_1_p4), .B(U1_b));
  Switch UG (.A(relay_1_p4), .B(UG_b));
  Switch D3 (.A(relay_2_p4), .B(D3_b));
  Switch D2 (.A(relay_2_p4), .B(D2_b));
  DiodeForward diodeforward_1 (.in(U2_b), .out(diodeforward_1_out));
  Switch D1 (.A(relay_2_p4), .B(D1_b));
  DiodeForward diodeforward_2 (.in(U1_b), .out(diodeforward_2_out));
  Switch C3 (.A(1'b1), .B(C3_b));
  DiodeForward diodeforward_3 (.in(D3_b), .out(C3_b));
  Switch C2 (.A(1'b1), .B(C2_b));
  DiodeForward diodeforward_4 (.in(D2_b), .out(diodeforward_1_out));
  DiodeForward diodeforward_5 (.in(diodeforward_1_out), .out(C2_b));
  PullDown pulldown_1 (.out(diodeforward_1_out));
  Switch C1 (.A(1'b1), .B(C1_b));
  DiodeForward diodeforward_6 (.in(D1_b), .out(diodeforward_2_out));
  DiodeForward diodeforward_7 (.in(diodeforward_2_out), .out(C1_b));
  PullDown pulldown_2 (.out(diodeforward_2_out));
  Switch CG (.A(1'b1), .B(CG_b));
  DiodeForward diodeforward_8 (.in(UG_b), .out(CG_b));
  DiodeForward diodeforward_9 (.in(C3_b), .out(diodeforward_9_out));
  PullDown pulldown_3 (.out(C3_b));
  DiodeForward diodeforward_10 (.in(C2_b), .out(diodeforward_10_out));
  PullDown pulldown_4 (.out(C2_b));
  DiodeForward diodeforward_11 (.in(C1_b), .out(diodeforward_11_out));
  PullDown pulldown_5 (.out(C1_b));
  DiodeForward diodeforward_12 (.in(CG_b), .out(diodeforward_12_out));
  PullDown pulldown_6 (.out(CG_b));
  PullDown pulldown_7 (.out(diodeforward_9_out));
  PullDown pulldown_8 (.out(diodeforward_10_out));
  PullDown pulldown_9 (.out(diodeforward_11_out));
  PullDown pulldown_10 (.out(diodeforward_12_out));
  // Relay #(.relayNormallyClosed("true")) relay_3: pin names not known; wires that end beside it: _3, 1'b0, relay_3_p3, diodeforward_9_out
  // Relay #(.relayNormallyClosed("true")) relay_4: pin names not known; wires that end beside it: _2, 1'b0, diodeforward_9_out, diodeforward_10_out
  // Relay #(.relayNormallyClosed("true")) relay_5: pin names not known; wires that end beside it: _1, 1'b0, diodeforward_10_out, diodeforward_11_out
  // Relay #(.relayNormallyClosed("true")) relay_6: pin names not known; wires that end beside it: G, 1'b0, diodeforward_11_out, relay_6_p4
  nor nor_1 (nor_1_out, relay_3_p3, D);
  or or_6 (or_6_out, diodeforward_12_out, relay_6_p4, rs_ff_1_q);
  // Relay #(.relayNormallyClosed("true")) relay_7: pin names not known; wires that end beside it: relay_7_p1, relay_3_p3, relay_7_p1, 1'b0, U, 1'b0
  // Relay #(.relayNormallyClosed("true")) relay_8: pin names not known; wires that end beside it: or_6_out, D
  // Relay relay_9: pin names not known; wires that end beside it: relay_7_p1, 1'b0
  // Relay relay_10: pin names not known; wires that end beside it: C3_b, relay_7_p1, _3, 1'b0
  // Relay relay_11: pin names not known; wires that end beside it: C2_b, relay_7_p1, _2, 1'b0
  // Relay relay_12: pin names not known; wires that end beside it: C1_b, relay_7_p1, CG_b, _1, 1'b0, G

  // Notes on the sheet:
  //   clk: Hz: 5000
endmodule
