// Digital circuit floor sel.dig as structural Verilog
module floor_sel (
  input  M,
  input  D,
  output [1:0] F
);

  wire [1:0] add_1_s, multiplexer_1_out, sub_1_s;

  Register #(.Bits(2)) register_1 (.D(multiplexer_1_out), .C(M), .en(1'b1), .Q(F));
  Add #(.Bits(2)) add_1 (.a(F), .b(2'b01), .c_i(1'b0), .s(add_1_s));  // open: c_o
  Sub #(.Bits(2)) sub_1 (.a(F), .b(2'b01), .c_i(1'b0), .s(sub_1_s));  // open: c_o
  Multiplexer #(.Bits(2)) multiplexer_1 (.sel(D), .in_0(add_1_s), .in_1(sub_1_s), .out(multiplexer_1_out));
endmodule
