// Digital circuit keyb.dig as structural Verilog
module keyb (
  input  clk
);

  wire d_ff_1_q, d_ff_2_q, d_ff_3_q, d_ff_4_q, delay_1_out, delay_2_out, not_1_out, switch_1_b, switch_2_b;

  not not_1 (not_1_out, clk);
  Switch switch_1 (.A(clk), .B(switch_1_b));
  Switch switch_2 (.A(clk), .B(switch_2_b));
  Delay delay_1 (.in(clk), .out(delay_1_out));
  Delay delay_2 (.in(not_1_out), .out(delay_2_out));
  Switch switch_3 (.A(not_1_out), .B(switch_1_b));
  Switch switch_4 (.A(not_1_out), .B(switch_2_b));
  PullDown pulldown_1 (.out(switch_2_b));
  PullDown pulldown_2 (.out(switch_1_b));
  D_FF #(.Default(15)) d_ff_1 (.D(switch_1_b), .C(delay_1_out), .Q(d_ff_1_q));  // open: nQ
  D_FF d_ff_2 (.D(switch_2_b), .C(delay_1_out), .Q(d_ff_2_q));  // open: nQ
  D_FF d_ff_3 (.D(switch_1_b), .C(delay_2_out), .Q(d_ff_3_q));  // open: nQ
  D_FF d_ff_4 (.D(switch_2_b), .C(delay_2_out), .Q(d_ff_4_q));  // open: nQ
  LED A (.in(d_ff_1_q));
  LED B (.in(d_ff_2_q));
  LED C (.in(d_ff_3_q));
  LED D (.in(d_ff_4_q));

  // Notes on the sheet:
  //   clk: Hz: 100
endmodule
