// Logisim project disk emulator.circ as structural Verilog: 4 circuits, main circuit main
module main (
  input  [1:0] segment,
  input  [2:0] sector,
  input  [3:0] line,
  input  [31:0] data_in,
  output [31:0] data_out
);

  wire load_out, store_out;

  Button store (.out(store_out));
  Button load (.out(load_out));
  disk Peter (
    .sel(1'b1), .segment(segment), .sector(sector), .line(line), .data_in(data_in), .store(store_out),
    .load(load_out), .data_out(data_out));
  disk Charlie ();  // open: sel, segment, sector, line, data_in, store, load, data_out

  // Notes on the sheet:
  //   line: pull=down
endmodule

module sector (
  input  [3:0] line,
  input  [31:0] data_in,
  input  store,
  input  sel,
  input  load,
  output [31:0] data_out
);

  RAM #(.addrWidth(4), .dataWidth(32), .bus("separate")) ram_1 (
    .addr(line), .din(data_in), .data(data_out), .str(store), .sel(sel), .clk(store), .ld(load));  // open: clr
endmodule

module segment (
  input  [2:0] sector,
  input  [3:0] line,
  input  [31:0] data_in,
  input  store,
  input  load,
  input  sel,
  output [31:0] data_out
);

  wire decoder_1_out0, decoder_1_out1, decoder_1_out2, decoder_1_out3, decoder_1_out4, decoder_1_out5,
       decoder_1_out6, decoder_1_out7;

  Decoder #(.select(3), .disabled(0)) decoder_1 (
    .out0(decoder_1_out0), .out1(decoder_1_out1), .out2(decoder_1_out2), .out3(decoder_1_out3),
    .out4(decoder_1_out4), .out5(decoder_1_out5), .out6(decoder_1_out6), .out7(decoder_1_out7), .en(sel));  // open: sel
  sector sector_1 (
    .line(line), .data_in(data_in), .store(store), .sel(decoder_1_out0), .load(load), .data_out(data_out));
  sector sector_2 (
    .line(line), .data_in(data_in), .store(store), .sel(decoder_1_out1), .load(load), .data_out(data_out));
  sector sector_3 (
    .line(line), .data_in(data_in), .store(store), .sel(decoder_1_out2), .load(load), .data_out(data_out));
  sector sector_4 (
    .line(line), .data_in(data_in), .store(store), .sel(decoder_1_out3), .load(load), .data_out(data_out));
  sector sector_5 (
    .line(line), .data_in(data_in), .store(store), .sel(decoder_1_out4), .load(load), .data_out(data_out));
  sector sector_6 (
    .line(line), .data_in(data_in), .store(store), .sel(decoder_1_out5), .load(load), .data_out(data_out));
  sector sector_7 (
    .line(line), .data_in(data_in), .store(store), .sel(decoder_1_out6), .load(load), .data_out(data_out));
  sector sector_8 (
    .line(line), .data_in(data_in), .store(store), .sel(decoder_1_out7), .load(load), .data_out(data_out));
endmodule

module disk (
  input  sel,
  input  [1:0] segment,
  input  [2:0] sector,
  input  [3:0] line,
  input  [31:0] data_in,
  input  store,
  input  load,
  output [31:0] data_out
);

  wire decoder_1_out0, decoder_1_out1, decoder_1_out2, decoder_1_out3;

  Decoder #(.select(2), .disabled(0)) decoder_1 (
    .out0(decoder_1_out0), .out1(decoder_1_out1), .out2(decoder_1_out2), .out3(decoder_1_out3),
    .sel(segment), .en(sel));
  segment segment_1 (
    .sector(sector), .line(line), .data_in(data_in), .store(store), .load(load), .sel(decoder_1_out0),
    .data_out(data_out));
  segment segment_2 (
    .sector(sector), .line(line), .data_in(data_in), .store(store), .load(load), .sel(decoder_1_out1),
    .data_out(data_out));
  segment segment_3 (
    .sector(sector), .line(line), .data_in(data_in), .store(store), .load(load), .sel(decoder_1_out2),
    .data_out(data_out));
  segment segment_4 (
    .sector(sector), .line(line), .data_in(data_in), .store(store), .load(load), .sel(decoder_1_out3),
    .data_out(data_out));
endmodule
