// Logisim project display driver (16x16) dmx.circ as structural Verilog: 2 circuits, main circuit main
module main (
  input  [3:0] in_1,
  input  [15:0] in_2,
  input  Prog,
  input  Store,
  input  reset
);

  wire and_1_out, clock_1_out, clock_2_out, not_1_out, or_1_out;
  wire [3:0] counter_1_q, multiplexer_1_out;
  wire [15:0] demultiplexer_1_out0, demultiplexer_1_out1, demultiplexer_1_out2, demultiplexer_1_out3,
       demultiplexer_1_out4, demultiplexer_1_out5, demultiplexer_1_out6, demultiplexer_1_out7,
       demultiplexer_1_out8, demultiplexer_1_out9, demultiplexer_1_out10, demultiplexer_1_out11,
       demultiplexer_1_out12, demultiplexer_1_out13, demultiplexer_1_out14, demultiplexer_1_out15, ram_1_data;

  Multiplexer #(.width(4), .disabled(0), .enable("false")) multiplexer_1 (
    .in0(counter_1_q), .in1(in_1), .out(multiplexer_1_out), .sel(Prog));
  or or_1 (or_1_out, Prog, reset);
  Clock clock_1 (.out(clock_1_out));
  not not_1 (not_1_out, Store);
  Clock clock_2 (.out(clock_2_out));
  Counter #(.width(4), .max('hf), .trigger("falling")) counter_1 (
    .Q(counter_1_q), .clk(clock_1_out), .clr(or_1_out));  // open: load, D, count, carry
  RAM #(.addrWidth(4), .dataWidth(16), .bus("separate")) ram_1 (
    .addr(multiplexer_1_out), .din(in_2), .data(ram_1_data), .str(Store), .clk(clock_2_out), .ld(not_1_out));  // open: sel, clr
  // Probe on ram_1_data
  and and_1 (and_1_out, ~or_1_out, clock_1_out);  // AND_Gate
  Demultiplexer #(.select(4), .width(16), .enable("false")) demultiplexer_1 (
    .out0(demultiplexer_1_out0), .out1(demultiplexer_1_out1), .out2(demultiplexer_1_out2),
    .out3(demultiplexer_1_out3), .out4(demultiplexer_1_out4), .out5(demultiplexer_1_out5),
    .out6(demultiplexer_1_out6), .out7(demultiplexer_1_out7), .out8(demultiplexer_1_out8),
    .out9(demultiplexer_1_out9), .out10(demultiplexer_1_out10), .out11(demultiplexer_1_out11),
    .out12(demultiplexer_1_out12), .out13(demultiplexer_1_out13), .out14(demultiplexer_1_out14),
    .out15(demultiplexer_1_out15), .in(ram_1_data), .sel(counter_1_q));
  DotMatrix #(.inputtype("row"), .matrixcols(16), .matrixrows(16), .persist(40)) dotmatrix_1 (
    .row0(demultiplexer_1_out0), .row1(demultiplexer_1_out1), .row2(demultiplexer_1_out2),
    .row3(demultiplexer_1_out3), .row4(demultiplexer_1_out4), .row5(demultiplexer_1_out5),
    .row6(demultiplexer_1_out6), .row7(demultiplexer_1_out7), .row8(demultiplexer_1_out8),
    .row9(demultiplexer_1_out9), .row10(demultiplexer_1_out10), .row11(demultiplexer_1_out11),
    .row12(demultiplexer_1_out12), .row13(demultiplexer_1_out13), .row14(demultiplexer_1_out14),
    .row15(demultiplexer_1_out15));
endmodule

module dreg (
  input  [15:0] in,
  input  clk,
  input  [3:0] sel,
  output [15:0] out_4,
  output [15:0] out_5,
  output [15:0] out_6,
  output [15:0] out_7,
  output [15:0] out_8,
  output [15:0] out_9,
  output [15:0] out_10,
  output [15:0] out_11,
  output [15:0] out_12,
  output [15:0] out_13,
  output [15:0] out_14,
  output [15:0] out_15,
  output [15:0] out_16,
  output [15:0] out_17,
  output [15:0] out_18,
  output [15:0] out_19
);

  wire decoder_1_out0, decoder_1_out1, decoder_1_out2, decoder_1_out3, decoder_1_out4, decoder_1_out5,
       decoder_1_out6, decoder_1_out7, decoder_1_out8, decoder_1_out9, decoder_1_out10, decoder_1_out11,
       decoder_1_out12, decoder_1_out13, decoder_1_out14, decoder_1_out15;

  Decoder #(.select(4), .disabled(0), .enable("false")) decoder_1 (
    .out0(decoder_1_out0), .out1(decoder_1_out1), .out2(decoder_1_out2), .out3(decoder_1_out3),
    .out4(decoder_1_out4), .out5(decoder_1_out5), .out6(decoder_1_out6), .out7(decoder_1_out7),
    .out8(decoder_1_out8), .out9(decoder_1_out9), .out10(decoder_1_out10), .out11(decoder_1_out11),
    .out12(decoder_1_out12), .out13(decoder_1_out13), .out14(decoder_1_out14), .out15(decoder_1_out15),
    .sel(sel));
  Register #(.width(16)) register_1 (.D(in), .en(decoder_1_out0), .Q(out_4), .clk(clk));  // open: clr
  Register #(.width(16)) register_2 (.D(in), .en(decoder_1_out1), .Q(out_5), .clk(clk));  // open: clr
  Register #(.width(16)) register_3 (.D(in), .en(decoder_1_out2), .Q(out_6), .clk(clk));  // open: clr
  Register #(.width(16)) register_4 (.D(in), .en(decoder_1_out3), .Q(out_7), .clk(clk));  // open: clr
  Register #(.width(16)) register_5 (.D(in), .en(decoder_1_out4), .Q(out_8), .clk(clk));  // open: clr
  Register #(.width(16)) register_6 (.D(in), .en(decoder_1_out5), .Q(out_9), .clk(clk));  // open: clr
  Register #(.width(16)) register_7 (.D(in), .en(decoder_1_out6), .Q(out_10), .clk(clk));  // open: clr
  Register #(.width(16)) register_8 (.D(in), .en(decoder_1_out7), .Q(out_11), .clk(clk));  // open: clr
  Register #(.width(16)) register_9 (.D(in), .en(decoder_1_out8), .Q(out_12), .clk(clk));  // open: clr
  Register #(.width(16)) register_10 (.D(in), .en(decoder_1_out9), .Q(out_13), .clk(clk));  // open: clr
  Register #(.width(16)) register_11 (.D(in), .en(decoder_1_out10), .Q(out_14), .clk(clk));  // open: clr
  Register #(.width(16)) register_12 (.D(in), .en(decoder_1_out11), .Q(out_15), .clk(clk));  // open: clr
  Register #(.width(16)) register_13 (.D(in), .en(decoder_1_out12), .Q(out_16), .clk(clk));  // open: clr
  Register #(.width(16)) register_14 (.D(in), .en(decoder_1_out13), .Q(out_17), .clk(clk));  // open: clr
  Register #(.width(16)) register_15 (.D(in), .en(decoder_1_out14), .Q(out_18), .clk(clk));  // open: clr
  Register #(.width(16)) register_16 (.D(in), .en(decoder_1_out15), .Q(out_19), .clk(clk));  // open: clr
endmodule
