// Logisim project display driver (16x24).circ as structural Verilog: 2 circuits, main circuit main
module main (
  input  [3:0] in_1,
  input  [23:0] in_2,
  input  Prog,
  input  Store,
  input  reset
);

  wire and_1_out, clock_1_out, clock_2_out, not_1_out, or_1_out;
  wire [3:0] counter_1_q, multiplexer_1_out;
  wire [23:0] dreg_1_out_4, dreg_1_out_5, dreg_1_out_6, dreg_1_out_7, dreg_1_out_8, dreg_1_out_9,
       dreg_1_out_10, dreg_1_out_11, dreg_1_out_12, dreg_1_out_13, dreg_1_out_14, dreg_1_out_15,
       dreg_1_out_16, dreg_1_out_17, dreg_1_out_18, dreg_1_out_19, ram_1_data;

  Multiplexer #(.width(4), .disabled(0), .enable("false")) multiplexer_1 (
    .in0(counter_1_q), .in1(in_1), .out(multiplexer_1_out), .sel(Prog));
  or or_1 (or_1_out, Prog, reset);
  Clock clock_1 (.out(clock_1_out));
  not not_1 (not_1_out, Store);
  Clock clock_2 (.out(clock_2_out));
  Counter #(.width(4), .max('hf), .trigger("falling")) counter_1 (
    .Q(counter_1_q), .clk(clock_1_out), .clr(or_1_out));  // open: load, D, count, carry
  RAM #(.addrWidth(4), .dataWidth(24), .bus("separate")) ram_1 (
    .addr(multiplexer_1_out), .din(in_2), .data(ram_1_data), .str(Store), .clk(clock_2_out), .ld(not_1_out));  // open: sel, clr
  // Probe on ram_1_data
  and and_1 (and_1_out, ~or_1_out, clock_1_out);  // AND_Gate
  DotMatrix #(.inputtype("row"), .matrixcols(24), .matrixrows(16)) dotmatrix_1 (
    .row0(dreg_1_out_4), .row1(dreg_1_out_5), .row2(dreg_1_out_6), .row3(dreg_1_out_7), .row4(dreg_1_out_8),
    .row5(dreg_1_out_9), .row6(dreg_1_out_10), .row7(dreg_1_out_11), .row8(dreg_1_out_12),
    .row9(dreg_1_out_13), .row10(dreg_1_out_14), .row11(dreg_1_out_15), .row12(dreg_1_out_16),
    .row13(dreg_1_out_17), .row14(dreg_1_out_18), .row15(dreg_1_out_19));
  dreg dreg_1 (
    .in(ram_1_data), .clk(and_1_out), .sel(counter_1_q), .out_4(dreg_1_out_4), .out_5(dreg_1_out_5),
    .out_6(dreg_1_out_6), .out_7(dreg_1_out_7), .out_8(dreg_1_out_8), .out_9(dreg_1_out_9),
    .out_10(dreg_1_out_10), .out_11(dreg_1_out_11), .out_12(dreg_1_out_12), .out_13(dreg_1_out_13),
    .out_14(dreg_1_out_14), .out_15(dreg_1_out_15), .out_16(dreg_1_out_16), .out_17(dreg_1_out_17),
    .out_18(dreg_1_out_18), .out_19(dreg_1_out_19));
endmodule

module dreg (
  input  [23:0] in,
  input  clk,
  input  [3:0] sel,
  output [23:0] out_4,
  output [23:0] out_5,
  output [23:0] out_6,
  output [23:0] out_7,
  output [23:0] out_8,
  output [23:0] out_9,
  output [23:0] out_10,
  output [23:0] out_11,
  output [23:0] out_12,
  output [23:0] out_13,
  output [23:0] out_14,
  output [23:0] out_15,
  output [23:0] out_16,
  output [23:0] out_17,
  output [23:0] out_18,
  output [23:0] out_19
);

  wire decoder_1_out0, decoder_1_out1, decoder_1_out2, decoder_1_out3, decoder_1_out4, decoder_1_out5,
       decoder_1_out6, decoder_1_out7, decoder_1_out8, decoder_1_out9, decoder_1_out10, decoder_1_out11,
       decoder_1_out12, decoder_1_out13, decoder_1_out14, decoder_1_out15;

  Decoder #(.select(4), .disabled(0), .enable("false")) decoder_1 (
    .out0(decoder_1_out0), .out1(decoder_1_out1), .out2(decoder_1_out2), .out3(decoder_1_out3),
    .out4(decoder_1_out4), .out5(decoder_1_out5), .out6(decoder_1_out6), .out7(decoder_1_out7),
    .out8(decoder_1_out8), .out9(decoder_1_out9), .out10(decoder_1_out10), .out11(decoder_1_out11),
    .out12(decoder_1_out12), .out13(decoder_1_out13), .out14(decoder_1_out14), .out15(decoder_1_out15),
    .sel(sel));
  Register #(.width(24)) register_1 (.D(in), .en(decoder_1_out0), .Q(out_4), .clk(clk));  // open: clr
  Register #(.width(24)) register_2 (.D(in), .en(decoder_1_out1), .Q(out_5), .clk(clk));  // open: clr
  Register #(.width(24)) register_3 (.D(in), .en(decoder_1_out2), .Q(out_6), .clk(clk));  // open: clr
  Register #(.width(24)) register_4 (.D(in), .en(decoder_1_out3), .Q(out_7), .clk(clk));  // open: clr
  Register #(.width(24)) register_5 (.D(in), .en(decoder_1_out4), .Q(out_8), .clk(clk));  // open: clr
  Register #(.width(24)) register_6 (.D(in), .en(decoder_1_out5), .Q(out_9), .clk(clk));  // open: clr
  Register #(.width(24)) register_7 (.D(in), .en(decoder_1_out6), .Q(out_10), .clk(clk));  // open: clr
  Register #(.width(24)) register_8 (.D(in), .en(decoder_1_out7), .Q(out_11), .clk(clk));  // open: clr
  Register #(.width(24)) register_9 (.D(in), .en(decoder_1_out8), .Q(out_12), .clk(clk));  // open: clr
  Register #(.width(24)) register_10 (.D(in), .en(decoder_1_out9), .Q(out_13), .clk(clk));  // open: clr
  Register #(.width(24)) register_11 (.D(in), .en(decoder_1_out10), .Q(out_14), .clk(clk));  // open: clr
  Register #(.width(24)) register_12 (.D(in), .en(decoder_1_out11), .Q(out_15), .clk(clk));  // open: clr
  Register #(.width(24)) register_13 (.D(in), .en(decoder_1_out12), .Q(out_16), .clk(clk));  // open: clr
  Register #(.width(24)) register_14 (.D(in), .en(decoder_1_out13), .Q(out_17), .clk(clk));  // open: clr
  Register #(.width(24)) register_15 (.D(in), .en(decoder_1_out14), .Q(out_18), .clk(clk));  // open: clr
  Register #(.width(24)) register_16 (.D(in), .en(decoder_1_out15), .Q(out_19), .clk(clk));  // open: clr
endmodule
