// Logisim project easy ram with clipboard.circ as structural Verilog: 1 circuit, main circuit main
module main (
  input  [23:0] address_in,
  input  [31:0] data__in,
  input  [7:0] clipboard_select
);

  wire cla, clear__RAM_out, clo, clock_1_out, clock_2_out, cp, not_1_out, not_2_out, or_1_out, or_2_out, pa,
       store_out;
  wire [31:0] multiplexer_1_out, multiplexer_2_out, multiplexer_3_out, ram_1_data, ram_2_data;

  Button store (.out(store_out));
  Button clear__RAM (.out(clear__RAM_out));
  Button copy (.out(cp));
  Button paste (.out(pa));
  Button clear__selected_clipboard (.out(clo));
  Button clear__all_clipboards (.out(cla));
  // Probe on ram_2_data
  // Probe on multiplexer_3_out
  Multiplexer #(.width(32), .disabled(0), .enable("false")) multiplexer_1 (
    .in0(data__in), .in1(ram_2_data), .out(multiplexer_1_out), .sel(pa));
  Clock clock_1 (.out(clock_1_out));
  not not_1 (not_1_out, or_1_out);
  or or_1 (or_1_out, store_out, pa);
  Multiplexer #(.width(32), .disabled(0), .enable("false")) multiplexer_2 (
    .in1({32{1'b0}}), .out(multiplexer_2_out), .sel(clo));  // open: in0
  RAM #(.addrWidth(24), .dataWidth(32), .bus("separate")) ram_1 (
    .addr(address_in), .din(multiplexer_1_out), .data(ram_1_data), .str(or_1_out), .clk(clock_1_out),
    .ld(not_1_out), .clr(clear__RAM_out));  // open: sel
  Multiplexer #(.width(32), .enable("false")) multiplexer_3 (
    .in0(ram_1_data), .out(multiplexer_3_out), .sel(or_1_out));  // open: in1
  or or_2 (or_2_out, cp, clo);
  not not_2 (not_2_out, or_2_out);
  Clock clock_2 (.out(clock_2_out));
  RAM #(.dataWidth(32), .bus("separate")) ram_2 (
    .addr(clipboard_select), .din(multiplexer_2_out), .data(ram_2_data), .str(or_2_out), .clk(clock_2_out),
    .ld(not_2_out), .clr(cla));  // open: sel

  // Other names for the same wires on the sheet: sel[7:0] = clipboard_select
endmodule
