// Logisim project easy ram.circ as structural Verilog: 2 circuits, main circuit RAM
module RAM (
  input  [23:0] address_in,
  input  [31:0] data__in,
  input  store_in,
  input  select_in,
  input  clear_in,
  output [31:0] data_out
);

  wire and_1_out, clock_1_out, not_1_out;

  Clock clock_1 (.out(clock_1_out));
  not not_1 (not_1_out, store_in);
  and and_1 (and_1_out, select_in, clear_in);
  RAM_part #(.addrWidth(24), .dataWidth(32), .bus("separate")) ram_1 (
    .addr(address_in), .din(data__in), .data(data_out), .str(store_in), .sel(select_in), .clk(clock_1_out),
    .ld(not_1_out), .clr(and_1_out));
endmodule

module RAMx2 (
  input  [23:0] a_in,
  input  [31:0] d_in,
  input  store,
  input  clear,
  input  sel,
  output [31:0] out_6
);

  wire not_1_out;

  RAM ram_1 (
    .address_in(a_in), .data__in(d_in), .store_in(store), .select_in(not_1_out), .clear_in(clear),
    .data_out(out_6));
  not not_1 (not_1_out, sel);
  RAM ram_2 (.address_in(a_in), .data__in(d_in), .store_in(store), .select_in(sel), .clear_in(clear), .data_out(out_6));
endmodule
