// Logisim project factor machine (8 & 6 only now, more soon!).circ as structural Verilog: 1 circuit, main circuit main
module main (
  input  [31:0] in
);

  wire and_1_out, and_2_out, and_3_out, clock_1_out, clock_2_out, clock_3_out, clock_4_out, comparator_1_eq,
       comparator_2_eq, comparator_3_eq, comparator_3_gt, comparator_3_lt, multiplexer_1_out, not_1_out,
       or_2_out;
  wire [1:0] counter_2_q;
  wire [23:0] counter_1_q, multiplexer_4_out;
  wire [31:0] multiplexer_2_out, multiplexer_3_out, ram_2_data;

  Comparator #(.width(32)) comparator_1 (.a(in), .b(32'h6), .eq(comparator_1_eq));  // open: gt, lt
  Multiplexer #(.disabled(0), .enable("false")) multiplexer_1 (
    .in0(comparator_1_eq), .in1(comparator_2_eq), .out(multiplexer_1_out), .sel(comparator_2_eq));
  Comparator #(.width(32)) comparator_2 (.a(in), .b(32'h8), .eq(comparator_2_eq));  // open: gt, lt
  and and_1 (and_1_out, multiplexer_1_out, ~comparator_3_eq);  // AND_Gate
  Multiplexer #(.width(32)) multiplexer_2 (
    .in0(32'h3), .in1(32'h2), .out(multiplexer_2_out), .sel(comparator_2_eq));  // open: en
  Counter #(.width(24), .max('hffffff)) counter_1 (
    .count(and_2_out), .Q(counter_1_q), .clk(clock_1_out));  // open: load, D, carry, clr
  and and_2 (and_2_out, or_2_out, and_1_out);
  Clock clock_1 (.out(clock_1_out));
  Multiplexer #(.select(2), .width(32), .disabled(0), .enable("false")) multiplexer_3 (
    .in0(32'h2), .in1(multiplexer_2_out), .in2(32'h2), .out(multiplexer_3_out), .sel(counter_2_q));  // open: in3
  Multiplexer #(.width(24), .enable("false")) multiplexer_4 (
    .in0(24'h2), .in1(24'h3), .out(multiplexer_4_out), .sel(comparator_2_eq));
  Clock clock_2 (.out(clock_2_out));
  Counter #(.width(2), .max('h3), .ongoal("stay")) counter_2 (
    .count(and_1_out), .Q(counter_2_q), .clk(clock_3_out), .clr(comparator_3_eq));  // open: load, D, carry
  Clock clock_3 (.out(clock_3_out));
  Comparator #(.width(24)) comparator_3 (
    .a(counter_1_q), .b(multiplexer_4_out), .gt(comparator_3_gt), .eq(comparator_3_eq), .lt(comparator_3_lt));
  // OR_Gate or_1 has open pins: in0=comparator_3_gt, in1=comparator_3_lt, out=open
  RAM #(.addrWidth(24), .dataWidth(32)) ram_1 (.clk(clock_2_out));  // open: addr, data, sel, ld, clr
  RAM #(.addrWidth(24), .dataWidth(32), .bus("separate")) ram_2 (
    .addr(counter_1_q), .din(multiplexer_3_out), .data(ram_2_data), .str(and_3_out), .clk(clock_4_out),
    .ld(not_1_out));  // open: sel, clr
  Clock clock_4 (.out(clock_4_out));
  not not_1 (not_1_out, and_3_out);
  and and_3 (and_3_out, and_1_out, ~comparator_3_eq);  // AND_Gate
  or or_2 (or_2_out, ram_2_data[0], ram_2_data[1], ram_2_data[2], ram_2_data[3], ram_2_data[4], ram_2_data[5], ram_2_data[6], ram_2_data[7], ram_2_data[8], ram_2_data[9], ram_2_data[10], ram_2_data[11], ram_2_data[12], ram_2_data[13], ram_2_data[14], ram_2_data[15], ram_2_data[17], ram_2_data[18], ram_2_data[19], ram_2_data[20], ram_2_data[21], ram_2_data[22], ram_2_data[23], ram_2_data[24], ram_2_data[25], ram_2_data[26], ram_2_data[27], ram_2_data[28], ram_2_data[29], ram_2_data[30], ram_2_data[31], ram_2_data[16]);
endmodule
