// Logisim project fibonacci series(Put a one in first two adresses of ram!).circ as structural Verilog: 1 circuit, main circuit main
module main (
  output [31:0] out
);

  wire and_1_out, and_2_out, clock_1_out, clock_2_out, clock_3_out, clock_4_out, clock_5_out, clock_6_out,
       clock_7_out, comparator_1_eq, comparator_2_eq, comparator_3_eq, comparator_4_eq, nand_1_out,
       not_1_out, or_1_out, t_ff_1_q, t_ff_2_q;
  wire [23:0] counter_1_q, multiplexer_1_out, register_1_q, subtractor_1_out;
  wire [31:0] multiplexer_2_out, multiplexer_3_out, ram_1_data, register_2_q, register_3_q;

  T_Flip_Flop t_ff_1 (.clk(clock_1_out), .T(comparator_1_eq), .Q(t_ff_1_q), .preset(t_ff_1_q));  // open: Qn, reset, en
  Clock clock_1 (.out(clock_1_out));
  Counter #(.width(24), .max('hffffff)) counter_1 (
    .Q(counter_1_q), .clk(clock_2_out));  // open: load, D, count, carry, clr
  Clock clock_2 (.out(clock_2_out));
  Multiplexer #(.width(24), .disabled(0), .enable("false")) multiplexer_1 (
    .in0(24'h2), .in1(24'h1), .out(multiplexer_1_out), .sel(t_ff_1_q));
  Register #(.width(24)) register_1 (
    .D(counter_1_q), .en(comparator_1_eq), .Q(register_1_q), .clk(clock_3_out));  // open: clr
  Clock clock_3 (.out(clock_3_out));
  Subtractor #(.width(24)) subtractor_1 (
    .a(counter_1_q), .b(multiplexer_1_out), .out(subtractor_1_out));  // open: bin, bout
  Clock clock_4 (.out(clock_4_out));
  not not_1 (not_1_out, comparator_1_eq);
  RAM #(.addrWidth(24), .dataWidth(32), .bus("separate")) ram_1 (
    .addr(counter_1_q), .din(out), .data(ram_1_data), .str(comparator_1_eq), .clk(clock_4_out), .ld(not_1_out));  // open: sel, clr
  Comparator #(.width(24)) comparator_1 (.a(subtractor_1_out), .b(register_1_q), .eq(comparator_1_eq));  // open: gt, lt
  Multiplexer #(.width(32), .disabled(0), .enable("false")) multiplexer_2 (
    .in0(ram_1_data), .in1(register_3_q), .out(multiplexer_2_out), .sel(t_ff_2_q));
  nand nand_1 (nand_1_out, and_1_out, ~t_ff_2_q);  // NAND_Gate
  Multiplexer #(.width(32), .disabled(0), .enable("false")) multiplexer_3 (
    .in0(ram_1_data), .in1(out), .out(multiplexer_3_out), .sel(comparator_1_eq));
  or or_1 (or_1_out, comparator_1_eq, and_1_out);
  and and_1 (and_1_out, comparator_2_eq, ~t_ff_2_q);  // AND_Gate
  // NAND_Gate nand_2 is placed but not wired
  Comparator #(.width(32)) comparator_2 (.a(register_2_q), .b(ram_1_data), .eq(comparator_2_eq));  // open: gt, lt
  Register #(.width(32)) register_2 (
    .D(multiplexer_2_out), .en(nand_1_out), .Q(register_2_q), .clk(clock_5_out));  // open: clr
  Clock clock_5 (.out(clock_5_out));
  Register #(.width(32)) register_3 (
    .D(multiplexer_3_out), .en(or_1_out), .Q(register_3_q), .clk(clock_6_out));  // open: clr
  Clock clock_6 (.out(clock_6_out));
  Comparator #(.width(32)) comparator_3 (.a(register_2_q), .b(32'h1), .eq(comparator_3_eq));  // open: gt, lt
  Pull_Resistor pull_resistor_1 (.node(comparator_2_eq));
  Adder #(.width(32)) adder_1 (.a(register_2_q), .b(register_3_q), .out(out));  // open: cin, cout
  Comparator #(.width(32)) comparator_4 (.a(register_3_q), .b(32'h1), .eq(comparator_4_eq));  // open: gt, lt
  and and_2 (and_2_out, comparator_3_eq, comparator_4_eq);
  T_Flip_Flop t_ff_2 (.clk(clock_7_out), .T(and_2_out), .Q(t_ff_2_q), .preset(t_ff_2_q));  // open: Qn, reset, en
  Clock clock_7 (.out(clock_7_out));
endmodule
