# Fritzing sketch arduino (saved by Fritzing 0.9.3b)
circuit board: 5.81914cm x 3.58935cm
breadboards: 1

parts:
  S1 = Momentary Switch [package=ksa_sealed_tac_switch]
  J1 = female pin header, 8 pins [form="♀ (female)"]
  J2 = female pin header, 8 pins [form="♀ (female)"]
  R1 = Resistor [tolerance=±5% resistance=1k package=THT]
  J3 = female pin header, 6 pins [form="♀ (female)"]
  J4 = female pin header, 2 pins [form="♀ (female)"]
  U2 = atmega328 [package=dip]

nets:
  N1: S1.2, R1.Pin_1, U2.RESET
  GND: S1.3, J4.pin2, U2.GND
  N2: J1.pin1, U2.D0_(RX)
  N3: J1.pin2, U2.D1_(TX)
  N4: J1.pin3, U2.D2
  N5: J1.pin4, U2.D3_(PWM)
  N6: J1.pin5, U2.D4
  N7: J1.pin6, U2.D5_(PWM)
  N8: J1.pin7, U2.D6_(PWM)
  N9: J1.pin8, U2.D7
  N10: J2.pin1, U2.D8
  N11: J2.pin2, U2.D9_(PWM)
  N12: J2.pin3, U2.D10_(PWM)
  N13: J2.pin4, U2.D11_(PWM)
  N14: J2.pin5, U2.D12
  N15: J2.pin6, U2.D13
  N16: J2.pin7, U2.XLAT1
  N17: J2.pin8, U2.XLAT2
  5V: R1.Pin_0, J4.pin1, U2.VCC, U2.AVCC, U2.AREF
  N18: J3.pin1, U2.A0
  N19: J3.pin2, U2.A1
  N20: J3.pin3, U2.A2
  N21: J3.pin4, U2.A3
  N22: J3.pin5, U2.A4
  N23: J3.pin6, U2.A5

notes:
  PD
  PB
  PC
  (ALG)
