# Fritzing sketch intercom (saved by Fritzing 0.9.3b)
circuit board: 8.47706cm x 5.73793cm

parts:
  U1 = atmega328 [package=dip]
  J1 = Power Jack [package=power_jack_pth]
  R1 = Resistor [tolerance=±5% resistance=1k package=THT]
  U2 = Voltage Regulator - 5V [package="TO220 [THT]"]
  J2 = female pin header, 4 pins [form="♀ (female)"]
  J3 = female pin header, 2 pins [form="♀ (female)"]
  J4 = female pin header, 3 pins [form="♀ (female)"]
  XTAL1 = Crystal [frequency="16 Mhz" package=THT]
  C1 = Capacitor [package=cap-pth-large]
  C2 = Capacitor [package=cap-pth-large]

nets:
  N1: U1.RESET, R1.Pin_1, J2.pin1
  N2: U1.D0_(RX), J2.pin2
  N3: U1.D1_(TX), J2.pin3
  5V: U1.VCC, U1.AVCC, U1.AREF, R1.Pin_0, U2.output_voltage, J4.pin3
  GND: U1.GND, J1.GND, U2.GND, J2.pin4, J3.pin2, J4.pin1, C1.2, C2.2
  N4: U1.XLAT1, XTAL1.pin_0, C1.1
  N5: U1.XLAT2, XTAL1.pin_1, C2.1
  N6: U1.D9_(PWM), J3.pin1
  N7: U1.A0, J4.pin2
  N8: J1.PWR, U2.input_voltage
