# Fritzing sketch psu (saved by Fritzing 0.9.3b)
circuit board: 2.63823cm x 1.42171cm
breadboards: 1

parts:
  U1 = Voltage Regulator - 5V [package="TO220 [THT]"]
  J1 = female pin header, 2 pins [form="♀ (female)"]
  J3 = Power Jack [package=power_jack_pth]

nets:
  N1: U1.input_voltage, J3.PWR
  GND: U1.GND, J1.pin2, J3.GND
  N2: U1.output_voltage, J1.pin1
