// Logisim project handy stuff.circ as structural Verilog: 1 circuit, main circuit one shot
module one_shot (
  input  in,
  output out
);

  wire clock_1_out, counter_1_carry, nor_1_out, or_1_out, t_ff_1_qn;

  Counter #(.width(2), .max('h3)) counter_1 (
    .count(in), .carry(counter_1_carry), .clk(clock_1_out), .clr(counter_1_carry));  // open: load, D, Q
  Clock clock_1 (.out(clock_1_out));
  T_Flip_Flop t_ff_1 (.clk(in), .T(1'b1), .Q(out), .Qn(t_ff_1_qn), .reset(or_1_out));  // open: preset, en
  or or_1 (or_1_out, nor_1_out, counter_1_carry);
  nor nor_1 (nor_1_out, t_ff_1_qn, in);
endmodule
