// Logisim project logic_block.circ as structural Verilog: 1 circuit, main circuit main
module main (
  input  PGM,
  input  [3:0] IN3,
  input  IN,
  input  [3:0] IN0,
  input  [3:0] IN2,
  input  [3:0] IN1,
  output OUT,
  output [3:0] OUT0,
  output [3:0] OUT1
);

  wire clock_1_out, clock_2_out, d_ff_1_q, multiplexer_4_out, multiplexer_5_out, shift_register_1_q15,
       shift_register_1_q16, shift_register_1_q17, shift_register_1_q18, shift_register_1_q19,
       shift_register_1_q20, shift_register_1_q21, shift_register_1_q22, shift_register_1_q23,
       shift_register_1_q24, shift_register_1_q25, shift_register_1_q26, shift_register_1_q27,
       shift_register_1_q28, shift_register_1_q29, shift_register_1_q30, shift_register_1_q31;
  wire [1:0] shift_register_1_q1, shift_register_1_q3, shift_register_1_q5, shift_register_1_q7;
  wire [3:0] multiplexer_6_out;
  wire [5:0] shift_register_1_q10;

  Multiplexer #(.select(2), .enable("false")) multiplexer_1 (
    .in0(IN3[0]), .in1(IN3[1]), .in2(IN3[2]), .in3(IN3[3]), .out(multiplexer_6_out[3]),
    .sel(shift_register_1_q1));
  Clock clock_1 (.out(clock_1_out));
  Multiplexer #(.select(2), .enable("false")) multiplexer_2 (
    .in0(IN2[0]), .in1(IN2[1]), .in2(IN2[2]), .in3(IN2[3]), .out(multiplexer_6_out[2]),
    .sel(shift_register_1_q3));
  Shift_Register #(.length(32)) shift_register_1 (
    .shift(PGM), .in(IN), .clk(clock_1_out), .out(OUT), .q0(shift_register_1_q1[1]),
    .q1(shift_register_1_q1[0]), .q2(shift_register_1_q3[1]), .q3(shift_register_1_q3[0]),
    .q4(shift_register_1_q5[1]), .q5(shift_register_1_q5[0]), .q6(shift_register_1_q7[1]),
    .q7(shift_register_1_q7[0]), .q8(shift_register_1_q10[5]), .q9(shift_register_1_q10[4]),
    .q10(shift_register_1_q10[3]), .q11(shift_register_1_q10[2]), .q12(shift_register_1_q10[1]),
    .q13(shift_register_1_q10[0]), .q15(shift_register_1_q15), .q16(shift_register_1_q16),
    .q17(shift_register_1_q17), .q18(shift_register_1_q18), .q19(shift_register_1_q19),
    .q20(shift_register_1_q20), .q21(shift_register_1_q21), .q22(shift_register_1_q22),
    .q23(shift_register_1_q23), .q24(shift_register_1_q24), .q25(shift_register_1_q25),
    .q26(shift_register_1_q26), .q27(shift_register_1_q27), .q28(shift_register_1_q28),
    .q29(shift_register_1_q29), .q30(shift_register_1_q30), .q31(shift_register_1_q31));  // open: load, clr, d0, d1, d2, d3, d4, d5, d6, d7, d8, d9, d10, d11, d12, d13, d14, q14, d15, d16, d17, d18, d19, d20, d21, d22, d23, d24, d25, d26, d27, d28, d29, d30, d31
  Multiplexer #(.select(2), .enable("false")) multiplexer_3 (
    .in0(IN1[0]), .in1(IN1[1]), .in2(IN1[2]), .in3(IN1[3]), .out(multiplexer_6_out[1]),
    .sel(shift_register_1_q5));
  Multiplexer #(.select(4), .enable("false")) multiplexer_4 (
    .in0(shift_register_1_q16), .in1(shift_register_1_q17), .in2(shift_register_1_q18),
    .in3(shift_register_1_q19), .in4(shift_register_1_q20), .in5(shift_register_1_q21),
    .in6(shift_register_1_q22), .in7(shift_register_1_q23), .in8(shift_register_1_q24),
    .in9(shift_register_1_q25), .in10(shift_register_1_q26), .in11(shift_register_1_q27),
    .in12(shift_register_1_q28), .in13(shift_register_1_q29), .in14(shift_register_1_q30),
    .in15(shift_register_1_q31), .out(multiplexer_4_out), .sel(multiplexer_6_out));
  Clock clock_2 (.out(clock_2_out));
  D_Flip_Flop d_ff_1 (.clk(clock_2_out), .D(multiplexer_4_out), .Q(d_ff_1_q));  // open: Qn, preset, en, reset
  Demultiplexer #(.select(3), .tristate("true"), .enable("false")) demultiplexer_1 (
    .out0(OUT1[3]), .out1(OUT1[2]), .out2(OUT1[1]), .out3(OUT1[0]), .in(multiplexer_5_out),
    .sel(shift_register_1_q10[5:3]));  // open: out4, out5, out6, out7
  Multiplexer #(.enable("false")) multiplexer_5 (
    .in0(multiplexer_4_out), .in1(d_ff_1_q), .out(multiplexer_5_out), .sel(shift_register_1_q15));
  Multiplexer #(.select(2), .enable("false")) multiplexer_6 (
    .in0(IN0[0]), .in1(IN0[1]), .in2(IN0[2]), .in3(IN0[3]), .out(multiplexer_6_out[0]),
    .sel(shift_register_1_q7));
  Demultiplexer #(.select(3), .tristate("true"), .enable("false")) demultiplexer_2 (
    .out0(OUT0[0]), .out1(OUT0[1]), .out2(OUT0[2]), .out3(OUT0[3]), .in(multiplexer_5_out),
    .sel(shift_register_1_q10[2:0]));  // open: out4, out5, out6, out7
endmodule
