// Logisim project 8080.circ as structural Verilog
module _8080 (
  input  [7:0] instruction,
  input  [7:0] ilow,
  input  [7:0] ihigh,
  input  clk,
  input  rst,
  input  [7:0] DIN,
  output [15:0] addr,
  output [7:0] DOUT,
  output nR_W
);

  wire alu_1_cmp, and_1_out, decoder_1_out0, decoder_1_out1, decoder_2_out0, decoder_2_out1, idec_1_al,
       idec_1_ali, idec_1_lda, idec_1_mov, idec_1_mvi, or_1_out, or_2_out, or_3_out, or_4_out, t_ff_1_q,
       t_ff_2_q;
  wire [1:0] priority_encoder_1_out;
  wire [2:0] multiplexer_1_out;
  wire [7:0] alu_1_r, atemp_q, controlled_buffer_1_out, controlled_buffer_4_out, multiplexer_2_out,
       rfile_1_a, rfile_1_rdata, rtemp_q;

  idec idec_1 (
    .Instruction(instruction), .MOV(idec_1_mov), .MVI(idec_1_mvi), .LDA(idec_1_lda), .STA(nR_W),
    .ALI(idec_1_ali), .AL(idec_1_al));  // open: ALNI
  T_Flip_Flop t_ff_1 (.clk(clk), .T(idec_1_mov), .Q(t_ff_1_q), .reset(rst));  // open: Qn, preset, en
  T_Flip_Flop t_ff_2 (.clk(clk), .T(idec_1_al), .Q(t_ff_2_q), .reset(rst));  // open: Qn, preset, en
  Decoder #(.disabled(0)) decoder_1 (.out0(decoder_1_out0), .out1(decoder_1_out1), .sel(t_ff_1_q), .en(idec_1_mov));
  Decoder #(.disabled(0)) decoder_2 (.out0(decoder_2_out0), .out1(decoder_2_out1), .sel(t_ff_2_q), .en(idec_1_al));
  assign controlled_buffer_1_out = idec_1_mvi ? ilow : 8'bz;  // Controlled_Buffer controlled_buffer_1
  assign controlled_buffer_1_out = decoder_1_out0 ? rtemp_q : 8'bz;  // Controlled_Buffer controlled_buffer_2
  Multiplexer #(.select(2), .width(3), .enable("false")) multiplexer_1 (
    .in0(instruction[2:0]), .in1(instruction[5:3]), .in2(3'b111), .out(multiplexer_1_out),
    .sel(priority_encoder_1_out));  // open: in3
  or or_1 (or_1_out, decoder_1_out1, idec_1_mvi, idec_1_lda, idec_1_al);
  rfile rfile_1 (
    .wdata(controlled_buffer_1_out), .wen(or_1_out), .sel(multiplexer_1_out), .clk(clk), .rst(rst),
    .A(rfile_1_a), .rdata(rfile_1_rdata));  // open: MHL, HL
  or or_2 (or_2_out, idec_1_mov, idec_1_al);
  or or_3 (or_3_out, decoder_1_out1, idec_1_mvi);
  or or_4 (or_4_out, idec_1_lda, nR_W, decoder_2_out1);
  Priority_Encoder #(.select(2)) priority_encoder_1 (
    .in0(or_2_out), .in1(or_3_out), .in2(or_4_out), .out(priority_encoder_1_out));  // open: in3, gs, en_out, en_in
  Multiplexer #(.width(8), .disabled(0), .enable("false")) multiplexer_2 (
    .in0(rfile_1_rdata), .in1(ilow), .out(multiplexer_2_out), .sel(idec_1_ali));
  Register rtemp (.D(rfile_1_rdata), .en(decoder_1_out0), .Q(rtemp_q), .clk(clk));  // open: clr
  ALU alu_1 (
    .op(instruction[5:3]), .A(rfile_1_a), .B(multiplexer_2_out), .R(alu_1_r), .CMP(alu_1_cmp));  // open: Cin, Cout
  and and_1 (and_1_out, ~alu_1_cmp, decoder_2_out0);  // AND_Gate
  assign controlled_buffer_1_out = idec_1_lda ? controlled_buffer_4_out : 8'bz;  // Controlled_Buffer controlled_buffer_3
  assign controlled_buffer_4_out = nR_W ? rfile_1_rdata : 8'bz;  // Controlled_Buffer controlled_buffer_4
  assign controlled_buffer_1_out = decoder_2_out1 ? atemp_q : 8'bz;  // Controlled_Buffer controlled_buffer_5
  Register atemp (.D(alu_1_r), .en(and_1_out), .Q(atemp_q), .clk(clk));  // open: clr
  assign controlled_buffer_4_out = idec_1_lda ? DIN : 8'bz;  // Controlled_Buffer controlled_buffer_6
  assign DOUT = nR_W ? controlled_buffer_4_out : 8'bz;  // Controlled_Buffer controlled_buffer_7

  assign addr = {ihigh, ilow};

  // Notes on the sheet:
  //   msrc
  //   mdest
endmodule

module idec (
  input  [7:0] Instruction,
  output MOV,
  output MVI,
  output LDA,
  output STA,
  output ALNI,
  output ALI,
  output AL
);

  wire comparator_2_eq, comparator_3_eq, comparator_4_eq, comparator_5_eq, comparator_7_eq;

  Comparator #(.width(2)) comparator_1 (.a(Instruction[7:6]), .b(2'b01), .eq(MOV));  // open: gt, lt
  Comparator #(.width(2)) comparator_2 (.a(Instruction[7:6]), .b(2'b00), .eq(comparator_2_eq));  // open: gt, lt
  Comparator #(.width(3)) comparator_3 (.a(Instruction[2:0]), .b(3'b110), .eq(comparator_3_eq));  // open: gt, lt
  Comparator #(.width(6)) comparator_4 (.a(Instruction[5:0]), .b(6'b111010), .eq(comparator_4_eq));  // open: gt, lt
  Comparator #(.width(6)) comparator_5 (.a(Instruction[5:0]), .b(6'b110010), .eq(comparator_5_eq));  // open: gt, lt
  Comparator #(.width(2)) comparator_6 (.a(Instruction[7:6]), .b(2'b10), .eq(ALNI));  // open: gt, lt
  Comparator #(.width(2)) comparator_7 (.a(Instruction[7:6]), .b(2'b11), .eq(comparator_7_eq));  // open: gt, lt
  Comparator #(.width(3)) comparator_8 (.a(Instruction[2:0]), .b(3'b110));  // open: gt, eq, lt
  and and_1 (MVI, comparator_2_eq, comparator_3_eq);
  and and_2 (LDA, comparator_2_eq, comparator_4_eq);
  and and_3 (STA, comparator_2_eq, comparator_5_eq);
  buf and_4 (ALI, comparator_7_eq);  // AND_Gate
  or or_1 (AL, ALI, ALNI);
  rfile rfile_1 ();  // open: wdata, wen, sel, clk, rst, A, rdata, MHL, HL
endmodule

module rfile (
  input  [7:0] wdata,
  input  wen,
  input  [2:0] sel,
  input  clk,
  input  rst,
  output [7:0] A,
  output [7:0] rdata,
  output MHL,
  output [15:0] HL
);

  wire decoder_1_out0, decoder_1_out1, decoder_1_out2, decoder_1_out3, decoder_1_out4, decoder_1_out5,
       decoder_1_out7;
  wire [7:0] B_q, C_q, D_q, E_q;

  Decoder #(.select(3), .disabled(0)) decoder_1 (
    .out0(decoder_1_out0), .out1(decoder_1_out1), .out2(decoder_1_out2), .out3(decoder_1_out3),
    .out4(decoder_1_out4), .out5(decoder_1_out5), .out6(MHL), .out7(decoder_1_out7), .sel(sel), .en(wen));
  Register u_A (.D(wdata), .en(decoder_1_out7), .Q(A), .clk(clk), .clr(rst));
  Register B (.D(wdata), .en(decoder_1_out0), .Q(B_q), .clk(clk), .clr(rst));
  Register C (.D(wdata), .en(decoder_1_out1), .Q(C_q), .clk(clk), .clr(rst));
  Register D (.D(wdata), .en(decoder_1_out2), .Q(D_q), .clk(clk), .clr(rst));
  Register E (.D(wdata), .en(decoder_1_out3), .Q(E_q), .clk(clk), .clr(rst));
  Register H (.D(wdata), .en(decoder_1_out4), .Q(HL[15:8]), .clk(clk), .clr(rst));
  Register L (.D(wdata), .en(decoder_1_out5), .Q(HL[7:0]), .clk(clk), .clr(rst));
  Multiplexer #(.select(3), .width(8), .disabled(0), .enable("false")) multiplexer_1 (
    .in0(B_q), .in1(C_q), .in2(D_q), .in3(E_q), .in4(HL[15:8]), .in5(HL[7:0]), .in7(A), .out(rdata), .sel(sel));  // open: in6

  // Notes on the sheet:
  //   wen: pull=up
endmodule

module ALU (
  input  Cin,
  input  [7:0] A,
  input  [7:0] B,
  input  [2:0] op,
  output [7:0] R,
  output CMP,
  output Cout
);

  wire adder_1_cout, controlled_buffer_3_out, controlled_buffer_5_out, decoder_1_out0, decoder_1_out1,
       decoder_1_out2, decoder_1_out3, decoder_1_out4, decoder_1_out5, decoder_1_out6, or_1_out, or_2_out,
       subtractor_1_bout;
  wire [7:0] adder_1_out, and_1_out, or_3_out, subtractor_1_out, xor_1_out;

  Decoder #(.select(3), .enable("false")) decoder_1 (
    .out0(decoder_1_out0), .out1(decoder_1_out1), .out2(decoder_1_out2), .out3(decoder_1_out3),
    .out4(decoder_1_out4), .out5(decoder_1_out5), .out6(decoder_1_out6), .out7(CMP), .sel(op));
  assign Cout = or_1_out ? adder_1_cout : 1'bz;  // Controlled_Buffer controlled_buffer_1
  assign Cout = or_2_out ? subtractor_1_bout : 1'bz;  // Controlled_Buffer controlled_buffer_2
  assign controlled_buffer_3_out = decoder_1_out1 ? Cin : 1'bz;  // Controlled_Buffer controlled_buffer_3
  Adder adder_1 (.a(A), .b(B), .out(adder_1_out), .cin(controlled_buffer_3_out), .cout(adder_1_cout));
  assign R = or_1_out ? adder_1_out : 8'bz;  // Controlled_Buffer controlled_buffer_4
  or or_1 (or_1_out, decoder_1_out0, decoder_1_out1);
  assign controlled_buffer_5_out = decoder_1_out3 ? Cin : 1'bz;  // Controlled_Buffer controlled_buffer_5
  assign R = or_2_out ? subtractor_1_out : 8'bz;  // Controlled_Buffer controlled_buffer_6
  Subtractor subtractor_1 (
    .a(A), .b(B), .out(subtractor_1_out), .bin(controlled_buffer_5_out), .bout(subtractor_1_bout));
  or or_2 (or_2_out, decoder_1_out2, CMP, decoder_1_out3);
  assign R = decoder_1_out4 ? and_1_out : 8'bz;  // Controlled_Buffer controlled_buffer_7
  assign and_1_out = A & B;  // AND_Gate and_1, 8 bits wide
  assign R = decoder_1_out5 ? xor_1_out : 8'bz;  // Controlled_Buffer controlled_buffer_8
  assign xor_1_out = A ^ B;  // XOR_Gate xor_1, 8 bits wide
  assign or_3_out = A | B;  // OR_Gate or_3, 8 bits wide
  assign R = decoder_1_out6 ? or_3_out : 8'bz;  // Controlled_Buffer controlled_buffer_9
endmodule
