// Logisim project PLG1.circ as structural Verilog: 3 circuits, main circuit main
module main (
  input  [4:0] Inputs,
  input  \program ,
  input  program_reset,
  input  [31:0] TT_in,
  input  TT_reg_to_HDD,
  input  [24:0] HDD_adress,
  input  HDD_to_TT_reg,
  output \output 
);

  wire clock_1_out, not_1_out, not_2_out, or_1_out;
  wire [31:0] multiplexer_1_out, multiplexer_2_out, multiplexer_3_out, ram_1_data, register_1_q, rom_1_data;

  Multiplexer #(.width(32), .disabled(0), .enable("false")) multiplexer_1 (
    .in0(TT_in), .in1(ram_1_data), .out(multiplexer_1_out), .sel(HDD_to_TT_reg));
  or or_1 (or_1_out, HDD_to_TT_reg, \program );
  Multiplexer #(.width(32), .disabled(0), .enable("false")) multiplexer_2 (
    .in0(multiplexer_3_out), .in1(rom_1_data), .out(multiplexer_2_out), .sel(not_1_out));
  not not_1 (not_1_out, HDD_adress[24]);
  Multiplexer #(.width(32), .disabled(0), .enable("false")) multiplexer_3 (
    .in0(multiplexer_1_out), .in1(ram_1_data), .out(multiplexer_3_out), .sel(HDD_adress[24]));
  not not_2 (not_2_out, TT_reg_to_HDD);
  Register #(.width(32), .trigger("high")) register_1 (
    .D(multiplexer_2_out), .en(or_1_out), .Q(register_1_q), .clk(or_1_out), .clr(program_reset));
  ROM #(.addrWidth(24), .dataWidth(32)) rom_1 (.addr(HDD_adress[23:0]), .data(rom_1_data));  // open: sel
  RAM #(.addrWidth(24), .dataWidth(32), .bus("separate")) ram_1 (
    .addr(HDD_adress[23:0]), .din(register_1_q), .data(ram_1_data), .str(TT_reg_to_HDD), .clk(clock_1_out),
    .ld(not_2_out));  // open: sel, clr
  Clock clock_1 (.out(clock_1_out));
  Multiplexer #(.select(5), .disabled(0), .enable("false")) multiplexer_4 (
    .in0(register_1_q[0]), .in1(register_1_q[1]), .in2(register_1_q[2]), .in3(register_1_q[3]),
    .in4(register_1_q[4]), .in5(register_1_q[5]), .in6(register_1_q[6]), .in7(register_1_q[7]),
    .in8(register_1_q[8]), .in9(register_1_q[9]), .in10(register_1_q[10]), .in11(register_1_q[11]),
    .in12(register_1_q[12]), .in13(register_1_q[13]), .in14(register_1_q[14]), .in15(register_1_q[15]),
    .in16(register_1_q[16]), .in17(register_1_q[17]), .in18(register_1_q[18]), .in19(register_1_q[19]),
    .in20(register_1_q[20]), .in21(register_1_q[21]), .in22(register_1_q[22]), .in23(register_1_q[23]),
    .in24(register_1_q[24]), .in25(register_1_q[25]), .in26(register_1_q[26]), .in27(register_1_q[27]),
    .in28(register_1_q[28]), .in29(register_1_q[29]), .in30(register_1_q[30]), .in31(register_1_q[31]),
    .out(\output ), .sel(Inputs));

  // Other names for the same wires on the sheet: Addr[23:0] = HDD_adress[23:0]

  // Notes on the sheet:
  //   contents of rom_1 (hex, n*v repeats v):
  //   fffffffe 80000000 1 7fffffff 7ffffffe 80000001 55555555 aaaaaaaa
endmodule

module main1 (
  input  [7:0] in_1,
  input  [7:0] in_2,
  input  in_3,
  output out_4
);

  wire and_1_out, and_2_out, and_3_out, and_4_out, and_5_out, and_6_out, and_7_out, and_8_out;
  wire [7:0] register_1_q;

  Register register_1 (.D(in_1), .en(in_3), .Q(register_1_q), .clk(in_3));  // open: clr
  and and_1 (and_1_out, in_2[7], register_1_q[7]);
  and and_2 (and_2_out, in_2[1], register_1_q[1]);
  and and_3 (and_3_out, in_2[2], register_1_q[2]);
  and and_4 (and_4_out, in_2[3], register_1_q[3]);
  and and_5 (and_5_out, in_2[4], register_1_q[4]);
  and and_6 (and_6_out, in_2[5], register_1_q[5]);
  and and_7 (and_7_out, in_2[6], register_1_q[6]);
  and and_8 (and_8_out, in_2[0], register_1_q[0]);
  or or_1 (out_4, and_8_out, and_2_out, and_3_out, and_4_out, and_5_out, and_6_out, and_7_out, and_1_out);
endmodule

module test (
  input  [4:0] Inputs,
  input  [31:0] TT,
  input  [24:0] HDD_ram_adress
);

  wire Clear_TT__reg_out, HDD_to_TT_reg_out, main_1_output, Store_TT__input_out, TT_reg_to_HDD_out;

  Button Store_TT__input (.out(Store_TT__input_out));
  Button Clear_TT__reg (.out(Clear_TT__reg_out));
  Button TT_reg_to_HDD (.out(TT_reg_to_HDD_out));
  Button HDD_to_TT_reg (.out(HDD_to_TT_reg_out));
  LED Output (.in(main_1_output));
  main main_1 (
    .Inputs(Inputs), .\program (Store_TT__input_out), .program_reset(Clear_TT__reg_out), .TT_in(TT),
    .TT_reg_to_HDD(TT_reg_to_HDD_out), .HDD_adress(HDD_ram_adress), .HDD_to_TT_reg(HDD_to_TT_reg_out),
    .\output (main_1_output));

  // Notes on the sheet:
  //   0 = or
  //   1 = and
  //   2 = nor
  //   3 = nand
  //   4 = xor
  //   5 = nxor
  //   6 = even
  //   7 = odd
  //   Pre implemented gates:
endmodule
