// Logisim project TK16v6.circ as structural Verilog: 7 circuits, main circuit main
// CPU
module main (
  input  auto_ex_manual_ex,
  input  [21:0] ins_in
);

  wire and_1_out, keyboard_1_avail, MCLK, mclock_out, not_1_out, not_2_out, not_3_out, q238_1_cleargdisp,
       q238_1_display_write, q238_1_halted, q238_1_invalid_instruction, q238_1_keyboard_read, q238_1_write,
       res_out, res_regs_out, store_out;
  wire [5:0] q238_1_ie;
  wire [6:0] keyboard_1_data, q238_1_address_2, q238_1_ascii_out;
  wire [15:0] multiplexer_1_out, pull_resistor_1_node, q238_1_ac, q238_1_address, q238_1_bc, q238_1_data_out,
       q238_1_pc, q238_1_pcc, q238_1_rc;
  wire [21:0] ram_1_data;

  Keyboard keyboard_1 (
    .clk(MCLK), .re(q238_1_keyboard_read), .avail(keyboard_1_avail), .data(keyboard_1_data));  // open: clr
  not not_1 (not_1_out, store_out);
  RAM #(.addrWidth(16), .dataWidth(22), .bus("separate"), .Select("high")) ram_1 (
    .addr(q238_1_pcc), .din(ins_in), .data(ram_1_data), .str(store_out), .clk(store_out), .ld(not_1_out));  // open: sel, clr
  Pull_Resistor pull_resistor_1 (.node(pull_resistor_1_node));
  Button mclock (.out(mclock_out));
  Button res_regs (.out(res_regs_out));
  Button res (.out(res_out));
  Button store (.out(store_out));
  LED Bad_Instruction (.in(q238_1_invalid_instruction));
  // Probe on q238_1_pcc
  // Probe on q238_1_ie
  // Probe on q238_1_ac
  // Probe on q238_1_bc
  // Probe on q238_1_rc
  // Probe on q238_1_pc
  // Probe on {q238_1_address[15:14], q238_1_address_2, q238_1_address[6:0]}
  // Probe on q238_1_data_out
  // Probe on pull_resistor_1_node
  q238 q238_1 (
    .Write(q238_1_write), .Data_Out(q238_1_data_out), .auto_ex_manual_ex(auto_ex_manual_ex),
    .Address({q238_1_address[15:14], q238_1_address_2, q238_1_address[6:0]}), .ac(q238_1_ac), .bc(q238_1_bc),
    .ascii_in(keyboard_1_data), .av_in(keyboard_1_avail), .ascii_out(q238_1_ascii_out),
    .Data_In(pull_resistor_1_node), .ie(q238_1_ie), .rc(q238_1_rc), .Display_Write(q238_1_display_write),
    .Keyboard_Read(q238_1_keyboard_read), .cleargdisp(q238_1_cleargdisp), .pc(q238_1_pc), .pcc(q238_1_pcc),
    .res_regs(res_regs_out), .Mclock_in(mclock_out), .clock_out(MCLK),
    .invalid_instruction(q238_1_invalid_instruction), .res(res_out), .halted(q238_1_halted),
    .ins_RAM_out(ram_1_data), .instruction_in(ins_in));
  not not_2 (not_2_out, q238_1_address[15]);
  RAM #(.addrWidth(15), .dataWidth(16), .bus("separate"), .Select("high")) ram_2 (
    .addr({q238_1_address[14], q238_1_address_2, q238_1_address[6:0]}), .din(q238_1_data_out),
    .data(pull_resistor_1_node), .str(q238_1_write), .sel(not_2_out), .clk(MCLK), .ld(not_3_out),
    .clr(q238_1_halted));
  not not_3 (not_3_out, q238_1_write);
  Multiplexer #(.width(16), .disabled(0), .enable("false")) multiplexer_1 (
    .in0(q238_1_data_out), .in1({16{1'b0}}), .out(multiplexer_1_out), .sel(q238_1_cleargdisp));
  TTY tty_1 (.data(q238_1_ascii_out), .clk(MCLK), .we(q238_1_display_write));  // open: clr
  and and_1 (and_1_out, q238_1_address[15], q238_1_address[14]);
  // LCD_Video lcd_video_1: pin names not known; wires that end beside it: q238_1_cleargdisp, MCLK, and_1_out, q238_1_address[6:0], q238_1_address_2, multiplexer_1_out

  // Notes on the sheet:
  //   auto_ex_manual_ex: pull=down
endmodule

// CPU
module q238 (
  input  [15:0] Data_In,
  input  [21:0] instruction_in,
  input  res,
  input  auto_ex_manual_ex,
  input  Mclock_in,
  input  av_in,
  input  [6:0] ascii_in,
  input  [21:0] ins_RAM_out,
  input  res_regs,
  output Write,
  output [15:0] Data_Out,
  output [15:0] Address,
  output [15:0] pc,
  output invalid_instruction,
  output [15:0] ac,
  output [5:0] ie,
  output [15:0] bc,
  output clock_out,
  output [15:0] pcc,
  output [15:0] rc,
  output cleargdisp,
  output halted,
  output Keyboard_Read,
  output Display_Write,
  output [6:0] ascii_out
);

  wire alu_1_store_r, clock_1_out, jump_control_1_store_pc, Key_Load, loadstore_1_ram_store,
       loadstore_1_store_a, loadstore_1_store_b, loadstore_1_store_p, loadstore_1_use_p, multiplexer_1_out,
       not_1_out, or_4_out, or_5_out, Program_Counter_p5;
  wire [15:0] adder_1_out, alu_1_r_value, ins_dec_1_a_out, jump_control_1_pcctbl,
       key_and_display_control_1_data_out, loadstore_1_output, multiplexer_4_out, multiplexer_5_out,
       multiplexer_7_out, Program_Counter_p2, stack_1_data_out;
  wire [31:0] ins_dec_1_high_bits, ins_dec_1_low_bits;

  or or_1 (halted, res, Program_Counter_p5);
  Clock clock_1 (.out(clock_1_out));
  Multiplexer #(.disabled(0), .enable("false")) multiplexer_1 (
    .in0(clock_1_out), .in1(Mclock_in), .out(multiplexer_1_out), .sel(auto_ex_manual_ex));
  and and_1 (clock_out, multiplexer_1_out, ~halted);  // AND_Gate
  not not_1 (not_1_out, jump_control_1_store_pc);
  or or_2 (cleargdisp, ins_dec_1_low_bits[27], halted);
  Jump_Control jump_control_1 (
    .PCC(pcc), .Instruction(ins_dec_1_low_bits), .clock(clock_out), .R_Value(rc),
    .PCCtbl(jump_control_1_pcctbl), .Store_PC(jump_control_1_store_pc));
  // Counter #(.width(16), .max('hffff)) Program_Counter: pin names not known; wires that end beside it: jump_control_1_store_pc, Program_Counter_p2, not_1_out, clock_out, Program_Counter_p5, pcc
  or or_3 (Program_Counter_p5, res, ins_dec_1_low_bits[28]);
  Multiplexer #(.width(16), .disabled(0), .enable("false")) multiplexer_2 (
    .in0(Address), .in1(jump_control_1_pcctbl), .out(Program_Counter_p2), .sel(ins_dec_1_low_bits[31]));
  Multiplexer #(.width(16), .disabled(0), .enable("false")) multiplexer_3 (
    .in0(ins_dec_1_a_out), .in1(pc), .out(Address), .sel(or_4_out));
  or or_4 (or_4_out, Key_Load, loadstore_1_use_p);
  Multiplexer #(.width(22), .disabled(0), .enable("false")) multiplexer_4 (
    .in0(ins_RAM_out), .in1(instruction_in), .out({ie, multiplexer_4_out}), .sel(auto_ex_manual_ex));
  Key_and_Display_Control key_and_display_control_1 (
    .ASCII_In(ascii_in), .M_Value(Data_In), .Instruction(ins_dec_1_low_bits),
    .Data_Out(key_and_display_control_1_data_out), .Memory_Write(Key_Load), .Keyboard_Enable(Keyboard_Read),
    .Display_Enable(Display_Write), .ASCII_Out(ascii_out));
  ins_dec ins_dec_1 (
    .ins_in({ie, multiplexer_4_out}), .a_out(ins_dec_1_a_out), .low_bits(ins_dec_1_low_bits),
    .high_bits(ins_dec_1_high_bits), .inv_ins(invalid_instruction));
  Pull_Resistor pull_resistor_1 (.node(ins_dec_1_a_out));
  Pull_Resistor pull_resistor_2 (.node(ins_dec_1_low_bits));
  LoadStore loadstore_1 (
    .RAM_In(Data_In), .Address(ins_dec_1_a_out), .Register_R(rc), .Codes(ins_dec_1_low_bits),
    .Use_P(loadstore_1_use_p), .Output(loadstore_1_output), .RAM_Store(loadstore_1_ram_store),
    .Store_A(loadstore_1_store_a), .Store_B(loadstore_1_store_b), .Store_P(loadstore_1_store_p));
  or or_5 (or_5_out, ins_dec_1_low_bits[29], loadstore_1_store_p);
  or or_6 (Write, Key_Load, ins_dec_1_high_bits[1], loadstore_1_ram_store);
  Register #(.width(16), .Select("low")) Register_P (
    .D(multiplexer_7_out), .en(or_5_out), .Q(pc), .clk(clock_out), .clr(res_regs));
  Register #(.width(16), .Select("low")) Register_A (
    .D(loadstore_1_output), .en(loadstore_1_store_a), .Q(ac), .clk(clock_out), .clr(res_regs));
  Register #(.width(16), .Select("low")) Register_B (
    .D(loadstore_1_output), .en(loadstore_1_store_b), .Q(bc), .clk(clock_out), .clr(res_regs));
  Register #(.width(16), .Select("low")) Register_R (
    .D(alu_1_r_value), .en(alu_1_store_r), .Q(rc), .clk(clock_out), .clr(res_regs));
  Multiplexer #(.width(16), .enable("false")) multiplexer_5 (
    .in0(loadstore_1_output), .in1(key_and_display_control_1_data_out), .out(multiplexer_5_out),
    .sel(Key_Load));
  Multiplexer #(.width(16), .disabled(0), .enable("false")) multiplexer_6 (
    .in0(multiplexer_5_out), .in1(stack_1_data_out), .out(Data_Out), .sel(ins_dec_1_high_bits[1]));
  Adder #(.width(16)) adder_1 (.a(pc), .b(ins_dec_1_a_out), .out(adder_1_out));  // open: cin, cout
  Multiplexer #(.width(16), .disabled(0), .enable("false")) multiplexer_7 (
    .in0(loadstore_1_output), .in1(adder_1_out), .out(multiplexer_7_out), .sel(ins_dec_1_low_bits[29]));
  Stack stack_1 (
    .Data_In(Data_In), .Push(ins_dec_1_high_bits[0]), .Pop(ins_dec_1_high_bits[1]),
    .Stack_Reset(ins_dec_1_high_bits[3]), .Data_Out(stack_1_data_out),
    .Clear_Popped_Value(ins_dec_1_high_bits[2]));
  ALU alu_1 (.b(bc), .a(ac), .ins(ins_dec_1_low_bits), .R_Value(alu_1_r_value), .Store_R(alu_1_store_r));

  // Other names for the same wires on the sheet: CLK = clock_out; M[15:0] = Data_In; R[15:0] = rc

  // Notes on the sheet:
  //   Mclock_in: pull=down
  //   res_regs: pull=down
  //   Jump Control
  //   Load/Store
  //   ALU
endmodule

module Jump_Control (
  input  [15:0] R_Value,
  input  clock,
  input  [15:0] PCC,
  input  [31:0] Instruction,
  output [15:0] PCCtbl,
  output Store_PC
);

  wire and_1_out, and_2_out, comparator_1_eq, not_1_out, not_2_out, or_1_out;
  wire [15:0] ram_1_data;
  wire [23:0] counter_1_p4;

  Comparator #(.width(16)) comparator_1 (.a({16{1'b0}}), .b(R_Value), .eq(comparator_1_eq));  // open: gt, lt
  not not_1 (not_1_out, comparator_1_eq);
  and and_1 (and_1_out, not_1_out, Instruction[26]);
  and and_2 (and_2_out, comparator_1_eq, Instruction[25]);
  or or_1 (or_1_out, Instruction[31], Instruction[30]);
  or or_2 (Store_PC, and_1_out, Instruction[31], and_2_out, Instruction[30], Instruction[24]);
  // Counter #(.width(24), .max('hffffff), .ongoal("stay"), .trigger("falling")) counter_1: pin names not known; wires that end beside it: Instruction[31], or_1_out, clock, counter_1_p4
  RAM #(.addrWidth(24), .dataWidth(16), .bus("separate"), .Select("high")) ram_1 (
    .addr(counter_1_p4), .din(PCC), .data(ram_1_data), .str(Instruction[30]), .clk(clock), .ld(not_2_out));  // open: sel, clr
  not not_2 (not_2_out, Instruction[30]);
  Adder #(.width(16)) adder_1 (.a(ram_1_data), .b(16'h1), .out(PCCtbl));  // open: cin, cout
endmodule

module ins_dec (
  input  [21:0] ins_in,
  output [15:0] a_out,
  output [31:0] low_bits,
  output [31:0] high_bits,
  output inv_ins
);

  wire decoder_1_out0, decoder_1_out1, decoder_1_out2, decoder_1_out3;

  Pull_Resistor pull_resistor_1 (.node(ins_in[19:16]));
  Pull_Resistor pull_resistor_2 (.node(ins_in[21:20]));
  Decoder #(.select(2), .enable("false")) decoder_1 (
    .out0(decoder_1_out0), .out1(decoder_1_out1), .out2(decoder_1_out2), .out3(decoder_1_out3),
    .sel(ins_in[21:20]));
  Decoder #(.select(4), .disabled(0)) decoder_2 (
    .out0(low_bits[0]), .out1(low_bits[1]), .out2(low_bits[2]), .out3(low_bits[3]), .out4(low_bits[4]),
    .out5(low_bits[5]), .out6(low_bits[6]), .out7(low_bits[7]), .out8(low_bits[8]), .out9(low_bits[9]),
    .out10(low_bits[10]), .out11(low_bits[11]), .out12(low_bits[12]), .out13(low_bits[13]),
    .out14(low_bits[14]), .out15(low_bits[15]), .sel(ins_in[19:16]), .en(decoder_1_out0));
  Decoder #(.select(4), .disabled(0)) decoder_3 (
    .out0(high_bits[0]), .out1(high_bits[1]), .out2(high_bits[2]), .out3(high_bits[3]), .out4(high_bits[4]),
    .out5(high_bits[5]), .out6(high_bits[6]), .out7(high_bits[7]), .out8(high_bits[8]), .out9(high_bits[9]),
    .out10(high_bits[10]), .out11(high_bits[11]), .out12(high_bits[12]), .out13(high_bits[13]),
    .out14(high_bits[14]), .out15(high_bits[15]), .sel(ins_in[19:16]), .en(decoder_1_out2));
  Decoder #(.select(4), .disabled(0)) decoder_4 (
    .out0(high_bits[16]), .out1(high_bits[17]), .out2(high_bits[18]), .out3(high_bits[19]),
    .out4(high_bits[20]), .out5(high_bits[21]), .out6(high_bits[22]), .out7(high_bits[23]),
    .out8(high_bits[24]), .out9(high_bits[25]), .out10(high_bits[26]), .out11(high_bits[27]),
    .out12(high_bits[28]), .out13(high_bits[29]), .out14(high_bits[30]), .out15(high_bits[31]),
    .sel(ins_in[19:16]), .en(decoder_1_out3));
  Decoder #(.select(4), .disabled(0)) decoder_5 (
    .out0(low_bits[16]), .out1(low_bits[17]), .out2(low_bits[18]), .out3(low_bits[19]), .out4(low_bits[20]),
    .out5(low_bits[21]), .out6(low_bits[22]), .out7(low_bits[23]), .out8(low_bits[24]), .out9(low_bits[25]),
    .out10(low_bits[26]), .out11(low_bits[27]), .out12(low_bits[28]), .out13(low_bits[29]),
    .out14(low_bits[30]), .out15(low_bits[31]), .sel(ins_in[19:16]), .en(decoder_1_out1));
  or or_1 (inv_ins, high_bits[4], high_bits[5], high_bits[6], high_bits[7], high_bits[8], high_bits[9], high_bits[10], high_bits[11], high_bits[12], high_bits[13], high_bits[14], high_bits[15], high_bits[16], high_bits[17], high_bits[19], high_bits[20], high_bits[21], high_bits[22], high_bits[23], high_bits[24], high_bits[25], high_bits[26], high_bits[27], high_bits[28], high_bits[29], high_bits[30], high_bits[31], high_bits[18]);

  assign a_out = ins_in[15:0];
endmodule

module LoadStore (
  input  [15:0] RAM_In,
  input  [15:0] Address,
  input  [15:0] Register_R,
  input  [31:0] Codes,
  output [15:0] Output,
  output RAM_Store,
  output Store_A,
  output Store_B,
  output Store_P,
  output Use_P
);

  wire or_1_out, or_2_out;
  wire [15:0] multiplexer_1_out;

  or or_1 (or_1_out, Codes[4], Codes[3]);
  Multiplexer #(.width(16), .enable("false")) multiplexer_1 (
    .in0(RAM_In), .in1(Address), .out(multiplexer_1_out), .sel(or_1_out));
  or or_2 (or_2_out, Codes[5], Codes[11], Codes[2]);
  Multiplexer #(.width(16), .disabled(0), .enable("false")) multiplexer_2 (
    .in0(multiplexer_1_out), .in1(Register_R), .out(Output), .sel(or_2_out));
  or or_3 (Use_P, Codes[7], Codes[11], Codes[6]);
  or or_4 (RAM_Store, Codes[2], Codes[8], Codes[11]);
  or or_5 (Store_A, Codes[0], Codes[3], Codes[6]);
  or or_6 (Store_B, Codes[1], Codes[4], Codes[7]);

  assign Store_P = Codes[5];

  // Notes on the sheet:
  //   Store_P: pull=down
  //   Address: pull=down
  //   Store_A: pull=down
  //   RAM_In: pull=down
  //   Output: pull=down
  //   Use_P: pull=down
  //   Register_R: pull=down
  //   Codes: pull=down
  //   RAM_Store: pull=down
  //   Store_B: pull=down
endmodule

module ALU (
  input  [15:0] b,
  input  [15:0] a,
  input  [31:0] ins,
  output [15:0] R_Value,
  output Store_R
);

  wire or_2_out, or_3_out, or_4_out;
  wire [15:0] adder_1_out, and_1_out, divider_1_out, multiplier_1_out, negator_1_out, or_1_out,
       shifter_1_out, shifter_2_out, subtractor_1_out;

  assign R_Value = ins[20] ? shifter_1_out : 16'bz;  // Controlled_Buffer controlled_buffer_1
  Shifter #(.width(16)) shifter_1 (.in(a), .\dist (b[3:0]), .out(shifter_1_out));
  assign R_Value = ins[21] ? shifter_2_out : 16'bz;  // Controlled_Buffer controlled_buffer_2
  Shifter #(.width(16), .shift("lr")) shifter_2 (.in(a), .\dist (b[3:0]), .out(shifter_2_out));
  Adder #(.width(16)) adder_1 (.a(a), .b(b), .out(adder_1_out));  // open: cin, cout
  assign R_Value = ins[12] ? adder_1_out : 16'bz;  // Controlled_Buffer controlled_buffer_3
  Subtractor #(.width(16)) subtractor_1 (.a(a), .b(b), .out(subtractor_1_out));  // open: bin, bout
  assign R_Value = ins[13] ? subtractor_1_out : 16'bz;  // Controlled_Buffer controlled_buffer_4
  assign R_Value = ins[14] ? multiplier_1_out : 16'bz;  // Controlled_Buffer controlled_buffer_5
  Multiplier #(.width(16)) multiplier_1 (.a(a), .b(b), .out(multiplier_1_out));  // open: cin, cout
  Divider #(.width(16)) divider_1 (.a(a), .b(b), .out(divider_1_out));  // open: upper, rem
  assign R_Value = ins[15] ? divider_1_out : 16'bz;  // Controlled_Buffer controlled_buffer_6
  Negator #(.width(16)) negator_1 (.in(a), .out(negator_1_out));
  assign R_Value = ins[16] ? negator_1_out : 16'bz;  // Controlled_Buffer controlled_buffer_7
  assign R_Value = ins[17] ? and_1_out : 16'bz;  // Controlled_Buffer controlled_buffer_8
  assign and_1_out = a & b;  // AND_Gate and_1, 16 bits wide
  assign or_1_out = a | b;  // OR_Gate or_1, 16 bits wide
  assign R_Value = ins[18] ? or_1_out : 16'bz;  // Controlled_Buffer controlled_buffer_9
  assign R_Value = ins[19] ? ~a : 16'bz;  // Controlled_Inverter controlled_inverter_1
  assign R_Value = ins[22] ? a : 16'bz;  // Controlled_Buffer controlled_buffer_10
  assign R_Value = ins[23] ? b : 16'bz;  // Controlled_Buffer controlled_buffer_11
  or or_2 (or_2_out, ins[12], ins[13], ins[14], ins[15]);
  or or_3 (or_3_out, ins[16], ins[17], ins[18], ins[19]);
  or or_4 (or_4_out, ins[20], ins[21], ins[22], ins[23]);
  or or_5 (Store_R, or_2_out, or_3_out, or_4_out);
endmodule

module Key_and_Display_Control (
  input  [6:0] ASCII_In,
  input  [15:0] M_Value,
  input  [31:0] Instruction,
  output [15:0] Data_Out,
  output Memory_Write,
  output Keyboard_Enable,
  output Display_Enable,
  output [6:0] ASCII_Out
);

  wire [15:7] multiplexer_1_out;

  Multiplexer #(.width(16), .disabled(0), .enable("false")) multiplexer_1 (
    .in0(M_Value), .in1({{9{1'b0}}, ASCII_In}), .out({multiplexer_1_out, ASCII_Out}), .sel(Instruction[10]));
  or or_1 (Keyboard_Enable, Instruction[8], Instruction[10]);
  or or_2 (Display_Enable, Instruction[10], Instruction[9]);

  assign Data_Out = {{9{1'b0}}, ASCII_In};
  assign Memory_Write = Instruction[8];

  // Notes on the sheet:
  //   Instruction: pull=down
  //   ASCII_Out: pull=down
  //   Keyboard_Enable: pull=down
  //   Display_Enable: pull=down
  //   Memory_Write: pull=down
  //   M_Value: pull=down
  //   Data_Out: pull=down
  //   ASCII_In: pull=down
endmodule
