// Logisim project TKStack16.circ as structural Verilog: 2 circuits, main circuit Stack
module Stack (
  input  [15:0] Data_In,
  input  Push,
  input  Pop,
  input  Stack_Reset,
  input  Clear_Popped_Value,
  output [15:0] Data_Out
);

  wire buffer_1_out, buffer_2_out, buffer_3_out, Clear_Popped_Value_out, clock_1_out,
       controlled_buffer_2_out, counter_1_q, not_1_out, or_1_out, or_2_out, or_3_out, or_4_out, or_5_out,
       or_6_out, or_7_out, or_8_out, or_9_out, Pop_out, pull_resistor_1_node, Push_out, s_r_ff_1_q,
       Stack_Reset_out, t_ff_1_q;
  wire [15:0] multiplexer_1_out, multiplexer_2_out, ram_1_data;
  wire [23:0] counter_2_q;

  Button u_Push (.out(Push_out));
  Button u_Pop (.out(Pop_out));
  Pull_Resistor pull_resistor_1 (.node(pull_resistor_1_node));
  or or_1 (or_1_out, Push_out, Push);
  assign pull_resistor_1_node = or_9_out ? or_1_out : 1'bz;  // Controlled_Buffer controlled_buffer_1
  or or_2 (or_2_out, Pop_out, Pop);
  assign controlled_buffer_2_out = s_r_ff_1_q ? or_2_out : 1'bz;  // Controlled_Buffer controlled_buffer_2
  Pull_Resistor pull_resistor_2 (.node(controlled_buffer_2_out));
  Button u_Stack_Reset (.out(Stack_Reset_out));
  or or_3 (or_3_out, Stack_Reset_out, Stack_Reset);
  Button u_Clear_Popped_Value (.out(Clear_Popped_Value_out));
  T_Flip_Flop t_ff_1 (.clk(clock_1_out), .T(counter_1_q), .Q(t_ff_1_q), .preset(t_ff_1_q));  // open: Qn, reset, en
  or or_4 (or_4_out, pull_resistor_1_node, controlled_buffer_2_out);
  or or_5 (or_5_out, Clear_Popped_Value, Clear_Popped_Value_out);
  Counter #(.width(1), .max('h1)) counter_1 (
    .count(clock_1_out), .Q(counter_1_q), .clk(clock_1_out), .clr(t_ff_1_q));  // open: load, D, carry
  or or_6 (or_6_out, counter_1_q, or_5_out);
  Clock clock_1 (.out(clock_1_out));
  Multiplexer #(.width(16), .enable("false")) multiplexer_1 (
    .in0(Data_In), .in1(ram_1_data), .out(multiplexer_1_out), .sel(controlled_buffer_2_out));
  Counter #(.width(24), .max('hffffff), .ongoal("stay")) counter_2 (
    .load(controlled_buffer_2_out), .count(or_4_out), .Q(counter_2_q), .clk(or_4_out), .clr(or_3_out));  // open: D, carry
  S_R_Flip_Flop s_r_ff_1 (
    .S(or_6_out), .clk(clock_1_out), .R(controlled_buffer_2_out), .Q(s_r_ff_1_q));  // open: Qn, preset, reset, en
  buf buffer_1 (buffer_1_out, controlled_buffer_2_out);
  Multiplexer #(.width(16), .disabled(0), .enable("false")) multiplexer_2 (
    .in0(Data_In), .in1({16{1'b0}}), .out(multiplexer_2_out), .sel(or_5_out));
  or or_7 (or_7_out, pull_resistor_1_node, or_5_out);
  buf buffer_2 (buffer_2_out, or_7_out);
  not not_1 (not_1_out, buffer_3_out);
  buf buffer_3 (buffer_3_out, buffer_2_out);
  Register #(.width(16), .trigger("high")) register_1 (
    .D(multiplexer_1_out), .en(buffer_1_out), .Q(Data_Out), .clk(buffer_1_out), .clr(or_8_out));
  RAM #(.addrWidth(24), .dataWidth(16), .bus("separate")) ram_1 (
    .addr(counter_2_q), .din(multiplexer_2_out), .data(ram_1_data), .str(buffer_3_out), .clk(buffer_3_out),
    .ld(not_1_out), .clr(or_3_out));  // open: sel
  or or_8 (or_8_out, or_3_out, or_5_out);
  or or_9 (or_9_out, Data_In[0], Data_In[1], Data_In[2], Data_In[3], Data_In[4], Data_In[5], Data_In[6], Data_In[7], Data_In[9], Data_In[10], Data_In[11], Data_In[12], Data_In[13], Data_In[14], Data_In[15], Data_In[8]);
endmodule

module test (
  input  [15:0] Data_In,
  input  [23:0] RAM_adress,
  input  View_RAM,
  output [15:0] Data_out
);

  wire Clear_Popped_Value_out, clock_1_out, nor_1_out, not_1_out, or_1_out, or_2_out, pop, Push_out,
       RAM_Pop_out, RAM_Push_out, Stack_Reset_out;
  wire [15:0] multiplexer_1_out, ram_1_data, stack_1_data_out;

  Button RAM_Push (.out(RAM_Push_out));
  Button Push (.out(Push_out));
  Button u_Pop (.out(pop));
  Button RAM_Pop (.out(RAM_Pop_out));
  Button Clear_Popped_Value (.out(Clear_Popped_Value_out));
  Button Stack_Reset (.out(Stack_Reset_out));
  or or_1 (or_1_out, RAM_Push_out, Push_out);
  Multiplexer #(.width(16), .disabled(0), .enable("false")) multiplexer_1 (
    .in0(Data_In), .in1(Data_out), .out(multiplexer_1_out), .sel(RAM_Push_out));
  Stack stack_1 (
    .Data_In(multiplexer_1_out), .Push(or_1_out), .Pop(or_2_out), .Stack_Reset(Stack_Reset_out),
    .Data_Out(stack_1_data_out), .Clear_Popped_Value(Clear_Popped_Value_out));
  nor nor_1 (nor_1_out, View_RAM, RAM_Push_out);
  or or_2 (or_2_out, pop, RAM_Pop_out);
  not not_1 (not_1_out, RAM_Pop_out);
  Clock clock_1 (.out(clock_1_out));
  RAM #(.addrWidth(24), .dataWidth(16), .bus("separate")) ram_1 (
    .addr(RAM_adress), .din(stack_1_data_out), .data(ram_1_data), .str(RAM_Pop_out), .clk(clock_1_out),
    .ld(not_1_out));  // open: sel, clr
  Multiplexer #(.width(16), .enable("false")) multiplexer_2 (
    .in0(ram_1_data), .in1(stack_1_data_out), .out(Data_out), .sel(nor_1_out));

  // Notes on the sheet:
  //   View_RAM: pull=down
  //   Data RAM
endmodule
