// Logisim project auto text editor.circ as structural Verilog: 2 circuits, main circuit test
module test (
  input  Loop
);

  wire and_1_out, clock_1_out, clock_2_out, clock_3_out, clr_out, counter_1_carry, keyboard_1_avail,
       n6345_1_disp_clock_en, n6345_1_zero, or_1_out, res_out;
  wire [6:0] keyboard_1_data, n6345_1_ascii_out;

  Clock clock_1 (.out(clock_1_out));
  Keyboard #(.buflen(200)) keyboard_1 (
    .clk(clock_1_out), .clr(or_1_out), .avail(keyboard_1_avail), .data(keyboard_1_data));  // open: re
  Button clr (.out(clr_out));
  Button res (.out(res_out));
  and and_1 (and_1_out, n6345_1_zero, Loop);
  or or_1 (or_1_out, counter_1_carry, res_out);
  Clock clock_2 (.out(clock_2_out));
  _6345 u_6345_1 (
    .clr(clr_out), .reset(or_1_out), .ASCII_in(keyboard_1_data), .av_in(keyboard_1_avail),
    .ASCII_out(n6345_1_ascii_out), .zero(n6345_1_zero), .disp_clock_en(n6345_1_disp_clock_en));
  Counter #(.width(3), .max('h5)) counter_1 (
    .count(and_1_out), .carry(counter_1_carry), .clk(clock_2_out), .clr(counter_1_carry));  // open: load, D, Q
  TTY #(.cols(40)) tty_1 (.data(n6345_1_ascii_out), .clk(clock_3_out), .we(n6345_1_disp_clock_en), .clr(or_1_out));
  Clock clock_3 (.out(clock_3_out));
endmodule

module _6345 (
  input  clr,
  input  reset,
  input  [6:0] ASCII_in,
  input  av_in,
  output [6:0] ASCII_out,
  output zero,
  output disp_clock_en
);

  wire and_1_out, clock_1_out, clock_2_out, not_1_out;
  wire [6:0] ram_1_data;
  wire [23:0] counter_1_q;

  Counter #(.width(24), .max('hffffff)) counter_1 (
    .count(and_1_out), .Q(counter_1_q), .clk(clock_1_out), .clr(reset));  // open: load, D, carry
  Clock clock_1 (.out(clock_1_out));
  and and_1 (and_1_out, disp_clock_en, ~reset);  // AND_Gate
  Clock clock_2 (.out(clock_2_out));
  not not_1 (not_1_out, av_in);
  RAM #(.addrWidth(24), .dataWidth(7), .bus("separate")) ram_1 (
    .addr(counter_1_q), .din(ASCII_in), .data(ram_1_data), .str(av_in), .clk(clock_2_out), .ld(not_1_out),
    .clr(clr));  // open: sel
  Multiplexer #(.width(7), .disabled(0), .enable("false")) multiplexer_1 (
    .in0(ram_1_data), .in1(ASCII_in), .out(ASCII_out), .sel(av_in));
  or or_1 (disp_clock_en, ASCII_out[0], ASCII_out[1], ASCII_out[2], ASCII_out[3], ASCII_out[4], ASCII_out[5], ASCII_out[6]);
  not not_2 (zero, disp_clock_en);

  // Notes on the sheet:
  //   reset: pull=down
endmodule
