// Logisim project cass_logic.circ as structural Verilog: 1 circuit, main circuit main
module main (
  input  Cartridge_in,
  input  Ready,
  output Motor_direction,
  output Cassete_motor,
  output Head_in,
  output Head_side
);

  wire and_1_out, and_2_out, and_3_out, and_4_out, and_5_out, and_6_out, and_7_out, Autostop_out,
       controlled_buffer_1_out, d_ff_1_q, Eject_out, Fast_forward_out, Flip_heads_out, not_1_out, not_2_out,
       or_1_out, or_2_out, or_3_out, or_5_out, Play_out, Rewind_out, s_r_ff_2_q, s_r_ff_3_q, s_r_ff_4_q,
       s_r_ff_4_qn, Stop_out;

  Button Play (.out(Play_out));
  Button Stop (.out(Stop_out));
  Button Rewind (.out(Rewind_out));
  Button Fast_forward (.out(Fast_forward_out));
  Button Eject (.out(Eject_out));
  Button Flip_heads (.out(Flip_heads_out));
  Button Autostop (.out(Autostop_out));
  and and_1 (and_1_out, Play_out, Ready);
  and and_2 (and_2_out, Stop_out, Ready);
  and and_3 (and_3_out, Rewind_out, Ready);
  and and_4 (and_4_out, Fast_forward_out, Ready);
  and and_5 (and_5_out, Eject_out, Ready);
  and and_6 (and_6_out, Flip_heads_out, ~Head_in);  // AND_Gate
  and and_7 (and_7_out, Cartridge_in, ~d_ff_1_q, ~Ready);  // AND_Gate
  S_R_Flip_Flop s_r_ff_1 (.Q(Head_in), .preset(and_1_out), .reset(or_1_out));  // open: S, clk, R, Qn, en
  or or_1 (or_1_out, or_2_out, and_2_out);
  S_R_Flip_Flop s_r_ff_2 (.Q(s_r_ff_2_q), .preset(and_3_out), .reset(or_2_out));  // open: S, clk, R, Qn, en
  or or_2 (or_2_out, Autostop_out, and_2_out);
  S_R_Flip_Flop s_r_ff_3 (.Q(s_r_ff_3_q), .preset(and_4_out), .reset(or_3_out));  // open: S, clk, R, Qn, en
  or or_3 (or_3_out, Autostop_out, and_2_out);
  S_R_Flip_Flop s_r_ff_4 (
    .Q(s_r_ff_4_q), .Qn(s_r_ff_4_qn), .preset(and_5_out), .reset(not_1_out));  // open: S, clk, R, en
  not not_1 (not_1_out, Ready);
  or or_4 (Motor_direction, s_r_ff_4_q, controlled_buffer_1_out, s_r_ff_2_q);
  or or_5 (or_5_out, Autostop_out, and_6_out);
  D_Flip_Flop d_ff_1 (.clk(s_r_ff_4_qn), .D(1'b1), .Q(d_ff_1_q), .reset(not_2_out));  // open: Qn, preset, en
  or or_6 (Cassete_motor, and_7_out, Head_in, s_r_ff_3_q, s_r_ff_4_q, s_r_ff_2_q);
  T_Flip_Flop t_ff_1 (.clk(or_5_out), .T(or_5_out), .Q(Head_side), .reset(and_5_out));  // open: Qn, preset, en
  not not_2 (not_2_out, Cartridge_in);
  assign controlled_buffer_1_out = Head_in ? Head_side : 1'bz;  // Controlled_Buffer controlled_buffer_1
  Pull_Resistor pull_resistor_1 (.node(controlled_buffer_1_out));
endmodule
