// Logisim project computer.circ as structural Verilog: 3 circuits, main circuit main
module cpu (
  input  [15:0] ins,
  input  clk,
  input  rst,
  input  [7:0] d_in,
  output [7:0] iaddr,
  output [6:0] waddr,
  output [6:0] addr,
  output [7:0] d_out,
  output nR_W
);

  wire and_1_out, and_2_out, comparator_1_eq, decoder_1_out0, decoder_1_out1, not_1_out, pdecoder_1_r_nw,
       pdecoder_2_r_nw, pdecoder_3_en, pdecoder_3_r_nw, pdecoder_4_en, pdecoder_4_r_nw;
  wire [1:0] counter_1_q;
  wire [7:0] adder_1_out, controlled_buffer_1_out, controlled_buffer_2_out, controlled_buffer_3_out,
       pdecoder_4_d_in_2, register_1_q, register_2_q, register_3_q, register_4_q;

  Decoder #(.select(2)) decoder_1 (
    .out0(decoder_1_out0), .out1(decoder_1_out1), .sel(counter_1_q));  // open: out2, out3, en
  Counter #(.width(2), .max('h2)) counter_1 (
    .count(pdecoder_3_en), .Q(counter_1_q), .clk(and_1_out), .clr(rst));  // open: load, D, carry
  and and_1 (and_1_out, clk, ~comparator_1_eq);  // AND_Gate
  Register register_1 (.D(controlled_buffer_3_out), .en(decoder_1_out0), .Q(register_1_q), .clk(and_1_out), .clr(rst));
  Adder adder_1 (.a(register_1_q), .b(controlled_buffer_3_out), .out(adder_1_out));  // open: cin, cout
  and and_2 (and_2_out, ~pdecoder_4_r_nw, pdecoder_4_en);  // AND_Gate
  Counter counter_2 (
    .load(and_2_out), .D(pdecoder_4_d_in_2), .count(not_1_out), .Q(iaddr), .clk(and_1_out), .clr(rst));  // open: carry
  not not_1 (not_1_out, and_2_out);
  assign controlled_buffer_1_out = pdecoder_1_r_nw ? register_2_q : 8'bz;  // Controlled_Buffer controlled_buffer_1
  Register register_2 (.D(controlled_buffer_1_out), .Q(register_2_q), .clk(and_1_out), .clr(rst));  // open: en
  assign controlled_buffer_2_out = pdecoder_2_r_nw ? register_3_q : 8'bz;  // Controlled_Buffer controlled_buffer_2
  Register register_3 (.D(controlled_buffer_2_out), .Q(register_3_q), .clk(and_1_out), .clr(rst));  // open: en
  assign controlled_buffer_3_out = pdecoder_3_r_nw ? register_4_q : 8'bz;  // Controlled_Buffer controlled_buffer_3
  Register register_4 (.D(adder_1_out), .en(decoder_1_out1), .Q(register_4_q), .clk(and_1_out), .clr(rst));
  pdecoder pdecoder_1 (
    .dev_addr({7{1'b0}}), .d_in_2(controlled_buffer_1_out), .d_out_2(controlled_buffer_1_out),
    .R_nW(pdecoder_1_r_nw), .waddr(waddr), .addr(ins[14:8]), .d_out(d_in), .d_in(d_in), .nR_W(ins[15]));  // open: En
  pdecoder pdecoder_2 (
    .dev_addr(7'b0000001), .d_in_2(controlled_buffer_2_out), .d_out_2(controlled_buffer_2_out),
    .R_nW(pdecoder_2_r_nw), .waddr(waddr), .addr(ins[14:8]), .d_out(d_in), .d_in(d_in), .nR_W(ins[15]));  // open: En
  pdecoder pdecoder_3 (
    .dev_addr(7'b0000010), .d_in_2(controlled_buffer_3_out), .d_out_2(controlled_buffer_3_out),
    .R_nW(pdecoder_3_r_nw), .En(pdecoder_3_en), .waddr(waddr), .addr(ins[14:8]), .d_out(d_in), .d_in(d_in),
    .nR_W(ins[15]));
  pdecoder pdecoder_4 (
    .dev_addr(7'b0000011), .d_in_2(pdecoder_4_d_in_2), .d_out_2(pdecoder_4_d_in_2), .R_nW(pdecoder_4_r_nw),
    .En(pdecoder_4_en), .waddr(waddr), .addr(ins[14:8]), .d_out(d_in), .d_in(d_in), .nR_W(ins[15]));
  Bit_Extender #(.out_width(7)) bit_extender_1 (.in(ins[7:0]), .out(waddr));
  assign d_in = ins[15] ? ins[7:0] : 8'bz;  // Controlled_Buffer controlled_buffer_4
  Comparator #(.width(16)) comparator_1 (.a(ins), .b({16{1'b1}}), .eq(comparator_1_eq));  // open: gt, lt
  // Probe on d_in
  Bit_Extender #(.out_width(7)) bit_extender_2 ();  // open: in, out

  assign addr = ins[14:8];
  assign d_out = d_in;
  assign nR_W = ins[15];
endmodule

module pdecoder (
  input  [6:0] waddr,
  input  [6:0] addr,
  input  [7:0] d_out,
  input  [6:0] dev_addr,
  input  [7:0] d_out_2,
  input  nR_W,
  output [7:0] d_in,
  output [7:0] d_in_2,
  output R_nW,
  output En
);

  wire and_1_out, and_2_out, and_3_out, and_4_out, comparator_1_eq, comparator_2_eq, comparator_3_eq,
       multiplexer_1_out;

  Comparator #(.width(7)) comparator_1 (.a(waddr), .b(addr), .eq(comparator_1_eq));  // open: gt, lt
  Comparator #(.width(7)) comparator_2 (.a(waddr), .b(dev_addr), .eq(comparator_2_eq));  // open: gt, lt
  Comparator #(.width(7)) comparator_3 (.a(addr), .b(dev_addr), .eq(comparator_3_eq));  // open: gt, lt
  Multiplexer #(.disabled(0), .enable("false")) multiplexer_1 (
    .in0(nR_W), .in1(1'b1), .out(multiplexer_1_out), .sel(and_1_out));
  and and_1 (and_1_out, ~comparator_1_eq, comparator_2_eq);  // AND_Gate
  and and_2 (and_2_out, and_1_out, ~nR_W);  // AND_Gate
  or or_1 (En, comparator_3_eq, and_2_out);
  and and_3 (and_3_out, En, ~multiplexer_1_out);  // AND_Gate
  assign d_in = and_3_out ? d_out_2 : 8'bz;  // Controlled_Buffer controlled_buffer_1
  and and_4 (and_4_out, En, multiplexer_1_out);
  assign d_in_2 = and_4_out ? d_out : 8'bz;  // Controlled_Buffer controlled_buffer_2
  not not_1 (R_nW, multiplexer_1_out);
endmodule

module main (
);

  wire clock_1_out, counter_1_q, cpu_1_nr_w, decoder_1_out0, decoder_1_out1, or_1_out, pdecoder_1_en,
       pdecoder_1_r_nw, Reset_and_clear_RAM_out, Reset_out;
  wire [6:0] cpu_1_addr, cpu_1_waddr;
  wire [7:0] cpu_1_d_out, cpu_1_iaddr, pdecoder_1_d_in, ram_1_data, register_1_q;
  wire [15:0] rom_1_data;

  Counter #(.width(1), .max('h1)) counter_1 (
    .count(pdecoder_1_en), .Q(counter_1_q), .clk(clock_1_out), .clr(or_1_out));  // open: load, D, carry
  Register register_1 (.D(ram_1_data), .en(decoder_1_out0), .Q(register_1_q), .clk(clock_1_out), .clr(or_1_out));
  Decoder #(.disabled(0), .enable("false")) decoder_1 (.out0(decoder_1_out0), .out1(decoder_1_out1), .sel(counter_1_q));
  RAM ram_1 (
    .addr(register_1_q), .data(ram_1_data), .sel(decoder_1_out1), .clk(clock_1_out), .ld(pdecoder_1_r_nw),
    .clr(Reset_and_clear_RAM_out));
  Button Reset_and_clear_RAM (.out(Reset_and_clear_RAM_out));
  Button Reset (.out(Reset_out));
  pdecoder pdecoder_1 (
    .dev_addr(7'b0000100), .d_in_2(ram_1_data), .d_out_2(ram_1_data), .R_nW(pdecoder_1_r_nw),
    .En(pdecoder_1_en), .waddr(cpu_1_waddr), .addr(cpu_1_addr), .d_out(cpu_1_d_out), .d_in(pdecoder_1_d_in),
    .nR_W(cpu_1_nr_w));
  or or_1 (or_1_out, Reset_and_clear_RAM_out, Reset_out);
  Clock clock_1 (.out(clock_1_out));
  cpu cpu_1 (
    .waddr(cpu_1_waddr), .addr(cpu_1_addr), .d_out(cpu_1_d_out), .d_in(pdecoder_1_d_in), .nR_W(cpu_1_nr_w),
    .ins(rom_1_data), .iaddr(cpu_1_iaddr), .clk(clock_1_out), .rst(or_1_out));
  // Probe on cpu_1_nr_w
  // Probe on pdecoder_1_d_in
  // Probe on cpu_1_d_out
  // Probe on cpu_1_addr
  // Probe on cpu_1_waddr
  ROM #(.dataWidth(16)) rom_1 (.addr(cpu_1_iaddr), .data(rom_1_data));  // open: sel

  // Notes on the sheet:
  //   contents of rom_1 (hex, n*v repeats v):
  //   8002 8106 2 102 200
endmodule
