// Logisim project forth.circ as structural Verilog: 2 circuits, main circuit main
module main (
);

  Stack Param ();  // open: Data_In, Pop_Push, Clear, Clock, Data_Out
  Stack Return ();  // open: Data_In, Pop_Push, Clear, Clock, Data_Out
endmodule

module Stack (
  input  [15:0] Data_In,
  input  Pop_Push,
  input  Clear,
  input  Clock,
  output [15:0] Data_Out
);

  wire buffer_1_out, buffer_2_out, buffer_3_out, buffer_4_out, buffer_5_out, multiplexer_1_out, not_1_out;
  wire [15:0] counter_1_q, ram_1_data;

  Counter #(.width(16), .max('hffff)) counter_1 (
    .load(Pop_Push), .Q(counter_1_q), .clk(Clock), .clr(Clear));  // open: D, count, carry
  buf buffer_1 (buffer_1_out, buffer_3_out);
  buf buffer_2 (buffer_2_out, buffer_4_out);
  buf buffer_3 (buffer_3_out, buffer_2_out);
  buf buffer_4 (buffer_4_out, Clock);
  not not_1 (not_1_out, Pop_Push);
  Multiplexer #(.disabled(0), .enable("false")) multiplexer_1 (
    .in0(Clock), .in1(buffer_5_out), .out(multiplexer_1_out), .sel(Pop_Push));
  buf buffer_5 (buffer_5_out, buffer_1_out);
  RAM #(.addrWidth(16), .dataWidth(16), .bus("separate")) ram_1 (
    .addr(counter_1_q), .din(Data_In), .data(ram_1_data), .str(Pop_Push), .clk(multiplexer_1_out),
    .ld(not_1_out), .clr(Clear));  // open: sel
  Register #(.width(16)) register_1 (
    .D(ram_1_data), .en(not_1_out), .Q(Data_Out), .clk(multiplexer_1_out), .clr(Clear));
endmodule
