// Logisim project text editor original.circ as structural Verilog: 1 circuit, main circuit main
module main (
  input  Mode__l_s
);

  wire clear_counter_out, clear_display_out, clear_keyboard_out, clear_ram_out, clk_out, comparator_1_gt,
       comparator_1_lt, decoder_1_out0, decoder_1_out1, keyboard_1_avail, or_1_out, or_2_out, xnor_1_out;
  wire [1:0] bit_extender_1_out;
  wire [6:0] keyboard_1_data, multiplexer_1_out, ram_1_data;
  wire [15:0] counter_1_q;

  Keyboard #(.buflen(200)) keyboard_1 (
    .clk(clk_out), .clr(clear_keyboard_out), .avail(keyboard_1_avail), .data(keyboard_1_data));  // open: re
  Button clear_keyboard (.out(clear_keyboard_out));
  Button clear_counter (.out(clear_counter_out));
  Button clk (.out(clk_out));
  Button clear_ram (.out(clear_ram_out));
  Button clear_display (.out(clear_display_out));
  Comparator #(.width(7)) comparator_1 (
    .a(multiplexer_1_out), .b({7{1'b0}}), .gt(comparator_1_gt), .lt(comparator_1_lt));  // open: eq
  assign bit_extender_1_out = {{1{1'b0}}, Mode__l_s};  // Bit_Extender bit_extender_1
  Counter #(.width(16), .max('hffff), .trigger("falling")) counter_1 (
    .count(or_1_out), .Q(counter_1_q), .clk(clk_out), .clr(clear_counter_out));  // open: load, D, carry
  or or_1 (or_1_out, comparator_1_gt, comparator_1_lt);
  or or_2 (or_2_out, ~Mode__l_s, xnor_1_out);  // OR_Gate
  xnor xnor_1 (xnor_1_out, keyboard_1_avail, Mode__l_s);
  Decoder #(.select(2), .disabled(0)) decoder_1 (
    .out0(decoder_1_out0), .out1(decoder_1_out1), .sel(bit_extender_1_out), .en(or_2_out));  // open: out2, out3
  RAM #(.addrWidth(16), .dataWidth(7), .bus("separate")) ram_1 (
    .addr(counter_1_q), .din(keyboard_1_data), .data(ram_1_data), .str(decoder_1_out1), .clk(clk_out),
    .ld(decoder_1_out0), .clr(clear_ram_out));  // open: sel
  Pull_Resistor pull_resistor_1 (.node(ram_1_data));
  Multiplexer #(.width(7), .disabled(0), .enable("false")) multiplexer_1 (
    .in0(ram_1_data), .in1(keyboard_1_data), .out(multiplexer_1_out), .sel(decoder_1_out1));
  TTY tty_1 (.data(multiplexer_1_out), .clk(clk_out), .clr(clear_display_out));  // open: we
endmodule
