// Logisim project train.circ as structural Verilog: 5 circuits, main circuit main
module main (
);

  wire clock_1_out, clock_2_out, not_1_out, not_2_out, or_1_out, or_2_out, or_3_out, s1, s2, s3,
       sigchecker_1_setsig, sigchecker_1_stop, sigchecker_2_setsig, sigchecker_2_stop, sigchecker_3_setsig,
       sigchecker_3_stop, sigchecker_4_setsig, sigchecker_4_stop, sigchecker_5_setsig, sigchecker_5_stop,
       sigchecker_6_setsig, sigchecker_6_stop, station_1_stop;
  wire [4:0] counter_1_q, counter_2_q;
  wire [31:0] driver_1_matrix_out, driver_2_matrix_out;

  DotMatrix #(.matrixcols(1), .matrixrows(1)) dotmatrix_1 (.col0(s1));
  DotMatrix #(.matrixcols(32), .matrixrows(1)) dotmatrix_2 (
    .col0(driver_1_matrix_out[0]), .col1(driver_1_matrix_out[1]), .col2(driver_1_matrix_out[2]),
    .col3(driver_1_matrix_out[3]), .col4(driver_1_matrix_out[4]), .col5(driver_1_matrix_out[5]),
    .col6(driver_1_matrix_out[6]), .col7(driver_1_matrix_out[7]), .col8(driver_1_matrix_out[8]),
    .col9(driver_1_matrix_out[9]), .col10(driver_1_matrix_out[10]), .col11(driver_1_matrix_out[11]),
    .col12(driver_1_matrix_out[12]), .col13(driver_1_matrix_out[13]), .col14(driver_1_matrix_out[14]),
    .col15(driver_1_matrix_out[15]), .col16(driver_1_matrix_out[16]), .col17(driver_1_matrix_out[17]),
    .col18(driver_1_matrix_out[18]), .col19(driver_1_matrix_out[19]), .col20(driver_1_matrix_out[20]),
    .col21(driver_1_matrix_out[21]), .col22(driver_1_matrix_out[22]), .col23(driver_1_matrix_out[23]),
    .col24(driver_1_matrix_out[24]), .col25(driver_1_matrix_out[25]), .col26(driver_1_matrix_out[26]),
    .col27(driver_1_matrix_out[27]), .col28(driver_1_matrix_out[28]), .col29(driver_1_matrix_out[29]),
    .col30(driver_1_matrix_out[30]), .col31(driver_1_matrix_out[31]));
  DotMatrix #(.matrixcols(32), .matrixrows(1)) dotmatrix_3 (
    .col0(driver_2_matrix_out[0]), .col1(driver_2_matrix_out[1]), .col2(driver_2_matrix_out[2]),
    .col3(driver_2_matrix_out[3]), .col4(driver_2_matrix_out[4]), .col5(driver_2_matrix_out[5]),
    .col6(driver_2_matrix_out[6]), .col7(driver_2_matrix_out[7]), .col8(driver_2_matrix_out[8]),
    .col9(driver_2_matrix_out[9]), .col10(driver_2_matrix_out[10]), .col11(driver_2_matrix_out[11]),
    .col12(driver_2_matrix_out[12]), .col13(driver_2_matrix_out[13]), .col14(driver_2_matrix_out[14]),
    .col15(driver_2_matrix_out[15]), .col16(driver_2_matrix_out[16]), .col17(driver_2_matrix_out[17]),
    .col18(driver_2_matrix_out[18]), .col19(driver_2_matrix_out[19]), .col20(driver_2_matrix_out[20]),
    .col21(driver_2_matrix_out[21]), .col22(driver_2_matrix_out[22]), .col23(driver_2_matrix_out[23]),
    .col24(driver_2_matrix_out[24]), .col25(driver_2_matrix_out[25]), .col26(driver_2_matrix_out[26]),
    .col27(driver_2_matrix_out[27]), .col28(driver_2_matrix_out[28]), .col29(driver_2_matrix_out[29]),
    .col30(driver_2_matrix_out[30]), .col31(driver_2_matrix_out[31]));
  or or_1 (or_1_out, sigchecker_1_setsig, sigchecker_4_setsig);
  sigchecker sigchecker_1 (
    .sigon(s1), .cpos(counter_1_q), .light_pos(5'b00011), .stop(sigchecker_1_stop),
    .setsig(sigchecker_1_setsig));  // open: stopin
  sigchecker sigchecker_2 (
    .stopin(sigchecker_1_stop), .sigon(s2), .cpos(counter_1_q), .light_pos(5'b01100),
    .stop(sigchecker_2_stop), .setsig(sigchecker_2_setsig));
  sigchecker sigchecker_3 (
    .stopin(sigchecker_2_stop), .sigon(s3), .cpos(counter_1_q), .light_pos(5'b10101),
    .stop(sigchecker_3_stop), .setsig(sigchecker_3_setsig));
  sigchecker sigchecker_4 (
    .sigon(s1), .cpos(counter_2_q), .light_pos(5'b00011), .stop(sigchecker_4_stop),
    .setsig(sigchecker_4_setsig));  // open: stopin
  sigchecker sigchecker_5 (
    .stopin(sigchecker_4_stop), .sigon(s2), .cpos(counter_2_q), .light_pos(5'b01100),
    .stop(sigchecker_5_stop), .setsig(sigchecker_5_setsig));
  sigchecker sigchecker_6 (
    .stopin(sigchecker_5_stop), .sigon(s3), .cpos(counter_2_q), .light_pos(5'b10101),
    .stop(sigchecker_6_stop), .setsig(sigchecker_6_setsig));
  srlatch srlatch_1 (.S(or_1_out), .R(or_2_out), .Q(s1));
  DotMatrix #(.matrixcols(1), .matrixrows(1)) dotmatrix_4 (.col0(s2));
  or or_2 (or_2_out, sigchecker_2_setsig, sigchecker_5_setsig);
  srlatch srlatch_2 (.S(or_2_out), .R(or_3_out), .Q(s2));
  DotMatrix #(.matrixcols(1), .matrixrows(1)) dotmatrix_5 (.col0(s3));
  or or_3 (or_3_out, sigchecker_3_setsig, sigchecker_6_setsig);
  srlatch srlatch_3 (.S(or_3_out), .R(or_1_out), .Q(s3));
  station station_1 (
    .stopin(sigchecker_3_stop), .location(5'b10001), .cycles(8'h9), .tloc(counter_1_q), .stop(station_1_stop));
  not not_1 (not_1_out, sigchecker_6_stop);
  DotMatrix #(.matrixcols(3), .matrixrows(1)) dotmatrix_6 (.col0(s1), .col1(s2), .col2(s3));
  driver driver_1 (.count_in(counter_1_q), .matrix_out(driver_1_matrix_out));
  not not_2 (not_2_out, station_1_stop);
  driver driver_2 (.count_in(counter_2_q), .matrix_out(driver_2_matrix_out));
  Counter #(.width(5), .max('h1f)) counter_1 (
    .count(not_2_out), .Q(counter_1_q), .clk(clock_1_out));  // open: load, D, carry, clr
  Clock clock_1 (.out(clock_1_out));
  Counter #(.width(5), .max('h1f)) counter_2 (
    .count(not_1_out), .Q(counter_2_q), .clk(clock_2_out));  // open: load, D, carry, clr
  Clock clock_2 (.out(clock_2_out));
endmodule

module sigchecker (
  input  stopin,
  input  sigon,
  input  [4:0] cpos,
  input  [4:0] light_pos,
  output stop,
  output setsig
);

  wire and_1_out, comparator_1_eq;
  wire [4:0] adder_1_out;

  Pull_Resistor pull_resistor_1 (.node(stopin));
  Adder #(.width(5)) adder_1 (.a(light_pos), .b(5'b00001), .out(adder_1_out));  // open: cin, cout
  Comparator #(.width(5), .mode("unsigned")) comparator_1 (
    .a(light_pos), .b(cpos), .eq(comparator_1_eq));  // open: gt, lt
  Comparator #(.width(5), .mode("unsigned")) comparator_2 (.a(adder_1_out), .b(cpos), .eq(setsig));  // open: gt, lt
  or or_1 (stop, stopin, and_1_out);
  and and_1 (and_1_out, sigon, comparator_1_eq);
endmodule

module station (
  input  stopin,
  input  [4:0] location,
  input  [7:0] cycles,
  input  [4:0] tloc,
  output stop
);

  wire clock_1_out, comparator_1_eq, comparator_2_eq, one_shot_1_out, s_r_ff_1_q, s_r_ff_1_qn;
  wire [7:0] counter_1_q;

  Pull_Resistor pull_resistor_1 (.node(stopin));
  Comparator #(.width(5), .mode("unsigned")) comparator_1 (
    .a(location), .b(tloc), .eq(comparator_1_eq));  // open: gt, lt
  one_shot one_shot_1 (.in(comparator_1_eq), .out(one_shot_1_out));
  Counter counter_1 (
    .count(comparator_1_eq), .Q(counter_1_q), .clk(clock_1_out), .clr(s_r_ff_1_qn));  // open: load, D, carry
  Clock clock_1 (.out(clock_1_out));
  S_R_Flip_Flop s_r_ff_1 (
    .Q(s_r_ff_1_q), .Qn(s_r_ff_1_qn), .preset(one_shot_1_out), .reset(comparator_2_eq));  // open: S, clk, R, en
  Comparator #(.mode("unsigned")) comparator_2 (.a(counter_1_q), .b(cycles), .eq(comparator_2_eq));  // open: gt, lt
  or or_1 (stop, stopin, s_r_ff_1_q);
endmodule

module driver (
  input  [4:0] count_in,
  output [31:0] matrix_out
);

  Decoder #(.select(5), .enable("false")) decoder_1 (
    .out0(matrix_out[0]), .out1(matrix_out[1]), .out2(matrix_out[2]), .out3(matrix_out[3]),
    .out4(matrix_out[4]), .out5(matrix_out[5]), .out6(matrix_out[6]), .out7(matrix_out[7]),
    .out8(matrix_out[8]), .out9(matrix_out[9]), .out10(matrix_out[10]), .out11(matrix_out[11]),
    .out12(matrix_out[12]), .out13(matrix_out[13]), .out14(matrix_out[14]), .out15(matrix_out[15]),
    .out16(matrix_out[16]), .out17(matrix_out[17]), .out18(matrix_out[18]), .out19(matrix_out[19]),
    .out20(matrix_out[20]), .out21(matrix_out[21]), .out22(matrix_out[22]), .out23(matrix_out[23]),
    .out24(matrix_out[24]), .out25(matrix_out[25]), .out26(matrix_out[26]), .out27(matrix_out[27]),
    .out28(matrix_out[28]), .out29(matrix_out[29]), .out30(matrix_out[30]), .out31(matrix_out[31]),
    .sel(count_in));
endmodule

module srlatch (
  input  S,
  input  R,
  output Q
);

  S_R_Flip_Flop s_r_ff_1 (.Q(Q), .preset(S), .reset(R));  // open: S, clk, R, Qn, en
endmodule
