// Logisim project mcode cpu.circ as structural Verilog: 2 circuits, main circuit main
module main (
  input  in_1
);

  wire and_1_out, and_2_out, clock_1_out, clock_2_out, ins_dec_1_a_ss, ins_dec_1_ars, ins_dec_1_cnt,
       ins_dec_1_data_in_sel, ins_dec_1_hlt, ins_dec_1_lxr, ins_dec_1_lyr, ins_dec_1_store, nor_1_out,
       not_1_out, not_2_out, not_3_out;
  wire [7:0] adder_1_out, multiplexer_1_out, multiplexer_2_out, ram_2_data, ram_3_data, register_1_q,
       register_2_q, register_3_q, subtractor_1_out;
  wire [15:0] controlled_buffer_1_out, counter_1_q, ram_1_data, ram_2_data_2;
  wire [16:16] ram_1_data_2;

  not not_1 (not_1_out, in_1);
  nor nor_1 (nor_1_out, ram_1_data_2[16], ~in_1);  // NOR_Gate
  and and_1 (and_1_out, nor_1_out, ins_dec_1_cnt);
  Counter #(.width(16), .max('hffff)) counter_1 (
    .load(ram_1_data_2[16]), .D(ram_1_data), .count(and_1_out), .Q(counter_1_q), .clk(and_2_out),
    .clr(not_1_out));  // open: carry
  Clock clock_1 (.out(clock_1_out));
  and and_2 (and_2_out, clock_1_out, ~ins_dec_1_hlt);  // AND_Gate
  RAM #(.addrWidth(16), .dataWidth(17), .bus("separate")) ram_1 (
    .addr(counter_1_q), .data({ram_1_data_2[16], ram_1_data}), .str(1'b0), .ld(1'b1));  // open: din, sel, clk, clr
  not not_2 (not_2_out, ram_1_data_2[16]);
  assign controlled_buffer_1_out = not_2_out ? ram_1_data : 16'bz;  // Controlled_Buffer controlled_buffer_1
  Pull_Resistor pull_resistor_1 (.node(controlled_buffer_1_out));
  RAM #(.addrWidth(16), .dataWidth(24), .bus("separate")) ram_2 (
    .addr(controlled_buffer_1_out), .data({ram_2_data, ram_2_data_2}), .str(1'b0), .ld(1'b1));  // open: din, sel, clk, clr
  Ins_dec ins_dec_1 (
    .ins(ram_2_data), .execute(not_1_out), .cnt(ins_dec_1_cnt), .HLT(ins_dec_1_hlt),
    .Data_in_sel(ins_dec_1_data_in_sel), .Store(ins_dec_1_store), .ARS(ins_dec_1_ars), .LXR(ins_dec_1_lxr),
    .LYR(ins_dec_1_lyr), .A_SS(ins_dec_1_a_ss));
  Multiplexer #(.width(8), .disabled(0), .enable("false")) multiplexer_1 (
    .in0(ram_2_data_2[15:8]), .in1(multiplexer_2_out), .out(multiplexer_1_out), .sel(ins_dec_1_data_in_sel));
  RAM #(.bus("separate")) ram_3 (
    .addr(register_3_q), .din(multiplexer_1_out), .data(ram_3_data), .str(ins_dec_1_store),
    .clk(clock_2_out), .ld(not_3_out));  // open: sel, clr
  Clock clock_2 (.out(clock_2_out));
  not not_3 (not_3_out, ins_dec_1_store);
  Register register_1 (.D(ram_3_data), .en(ins_dec_1_lxr), .Q(register_1_q), .clk(and_2_out), .clr(not_1_out));
  Register register_2 (.D(ram_3_data), .en(ins_dec_1_lyr), .Q(register_2_q), .clk(and_2_out), .clr(not_1_out));
  Adder adder_1 (.a(register_1_q), .b(register_2_q), .out(adder_1_out));  // open: cin, cout
  Subtractor subtractor_1 (.a(register_1_q), .b(register_2_q), .out(subtractor_1_out));  // open: bin, bout
  Register register_3 (.D(ram_2_data_2[7:0]), .en(ins_dec_1_ars), .Q(register_3_q), .clk(and_2_out), .clr(not_1_out));
  Multiplexer #(.width(8), .disabled(0), .enable("false")) multiplexer_2 (
    .in0(adder_1_out), .in1(subtractor_1_out), .out(multiplexer_2_out), .sel(ins_dec_1_a_ss));
endmodule

module Ins_dec (
  input  [7:0] ins,
  input  execute,
  output HLT,
  output Data_in_sel,
  output Store,
  output ARS,
  output LXR,
  output LYR,
  output A_SS,
  output cnt
);

  wire and_1_out, and_3_out, and_5_out, clock_1_out, comparator_1_eq, comparator_1_lt, comparator_2_eq,
       comparator_2_lt, comparator_3_eq, comparator_3_lt, counter_1_carry;
  wire [1:0] or_1_out;
  wire [7:0] multiplier_1_out;
  wire [11:0] rom_1_data;
  wire [15:0] adder_1_out, bit_extender_1_out, multiplexer_1_out, register_1_q;

  Clock clock_1 (.out(clock_1_out));
  and and_1 (and_1_out, clock_1_out, ~HLT);  // AND_Gate
  Adder #(.width(16)) adder_1 (.a(register_1_q), .b(16'h1), .out(adder_1_out));  // open: cin, cout
  Counter #(.width(2), .max('h1)) counter_1 (
    .carry(counter_1_carry), .clk(and_1_out), .clr(execute));  // open: load, D, count, Q
  Multiplexer #(.select(2), .width(16), .disabled(0), .enable("false")) multiplexer_1 (
    .in0({16{1'b0}}), .in1(adder_1_out), .in2(bit_extender_1_out), .out(multiplexer_1_out), .sel(or_1_out));  // open: in3
  Multiplier multiplier_1 (.a(8'h4), .b(ins), .out(multiplier_1_out));  // open: cin, cout
  Register #(.width(16)) register_1 (
    .D(multiplexer_1_out), .en(counter_1_carry), .Q(register_1_q), .clk(and_1_out), .clr(execute));
  assign bit_extender_1_out = {{8{1'b0}}, multiplier_1_out};  // Bit_Extender bit_extender_1
  or or_1 (or_1_out[0], and_5_out, and_3_out);
  ROM #(.addrWidth(16), .dataWidth(12)) rom_1 (
    .addr(register_1_q),
    .data({rom_1_data[11], A_SS, LYR, LXR, ARS, rom_1_data[6], Store, Data_in_sel, rom_1_data[3:0]}));  // open: sel
  and and_2 (cnt, rom_1_data[11], ~counter_1_carry);  // AND_Gate
  and and_3 (and_3_out, comparator_1_eq, ~comparator_1_lt);  // AND_Gate
  Comparator #(.width(4)) comparator_1 (
    .a(rom_1_data[3:0]), .b(4'b0001), .eq(comparator_1_eq), .lt(comparator_1_lt));  // open: gt
  Comparator #(.width(4)) comparator_2 (
    .a(rom_1_data[3:0]), .b(4'b0010), .eq(comparator_2_eq), .lt(comparator_2_lt));  // open: gt
  and and_4 (or_1_out[1], comparator_2_eq, ~comparator_2_lt);  // AND_Gate
  and and_5 (and_5_out, comparator_3_eq, ~comparator_3_lt);  // AND_Gate
  Comparator #(.width(4)) comparator_3 (
    .a(rom_1_data[3:0]), .b(4'b0011), .eq(comparator_3_eq), .lt(comparator_3_lt));  // open: gt
  D_Flip_Flop d_ff_1 (.Q(HLT), .preset(and_5_out), .reset(execute));  // open: clk, D, Qn, en

  // Notes on the sheet:
  //   Nibble 1-jdest nibbles 2-3 contsignals
  //   contents of rom_1 (hex, n*v repeats v):
  //   2 0 0 0 41 900 0 0 41 a00 0 0 41 830 0 0 41 c30 0 0 41 820 0 0 3
endmodule
