// Logisim project cpu.circ as structural Verilog: 7 circuits, main circuit main
module main (
  input  [7:0] _0___7,
  input  [7:0] _8___15,
  input  [7:0] dout,
  input  reset,
  output [7:0] din,
  output c,
  output str,
  output ld,
  output [1:0] phase,
  output [7:0] a_value,
  output [7:0] b_value,
  output [7:0] r_value,
  output [7:0] PC,
  output [7:0] ins,
  output [7:0] a_in_b_in,
  output [7:0] r_in_alu_out,
  output [7:0] mem_out
);

  wire and_1_out, and_2_out, au_1_zero, clock_1_out, comparator_1_eq, comparator_2_eq, ins_decoder_1_add,
       ins_decoder_1_div, ins_decoder_1_jmp, ins_decoder_1_jmpifc, ins_decoder_1_jmpifz, ins_decoder_1_lda,
       ins_decoder_1_ldai, ins_decoder_1_ldb, ins_decoder_1_ldbi, ins_decoder_1_mult, ins_decoder_1_sta,
       ins_decoder_1_stb, ins_decoder_1_str, ins_decoder_1_sub, not_1_out, or_1_out, or_2_out, or_3_out,
       or_4_out, Phase_carry, reg_mem_decoder_1_a_en, reg_mem_decoder_1_b_en, reg_mem_decoder_1_ild;
  wire [1:0] reg_mem_decoder_1_r_mux_sel;
  wire [7:0] multiplexer_1_out;

  not not_1 (not_1_out, or_1_out);
  or or_1 (or_1_out, or_2_out, Phase_carry);
  Multiplexer #(.width(8), .disabled(0), .enable("false")) multiplexer_1 (
    .in0(dout), .in1(_0___7), .out(multiplexer_1_out), .sel(reset));
  Multiplexer #(.width(8), .disabled(0), .enable("false")) multiplexer_2 (
    .in0(multiplexer_1_out), .in1(_0___7), .out(a_in_b_in), .sel(reg_mem_decoder_1_ild));
  rf rf_1 (
    .a_in(a_in_b_in), .b_in(a_in_b_in), .r_in(r_in_alu_out), .a_en(reg_mem_decoder_1_a_en),
    .b_en(reg_mem_decoder_1_b_en), .r_en(or_3_out), .clk(clock_1_out), .res(reset), .a_out(a_value),
    .b_out(b_value), .r_out(r_value));
  Counter #(.max('hfe)) u_PC (
    .load(or_2_out), .D(_0___7), .count(not_1_out), .Q(PC), .clk(clock_1_out), .clr(reset));  // open: carry
  Clock clock_1 (.out(clock_1_out));
  Multiplexer #(.select(2), .width(8), .disabled(0), .enable("false")) multiplexer_3 (
    .in1(a_value), .in2(b_value), .in3(r_value), .out(din), .sel(reg_mem_decoder_1_r_mux_sel));  // open: in0
  or or_2 (or_2_out, ins_decoder_1_jmp, and_2_out, and_1_out);
  and and_1 (and_1_out, ins_decoder_1_jmpifc, c);
  and and_2 (and_2_out, ins_decoder_1_jmpifz, au_1_zero);
  ins_decoder ins_decoder_1 (
    .ins(_8___15), .enable_disable(or_4_out), .jmpifc(ins_decoder_1_jmpifc), .jmpifz(ins_decoder_1_jmpifz),
    .lda(ins_decoder_1_lda), .ldb(ins_decoder_1_ldb), .ldai(ins_decoder_1_ldai), .ldbi(ins_decoder_1_ldbi),
    .add(ins_decoder_1_add), .sub(ins_decoder_1_sub), .mult(ins_decoder_1_mult), .div(ins_decoder_1_div),
    .sta(ins_decoder_1_sta), .stb(ins_decoder_1_stb), .str(ins_decoder_1_str), .jmp(ins_decoder_1_jmp));
  au au_1 (
    .a(a_value), .b(b_value), .add(ins_decoder_1_add), .sub(ins_decoder_1_sub), .mult(ins_decoder_1_mult),
    .div(ins_decoder_1_div), .cout(c), .zero(au_1_zero), .out(r_in_alu_out));
  Counter #(.width(2), .max('h2)) u_Phase (
    .Q(phase), .carry(Phase_carry), .clk(clock_1_out), .clr(reset));  // open: load, D, count
  or or_3 (or_3_out, ins_decoder_1_add, ins_decoder_1_sub, ins_decoder_1_mult, ins_decoder_1_div);
  reg_mem_decoder reg_mem_decoder_1 (
    .lda(ins_decoder_1_lda), .ldb(ins_decoder_1_ldb), .ldai(ins_decoder_1_ldai), .ldbi(ins_decoder_1_ldbi),
    .sta(ins_decoder_1_sta), .stb(ins_decoder_1_stb), .str(ins_decoder_1_str), .ild(reg_mem_decoder_1_ild),
    .str_2(str), .ld(ld), .a_en(reg_mem_decoder_1_a_en), .b_en(reg_mem_decoder_1_b_en),
    .r_mux_sel(reg_mem_decoder_1_r_mux_sel));
  Comparator #(.width(2)) comparator_1 (.a(phase), .b(2'b01), .eq(comparator_1_eq));  // open: gt, lt
  Comparator #(.width(2)) comparator_2 (.a(phase), .b(2'b00), .eq(comparator_2_eq));  // open: gt, lt
  or or_4 (or_4_out, comparator_2_eq, comparator_1_eq);

  assign ins = _8___15;
  assign mem_out = dout;
endmodule

module au (
  input  [7:0] a,
  input  [7:0] b,
  input  add,
  input  sub,
  input  mult,
  input  div,
  output [7:0] out,
  output cout,
  output zero
);

  wire adder_1_cout, clock_1_out, comparator_1_eq, comparator_2_eq, comparator_3_eq, comparator_4_eq,
       multiplexer_2_out, or_1_out, subtractor_1_bout;
  wire [1:0] priority_encoder_1_out;
  wire [7:0] adder_1_out, divider_1_out, multiplier_1_out, subtractor_1_out;

  Priority_Encoder #(.select(2), .disabled(0)) priority_encoder_1 (
    .in0(add), .in1(sub), .in2(mult), .in3(div), .out(priority_encoder_1_out));  // open: gs, en_out, en_in
  or or_1 (or_1_out, add, sub, mult, div);
  Adder adder_1 (.a(a), .b(b), .out(adder_1_out), .cout(adder_1_cout));  // open: cin
  Subtractor subtractor_1 (.a(a), .b(b), .out(subtractor_1_out), .bout(subtractor_1_bout));  // open: bin
  Multiplier multiplier_1 (.a(a), .b(b), .out(multiplier_1_out));  // open: cin, cout
  Pull_Resistor pull_resistor_1 (.node(zero));
  Divider divider_1 (.a(a), .b(b), .out(divider_1_out));  // open: upper, rem
  Multiplexer #(.select(2), .disabled(0), .enable("false")) multiplexer_1 (
    .in0(comparator_1_eq), .in1(comparator_2_eq), .in2(comparator_3_eq), .in3(comparator_4_eq), .out(zero),
    .sel(priority_encoder_1_out));
  Multiplexer #(.disabled(0), .enable("false")) multiplexer_2 (
    .in0(adder_1_cout), .in1(subtractor_1_bout), .out(multiplexer_2_out), .sel(sub));
  Multiplexer #(.select(2), .width(8), .disabled(0), .enable("false")) multiplexer_3 (
    .in0(adder_1_out), .in1(subtractor_1_out), .in2(multiplier_1_out), .in3(divider_1_out), .out(out),
    .sel(priority_encoder_1_out));
  Register #(.width(1)) register_1 (.D(multiplexer_2_out), .en(or_1_out), .Q(cout), .clk(clock_1_out));  // open: clr
  Clock clock_1 (.out(clock_1_out));
  Comparator comparator_1 (.a(adder_1_out), .b({8{1'b0}}), .eq(comparator_1_eq));  // open: gt, lt
  Comparator comparator_2 (.a(subtractor_1_out), .b({8{1'b0}}), .eq(comparator_2_eq));  // open: gt, lt
  Comparator comparator_3 (.a(multiplier_1_out), .b({8{1'b0}}), .eq(comparator_3_eq));  // open: gt, lt
  Comparator comparator_4 (.a(divider_1_out), .b({8{1'b0}}), .eq(comparator_4_eq));  // open: gt, lt

  // Notes on the sheet:
  //   zero: pull=down
endmodule

module ins_decoder (
  input  [7:0] ins,
  input  enable_disable,
  output lda,
  output ldb,
  output ldai,
  output ldbi,
  output add,
  output sub,
  output mult,
  output div,
  output sta,
  output stb,
  output str,
  output jmp,
  output jmpifc,
  output jmpifz
);

  wire not_1_out;
  wire [7:0] controlled_buffer_1_out;

  Pull_Resistor pull_resistor_1 (.node(enable_disable));
  not not_1 (not_1_out, enable_disable);
  assign controlled_buffer_1_out = not_1_out ? ins : 8'bz;  // Controlled_Buffer controlled_buffer_1
  Comparator comparator_1 (.a(controlled_buffer_1_out), .b({8{1'b0}}), .eq(lda));  // open: gt, lt
  Comparator comparator_2 (.a(controlled_buffer_1_out), .b(8'h1), .eq(ldb));  // open: gt, lt
  Comparator comparator_3 (.a(controlled_buffer_1_out), .b(8'h2), .eq(ldai));  // open: gt, lt
  Comparator comparator_4 (.a(controlled_buffer_1_out), .b(8'h3), .eq(ldbi));  // open: gt, lt
  Comparator comparator_5 (.a(controlled_buffer_1_out), .b(8'h4), .eq(add));  // open: gt, lt
  Comparator comparator_6 (.a(controlled_buffer_1_out), .b(8'h5), .eq(sub));  // open: gt, lt
  Comparator comparator_7 (.a(controlled_buffer_1_out), .b(8'h6), .eq(mult));  // open: gt, lt
  Comparator comparator_8 (.a(controlled_buffer_1_out), .b(8'h7), .eq(div));  // open: gt, lt
  Comparator comparator_9 (.a(controlled_buffer_1_out), .b(8'h8), .eq(sta));  // open: gt, lt
  Comparator comparator_10 (.a(controlled_buffer_1_out), .b(8'h9), .eq(stb));  // open: gt, lt
  Comparator comparator_11 (.a(controlled_buffer_1_out), .b(8'ha), .eq(str));  // open: gt, lt
  Comparator comparator_12 (.a(controlled_buffer_1_out), .b(8'hb), .eq(jmp));  // open: gt, lt
  Comparator comparator_13 (.a(controlled_buffer_1_out), .b(8'hc), .eq(jmpifc));  // open: gt, lt
  Comparator comparator_14 (.a(controlled_buffer_1_out), .b(8'hd), .eq(jmpifz));  // open: gt, lt
  Pull_Resistor pull_resistor_2 (.node(sta));
  Pull_Resistor pull_resistor_3 (.node(stb));
  Pull_Resistor pull_resistor_4 (.node(jmpifz));
  Pull_Resistor pull_resistor_5 (.node(lda));
  Pull_Resistor pull_resistor_6 (.node(mult));
  Pull_Resistor pull_resistor_7 (.node(div));
  Pull_Resistor pull_resistor_8 (.node(str));
  Pull_Resistor pull_resistor_9 (.node(jmp));
  Pull_Resistor pull_resistor_10 (.node(jmpifc));
  Pull_Resistor pull_resistor_11 (.node(ldb));
  Pull_Resistor pull_resistor_12 (.node(ldai));
  Pull_Resistor pull_resistor_13 (.node(ldbi));
  Pull_Resistor pull_resistor_14 (.node(add));
  Pull_Resistor pull_resistor_15 (.node(sub));

  // Notes on the sheet:
  //   jmpifz: pull=down
endmodule

module reg_mem_decoder (
  input  lda,
  input  ldb,
  input  ldai,
  input  ldbi,
  input  sta,
  input  stb,
  input  str,
  output str_2,
  output ld,
  output a_en,
  output b_en,
  output [1:0] r_mux_sel,
  output ild
);

  wire or_4_out, or_5_out;

  or or_1 (str_2, r_mux_sel[0], r_mux_sel[1]);
  or or_2 (r_mux_sel[0], sta, str);
  or or_3 (r_mux_sel[1], stb, str);
  or or_4 (or_4_out, lda, ldai);
  or or_5 (or_5_out, ldbi, ldb);
  or or_6 (a_en, lda, ldai, sta);
  or or_7 (b_en, ldb, ldbi, stb);
  or or_8 (ld, or_4_out, or_5_out);
  or or_9 (ild, ldai, ldbi);
endmodule

module ins_data_mem (
  input  [7:0] adress,
  input  [7:0] ins_adress,
  input  [7:0] data_in,
  input  str,
  input  ld,
  input  clk,
  input  res,
  input  ins_not_0,
  input  [1:0] phase,
  output [7:0] _0___7,
  output [7:0] _8___15,
  output [7:0] data_out
);

  wire decoder_1_out0, decoder_1_out1, or_1_out, or_2_out;
  wire [7:0] multiplexer_1_out;

  or or_1 (or_1_out, ld, or_2_out);
  assign adress = ins_not_0 ? ins_adress : 8'bz;  // Controlled_Buffer controlled_buffer_1
  Multiplexer #(.width(8), .disabled(0), .enable("false")) multiplexer_1 (
    .in0(_0___7), .in1(adress), .out(multiplexer_1_out), .sel(or_2_out));
  RAM #(.bus("separate")) ram_1 (
    .addr(multiplexer_1_out), .din(data_in), .data(data_out), .str(str), .clk(clk), .ld(or_1_out), .clr(res));  // open: sel
  Decoder #(.select(2), .disabled(0), .enable("false")) decoder_1 (
    .out0(decoder_1_out0), .out1(decoder_1_out1), .sel(phase));  // open: out2, out3
  or or_2 (or_2_out, decoder_1_out0, decoder_1_out1);
  Register register_1 (.D(data_out), .en(decoder_1_out0), .Q(_8___15), .clk(clk));  // open: clr
  Register #(.trigger("high")) register_2 (.D(data_out), .en(decoder_1_out1), .Q(_0___7), .clk(clk));  // open: clr
endmodule

module rf (
  input  [7:0] a_in,
  input  [7:0] b_in,
  input  [7:0] r_in,
  input  a_en,
  input  b_en,
  input  r_en,
  input  clk,
  input  res,
  output [7:0] a_out,
  output [7:0] b_out,
  output [7:0] r_out
);

  Register register_1 (.D(a_in), .en(a_en), .Q(a_out), .clk(clk), .clr(res));
  Register register_2 (.D(b_in), .en(b_en), .Q(b_out), .clk(clk), .clr(res));
  Register register_3 (.D(r_in), .en(r_en), .Q(r_out), .clk(clk), .clr(res));
endmodule

module main_fun (
);

  wire clear_mem_out, clock_1_out, decoder_1_out0, decoder_1_out1, main_1_c, main_1_ld, main_1_str, or_1_out,
       or_2_out, reset_out;
  wire [1:0] main_1_phase;
  wire [7:0] main_1_a_in_b_in, main_1_a_value, main_1_b_value, main_1_din, main_1_ins, main_1_mem_out,
       main_1_pc, main_1_r_value, multiplexer_1_out, pull_resistor_1_node, ram_1_data, register_1_q,
       register_2_q;

  or or_1 (or_1_out, main_1_ld, or_2_out);
  Clock clock_1 (.out(clock_1_out));
  Multiplexer #(.width(8), .disabled(0), .enable("false")) multiplexer_1 (
    .in0(register_2_q), .in1(main_1_pc), .out(multiplexer_1_out), .sel(or_2_out));
  // Probe on main_1_c
  // Probe on main_1_a_value
  // Probe on main_1_b_value
  // Probe on main_1_r_value
  // Probe on main_1_pc
  // Probe on multiplexer_1_out
  // Probe on main_1_ins
  // Probe on main_1_a_in_b_in
  // Probe on pull_resistor_1_node
  // Probe on main_1_mem_out
  Button reset (.out(reset_out));
  Button clear_mem (.out(clear_mem_out));
  RAM #(.bus("separate")) ram_1 (
    .addr(multiplexer_1_out), .din(main_1_din), .data(ram_1_data), .str(main_1_str), .clk(clock_1_out),
    .ld(or_1_out), .clr(clear_mem_out));  // open: sel
  Decoder #(.select(2), .disabled(0), .enable("false")) decoder_1 (
    .out0(decoder_1_out0), .out1(decoder_1_out1), .sel(main_1_phase));  // open: out2, out3
  Pull_Resistor pull_resistor_1 (.node(pull_resistor_1_node));
  Register register_1 (.D(ram_1_data), .en(decoder_1_out0), .Q(register_1_q), .clk(clock_1_out), .clr(reset_out));
  Register #(.trigger("high")) register_2 (
    .D(ram_1_data), .en(decoder_1_out1), .Q(register_2_q), .clk(clock_1_out), .clr(reset_out));
  or or_2 (or_2_out, decoder_1_out0, decoder_1_out1);
  main main_1 (
    .a_value(main_1_a_value), .b_value(main_1_b_value), .r_value(main_1_r_value), .PC(main_1_pc),
    .ins(main_1_ins), .a_in_b_in(main_1_a_in_b_in), .r_in_alu_out(pull_resistor_1_node), .reset(reset_out),
    .mem_out(main_1_mem_out), .str(main_1_str), .ld(main_1_ld), .phase(main_1_phase), .din(main_1_din),
    ._8___15(register_1_q), ._0___7(register_2_q), .c(main_1_c), .dout(ram_1_data));
endmodule
