// Logisim project multicycle.circ as structural Verilog: 5 circuits, main circuit main
module main (
);

  wire clock_1_out, cpu_1_write, not_1_out, not_2_out, ram_rom_decoder_1_b00, ram_rom_decoder_1_b01,
       ram_rom_decoder_1_b02, ram_rom_decoder_1_rom_write_error, ram_rom_decoder_1_str_2, Reset_out;
  wire [2:0] cpu_1_phase;
  wire [3:0] cpu_1_addr_2, pull_resistor_1_node;
  wire [7:0] cpu_1_a, cpu_1_b, cpu_1_c, cpu_1_d, cpu_1_data_out, cpu_1_ins;
  wire [7:4] pull_resistor_1_node_2;
  wire [11:0] cpu_1_addr, ram_rom_decoder_1_addr_2;
  wire [15:0] cpu_1_addr_2_2, cpu_1_pc;

  Hex_Digit_Display hex_digit_display_1 (.value(pull_resistor_1_node_2));  // open: dp
  Hex_Digit_Display hex_digit_display_2 (.value(pull_resistor_1_node));  // open: dp
  Button Reset (.out(Reset_out));
  Hex_Digit_Display hex_digit_display_3 (.value(cpu_1_addr_2));  // open: dp
  CPU cpu_1 (
    .A(cpu_1_a), .B(cpu_1_b), .C(cpu_1_c), .PC(cpu_1_pc), .INS(cpu_1_ins), .Addr({cpu_1_addr_2, cpu_1_addr}),
    .Data_In({pull_resistor_1_node_2, pull_resistor_1_node}), .Data_Out(cpu_1_data_out), .Clock(clock_1_out),
    .Write(cpu_1_write), .Reset(Reset_out), .D(cpu_1_d), .ADDR_2(cpu_1_addr_2_2), .Phase(cpu_1_phase));
  Hex_Digit_Display hex_digit_display_4 (.value(cpu_1_addr[11:8]));  // open: dp
  Hex_Digit_Display hex_digit_display_5 (.value(cpu_1_addr[7:4]));  // open: dp
  RAM_ROM_Decoder ram_rom_decoder_1 (
    .ROM_Selector(16'h1), .addr({cpu_1_addr_2, cpu_1_addr}), .str(cpu_1_write),
    .ROM_Write_Error(ram_rom_decoder_1_rom_write_error), .b00(ram_rom_decoder_1_b00),
    .b01(ram_rom_decoder_1_b01), .b02(ram_rom_decoder_1_b02), .str_2(ram_rom_decoder_1_str_2),
    .addr_2(ram_rom_decoder_1_addr_2));  // open: b03, b04, b05, b06, b07, b08, b09, b10, b11, b12, b13, b14, b15
  Hex_Digit_Display hex_digit_display_6 (.value(cpu_1_addr[3:0]));  // open: dp
  // Probe on cpu_1_a
  // Probe on cpu_1_b
  // Probe on cpu_1_c
  // Probe on cpu_1_d
  // Probe on cpu_1_ins
  // Probe on cpu_1_addr_2_2
  // Probe on cpu_1_pc
  // Probe on cpu_1_phase
  LED ROM_Write_Error (.in(ram_rom_decoder_1_rom_write_error));
  Clock clock_1 (.out(clock_1_out));
  not not_1 (not_1_out, ram_rom_decoder_1_str_2);
  not not_2 (not_2_out, ram_rom_decoder_1_str_2);
  Pull_Resistor pull_resistor_1 (.node({pull_resistor_1_node_2, pull_resistor_1_node}));
  ROM #(.addrWidth(12)) rom_1 (
    .addr(ram_rom_decoder_1_addr_2), .data({pull_resistor_1_node_2, pull_resistor_1_node}),
    .sel(ram_rom_decoder_1_b00));
  RAM #(.addrWidth(12), .bus("separate")) ram_1 (
    .addr(ram_rom_decoder_1_addr_2), .din(cpu_1_data_out),
    .data({pull_resistor_1_node_2, pull_resistor_1_node}), .str(ram_rom_decoder_1_str_2),
    .sel(ram_rom_decoder_1_b01), .clk(clock_1_out), .ld(not_1_out));  // open: clr
  RAM #(.addrWidth(12), .bus("separate")) ram_2 (
    .addr(ram_rom_decoder_1_addr_2), .din(cpu_1_data_out),
    .data({pull_resistor_1_node_2, pull_resistor_1_node}), .str(ram_rom_decoder_1_str_2),
    .sel(ram_rom_decoder_1_b02), .clk(clock_1_out), .ld(not_2_out));  // open: clr

  // Notes on the sheet:
  //   0-Fetch instruction byte 1
  //   1-Fetch instruction byte 2
  //   2-Fetch instruction byte 3
  //   3-Execute
  //   contents of rom_1 (hex, n*v repeats v):
  //   5 a 0 9 10
endmodule

module RAM_ROM_Decoder (
  input  [15:0] ROM_Selector,
  input  [15:0] addr,
  input  str,
  output ROM_Write_Error,
  output b00,
  output b01,
  output b02,
  output b03,
  output b04,
  output b05,
  output b06,
  output b07,
  output b08,
  output b09,
  output b10,
  output b11,
  output b12,
  output b13,
  output b14,
  output b15,
  output str_2,
  output [11:0] addr_2
);

  wire and_1_out, and_2_out, and_3_out, and_4_out, and_5_out, and_6_out, and_7_out, and_8_out, and_9_out,
       and_10_out, and_11_out, and_12_out, and_13_out, and_14_out, and_15_out, and_16_out, decoder_2_out0,
       decoder_2_out1, decoder_2_out2, decoder_2_out3, decoder_2_out4, decoder_2_out5, decoder_2_out6,
       decoder_2_out7, decoder_2_out8, decoder_2_out9, decoder_2_out10, decoder_2_out11, decoder_2_out12,
       decoder_2_out13, decoder_2_out14, decoder_2_out15;

  Decoder #(.select(4), .disabled(0), .enable("false")) decoder_1 (
    .out0(b00), .out1(b01), .out2(b02), .out3(b03), .out4(b04), .out5(b05), .out6(b06), .out7(b07),
    .out8(b08), .out9(b09), .out10(b10), .out11(b11), .out12(b12), .out13(b13), .out14(b14), .out15(b15),
    .sel(addr[15:12]));
  Decoder #(.select(4), .disabled(0), .enable("false")) decoder_2 (
    .out0(decoder_2_out0), .out1(decoder_2_out1), .out2(decoder_2_out2), .out3(decoder_2_out3),
    .out4(decoder_2_out4), .out5(decoder_2_out5), .out6(decoder_2_out6), .out7(decoder_2_out7),
    .out8(decoder_2_out8), .out9(decoder_2_out9), .out10(decoder_2_out10), .out11(decoder_2_out11),
    .out12(decoder_2_out12), .out13(decoder_2_out13), .out14(decoder_2_out14), .out15(decoder_2_out15),
    .sel(addr[15:12]));
  and and_1 (and_1_out, ROM_Selector[0], decoder_2_out0, str);
  and and_2 (and_2_out, ROM_Selector[1], decoder_2_out1, str);
  and and_3 (and_3_out, ROM_Selector[2], decoder_2_out2, str);
  and and_4 (and_4_out, ROM_Selector[3], decoder_2_out3, str);
  and and_5 (and_5_out, ROM_Selector[4], decoder_2_out4, str);
  and and_6 (and_6_out, ROM_Selector[5], decoder_2_out5, str);
  and and_7 (and_7_out, ROM_Selector[6], decoder_2_out6, str);
  and and_8 (and_8_out, ROM_Selector[7], decoder_2_out7, str);
  and and_9 (and_9_out, ROM_Selector[8], decoder_2_out8, str);
  and and_10 (and_10_out, ROM_Selector[9], decoder_2_out9, str);
  and and_11 (and_11_out, ROM_Selector[10], decoder_2_out10, str);
  and and_12 (and_12_out, ROM_Selector[11], decoder_2_out11, str);
  and and_13 (and_13_out, ROM_Selector[12], decoder_2_out12, str);
  and and_14 (and_14_out, ROM_Selector[13], decoder_2_out13, str);
  and and_15 (and_15_out, ROM_Selector[14], decoder_2_out14, str);
  and and_16 (and_16_out, ROM_Selector[15], decoder_2_out15, str);
  or or_1 (ROM_Write_Error, and_1_out, and_2_out, and_3_out, and_4_out, and_5_out, and_6_out, and_7_out, and_8_out, and_9_out, and_10_out, and_11_out, and_12_out, and_13_out, and_14_out, and_15_out, and_16_out);
  and and_17 (str_2, str, ~ROM_Write_Error);  // AND_Gate

  assign addr_2 = addr[11:0];
endmodule

module CPU (
  input  [7:0] Data_In,
  input  Clock,
  input  Reset,
  output [7:0] A,
  output [15:0] Addr,
  output [7:0] B,
  output [7:0] C,
  output [7:0] Data_Out,
  output [7:0] D,
  output Write,
  output [7:0] INS,
  output [15:0] ADDR_2,
  output [15:0] PC,
  output [2:0] Phase
);

  wire and_1_out, comparator_1_eq, comparator_2_eq, comparator_3_eq, comparator_4_eq, comparator_5_eq,
       counter_2_carry, decoder_1_out0, decoder_1_out1, decoder_1_out2, decoder_1_out3, ins_dec_1_w,
       or_1_out, or_2_out, or_3_out;
  wire [1:0] ins_dec_1_m_i_a_r, ins_dec_1_r_reg_a, ins_dec_1_r_reg_b, ins_dec_1_w_reg;
  wire [2:0] ins_dec_1_op;
  wire [7:0] alu_1_r, multiplexer_2_out, multiplexer_4_out, register_1_q, register_2_q;

  Register register_1 (.D(Data_In), .en(comparator_1_eq), .Q(register_1_q), .clk(Clock), .clr(Reset));
  Register register_2 (.D(Data_In), .en(comparator_2_eq), .Q(register_2_q), .clk(Clock), .clr(Reset));
  buf and_1 (and_1_out, or_1_out);  // AND_Gate AND_Gate
  or or_1 (or_1_out, comparator_1_eq, comparator_2_eq, comparator_3_eq);
  Register #(.width(24)) register_3 (
    .D({register_2_q, Data_In, register_1_q}), .en(comparator_3_eq), .Q({ADDR_2, INS}), .clk(Clock),
    .clr(Reset));
  Counter #(.width(16), .max('hffff)) counter_1 (
    .D(ADDR_2), .count(and_1_out), .Q(PC), .clk(Clock), .clr(Reset));  // open: load, carry
  Counter #(.width(3), .max('h4)) counter_2 (
    .Q(Phase), .carry(counter_2_carry), .clk(Clock), .clr(or_2_out));  // open: load, D, count
  or or_2 (or_2_out, Reset, counter_2_carry);
  Multiplexer #(.width(16), .disabled(0), .enable("false")) multiplexer_1 (
    .in0(ADDR_2), .in1(PC), .out(Addr), .sel(and_1_out));
  Comparator #(.width(3), .mode("unsigned")) comparator_1 (
    .a(Phase), .b(3'b000), .eq(comparator_1_eq));  // open: gt, lt
  Comparator #(.width(3), .mode("unsigned")) comparator_2 (
    .a(Phase), .b(3'b001), .eq(comparator_2_eq));  // open: gt, lt
  Comparator #(.width(3), .mode("unsigned")) comparator_3 (
    .a(Phase), .b(3'b010), .eq(comparator_3_eq));  // open: gt, lt
  Comparator #(.width(3), .mode("unsigned")) comparator_4 (
    .a(Phase), .b(3'b011), .eq(comparator_4_eq));  // open: gt, lt
  Comparator #(.width(2), .mode("unsigned")) comparator_5 (
    .a(ins_dec_1_m_i_a_r), .b(2'b10), .eq(comparator_5_eq));  // open: gt, lt
  Ins_Dec ins_dec_1 (
    .ins(INS), .en(comparator_4_eq), .W(ins_dec_1_w), .W_Reg(ins_dec_1_w_reg), .R_Reg_A(ins_dec_1_r_reg_a),
    .R_Reg_B(ins_dec_1_r_reg_b), .OP(ins_dec_1_op), .M_I_A_R(ins_dec_1_m_i_a_r), .WM(Write), .addr(ADDR_2));  // open: JMP
  Decoder #(.select(2), .disabled(0)) decoder_1 (
    .out0(decoder_1_out0), .out1(decoder_1_out1), .out2(decoder_1_out2), .out3(decoder_1_out3),
    .sel(ins_dec_1_w_reg), .en(ins_dec_1_w));
  or or_3 (or_3_out, comparator_5_eq, decoder_1_out0);
  Multiplexer #(.select(2), .width(8), .disabled(0), .enable("false")) multiplexer_2 (
    .in0(Data_In), .in1(register_2_q), .in2(alu_1_r), .in3(Data_Out), .out(multiplexer_2_out),
    .sel(ins_dec_1_m_i_a_r));
  Register register_4 (.D(multiplexer_2_out), .en(or_3_out), .Q(A), .clk(Clock), .clr(Reset));
  Register register_5 (.D(multiplexer_2_out), .en(decoder_1_out1), .Q(B), .clk(Clock), .clr(Reset));
  Register register_6 (.D(multiplexer_2_out), .en(decoder_1_out2), .Q(C), .clk(Clock), .clr(Reset));
  Register register_7 (.D(multiplexer_2_out), .en(decoder_1_out3), .Q(D), .clk(Clock), .clr(Reset));
  Pull_Resistor pull_resistor_1 (.node(Data_Out));
  Multiplexer #(.select(2), .width(8), .disabled(0), .enable("false")) multiplexer_3 (
    .in0(A), .in1(B), .in2(C), .in3(D), .out(Data_Out), .sel(ins_dec_1_r_reg_a));
  Multiplexer #(.select(2), .width(8), .disabled(0), .enable("false")) multiplexer_4 (
    .in0(B), .in1(C), .in2(D), .out(multiplexer_4_out), .sel(ins_dec_1_r_reg_b));  // open: in3
  ALU alu_1 (.A(A), .B(multiplexer_4_out), .OP(ins_dec_1_op), .R(alu_1_r));
endmodule

module Ins_Dec (
  input  [7:0] ins,
  input  [15:0] addr,
  input  en,
  output W,
  output [1:0] W_Reg,
  output [1:0] R_Reg_A,
  output [1:0] R_Reg_B,
  output [2:0] OP,
  output [1:0] M_I_A_R,
  output WM,
  output JMP
);

  wire comparator_1_eq, comparator_2_eq, comparator_3_eq, comparator_4_eq, comparator_5_eq, comparator_6_eq,
       comparator_7_eq, comparator_8_eq, comparator_9_eq, comparator_10_eq, comparator_11_eq,
       comparator_12_eq, comparator_13_eq, comparator_14_eq, comparator_15_eq, comparator_16_eq,
       comparator_17_eq, comparator_18_eq, or_1_out, or_2_out, or_3_out, or_4_out, or_5_out, or_6_out,
       or_7_out, or_8_out, or_9_out, or_10_out, or_11_out, priority_encoder_1_gs, pull_resistor_2_node;
  wire [1:0] priority_encoder_1_out, priority_encoder_2_out;
  wire [3:0] controlled_buffer_2_out;
  wire [7:0] controlled_buffer_1_out;

  assign controlled_buffer_1_out = en ? ins : 8'bz;  // Controlled_Buffer controlled_buffer_1
  Pull_Resistor pull_resistor_1 (.node(controlled_buffer_1_out));
  assign controlled_buffer_2_out = pull_resistor_2_node ? addr[11:8] : 4'bz;  // Controlled_Buffer controlled_buffer_2
  Comparator #(.mode("unsigned")) comparator_1 (
    .a(8'h1), .b(controlled_buffer_1_out), .eq(comparator_1_eq));  // open: gt, lt
  Comparator #(.mode("unsigned")) comparator_2 (
    .a(8'h2), .b(controlled_buffer_1_out), .eq(comparator_2_eq));  // open: gt, lt
  Comparator #(.mode("unsigned")) comparator_3 (
    .a(8'h3), .b(controlled_buffer_1_out), .eq(comparator_3_eq));  // open: gt, lt
  Comparator #(.mode("unsigned")) comparator_4 (
    .a(8'h4), .b(controlled_buffer_1_out), .eq(comparator_4_eq));  // open: gt, lt
  Comparator #(.mode("unsigned")) comparator_5 (
    .a(8'h5), .b(controlled_buffer_1_out), .eq(comparator_5_eq));  // open: gt, lt
  Comparator #(.mode("unsigned")) comparator_6 (
    .a(8'h6), .b(controlled_buffer_1_out), .eq(comparator_6_eq));  // open: gt, lt
  Comparator #(.mode("unsigned")) comparator_7 (
    .a(8'h7), .b(controlled_buffer_1_out), .eq(comparator_7_eq));  // open: gt, lt
  Comparator #(.mode("unsigned")) comparator_8 (
    .a(8'h8), .b(controlled_buffer_1_out), .eq(comparator_8_eq));  // open: gt, lt
  Comparator #(.mode("unsigned")) comparator_9 (
    .a(8'h9), .b(controlled_buffer_1_out), .eq(comparator_9_eq));  // open: gt, lt
  Comparator #(.mode("unsigned")) comparator_10 (
    .a(8'ha), .b(controlled_buffer_1_out), .eq(comparator_10_eq));  // open: gt, lt
  Comparator #(.mode("unsigned")) comparator_11 (
    .a(8'hb), .b(controlled_buffer_1_out), .eq(comparator_11_eq));  // open: gt, lt
  Comparator #(.mode("unsigned")) comparator_12 (
    .a(8'hc), .b(controlled_buffer_1_out), .eq(comparator_12_eq));  // open: gt, lt
  Comparator #(.mode("unsigned")) comparator_13 (
    .a(8'hd), .b(controlled_buffer_1_out), .eq(comparator_13_eq));  // open: gt, lt
  Comparator #(.mode("unsigned")) comparator_14 (
    .a(8'he), .b(controlled_buffer_1_out), .eq(comparator_14_eq));  // open: gt, lt
  Comparator #(.mode("unsigned")) comparator_15 (
    .a(8'hf), .b(controlled_buffer_1_out), .eq(comparator_15_eq));  // open: gt, lt
  Comparator #(.mode("unsigned")) comparator_16 (
    .a(8'h10), .b(controlled_buffer_1_out), .eq(comparator_16_eq));  // open: gt, lt
  Comparator #(.mode("unsigned")) comparator_17 (
    .a(8'h11), .b(controlled_buffer_1_out), .eq(comparator_17_eq));  // open: gt, lt
  Comparator #(.mode("unsigned")) comparator_18 (
    .a(8'h12), .b(controlled_buffer_1_out), .eq(comparator_18_eq));  // open: gt, lt
  Comparator #(.mode("unsigned")) comparator_19 (.a(8'h13), .b(controlled_buffer_1_out));  // open: gt, eq, lt
  Pull_Resistor pull_resistor_2 (.node(pull_resistor_2_node));
  or or_1 (or_1_out, comparator_1_eq, comparator_5_eq);
  or or_2 (or_2_out, comparator_2_eq, comparator_6_eq);
  or or_3 (or_3_out, comparator_3_eq, comparator_7_eq);
  or or_4 (or_4_out, comparator_4_eq, comparator_8_eq);
  or or_5 (or_5_out, comparator_13_eq, comparator_14_eq, comparator_15_eq);
  or or_6 (or_6_out, comparator_13_eq, comparator_16_eq);
  or or_7 (or_7_out, comparator_14_eq, comparator_17_eq);
  or or_8 (or_8_out, comparator_15_eq, comparator_18_eq);
  or or_9 (or_9_out, comparator_16_eq, comparator_17_eq, comparator_18_eq);
  or or_10 (or_10_out, comparator_1_eq, comparator_2_eq, comparator_3_eq, comparator_4_eq);
  or or_11 (or_11_out, comparator_5_eq, comparator_6_eq, comparator_7_eq, comparator_8_eq);
  or or_12 (WM, comparator_9_eq, comparator_10_eq, comparator_11_eq, comparator_12_eq);
  Priority_Encoder #(.select(2)) priority_encoder_1 (
    .in0(or_1_out), .in1(or_2_out), .in2(or_3_out), .in3(or_4_out), .out(priority_encoder_1_out),
    .gs(priority_encoder_1_gs));  // open: en_out, en_in
  Priority_Encoder #(.select(2)) priority_encoder_2 (
    .in0(comparator_9_eq), .in1(comparator_10_eq), .in2(comparator_11_eq), .in3(comparator_12_eq),
    .out(priority_encoder_2_out));  // open: gs, en_out, en_in
  Pull_Resistor pull_resistor_3 (.node(controlled_buffer_2_out[1:0]));
  Pull_Resistor pull_resistor_4 (.node(priority_encoder_1_out));
  assign W_Reg = priority_encoder_1_out | controlled_buffer_2_out[1:0];  // OR_Gate or_13, 2 bits wide
  or or_14 (W, priority_encoder_1_gs, pull_resistor_2_node);
  Pull_Resistor pull_resistor_5 (.node(priority_encoder_2_out));
  assign R_Reg_A = priority_encoder_2_out | controlled_buffer_2_out[3:2];  // OR_Gate or_15, 2 bits wide
  Pull_Resistor pull_resistor_6 (.node(controlled_buffer_2_out[3:2]));
  Pull_Resistor pull_resistor_7 (.node(R_Reg_B));
  Pull_Resistor pull_resistor_8 (.node(OP));
  Priority_Encoder #(.select(2)) priority_encoder_3 (
    .in0(or_6_out), .in1(or_7_out), .in2(or_8_out), .out(R_Reg_B));  // open: in3, gs, en_out, en_in
  Priority_Encoder priority_encoder_4 (
    .in0(or_5_out), .in1(or_9_out), .out(OP));  // open: in2, in3, in4, in5, in6, in7, en_in, gs, en_out
  Pull_Resistor pull_resistor_9 (.node(M_I_A_R));
  Priority_Encoder #(.select(2)) priority_encoder_5 (
    .in0(or_10_out), .in1(or_11_out), .in2(or_5_out), .in3(pull_resistor_2_node), .out(M_I_A_R));  // open: gs, en_out, en_in
endmodule

module ALU (
  input  [7:0] A,
  input  [7:0] B,
  input  [2:0] OP,
  output [7:0] R
);

  wire decoder_1_out0, decoder_1_out1, decoder_1_out2, decoder_1_out3, decoder_1_out4, decoder_1_out5;
  wire [7:0] adder_1_out, and_1_out, not_1_out, or_1_out, subtractor_1_out, xor_1_out;

  Decoder #(.select(3), .disabled(0), .enable("false")) decoder_1 (
    .out0(decoder_1_out0), .out1(decoder_1_out1), .out2(decoder_1_out2), .out3(decoder_1_out3),
    .out4(decoder_1_out4), .out5(decoder_1_out5), .sel(OP));  // open: out6, out7
  assign or_1_out = A | B;  // OR_Gate or_1, 8 bits wide
  assign and_1_out = A & B;  // AND_Gate and_1, 8 bits wide
  assign not_1_out = ~A;  // NOT_Gate not_1, 8 bits wide
  Adder adder_1 (.a(A), .b(B), .out(adder_1_out));  // open: cin, cout
  Subtractor subtractor_1 (.a(A), .b(B), .out(subtractor_1_out));  // open: bin, bout
  assign R = decoder_1_out2 ? or_1_out : 8'bz;  // Controlled_Buffer controlled_buffer_1
  assign R = decoder_1_out3 ? and_1_out : 8'bz;  // Controlled_Buffer controlled_buffer_2
  assign R = decoder_1_out4 ? not_1_out : 8'bz;  // Controlled_Buffer controlled_buffer_3
  assign R = decoder_1_out5 ? xor_1_out : 8'bz;  // Controlled_Buffer controlled_buffer_4
  assign xor_1_out = A ^ B;  // XOR_Gate xor_1, 8 bits wide
  assign R = decoder_1_out0 ? adder_1_out : 8'bz;  // Controlled_Buffer controlled_buffer_5
  assign R = decoder_1_out1 ? subtractor_1_out : 8'bz;  // Controlled_Buffer controlled_buffer_6
endmodule
