// Logisim project mcode_machine.circ as structural Verilog: 3 circuits, main circuit main
module main (
  input  [7:0] mcodeaddr,
  input  [5:0] aluop,
  input  writetoreg,
  input  writetomem,
  input  [2:0] regtowrite,
  input  [2:0] areg_memaddr,
  input  [2:0] breg,
  input  memtob,
  input  [3:0] jmpsetting
);

  wire ALU_carry, ALU_zero, clock_1_out, MCODE_mem_rd, MCODE_mem_wr, MCODE_reg_wr, next_out, or_1_out,
       or_2_out, RESET_out, RESETFULL_out, strop_out;
  wire [2:0] MCODE_a_addr, MCODE_b_addr, MCODE_wr_addr;
  wire [5:0] MCODE_opcode;
  wire [7:0] MCODE_mcodeaddr;
  wire [15:0] ALU_r, multiplexer_1_out, ram_1_data, REGISTERS_a_data, REGISTERS_b_data, REGISTERS_r0,
       REGISTERS_r1, REGISTERS_r2, REGISTERS_r3, REGISTERS_r4, REGISTERS_r5, REGISTERS_r6, REGISTERS_r7;

  Button RESETFULL (.out(RESETFULL_out));
  Button RESET (.out(RESET_out));
  Clock clock_1 (.out(clock_1_out));
  // Probe on MCODE_mcodeaddr
  or or_1 (or_1_out, RESETFULL_out, RESET_out);
  or or_2 (or_2_out, RESET_out, or_1_out);
  Button strop (.out(strop_out));
  Button next (.out(next_out));
  mcode MCODE (
    .CARRY(ALU_carry), .ZERO(ALU_zero), .CLK(clock_1_out), .RESET(or_2_out), .OPCODE(MCODE_opcode),
    .REG_WR(MCODE_reg_wr), .MEM_WR(MCODE_mem_wr), .WR_ADDR(MCODE_wr_addr), .A_ADDR(MCODE_a_addr),
    .B_ADDR(MCODE_b_addr), .MEM(ram_1_data), .NEXT(next_out), .STROP(strop_out),
    .OP({jmpsetting, 2'b00, memtob, breg, areg_memaddr, regtowrite, writetomem, writetoreg, aluop, mcodeaddr}),
    .MCODEADDR(MCODE_mcodeaddr), .MEM_RD(MCODE_mem_rd));
  regfile_main REGISTERS (
    .WRITE(MCODE_reg_wr), .WR_ADDR(MCODE_wr_addr), .WR_DATA(ALU_r), .RESET(or_1_out), .CLK(clock_1_out),
    .A_ADDR(MCODE_a_addr), .A_DATA(REGISTERS_a_data), .B_ADDR(MCODE_b_addr), .B_DATA(REGISTERS_b_data),
    .R0(REGISTERS_r0), .R1(REGISTERS_r1), .R2(REGISTERS_r2), .R3(REGISTERS_r3), .R4(REGISTERS_r4),
    .R5(REGISTERS_r5), .R6(REGISTERS_r6), .R7(REGISTERS_r7));
  Multiplexer #(.width(16), .enable("false")) multiplexer_1 (
    .in0(REGISTERS_b_data), .in1(ram_1_data), .out(multiplexer_1_out), .sel(MCODE_mem_rd));
  ALU ALU (
    .OP(MCODE_opcode), .A(REGISTERS_a_data), .B(multiplexer_1_out), .CARRY(ALU_carry), .ZERO(ALU_zero),
    .R(ALU_r));
  // Probe on REGISTERS_r0
  // Probe on REGISTERS_r1
  // Probe on REGISTERS_r2
  // Probe on REGISTERS_r3
  // Probe on REGISTERS_r4
  // Probe on REGISTERS_r5
  // Probe on REGISTERS_r6
  // Probe on REGISTERS_r7
  RAM #(.addrWidth(16), .dataWidth(16), .bus("separate")) ram_1 (
    .addr(REGISTERS_a_data), .din(ALU_r), .data(ram_1_data), .str(MCODE_mem_wr), .clk(clock_1_out),
    .ld(MCODE_mem_rd), .clr(RESETFULL_out));  // open: sel
endmodule

module ALU (
  input  [15:0] A,
  input  [15:0] B,
  input  [5:0] OP,
  output CARRY,
  output ZERO,
  output [15:0] R
);

  wire adder_2_cout, subtractor_1_bout;
  wire [15:0] adder_1_out, adder_2_out, and_1_out, negator_1_out, or_1_out, shifter_1_out, subtractor_1_out;

  Adder #(.width(16)) adder_1 (.a(A), .b(16'h1), .out(adder_1_out));  // open: cin, cout
  Multiplexer #(.enable("false")) multiplexer_1 (.in0(adder_2_cout), .in1(subtractor_1_bout), .out(CARRY), .sel(OP[0]));
  Adder #(.width(16)) adder_2 (.a(A), .b(B), .out(adder_2_out), .cout(adder_2_cout));  // open: cin
  Subtractor #(.width(16)) subtractor_1 (.a(A), .b(B), .out(subtractor_1_out), .bout(subtractor_1_bout));  // open: bin
  assign or_1_out = A | B;  // OR_Gate or_1, 16 bits wide
  assign and_1_out = A & B;  // AND_Gate and_1, 16 bits wide
  Negator #(.width(16)) negator_1 (.in(A), .out(negator_1_out));
  Shifter #(.width(16), .shift("lr")) shifter_1 (.in(A), .\dist (4'b0001), .out(shifter_1_out));
  Comparator #(.width(16)) comparator_1 (.a(R), .b({16{1'b0}}), .eq(ZERO));  // open: gt, lt
  Multiplexer #(.select(4), .width(16), .enable("false")) multiplexer_2 (
    .in0(adder_2_out), .in1(subtractor_1_out), .in2(or_1_out), .in3(and_1_out), .in4(negator_1_out),
    .in5(shifter_1_out), .in6(A), .in7(B), .in8({16{1'b0}}), .in9(16'h1), .in10(adder_1_out), .out(R),
    .sel(OP[3:0]));  // open: in11, in12, in13, in14, in15

  // Notes on the sheet:
  //   See pg 36
  //   ALU Design from Elements of Computing Systems
endmodule

module mcode (
  input  NEXT,
  input  STROP,
  input  [31:0] OP,
  input  CARRY,
  input  ZERO,
  input  CLK,
  input  RESET,
  input  [15:0] MEM,
  output [5:0] OPCODE,
  output REG_WR,
  output MEM_WR,
  output [2:0] WR_ADDR,
  output [2:0] A_ADDR,
  output [2:0] B_ADDR,
  output [7:0] MCODEADDR,
  output MEM_RD
);

  wire ALWAYS, and_1_out, and_2_out, IF_CARRY, IF_ZERO, not_1_out, or_1_out, or_2_out;
  wire [7:0] adder_1_out, multiplexer_1_out, multiplexer_2_out, ram_1_data;
  wire [31:26] ram_1_data_2;

  and and_1 (and_1_out, CARRY, IF_CARRY);
  and and_2 (and_2_out, ZERO, IF_ZERO);
  or or_1 (or_1_out, CLK, NEXT);
  or or_2 (or_2_out, ALWAYS, and_1_out, and_2_out);
  Multiplexer #(.width(8), .enable("false")) multiplexer_1 (
    .in0(multiplexer_2_out), .in1(MEM[15:8]), .out(multiplexer_1_out), .sel(ram_1_data_2[31]));
  Register R0 (.D(multiplexer_1_out), .en(or_1_out), .Q(MCODEADDR), .clk(or_1_out), .clr(RESET));
  Multiplexer #(.width(8), .enable("false")) multiplexer_2 (
    .in0(adder_1_out), .in1(ram_1_data), .out(multiplexer_2_out), .sel(or_2_out));
  Adder adder_1 (.a(8'h1), .b(MCODEADDR), .out(adder_1_out));  // open: cin, cout
  not not_1 (not_1_out, STROP);
  RAM #(.dataWidth(32), .bus("separate")) ram_1 (
    .addr(MCODEADDR), .din(OP),
    .data({ram_1_data_2[31], IF_ZERO, IF_CARRY, ALWAYS, ram_1_data_2[27:26], MEM_RD, B_ADDR, A_ADDR, WR_ADDR, MEM_WR, REG_WR, OPCODE, ram_1_data}),
    .str(STROP), .clk(STROP), .ld(not_1_out));  // open: sel, clr
  Pull_Resistor pull_resistor_1 (.node({ram_1_data_2[31], IF_ZERO, IF_CARRY, ALWAYS, ram_1_data_2[27:26], MEM_RD, B_ADDR, A_ADDR, WR_ADDR, MEM_WR, REG_WR, OPCODE, ram_1_data}));

  // Notes on the sheet:
  //   Get MCode from Mem
  //   Mcode Jump Address
endmodule
