// Logisim project regfile.circ as structural Verilog: 1 circuit, main circuit main
module main (
  input  WRITE,
  input  [2:0] WR_ADDR,
  input  [15:0] WR_DATA,
  input  RESET,
  input  CLK,
  input  [2:0] B_ADDR,
  input  [2:0] A_ADDR,
  output [15:0] R0,
  output [15:0] R1,
  output [15:0] R2,
  output [15:0] R3,
  output [15:0] R4,
  output [15:0] R5,
  output [15:0] R6,
  output [15:0] R7,
  output [15:0] B_DATA,
  output [15:0] A_DATA
);

  wire demultiplexer_1_out0, demultiplexer_1_out1, demultiplexer_1_out2, demultiplexer_1_out3,
       demultiplexer_1_out4, demultiplexer_1_out5, demultiplexer_1_out6, demultiplexer_1_out7;

  Demultiplexer #(.select(3), .disabled(0), .enable("false")) demultiplexer_1 (
    .out0(demultiplexer_1_out0), .out1(demultiplexer_1_out1), .out2(demultiplexer_1_out2),
    .out3(demultiplexer_1_out3), .out4(demultiplexer_1_out4), .out5(demultiplexer_1_out5),
    .out6(demultiplexer_1_out6), .out7(demultiplexer_1_out7), .in(WRITE), .sel(WR_ADDR));
  Register #(.width(16)) u_R7 (.D(WR_DATA), .en(demultiplexer_1_out7), .Q(R7), .clk(CLK), .clr(RESET));
  Multiplexer #(.select(3), .width(16), .enable("false")) multiplexer_1 (
    .in0(R0), .in1(R1), .in2(R2), .in3(R3), .in4(R4), .in5(R5), .in6(R6), .in7(R7), .out(A_DATA), .sel(A_ADDR));
  Register #(.width(16)) u_R6 (.D(WR_DATA), .en(demultiplexer_1_out6), .Q(R6), .clk(CLK), .clr(RESET));
  Register #(.width(16)) u_R5 (.D(WR_DATA), .en(demultiplexer_1_out5), .Q(R5), .clk(CLK), .clr(RESET));
  Register #(.width(16)) u_R4 (.D(WR_DATA), .en(demultiplexer_1_out4), .Q(R4), .clk(CLK), .clr(RESET));
  Register #(.width(16)) u_R3 (.D(WR_DATA), .en(demultiplexer_1_out3), .Q(R3), .clk(CLK), .clr(RESET));
  Register #(.width(16)) u_R2 (.D(WR_DATA), .en(demultiplexer_1_out2), .Q(R2), .clk(CLK), .clr(RESET));
  Multiplexer #(.select(3), .width(16), .enable("false")) multiplexer_2 (
    .in0(R0), .in1(R1), .in2(R2), .in3(R3), .in4(R4), .in5(R5), .in6(R6), .in7(R7), .out(B_DATA), .sel(B_ADDR));
  Register #(.width(16)) u_R1 (.D(WR_DATA), .en(demultiplexer_1_out1), .Q(R1), .clk(CLK), .clr(RESET));
  Register #(.width(16)) u_R0 (.D(WR_DATA), .en(demultiplexer_1_out0), .Q(R0), .clk(CLK), .clr(RESET));
endmodule
