// Logisim project regfile_test.circ as structural Verilog: 1 circuit, main circuit main
module main (
  input  in_1
);

  wire clock_1_out, RESET_out;
  wire [2:0] counter_2_q, counter_3_q, counter_4_q;
  wire [15:0] counter_1_q, REGISTERS_a_data, REGISTERS_b_data, REGISTERS_r0, REGISTERS_r1, REGISTERS_r2,
       REGISTERS_r3, REGISTERS_r4, REGISTERS_r5, REGISTERS_r6, REGISTERS_r7;

  Clock clock_1 (.out(clock_1_out));
  Button RESET (.out(RESET_out));
  Counter #(.width(16), .max('hffff)) counter_1 (
    .Q(counter_1_q), .clk(clock_1_out));  // open: load, D, count, carry, clr
  Counter #(.width(3), .max('h7)) counter_2 (.Q(counter_2_q), .clk(clock_1_out));  // open: load, D, count, carry, clr
  Counter #(.width(3), .max('h7)) counter_3 (.Q(counter_3_q), .clk(clock_1_out));  // open: load, D, count, carry, clr
  Counter #(.width(3), .max('h7)) counter_4 (.Q(counter_4_q), .clk(clock_1_out));  // open: load, D, count, carry, clr
  regfile_main REGISTERS (
    .WRITE(in_1), .WR_ADDR(counter_3_q), .WR_DATA(counter_1_q), .RESET(RESET_out), .CLK(clock_1_out),
    .A_ADDR(counter_4_q), .A_DATA(REGISTERS_a_data), .B_ADDR(counter_2_q), .B_DATA(REGISTERS_b_data),
    .R0(REGISTERS_r0), .R1(REGISTERS_r1), .R2(REGISTERS_r2), .R3(REGISTERS_r3), .R4(REGISTERS_r4),
    .R5(REGISTERS_r5), .R6(REGISTERS_r6), .R7(REGISTERS_r7));
  // Probe on REGISTERS_r0
  // Probe on REGISTERS_r1
  // Probe on REGISTERS_r2
  // Probe on REGISTERS_r3
  // Probe on REGISTERS_r4
  // Probe on REGISTERS_r5
  // Probe on REGISTERS_r6
  // Probe on REGISTERS_r7
  // Probe on REGISTERS_b_data
  // Probe on REGISTERS_a_data
endmodule
