// Logisim project cpu.circ as structural Verilog: 5 circuits, main circuit main
module reg_file (
  input  [7:0] in,
  input  [2:0] isel,
  input  [2:0] osel1,
  input  [2:0] osel2,
  input  _8_16,
  input  clear,
  input  clk,
  output [7:0] out81,
  output [7:0] out82,
  output [15:0] out16
);

  wire decoder_1_out0, decoder_1_out1, decoder_1_out2, decoder_1_out3, decoder_1_out4, decoder_1_out5,
       decoder_1_out6, decoder_1_out7;
  wire [7:0] register_1_q, register_2_q, register_3_q, register_4_q, register_5_q, register_6_q,
       register_7_q, register_8_q;

  Decoder #(.select(3), .disabled(0), .enable("false")) decoder_1 (
    .out0(decoder_1_out0), .out1(decoder_1_out1), .out2(decoder_1_out2), .out3(decoder_1_out3),
    .out4(decoder_1_out4), .out5(decoder_1_out5), .out6(decoder_1_out6), .out7(decoder_1_out7), .sel(isel));
  Register register_1 (.D(in), .en(decoder_1_out0), .Q(register_1_q), .clk(clk), .clr(clear));
  Register register_2 (.D(in), .en(decoder_1_out1), .Q(register_2_q), .clk(clk), .clr(clear));
  Register register_3 (.D(in), .en(decoder_1_out2), .Q(register_3_q), .clk(clk), .clr(clear));
  Register register_4 (.D(in), .en(decoder_1_out3), .Q(register_4_q), .clk(clk), .clr(clear));
  Register register_5 (.D(in), .en(decoder_1_out4), .Q(register_5_q), .clk(clk), .clr(clear));
  Register register_6 (.D(in), .en(decoder_1_out5), .Q(register_6_q), .clk(clk), .clr(clear));
  Register register_7 (.D(in), .en(decoder_1_out6), .Q(register_7_q), .clk(clk), .clr(clear));
  Register register_8 (.D(in), .en(decoder_1_out7), .Q(register_8_q), .clk(clk), .clr(clear));
  Multiplexer #(.select(3), .width(8)) multiplexer_1 (
    .in0(register_1_q), .in1(register_2_q), .in2(register_3_q), .in3(register_4_q), .in4(register_5_q),
    .in5(register_6_q), .out(out81), .sel(osel1));  // open: in6, in7, en
  Multiplexer #(.select(3), .width(8)) multiplexer_2 (
    .in0(register_1_q), .in1(register_2_q), .in2(register_3_q), .in3(register_4_q), .in4(register_5_q),
    .in5(register_6_q), .in6(register_7_q), .in7(register_8_q), .out(out82), .sel(osel2));  // open: en
  Multiplexer #(.select(2), .width(16)) multiplexer_3 (
    .in0({register_2_q, register_1_q}), .in1({register_4_q, register_3_q}),
    .in2({register_6_q, register_5_q}), .in3({register_8_q, register_7_q}), .out(out16), .sel(osel1[1:0]));  // open: en
endmodule

module cpu (
  input  [7:0] din,
  input  clk,
  input  reset,
  output R_W,
  output [7:0] dout,
  output [15:0] addr
);

  wire control_1_aclk, control_1_rclk, decoder_1_out0, decoder_1_out1, decoder_1_out2, decoder_1_out3;
  wire [1:0] control_1_asel, control_1_rinsel, counter_1_q;
  wire [2:0] control_1_aluop, control_1_isel, control_1_osel1, control_1_osel2;
  wire [7:0] alu_1_r, multiplexer_1_out, reg_file_1_out81, register_1_q, register_2_q, register_3_q,
       register_3_q_2;
  wire [15:0] counter_2_q, reg_file_1_out16;
  wire [15:8] register_3_q_3;

  Decoder #(.select(2), .disabled(0), .enable("false")) decoder_1 (
    .out0(decoder_1_out0), .out1(decoder_1_out1), .out2(decoder_1_out2), .out3(decoder_1_out3),
    .sel(counter_1_q));
  Counter #(.width(2), .max('h3)) counter_1 (.Q(counter_1_q), .clk(clk), .clr(reset));  // open: load, D, count, carry
  Counter #(.width(16), .max('hffff)) counter_2 (
    .Q(counter_2_q), .clk(clk), .clr(reset));  // open: load, D, count, carry
  control control_1 (
    .op({register_3_q_3, register_3_q_2, register_3_q}), .en(decoder_1_out3), .clk(clk),
    .asel(control_1_asel), .isel(control_1_isel), .osel1(control_1_osel1), .osel2(control_1_osel2),
    .aluop(control_1_aluop), .rinsel(control_1_rinsel), .R_W(R_W), .rclk(control_1_rclk),
    .aclk(control_1_aclk));  // open: _8_16
  Multiplexer #(.select(2), .width(8), .disabled(0), .enable("false")) multiplexer_1 (
    .in0(alu_1_r), .in1(din), .in2(register_3_q_2), .out(multiplexer_1_out), .sel(control_1_rinsel));  // open: in3
  reg_file reg_file_1 (
    .in(multiplexer_1_out), .isel(control_1_isel), .osel1(control_1_osel1), .osel2(control_1_osel2),
    .clear(reset), .clk(control_1_rclk), .out81(reg_file_1_out81), .out82(dout), .out16(reg_file_1_out16));  // open: _8_16
  Multiplexer #(.select(2), .width(16), .disabled(0), .enable("false")) multiplexer_2 (
    .in0(counter_2_q), .in1(reg_file_1_out16), .in2({register_3_q_3, register_3_q_2}), .out(addr),
    .sel(control_1_asel));  // open: in3
  alu alu_1 (
    .A(reg_file_1_out81), .B(dout), .sel(control_1_aluop), .clk(control_1_aclk), .R(alu_1_r));  // open: zero, carry
  Register register_1 (.D(din), .en(decoder_1_out0), .Q(register_1_q), .clk(clk), .clr(reset));
  Register register_2 (.D(din), .en(decoder_1_out1), .Q(register_2_q), .clk(clk), .clr(reset));
  Register #(.width(24)) register_3 (
    .D({din, register_2_q, register_1_q}), .en(decoder_1_out2),
    .Q({register_3_q_3, register_3_q_2, register_3_q}), .clk(clk), .clr(reset));
endmodule

module alu (
  input  [7:0] A,
  input  [7:0] B,
  input  [2:0] sel,
  input  clk,
  output [7:0] R,
  output zero,
  output carry
);

  wire adder_1_cout, comparator_1_eq, comparator_2_eq, controlled_buffer_1_out, multiplexer_2_out, nor_1_out,
       nor_2_out, not_1_out, or_1_out, subtractor_1_bout;
  wire [7:0] adder_1_out, and_1_out, not_2_out, or_2_out, shifter_1_out, shifter_2_out, subtractor_1_out;

  Pull_Resistor pull_resistor_1 (.node(R));
  not not_1 (not_1_out, nor_1_out);
  nor nor_1 (nor_1_out, sel[0], sel[1], sel[2]);
  assign controlled_buffer_1_out = not_1_out ? clk : 1'bz;  // Controlled_Buffer controlled_buffer_1
  Pull_Resistor pull_resistor_2 (.node(controlled_buffer_1_out));
  Comparator #(.width(3), .mode("unsigned")) comparator_1 (.a(sel), .b(3'b001), .eq(comparator_1_eq));  // open: gt, lt
  or or_1 (or_1_out, comparator_1_eq, comparator_2_eq);
  Comparator #(.width(3), .mode("unsigned")) comparator_2 (.a(sel), .b(3'b010), .eq(comparator_2_eq));  // open: gt, lt
  Adder adder_1 (.a(A), .b(B), .out(adder_1_out), .cout(adder_1_cout));  // open: cin
  Subtractor subtractor_1 (.a(A), .b(B), .out(subtractor_1_out), .bout(subtractor_1_bout));  // open: bin
  Shifter shifter_1 (.in(A), .\dist (B[2:0]), .out(shifter_1_out));
  Shifter #(.shift("lr")) shifter_2 (.in(A), .\dist (B[2:0]), .out(shifter_2_out));
  assign and_1_out = A & B;  // AND_Gate and_1, 8 bits wide
  assign or_2_out = A | B;  // OR_Gate or_2, 8 bits wide
  assign not_2_out = ~A;  // NOT_Gate not_2, 8 bits wide
  nor nor_2 (nor_2_out, R[0], R[1], R[2], R[3], R[4], R[5], R[6], R[7]);
  Multiplexer #(.select(3), .width(8), .disabled(0), .enable("false")) multiplexer_1 (
    .in1(adder_1_out), .in2(subtractor_1_out), .in3(shifter_1_out), .in4(shifter_2_out), .in5(and_1_out),
    .in6(or_2_out), .in7(not_2_out), .out(R), .sel(sel));  // open: in0
  Multiplexer #(.disabled(0)) multiplexer_2 (
    .in0(adder_1_cout), .in1(subtractor_1_bout), .out(multiplexer_2_out), .sel(comparator_2_eq), .en(or_1_out));
  D_Flip_Flop d_ff_1 (.clk(controlled_buffer_1_out), .D(nor_2_out), .Q(zero));  // open: Qn, preset, en, reset
  D_Flip_Flop d_ff_2 (.clk(controlled_buffer_1_out), .D(multiplexer_2_out), .Q(carry));  // open: Qn, preset, en, reset
endmodule

module main (
  input  in_1
);

  wire clock_1_out, cpu_1_r_w, not_1_out;
  wire [7:0] cpu_1_dout, ram_1_data;
  wire [15:0] cpu_1_addr;

  Clock clock_1 (.out(clock_1_out));
  cpu cpu_1 (.din(ram_1_data), .clk(clock_1_out), .reset(in_1), .R_W(cpu_1_r_w), .dout(cpu_1_dout), .addr(cpu_1_addr));
  not not_1 (not_1_out, cpu_1_r_w);
  RAM #(.addrWidth(16), .bus("separate")) ram_1 (
    .addr(cpu_1_addr), .din(cpu_1_dout), .data(ram_1_data), .str(cpu_1_r_w), .clk(clock_1_out), .ld(not_1_out));  // open: sel, clr
endmodule

module control (
  input  [23:0] op,
  input  en,
  input  clk,
  output [1:0] asel,
  output [2:0] isel,
  output [2:0] osel1,
  output [2:0] osel2,
  output _8_16,
  output [2:0] aluop,
  output [1:0] rinsel,
  output R_W,
  output rclk,
  output aclk
);

  wire comparator_1_eq, comparator_2_eq, comparator_3_eq, comparator_4_eq, comparator_5_eq, or_1_out,
       or_2_out, or_3_out, or_4_out, or_7_out, or_8_out, priority_encoder_1_out, priority_encoder_3_out,
       priority_encoder_4_out;
  wire [2:0] bit_extender_1_out;
  wire [7:0] pull_resistor_1_node, pull_resistor_1_node_2, pull_resistor_1_node_3;

  Pull_Resistor pull_resistor_1 (.node({pull_resistor_1_node_3, pull_resistor_1_node_2, pull_resistor_1_node}));
  assign {pull_resistor_1_node_3, pull_resistor_1_node_2, pull_resistor_1_node} = en ? op : 24'bz;  // Controlled_Buffer controlled_buffer_1
  Comparator #(.mode("unsigned")) comparator_1 (
    .a(pull_resistor_1_node), .b(8'h1), .eq(comparator_1_eq));  // open: gt, lt
  Comparator #(.mode("unsigned")) comparator_2 (
    .a(pull_resistor_1_node), .b(8'h2), .eq(comparator_2_eq));  // open: gt, lt
  Comparator #(.mode("unsigned")) comparator_3 (
    .a(pull_resistor_1_node), .b(8'h3), .eq(comparator_3_eq));  // open: gt, lt
  Comparator #(.mode("unsigned")) comparator_4 (
    .a(pull_resistor_1_node), .b(8'h4), .eq(comparator_4_eq));  // open: gt, lt
  Comparator #(.mode("unsigned")) comparator_5 (
    .a(pull_resistor_1_node), .b(8'h5), .eq(comparator_5_eq));  // open: gt, lt
  assign bit_extender_1_out = {{1{1'b0}}, pull_resistor_1_node_2[4:3]};  // Bit_Extender bit_extender_1
  or or_1 (or_1_out, comparator_1_eq, comparator_4_eq, comparator_3_eq);
  Multiplexer #(.width(3), .disabled(0), .enable("false")) multiplexer_1 (
    .in0(pull_resistor_1_node_2[2:0]), .out(isel), .sel(priority_encoder_1_out));  // open: in1
  Priority_Encoder #(.select(1)) priority_encoder_1 (
    .in0(or_1_out), .out(priority_encoder_1_out));  // open: in1, gs, en_out, en_in
  or or_2 (or_2_out, comparator_2_eq, comparator_5_eq);
  or or_3 (or_3_out, comparator_4_eq, comparator_5_eq);
  or or_4 (or_4_out, or_1_out, or_2_out);
  Priority_Encoder #(.select(2)) priority_encoder_2 (
    .in1(comparator_1_eq), .in2(comparator_3_eq), .out(rinsel));  // open: in0, in3, gs, en_out, en_in
  Multiplexer #(.width(3), .disabled(0), .enable("false")) multiplexer_2 (
    .in0(pull_resistor_1_node_2[2:0]), .out(osel2), .sel(priority_encoder_3_out));  // open: in1
  Priority_Encoder #(.select(1)) priority_encoder_3 (
    .in0(or_2_out), .out(priority_encoder_3_out));  // open: in1, gs, en_out, en_in
  Multiplexer #(.width(3), .disabled(0), .enable("false")) multiplexer_3 (
    .in0(bit_extender_1_out), .out(osel1), .sel(priority_encoder_4_out));  // open: in1
  Priority_Encoder #(.select(1)) priority_encoder_4 (
    .in0(or_3_out), .out(priority_encoder_4_out));  // open: in1, gs, en_out, en_in
  and and_1 (aclk, or_4_out, clk);
  Pull_Resistor pull_resistor_2 (.node(rclk));
  or or_5 (_8_16, comparator_4_eq, comparator_5_eq);
  or or_6 (R_W, comparator_5_eq, comparator_2_eq);
  or or_7 (or_7_out, comparator_4_eq, comparator_5_eq);
  or or_8 (or_8_out, comparator_1_eq, comparator_2_eq);
  Pull_Resistor pull_resistor_3 (.node(aluop));
  Pull_Resistor pull_resistor_4 (.node(R_W));
  Pull_Resistor pull_resistor_5 (.node(rinsel));
  Pull_Resistor pull_resistor_6 (.node(_8_16));
  Pull_Resistor pull_resistor_7 (.node(aclk));
  Priority_Encoder #(.select(2)) priority_encoder_5 (
    .in1(or_7_out), .in2(or_8_out), .out(asel));  // open: in0, in3, gs, en_out, en_in
  Pull_Resistor pull_resistor_8 (.node(asel));
  Pull_Resistor pull_resistor_9 (.node(osel2));
  Pull_Resistor pull_resistor_10 (.node(osel1));
  Pull_Resistor pull_resistor_11 (.node(isel));
endmodule
