// Logisim project pass test.circ as structural Verilog: 2 circuits, main circuit manager
module manager (
  input  [23:0] user_id,
  input  [31:0] new_pass,
  input  create,
  input  log_on,
  input  log_off,
  input  [31:0] pass,
  output logged_on
);

  wire clock_1_out, clock_2_out, clock_3_out, comparator_1_eq, multiplexer_1_out, not_1_out, not_2_out,
       or_1_out, ram_2_data, register_1_q;
  wire [31:0] ram_1_data;

  or or_1 (or_1_out, log_on, log_off);
  Clock clock_1 (.out(clock_1_out));
  not not_1 (not_1_out, create);
  RAM #(.addrWidth(24), .dataWidth(32), .bus("separate")) ram_1 (
    .addr(user_id), .din(new_pass), .data(ram_1_data), .str(create), .clk(clock_1_out), .ld(not_1_out));  // open: sel, clr
  Comparator #(.width(32)) comparator_1 (.a(ram_1_data), .b(pass), .eq(comparator_1_eq));  // open: gt, lt
  Register #(.width(1)) register_1 (
    .D(comparator_1_eq), .en(log_on), .Q(register_1_q), .clk(clock_2_out), .clr(log_off));
  Clock clock_2 (.out(clock_2_out));
  Multiplexer #(.disabled(0), .enable("false")) multiplexer_1 (
    .in0(register_1_q), .in1(1'b0), .out(multiplexer_1_out), .sel(log_off));
  Clock clock_3 (.out(clock_3_out));
  not not_2 (not_2_out, or_1_out);
  RAM #(.addrWidth(24), .dataWidth(1), .bus("separate")) ram_2 (
    .addr(user_id), .din(multiplexer_1_out), .data(ram_2_data), .str(or_1_out), .clk(clock_3_out),
    .ld(not_2_out));  // open: sel, clr
  Multiplexer #(.disabled(0), .enable("false")) multiplexer_2 (
    .in0(ram_2_data), .in1(multiplexer_1_out), .out(logged_on), .sel(or_1_out));
endmodule

module test1 (
  input  [23:0] user_id,
  input  [31:0] new_pass,
  input  create,
  input  log_on,
  input  log_off,
  input  [31:0] pass,
  output logged_on
);

  manager manager_1 (
    .user_id(user_id), .new_pass(new_pass), .create(create), .log_on(log_on), .log_off(log_off), .pass(pass),
    .logged_on(logged_on));
endmodule
