// Logisim project rock paper scissors.circ as structural Verilog: 4 circuits, main circuit rps
module rps (
  input  Ar,
  input  Ap,
  input  As,
  input  Br,
  input  Bp,
  input  Bs,
  output Idle,
  output A_Wins,
  output B_Wins,
  output A_Cheats,
  output B_Cheats,
  output Both_Cheat
);

  wire and_1_out, and_5_out, and_6_out, and_8_out, and_9_out, and_10_out, and_11_out, and_13_out, or_1_out,
       or_2_out, or_3_out, or_4_out, or_5_out, xnor_1_out, xnor_2_out;

  nor nor_1 (Idle, A_Wins, B_Wins, A_Cheats, B_Cheats, Both_Cheat);
  Pull_Resistor pull_resistor_1 (.node(Ap));
  NotExactlyOne xnor_1 (.out(xnor_1_out), .in0(Ar), .in1(Ap), .in2(As));
  Pull_Resistor pull_resistor_2 (.node(Ar));
  Pull_Resistor pull_resistor_3 (.node(As));
  or or_1 (or_1_out, Ar, Ap, As);
  and and_1 (and_1_out, xnor_1_out, or_1_out);
  and and_2 (Both_Cheat, and_1_out, and_13_out);
  and and_3 (A_Cheats, and_1_out, ~Both_Cheat);  // AND_Gate
  or or_2 (or_2_out, and_1_out, and_13_out);
  and and_4 (B_Cheats, and_13_out, ~Both_Cheat);  // AND_Gate
  and and_5 (and_5_out, As, Bp);
  and and_6 (and_6_out, Ap, Br);
  or or_3 (or_3_out, and_5_out, and_6_out, and_8_out);
  and and_7 (A_Wins, or_3_out, ~or_2_out);  // AND_Gate
  and and_8 (and_8_out, Ar, Bs);
  and and_9 (and_9_out, As, Br);
  and and_10 (and_10_out, Bp, Ar);
  or or_4 (or_4_out, and_9_out, and_10_out, and_11_out);
  and and_11 (and_11_out, Bs, Ap);
  and and_12 (B_Wins, or_4_out, ~or_2_out);  // AND_Gate
  Pull_Resistor pull_resistor_4 (.node(Bp));
  Pull_Resistor pull_resistor_5 (.node(Br));
  NotExactlyOne xnor_2 (.out(xnor_2_out), .in0(Br), .in1(Bp), .in2(Bs));
  Pull_Resistor pull_resistor_6 (.node(Bs));
  or or_5 (or_5_out, Br, Bp, Bp);
  and and_13 (and_13_out, xnor_2_out, or_5_out);
endmodule

module main (
);

  wire a_buttons_1_out_2, a_buttons_1_out_3, a_buttons_1_out_4, b_buttons_1_out_2, b_buttons_1_out_3,
       b_buttons_1_out_4, Reset_out, rps_1_a_cheats, rps_1_a_wins, rps_1_b_cheats, rps_1_b_wins,
       rps_1_both_cheat, rps_1_idle;

  Button Reset (.out(Reset_out));
  A_buttons a_buttons_1 (
    .Reset(Reset_out), .out_2(a_buttons_1_out_2), .out_3(a_buttons_1_out_3), .out_4(a_buttons_1_out_4));
  LED Idle (.in(rps_1_idle));
  LED A_Wins (.in(rps_1_a_wins));
  LED B_Wins (.in(rps_1_b_wins));
  LED A_Cheats (.in(rps_1_a_cheats));
  LED B_Cheats (.in(rps_1_b_cheats));
  LED Both_Cheat (.in(rps_1_both_cheat));
  rps rps_1 (
    .Ar(a_buttons_1_out_2), .Ap(a_buttons_1_out_3), .As(a_buttons_1_out_4), .Idle(rps_1_idle),
    .A_Wins(rps_1_a_wins), .B_Wins(rps_1_b_wins), .A_Cheats(rps_1_a_cheats), .B_Cheats(rps_1_b_cheats),
    .Both_Cheat(rps_1_both_cheat), .Br(b_buttons_1_out_2), .Bp(b_buttons_1_out_3), .Bs(b_buttons_1_out_4));
  B_buttons b_buttons_1 (
    .Reset(Reset_out), .out_2(b_buttons_1_out_2), .out_3(b_buttons_1_out_3), .out_4(b_buttons_1_out_4));
endmodule

module A_buttons (
  input  Reset,
  output out_2,
  output out_3,
  output out_4
);

  wire clock_1_out, Paper_out, Rock_out, Scissors_out;

  Button Rock (.out(Rock_out));
  Button Paper (.out(Paper_out));
  Button Scissors (.out(Scissors_out));
  Clock clock_1 (.out(clock_1_out));
  T_Flip_Flop t_ff_1 (.clk(clock_1_out), .T(Rock_out), .Q(out_2), .reset(Reset));  // open: Qn, preset, en
  T_Flip_Flop t_ff_2 (.clk(clock_1_out), .T(Paper_out), .Q(out_3), .reset(Reset));  // open: Qn, preset, en
  T_Flip_Flop t_ff_3 (.clk(clock_1_out), .T(Scissors_out), .Q(out_4), .reset(Reset));  // open: Qn, preset, en
endmodule

module B_buttons (
  input  Reset,
  output out_2,
  output out_3,
  output out_4
);

  wire clock_1_out, Paper_out, Rock_out, Scissors_out;

  Button Rock (.out(Rock_out));
  Button Paper (.out(Paper_out));
  Button Scissors (.out(Scissors_out));
  Clock clock_1 (.out(clock_1_out));
  T_Flip_Flop t_ff_1 (.clk(clock_1_out), .T(Rock_out), .Q(out_2), .reset(Reset));  // open: Qn, preset, en
  T_Flip_Flop t_ff_2 (.clk(clock_1_out), .T(Paper_out), .Q(out_3), .reset(Reset));  // open: Qn, preset, en
  T_Flip_Flop t_ff_3 (.clk(clock_1_out), .T(Scissors_out), .Q(out_4), .reset(Reset));  // open: Qn, preset, en
endmodule
