// Logisim project text editor 3 disp.circ as structural Verilog: 1 circuit, main circuit main
module main (
);

  wire and_1_out, and_2_out, and_3_out, and_4_out, and_5_out, and_6_out, and_7_out, clock_1_out,
       decoder_1_out0, decoder_1_out1, decoder_1_out2, er_out, keyboard_1_avail, not_1_out, not_2_out,
       or_1_out, or_2_out, or_3_out, or_4_out, or_5_out, or_6_out, or_7_out, or_8_out, or_9_out, or_10_out,
       or_11_out, or_12_out, psi_out, res_out;
  wire [1:0] counter_1_q;
  wire [6:0] keyboard_1_data, multiplexer_1_out, multiplexer_2_out, multiplexer_3_out, ram_1_data,
       ram_2_data, ram_3_data;
  wire [23:0] counter_2_q, counter_3_q, counter_4_q;

  TTY tty_1 (.data(multiplexer_2_out), .clk(and_1_out), .we(decoder_1_out0), .clr(or_1_out));
  Keyboard keyboard_1 (.clk(and_1_out), .avail(keyboard_1_avail), .data(keyboard_1_data));  // open: re, clr
  and and_1 (and_1_out, clock_1_out, ~res_out);  // AND_Gate
  Clock clock_1 (.out(clock_1_out));
  Button res (.out(res_out));
  Button er (.out(er_out));
  and and_2 (and_2_out, er_out, decoder_1_out0);
  and and_3 (and_3_out, res_out, decoder_1_out0);
  or or_1 (or_1_out, res_out, ~decoder_1_out0);  // OR_Gate
  or or_2 (or_2_out, and_4_out, ~decoder_1_out1);  // OR_Gate
  and and_4 (and_4_out, res_out, decoder_1_out1);
  Counter #(.width(2), .max('h2)) counter_1 (
    .count(psi_out), .Q(counter_1_q), .clk(psi_out));  // open: load, D, carry, clr
  Button psi (.out(psi_out));
  or or_3 (or_3_out, and_3_out, ~decoder_1_out0);  // OR_Gate
  or or_4 (or_4_out, res_out, ~decoder_1_out1);  // OR_Gate
  Counter #(.width(24), .max('hffffff)) counter_2 (
    .count(or_6_out), .Q(counter_2_q), .clk(and_1_out), .clr(or_2_out));  // open: load, D, carry
  and and_5 (and_5_out, decoder_1_out1, er_out);
  Decoder #(.select(2), .disabled(0), .enable("false")) decoder_1 (
    .out0(decoder_1_out0), .out1(decoder_1_out1), .out2(decoder_1_out2), .sel(counter_1_q));  // open: out3
  Counter #(.width(24), .max('hffffff)) counter_3 (
    .count(or_6_out), .Q(counter_3_q), .clk(and_1_out), .clr(or_3_out));  // open: load, D, carry
  TTY tty_2 (.data(multiplexer_1_out), .clk(and_1_out), .we(decoder_1_out1), .clr(or_4_out));
  RAM #(.addrWidth(24), .dataWidth(7), .bus("separate")) ram_1 (
    .addr(counter_2_q), .din(keyboard_1_data), .data(ram_1_data), .str(keyboard_1_avail),
    .sel(decoder_1_out1), .clk(and_1_out), .ld(not_1_out), .clr(and_5_out));
  not not_1 (not_1_out, keyboard_1_avail);
  not not_2 (not_2_out, keyboard_1_avail);
  Pull_Resistor pull_resistor_1 (.node(ram_1_data));
  Multiplexer #(.width(7), .disabled(0), .enable("false")) multiplexer_1 (
    .in0(ram_1_data), .in1(keyboard_1_data), .out(multiplexer_1_out), .sel(keyboard_1_avail));
  or or_5 (or_5_out, and_6_out, ~decoder_1_out2);  // OR_Gate
  Multiplexer #(.width(7), .disabled(0), .enable("false")) multiplexer_2 (
    .in0(ram_2_data), .in1(keyboard_1_data), .out(multiplexer_2_out), .sel(keyboard_1_avail));
  RAM #(.addrWidth(24), .dataWidth(7), .bus("separate")) ram_2 (
    .addr(counter_3_q), .din(keyboard_1_data), .data(ram_2_data), .str(keyboard_1_avail),
    .sel(decoder_1_out0), .clk(and_1_out), .ld(not_2_out), .clr(and_2_out));
  Counter #(.width(24), .max('hffffff)) counter_4 (
    .count(or_6_out), .Q(counter_4_q), .clk(and_1_out), .clr(or_5_out));  // open: load, D, carry
  Pull_Resistor pull_resistor_2 (.node(ram_2_data));
  and and_6 (and_6_out, decoder_1_out2, res_out);
  TTY tty_3 (.data(multiplexer_3_out), .clk(and_1_out), .we(decoder_1_out2), .clr(or_7_out));
  or or_6 (or_6_out, or_9_out, or_12_out, or_11_out);
  or or_7 (or_7_out, res_out, ~decoder_1_out2);  // OR_Gate
  or or_8 (or_8_out, keyboard_1_data[0], keyboard_1_data[1], keyboard_1_data[2], keyboard_1_data[3], keyboard_1_data[4], keyboard_1_data[5], keyboard_1_data[6]);
  or or_9 (or_9_out, or_8_out, or_10_out);
  or or_10 (or_10_out, ram_2_data[0], ram_2_data[1], ram_2_data[2], ram_2_data[3], ram_2_data[4], ram_2_data[5], ram_2_data[6]);
  RAM #(.addrWidth(24), .dataWidth(7), .bus("separate")) ram_3 (
    .addr(counter_4_q), .din(keyboard_1_data), .data(ram_3_data), .str(keyboard_1_avail),
    .sel(decoder_1_out2), .clk(and_1_out), .ld(not_2_out), .clr(and_7_out));
  Multiplexer #(.width(7), .disabled(0), .enable("false")) multiplexer_3 (
    .in0(ram_3_data), .in1(keyboard_1_data), .out(multiplexer_3_out), .sel(keyboard_1_avail));
  and and_7 (and_7_out, decoder_1_out2, res_out);
  Pull_Resistor pull_resistor_3 (.node(ram_3_data));
  or or_11 (or_11_out, ram_3_data[0], ram_3_data[1], ram_3_data[2], ram_3_data[3], ram_3_data[4], ram_3_data[5], ram_3_data[6]);
  or or_12 (or_12_out, ram_1_data[0], ram_1_data[1], ram_1_data[2], ram_1_data[3], ram_1_data[4], ram_1_data[5], ram_1_data[6]);
endmodule
