// Logisim project text editor IM.circ as structural Verilog: 3 circuits, main circuit main
module main (
);

  wire clock_1_out, keyboard_1_avail, res_disp_out, res_key_out, res_out;
  wire [6:0] keyboard_1_data, n8609_1_ascii_out;

  Button res (.out(res_out));
  Clock clock_1 (.out(clock_1_out));
  Button res_key (.out(res_key_out));
  Button res_disp (.out(res_disp_out));
  Keyboard keyboard_1 (
    .clk(clock_1_out), .clr(res_key_out), .avail(keyboard_1_avail), .data(keyboard_1_data));  // open: re
  TTY tty_1 (.data(n8609_1_ascii_out), .clk(clock_1_out), .clr(res_disp_out));  // open: we
  _8609 u_8609_1 (
    .reset(res_out), .load_chars(keyboard_1_avail), .ASCII_in(keyboard_1_data), .ASCII_out(n8609_1_ascii_out));
endmodule

module _7_8_show (
  input  [7:0] _8_in,
  input  [6:0] _7_in,
  output [3:0] d_2,
  output [3:0] d_1,
  output [3:0] d_2_ASCII,
  output [3:0] d_1_ASCII
);

  assign {d_2_ASCII, d_1_ASCII} = {{1{1'b0}}, _7_in};  // Bit_Extender bit_extender_1

  assign d_1 = _8_in[3:0];
  assign d_2 = _8_in[7:4];
endmodule

module _8609 (
  input  reset,
  input  load_chars,
  input  [6:0] ASCII_in,
  output [6:0] ASCII_out
);

  wire multiplexer_1_out, not_1_out, not_2_out, or_1_out, or_2_out;
  wire [6:0] ram_1_data;
  wire [23:0] counter_1_q;

  Counter #(.width(24), .max('hffffff)) counter_1 (
    .count(multiplexer_1_out), .Q(counter_1_q), .clk(multiplexer_1_out), .clr(reset));  // open: load, D, carry
  or or_1 (or_1_out, ASCII_in[0], ASCII_in[1], ASCII_in[2], ASCII_in[3], ASCII_in[4], ASCII_in[5], ASCII_in[6]);
  Multiplexer #(.disabled(0), .enable("false")) multiplexer_1 (
    .in0(or_1_out), .in1(or_2_out), .out(multiplexer_1_out), .sel(not_1_out));
  not not_1 (not_1_out, load_chars);
  or or_2 (or_2_out, ram_1_data[0], ram_1_data[1], ram_1_data[2], ram_1_data[3], ram_1_data[4], ram_1_data[5], ram_1_data[6]);
  RAM #(.addrWidth(24), .dataWidth(7), .bus("separate")) ram_1 (
    .addr(counter_1_q), .din(ASCII_in), .data(ram_1_data), .str(load_chars), .clk(load_chars), .ld(not_2_out));  // open: sel, clr
  not not_2 (not_2_out, load_chars);
  Multiplexer #(.width(7), .disabled(0), .enable("false")) multiplexer_2 (
    .in0(ram_1_data), .in1(ASCII_in), .out(ASCII_out), .sel(load_chars));
endmodule
