// Logisim project text editor original.circ as structural Verilog: 1 circuit, main circuit main
module main (
  input  in_1
);

  wire and_1_out, and_2_out, button_1_out, button_2_out, button_3_out, button_4_out, clock_1_out,
       controlled_buffer_7_out, decoder_1_out0, decoder_1_out1, keyboard_1_avail, not_1_out, not_2_out,
       not_3_out, or_1_out, pull_resistor_1_node, pull_resistor_2_node;
  wire [1:0] bit_extender_1_out;
  wire [6:0] controlled_buffer_5_out, keyboard_1_data, or_3_out, pull_resistor_3_node;
  wire [6:6] and_3_out, or_2_out;
  wire [15:0] counter_1_q;

  Keyboard #(.buflen(200)) keyboard_1 (
    .clk(button_2_out), .avail(keyboard_1_avail), .data(keyboard_1_data));  // open: re, clr
  Pull_Resistor pull_resistor_1 (.node(pull_resistor_1_node));
  assign pull_resistor_1_node = keyboard_1_avail ? keyboard_1_avail : 1'bz;  // Controlled_Buffer controlled_buffer_1
  assign pull_resistor_1_node = button_2_out ? button_2_out : 1'bz;  // Controlled_Buffer controlled_buffer_2
  Button button_1 (.out(button_1_out));
  not not_1 (not_1_out, pull_resistor_1_node);
  Button button_2 (.out(button_2_out));
  Button button_3 (.out(button_3_out));
  Clock clock_1 (.out(clock_1_out));
  Button button_4 (.out(button_4_out));
  Pull_Resistor pull_resistor_2 (.node(pull_resistor_2_node));
  assign pull_resistor_2_node = button_2_out ? button_2_out : 1'bz;  // Controlled_Buffer controlled_buffer_3
  and and_1 (and_1_out, pull_resistor_1_node, button_2_out);
  assign bit_extender_1_out = {{1{1'b0}}, in_1};  // Bit_Extender bit_extender_1
  and and_2 (and_2_out, in_1, not_1_out);
  assign pull_resistor_2_node = clock_1_out ? clock_1_out : 1'bz;  // Controlled_Buffer controlled_buffer_4
  Counter #(.width(16), .max('hffff), .trigger("falling")) counter_1 (
    .count(or_1_out), .Q(counter_1_q), .clk(pull_resistor_2_node), .clr(button_1_out));  // open: load, D, carry
  buf or_1 (or_1_out, and_1_out);  // OR_Gate
  not not_2 (not_2_out, and_2_out);
  Decoder #(.select(2), .disabled(0)) decoder_1 (
    .out0(decoder_1_out0), .out1(decoder_1_out1), .sel(bit_extender_1_out), .en(not_2_out));  // open: out2, out3
  or or_2 (or_2_out[6], clock_1_out, pull_resistor_2_node);
  Pull_Resistor pull_resistor_3 (.node(pull_resistor_3_node));
  assign controlled_buffer_5_out = decoder_1_out0 ? pull_resistor_3_node : 7'bz;  // Controlled_Buffer controlled_buffer_5
  RAM #(.addrWidth(16), .dataWidth(7), .bus("separate")) ram_1 (
    .addr(counter_1_q), .din(keyboard_1_data), .data(pull_resistor_3_node), .str(decoder_1_out1),
    .clk(pull_resistor_2_node), .ld(decoder_1_out0), .clr(button_3_out));  // open: sel
  not not_3 (not_3_out, decoder_1_out0);
  assign controlled_buffer_5_out = not_3_out ? keyboard_1_data : 7'bz;  // Controlled_Buffer controlled_buffer_6
  TTY tty_1 (.data(controlled_buffer_5_out), .clk(or_2_out[6]), .we(controlled_buffer_7_out), .clr(button_4_out));
  assign controlled_buffer_7_out = pull_resistor_2_node ? pull_resistor_2_node : 1'bz;  // Controlled_Buffer controlled_buffer_7
  assign controlled_buffer_7_out = and_3_out[6] ? and_3_out[6] : 1'bz;  // Controlled_Buffer controlled_buffer_8
  assign or_3_out = pull_resistor_3_node | {7{1'b0}};  // OR_Gate or_3, 7 bits wide
  assign {7{and_3_out[6]}} = or_3_out & {7{or_2_out[6]}};  // AND_Gate and_3, 7 bits wide
  Pull_Resistor pull_resistor_4 (.node(controlled_buffer_7_out));
endmodule
