// Logisim project text editor.circ as structural Verilog: 3 circuits, main circuit main
module main (
  input  load_chars
);

  wire clear_out, cpu_1_clock_enable_out, display_clock_out, DO_NOT_TOUCH_out, keyboard_1_avail,
       main_clock_out, reset_out;
  wire [6:0] cpu_1_ascii_out, keyboard_1_data;

  Button clear (.out(clear_out));
  Button DO_NOT_TOUCH (.out(DO_NOT_TOUCH_out));
  Button reset (.out(reset_out));
  Button main_clock (.out(main_clock_out));
  Clock display_clock (.out(display_clock_out));
  Keyboard keyboard_1 (.clk(main_clock_out), .avail(keyboard_1_avail), .data(keyboard_1_data));  // open: re, clr
  cpu cpu_1 (
    .ASCII_in(keyboard_1_data), .avalible_in(keyboard_1_avail), .reset(reset_out),
    .main_clock_in(main_clock_out), .R_W(load_chars), .clear_in(DO_NOT_TOUCH_out),
    .display_clock_in(display_clock_out), .ASCII_out(cpu_1_ascii_out),
    .clock_enable_out(cpu_1_clock_enable_out));
  TTY tty_1 (.data(cpu_1_ascii_out), .clk(display_clock_out), .we(cpu_1_clock_enable_out), .clr(clear_out));
endmodule

module cpu (
  input  [6:0] ASCII_in,
  input  avalible_in,
  input  reset,
  input  main_clock_in,
  input  R_W,
  input  clear_in,
  input  display_clock_in,
  output [6:0] ASCII_out,
  output clock_enable_out
);

  wire control_mem_1_r_out, not_1_out, not_2_out, pull_resistor_1_node;
  wire [6:0] pull_resistor_3_node;

  Pull_Resistor pull_resistor_1 (.node(pull_resistor_1_node));
  assign pull_resistor_1_node = main_clock_in ? main_clock_in : 1'bz;  // Controlled_Buffer controlled_buffer_1
  assign pull_resistor_1_node = display_clock_in ? display_clock_in : 1'bz;  // Controlled_Buffer controlled_buffer_2
  Pull_Resistor pull_resistor_2 (.node(clear_in));
  Pull_Resistor pull_resistor_3 (.node(pull_resistor_3_node));
  assign ASCII_out = control_mem_1_r_out ? pull_resistor_3_node : 7'bz;  // Controlled_Buffer controlled_buffer_3
  not not_1 (not_1_out, control_mem_1_r_out);
  assign ASCII_out = not_1_out ? ASCII_in : 7'bz;  // Controlled_Buffer controlled_buffer_4
  not not_2 (not_2_out, avalible_in);
  control_mem control_mem_1 (
    .main_clock_in(pull_resistor_1_node), .data_in(ASCII_in), .data_out(pull_resistor_3_node),
    .count_in(main_clock_in), .reset_in(reset), .r_w(R_W), .avalible(not_2_out), .r_out(control_mem_1_r_out),
    .clock_enable_out(clock_enable_out));
endmodule

module control_mem (
  input  [6:0] data_in,
  input  main_clock_in,
  input  count_in,
  input  reset_in,
  input  r_w,
  input  avalible,
  output [6:0] data_out,
  output clock_enable_out,
  output r_out
);

  wire and_1_out, decoder_1_out1, not_1_out, not_2_out, or_1_out;
  wire [1:0] bit_extender_1_out;
  wire [6:0] and_2_out, ram_1_data;
  wire [15:0] counter_1_q;

  assign data_out = r_w ? data_in : 7'bz;  // Controlled_Buffer controlled_buffer_1
  assign bit_extender_1_out = {{1{1'b0}}, r_w};  // Bit_Extender bit_extender_1
  and and_1 (and_1_out, r_w, avalible);
  Counter #(.width(16), .max('hffff), .trigger("falling")) counter_1 (
    .count(main_clock_in), .Q(counter_1_q), .clk(count_in), .clr(reset_in));  // open: load, D, carry
  not not_1 (not_1_out, and_1_out);
  Decoder #(.select(2), .disabled(0)) decoder_1 (
    .out0(r_out), .out1(decoder_1_out1), .sel(bit_extender_1_out), .en(not_1_out));  // open: out2, out3
  not not_2 (not_2_out, r_w);
  assign data_out = not_2_out ? ram_1_data : 7'bz;  // Controlled_Buffer controlled_buffer_2
  RAM #(.addrWidth(16), .dataWidth(7), .bus("separate")) ram_1 (
    .addr(counter_1_q), .din(data_in), .data(ram_1_data), .str(decoder_1_out1), .clk(main_clock_in),
    .ld(r_out));  // open: sel, clr
  // Probe on data_out
  // Probe on data_out
  assign clock_enable_out = or_1_out ? or_1_out : 1'bz;  // Controlled_Buffer controlled_buffer_3
  assign clock_enable_out = main_clock_in ? main_clock_in : 1'bz;  // Controlled_Buffer controlled_buffer_4
  // Probe on and_2_out
  assign and_2_out = data_out & {7{main_clock_in}};  // AND_Gate and_2, 7 bits wide
  Pull_Resistor pull_resistor_1 (.node(clock_enable_out));
  or or_1 (or_1_out, and_2_out[0], and_2_out[1], and_2_out[2], and_2_out[3], and_2_out[4], and_2_out[5], and_2_out[6]);
endmodule
