// Logisim project textart.circ as structural Verilog: 2 circuits, main circuit main
module main (
  input  [6:0] din,
  input  clk,
  input  res,
  output [6:0] out1,
  output [6:0] out2,
  output [6:0] out3,
  output [6:0] out4,
  output [6:0] out5,
  output [6:0] out6,
  output [6:0] out7,
  output [6:0] out8,
  output [6:0] out9,
  output [6:0] out10,
  output [6:0] out11,
  output [6:0] out12,
  output [6:0] out13,
  output [6:0] out14,
  output [6:0] out15,
  output [6:0] out16
);

  wire decoder_1_out0, decoder_1_out1, decoder_1_out2, decoder_1_out3, decoder_1_out4, decoder_1_out5,
       decoder_1_out6, decoder_1_out7, decoder_1_out8, decoder_1_out9, decoder_1_out10, decoder_1_out11,
       decoder_1_out12, decoder_1_out13, decoder_1_out14, decoder_1_out15;
  wire [3:0] counter_1_q;

  Decoder #(.select(4), .disabled(0), .enable("false")) decoder_1 (
    .out0(decoder_1_out0), .out1(decoder_1_out1), .out2(decoder_1_out2), .out3(decoder_1_out3),
    .out4(decoder_1_out4), .out5(decoder_1_out5), .out6(decoder_1_out6), .out7(decoder_1_out7),
    .out8(decoder_1_out8), .out9(decoder_1_out9), .out10(decoder_1_out10), .out11(decoder_1_out11),
    .out12(decoder_1_out12), .out13(decoder_1_out13), .out14(decoder_1_out14), .out15(decoder_1_out15),
    .sel(counter_1_q));
  Counter #(.width(4), .max('hf), .ongoal("stay"), .trigger("falling")) counter_1 (
    .Q(counter_1_q), .clk(clk), .clr(res));  // open: load, D, count, carry
  Register #(.width(7)) register_1 (.D(din), .en(decoder_1_out0), .Q(out1), .clk(clk), .clr(res));
  Register #(.width(7)) register_2 (.D(din), .en(decoder_1_out1), .Q(out2), .clk(clk), .clr(res));
  Register #(.width(7)) register_3 (.D(din), .en(decoder_1_out2), .Q(out3), .clk(clk), .clr(res));
  Register #(.width(7)) register_4 (.D(din), .en(decoder_1_out3), .Q(out4), .clk(clk), .clr(res));
  Register #(.width(7)) register_5 (.D(din), .en(decoder_1_out4), .Q(out5), .clk(clk), .clr(res));
  Register #(.width(7)) register_6 (.D(din), .en(decoder_1_out5), .Q(out6), .clk(clk), .clr(res));
  Register #(.width(7)) register_7 (.D(din), .en(decoder_1_out6), .Q(out7), .clk(clk), .clr(res));
  Register #(.width(7)) register_8 (.D(din), .en(decoder_1_out7), .Q(out8), .clk(clk), .clr(res));
  Register #(.width(7)) register_9 (.D(din), .en(decoder_1_out8), .Q(out9), .clk(clk), .clr(res));
  Register #(.width(7)) register_10 (.D(din), .en(decoder_1_out9), .Q(out10), .clk(clk), .clr(res));
  Register #(.width(7)) register_11 (.D(din), .en(decoder_1_out10), .Q(out11), .clk(clk), .clr(res));
  Register #(.width(7)) register_12 (.D(din), .en(decoder_1_out11), .Q(out12), .clk(clk), .clr(res));
  Register #(.width(7)) register_13 (.D(din), .en(decoder_1_out12), .Q(out13), .clk(clk), .clr(res));
  Register #(.width(7)) register_14 (.D(din), .en(decoder_1_out13), .Q(out14), .clk(clk), .clr(res));
  Register #(.width(7)) register_15 (.D(din), .en(decoder_1_out14), .Q(out15), .clk(clk), .clr(res));
  Register #(.width(7)) register_16 (.D(din), .en(decoder_1_out15), .Q(out16), .clk(clk), .clr(res));

  // Other names for the same wires on the sheet: z = res
endmodule

module fun (
);

  wire and_1_out, clk_out, clr_out, counter_1_carry, demultiplexer_2_out0, demultiplexer_2_out1, or_1_out,
       res_out;
  wire [4:0] counter_1_q;
  wire [6:0] demultiplexer_1_out0, demultiplexer_1_out1, keyboard_1_data, main_1_out1, main_1_out2,
       main_1_out3, main_1_out4, main_1_out5, main_1_out6, main_1_out7, main_1_out8, main_1_out9,
       main_1_out10, main_1_out11, main_1_out12, main_1_out13, main_1_out14, main_1_out15, main_1_out16,
       main_2_out1, main_2_out2, main_2_out3, main_2_out4, main_2_out5, main_2_out6, main_2_out7,
       main_2_out8, main_2_out9, main_2_out10, main_2_out11, main_2_out12, main_2_out13, main_2_out14,
       main_2_out15, main_2_out16;

  Counter #(.width(4), .max('hf), .trigger("falling")) counter_1 (
    .Q(counter_1_q[3:0]), .carry(counter_1_carry), .clk(clk_out), .clr(res_out));  // open: load, D, count
  Keyboard keyboard_1 (.clk(clk_out), .clr(or_1_out), .data(keyboard_1_data));  // open: re, avail
  Button clk (.out(clk_out));
  Button clr (.out(clr_out));
  or or_1 (or_1_out, clr_out, res_out);
  Button res (.out(res_out));
  and and_1 (and_1_out, clk_out, ~counter_1_q[4]);  // AND_Gate
  T_Flip_Flop t_ff_1 (
    .clk(and_1_out), .T(counter_1_carry), .Q(counter_1_q[4]), .reset(res_out));  // open: Qn, preset, en
  Demultiplexer #(.width(7), .disabled(0), .enable("false")) demultiplexer_1 (
    .out0(demultiplexer_1_out0), .out1(demultiplexer_1_out1), .in(keyboard_1_data), .sel(counter_1_q[4]));
  Demultiplexer #(.disabled(0), .enable("false")) demultiplexer_2 (
    .out0(demultiplexer_2_out0), .out1(demultiplexer_2_out1), .in(clk_out), .sel(counter_1_q[4]));
  DotMatrix #(.inputtype("row"), .matrixcols(7), .matrixrows(32)) dotmatrix_1 (
    .row0(main_1_out1), .row1(main_1_out2), .row2(main_1_out3), .row3(main_1_out4), .row4(main_1_out5),
    .row5(main_1_out6), .row6(main_1_out7), .row7(main_1_out8), .row8(main_1_out9), .row9(main_1_out10),
    .row10(main_1_out11), .row11(main_1_out12), .row12(main_1_out13), .row13(main_1_out14),
    .row14(main_1_out15), .row15(main_1_out16), .row16(main_2_out1), .row17(main_2_out2),
    .row18(main_2_out3), .row19(main_2_out4), .row20(main_2_out5), .row21(main_2_out6), .row22(main_2_out7),
    .row23(main_2_out8), .row24(main_2_out9), .row25(main_2_out10), .row26(main_2_out11),
    .row27(main_2_out12), .row28(main_2_out13), .row29(main_2_out14), .row30(main_2_out15),
    .row31(main_2_out16));
  main main_1 (
    .din(demultiplexer_1_out0), .clk(demultiplexer_2_out0), .res(res_out), .out1(main_1_out1),
    .out2(main_1_out2), .out3(main_1_out3), .out4(main_1_out4), .out5(main_1_out5), .out6(main_1_out6),
    .out7(main_1_out7), .out8(main_1_out8), .out9(main_1_out9), .out10(main_1_out10), .out11(main_1_out11),
    .out12(main_1_out12), .out13(main_1_out13), .out14(main_1_out14), .out15(main_1_out15),
    .out16(main_1_out16));
  main main_2 (
    .din(demultiplexer_1_out1), .clk(demultiplexer_2_out1), .res(res_out), .out1(main_2_out1),
    .out2(main_2_out2), .out3(main_2_out3), .out4(main_2_out4), .out5(main_2_out5), .out6(main_2_out6),
    .out7(main_2_out7), .out8(main_2_out8), .out9(main_2_out9), .out10(main_2_out10), .out11(main_2_out11),
    .out12(main_2_out12), .out13(main_2_out13), .out14(main_2_out14), .out15(main_2_out15),
    .out16(main_2_out16));
  RAM #(.addrWidth(5), .dataWidth(7), .bus("separate")) ram_1 (
    .addr(counter_1_q), .din(keyboard_1_data), .str(1'b1), .clk(clk_out), .ld(1'b0), .clr(res_out));  // open: data, sel
endmodule
