// Logisim project turing.circ as structural Verilog: 1 circuit, main circuit main
module main (
  input  en
);

  wire and_1_out, and_2_out, and_3_out, clock_1_out, comparator_1_eq, comparator_2_eq, decoder_1_out0,
       decoder_1_out1, decoder_1_out2, or_1_out;
  wire [1:0] counter_3_q;
  wire [7:0] counter_1_q, counter_2_q, ram_1_data, ram_2_data, register_1_q, rom_1_data, rom_2_data,
       rom_3_data;

  or or_1 (or_1_out, decoder_1_out2, and_3_out);
  Counter counter_1 (.count(or_1_out), .Q(counter_1_q), .clk(clock_1_out));  // open: load, D, carry, clr
  Clock clock_1 (.out(clock_1_out));
  ROM rom_1 (.addr(counter_1_q), .data(rom_1_data));  // open: sel
  ROM rom_2 (.addr(counter_1_q), .data(rom_2_data));  // open: sel
  RAM ram_1 (.addr(counter_1_q), .data(ram_1_data));  // open: sel, clk, ld, clr
  Register register_1 (.D(rom_3_data), .en(decoder_1_out1), .Q(register_1_q), .clk(clock_1_out));  // open: clr
  ROM rom_3 (.addr(counter_1_q), .data(rom_3_data));  // open: sel
  Comparator comparator_1 (.a(register_1_q), .b(rom_1_data), .eq(comparator_1_eq));  // open: gt, lt
  Counter counter_2 (.count(decoder_1_out2), .Q(counter_2_q), .clk(clock_1_out));  // open: load, D, carry, clr
  RAM #(.bus("separate")) ram_2 (
    .addr(counter_2_q), .din(ram_1_data), .data(ram_2_data), .str(decoder_1_out1), .clk(clock_1_out),
    .ld(decoder_1_out0));  // open: sel, clr
  Counter #(.width(2), .max('h2)) counter_3 (
    .count(clock_1_out), .Q(counter_3_q), .clk(clock_1_out));  // open: load, D, carry, clr
  Comparator comparator_2 (.a(ram_2_data), .b(rom_2_data), .eq(comparator_2_eq));  // open: gt, lt
  and and_1 (and_1_out, and_2_out, en);
  and and_2 (and_2_out, comparator_2_eq, comparator_1_eq);
  Decoder #(.select(2), .disabled(0)) decoder_1 (
    .out0(decoder_1_out0), .out1(decoder_1_out1), .out2(decoder_1_out2), .sel(counter_3_q), .en(and_1_out));  // open: out3
  and and_3 (and_3_out, ~and_2_out, en);  // AND_Gate

  // Notes on the sheet:
  //   req state
  //   contents of rom_1 (hex, n*v repeats v):
  //   0 1
  //   req sym
  //   new sym
  //   new state
endmodule
