// Logisim project wip 3.circ as structural Verilog: 2 circuits, main circuit main
module main (
  input  inc
);

  wire and_1_out, clock_1_out, keyboard_queue_1_p3, or_1_out, res_out;
  wire [4:0] keyboard_queue_1_p7;
  wire [7:0] keyboard_queue_1_p8;

  Button res (.out(res_out));
  Pull_Resistor pull_resistor_1 (.node(res_out));
  Clock clock_1 (.out(clock_1_out));
  // Keyboard_Queue keyboard_queue_1: pin names not known; wires that end beside it: res_out, res_out, keyboard_queue_1_p3, keyboard_queue_1_p3, inc, clock_1_out, keyboard_queue_1_p7, keyboard_queue_1_p8, keyboard_queue_1_p8
  Counter counter_1 (.inc(and_1_out), .res(res_out), .out(keyboard_queue_1_p7));  // open: dec, in, jmp
  or or_1 (or_1_out, keyboard_queue_1_p8[0], keyboard_queue_1_p8[1], keyboard_queue_1_p8[2], keyboard_queue_1_p8[3], keyboard_queue_1_p8[4], keyboard_queue_1_p8[5], keyboard_queue_1_p8[6], keyboard_queue_1_p8[7]);
  and and_1 (and_1_out, inc, or_1_out);
endmodule

module Counter (
  input  dec,
  input  jmp,
  input  inc,
  input  [4:0] in,
  input  res,
  output [4:0] out
);

  wire or_1_out, or_2_out;

  Pull_Resistor pull_resistor_1 (.node(jmp));
  or or_1 (or_1_out, dec, jmp);
  or or_2 (or_2_out, dec, inc);
  Counter_part #(.width(5), .max('h1f)) counter_1 (
    .load(or_1_out), .D(in), .count(or_2_out), .Q(out), .clk(or_2_out), .clr(res));  // open: carry
endmodule
